// Logisim project TeamWork_v1.0.circ as structural Verilog
module \单周期MIPS_单级中断  (
  input  IR1,
  input  IR2,
  input  IR3,
  output RegWrite,
  output MemWrite,
  output [31:0] PC,
  output [31:0] IR,
  output [31:0] RDin,
  output [31:0] MDin,
  output [31:0] LedData
);

  wire and_1_out, and_2_out, and_3_out, and_5_out, and_6_out, and_7_out, CLK, comparator_1_eq, d_ff_1_q,
       decoder_1_out0, decoder_1_out1, decoder_1_out2, ERET, Go, Halt, IR1_t, IR2_t, IR3_t, IRA, IRB, IRC,
       JAL, JR, mips_alu_1_equal, multiplexer_3_out, nIE_q, not_1_out, or_1_out, priority_encoder_1_en_out,
       priority_encoder_1_gs, SignedExt, Syscall, W1, W2, W3, \中断按键参考电路_1_ir_2 , \中断按键参考电路_2_ir_2 ,
       \中断按键参考电路_3_ir_2 , \单周期硬布线控制器_1_alu_src , \单周期硬布线控制器_1_beq , \单周期硬布线控制器_1_bne ,
       \单周期硬布线控制器_1_memtoreg , \单周期硬布线控制器_1_regdst ;
  wire [1:0] or_5_out, priority_encoder_1_out, register_1_q;
  wire [1:1] nor_1_out;
  wire [3:0] \单周期硬布线控制器_1_alu_op ;
  wire [4:0] multiplexer_5_out, multiplexer_6_out, multiplexer_7_out, multiplexer_8_out;
  wire [15:0] \总周期数 , \无条件分支数 , \条件分支成功数 ;
  wire [27:0] adder_1_out;
  wire [31:0] adder_2_out, bit_extender_1_out, bit_extender_2_out, EPC_q, in_PC, mips_alu_1_result,
       multiplexer_2_out, multiplexer_4_out, multiplexer_9_out, multiplexer_12_out, multiplexer_13_out,
       next_PC, R1, ram_1_data, shifter_1_out;
  wire [31:28] adder_1_out_2;

  Clock #(.highDuration(1), .lowDuration(1)) clock_1 (.out(CLK));
  Button _1 (.out(IRA));
  Button _2 (.out(IRB));
  Button _3 (.out(IRC));
  Button \u_继续运行  (.out(Go));
  LED #(.active("true")) led_1 (.in(W1));
  LED #(.active("true")) led_2 (.in(W2));
  LED #(.active("true")) led_3 (.in(W3));
  Hex_Digit_Display hex_digit_display_1 (.value(LedData[31:28]));  // open: dp
  Hex_Digit_Display hex_digit_display_2 (.value(LedData[23:20]));  // open: dp
  Hex_Digit_Display hex_digit_display_3 (.value(LedData[27:24]));  // open: dp
  or or_1 (or_1_out, ~Halt, d_ff_1_q);  // OR_Gate
  Multiplexer #(.select(2), .width(32), .disabled("Z"), .enable("false")) multiplexer_1 (
    .in0({adder_1_out_2, adder_1_out}), .in1(adder_2_out), .in2(multiplexer_2_out), .out(next_PC),
    .sel(or_5_out));  // open: in3
  Multiplexer #(.select(1), .width(32), .disabled("Z"), .enable("false")) multiplexer_2 (
    .in0({adder_1_out_2, IR[25:0], 2'b00}), .in1(R1), .out(multiplexer_2_out), .sel(JR));
  Decoder #(.select(2), .tristate("false"), .disabled("Z"), .enable("false")) decoder_1 (
    .out0(decoder_1_out0), .out1(decoder_1_out1), .out2(decoder_1_out2), .sel(register_1_q));  // open: out3
  Hex_Digit_Display hex_digit_display_4 (.value(LedData[19:16]));  // open: dp
  Hex_Digit_Display hex_digit_display_5 (.value(LedData[15:12]));  // open: dp
  Counter #(.width(16), .max('hffff), .ongoal("wrap"), .trigger("rising"), .behavior("old")) counter_1 (
    .count(or_5_out[0]), .Q(\条件分支成功数 ), .clk(CLK));  // open: load, D, carry, clr, preset
  Counter #(.width(16), .max('hffff), .ongoal("wrap"), .trigger("rising"), .behavior("old")) counter_2 (
    .count(or_5_out[1]), .Q(\无条件分支数 ), .clk(CLK));  // open: load, D, carry, clr, preset
  Register #(.width(32), .trigger("rising"), .Select("low")) u_PC (
    .D(in_PC), .en(or_1_out), .Q(PC), .clk(CLK));  // open: clr
  and and_1 (and_1_out, ERET, decoder_1_out0);
  and and_2 (and_2_out, ERET, decoder_1_out1);
  and and_3 (and_3_out, ERET, decoder_1_out2);
  Hex_Digit_Display hex_digit_display_6 (.value(LedData[11:8]));  // open: dp
  Hex_Digit_Display hex_digit_display_7 (.value(LedData[7:4]));  // open: dp
  // Probe on \总周期数 
  D_Flip_Flop #(.trigger("rising"), .Pre_Clr_Positions("LEGACY"), .NegatePresetClear("false"), .enable("true"), .NewFFLayout("false")) d_ff_1 (
    .clk(CLK), .D(1'b0), .Q(d_ff_1_q), .preset(Go));  // open: Qn, en, reset
  Adder #(.width(32)) adder_1 (.a(PC), .b(32'h4), .out({adder_1_out_2, adder_1_out}));  // open: cin, cout
  \中断按键参考电路  \u_中断按键参考电路_1  (.IR_2(\中断按键参考电路_1_ir_2 ), .Clr(and_1_out), .clk(CLK), .W(W1), .IR(IR1_t));
  \中断按键参考电路  \u_中断按键参考电路_2  (.IR_2(\中断按键参考电路_2_ir_2 ), .Clr(and_2_out), .clk(CLK), .W(W2), .IR(IR2_t));
  \中断按键参考电路  \u_中断按键参考电路_3  (.IR_2(\中断按键参考电路_3_ir_2 ), .Clr(and_3_out), .clk(CLK), .W(W3), .IR(IR3_t));
  Hex_Digit_Display hex_digit_display_8 (.value(LedData[3:0]));  // open: dp
  Adder #(.width(32)) adder_2 (
    .a({adder_1_out_2, adder_1_out}), .b(shifter_1_out), .out(adder_2_out));  // open: cin, cout
  ROM #(.addrWidth(10), .dataWidth(32), .Select("high")) rom_1 (.addr(PC[11:2]), .data(IR));
  Multiplexer #(.select(1), .width(1), .disabled("Z"), .enable("false")) multiplexer_3 (
    .in0(priority_encoder_1_gs), .in1(1'b0), .out(multiplexer_3_out), .sel(ERET));
  or or_2 (IR1_t, IR1, IRA);
  Register #(.width(1), .trigger("rising"), .Select("low")) nIE (
    .D(multiplexer_3_out), .Q(nIE_q), .clk(CLK));  // open: en, clr
  Priority_Encoder #(.select(2), .disabled("Z")) priority_encoder_1 (
    .in0(\中断按键参考电路_1_ir_2 ), .in1(\中断按键参考电路_2_ir_2 ), .in2(\中断按键参考电路_3_ir_2 ), .in3(1'b0),
    .out(priority_encoder_1_out), .gs(priority_encoder_1_gs), .en_out(priority_encoder_1_en_out), .en_in(1'b1));
  Multiplexer #(.select(2), .width(32), .disabled("Z"), .enable("false")) multiplexer_4 (
    .in0(32'h30ac), .in1(32'h3150), .in2(32'h31f4), .out(multiplexer_4_out), .sel(priority_encoder_1_out));  // open: in3
  or or_3 (IR2_t, IR2, IRB);
  \单周期硬布线控制器  \u_单周期硬布线控制器_1  (
    .Func(IR[5:0]), .OP(IR[31:26]), .ALU_OP(\单周期硬布线控制器_1_alu_op ), .MemToReg(\单周期硬布线控制器_1_memtoreg ),
    .MemWrite(MemWrite), .ALU_SRC(\单周期硬布线控制器_1_alu_src ), .RegWrite(RegWrite), .SysCALL(Syscall),
    .SignedExt(SignedExt), .RegDst(\单周期硬布线控制器_1_regdst ), .JR(JR), .JMP(or_5_out[1]),
    .Beq(\单周期硬布线控制器_1_beq ), .JAL(JAL), .Bne(\单周期硬布线控制器_1_bne ), .ERET(ERET));
  Multiplexer #(.select(1), .width(5), .disabled("Z"), .enable("false")) multiplexer_5 (
    .in0(IR[20:16]), .in1(IR[15:11]), .out(multiplexer_5_out), .sel(\单周期硬布线控制器_1_regdst ));
  assign bit_extender_1_out = {{16{1'b0}}, IR[15:0]};  // Bit_Extender bit_extender_1
  assign bit_extender_2_out = {{16{IR[15]}}, IR[15:0]};  // Bit_Extender bit_extender_2
  nor nor_1 (nor_1_out[1], nIE_q, priority_encoder_1_en_out);
  Register #(.width(2), .trigger("rising"), .Select("low")) register_1 (
    .D(priority_encoder_1_out), .en(nor_1_out[1]), .Q(register_1_q), .clk(CLK));  // open: clr
  Multiplexer #(.select(1), .width(5), .disabled("Z"), .enable("false")) multiplexer_6 (
    .in0(IR[25:21]), .in1(5'b00010), .out(multiplexer_6_out), .sel(Syscall));
  Multiplexer #(.select(1), .width(5), .disabled("Z"), .enable("false")) multiplexer_7 (
    .in0(IR[20:16]), .in1(5'b00100), .out(multiplexer_7_out), .sel(Syscall));
  Multiplexer #(.select(1), .width(5), .disabled("Z"), .enable("false")) multiplexer_8 (
    .in0(multiplexer_5_out), .in1({5{1'b1}}), .out(multiplexer_8_out), .sel(JAL));
  Multiplexer #(.select(1), .width(32), .disabled("Z"), .enable("false")) multiplexer_9 (
    .in0(bit_extender_1_out), .in1(bit_extender_2_out), .out(multiplexer_9_out), .sel(SignedExt));
  Shifter #(.width(32), .shift("ll")) shifter_1 (.in(bit_extender_2_out), .\dist (5'b00010), .out(shifter_1_out));
  Register #(.width(32), .trigger("rising"), .Select("low")) EPC (
    .D(next_PC), .en(nor_1_out[1]), .Q(EPC_q), .clk(CLK));  // open: clr
  or or_4 (IR3_t, IR3, IRC);
  not not_1 (not_1_out, Halt);
  MIPS_Regifile mips_regifile_1 (
    .Din(RDin), .Clk(CLK), .R1(R1), .R2(MDin), .WE(RegWrite), .W_num(multiplexer_8_out),
    .R1_num(multiplexer_6_out), .R2_num(multiplexer_7_out));
  Multiplexer #(.select(1), .width(32), .disabled("Z"), .enable("false")) multiplexer_10 (
    .in0(multiplexer_13_out), .in1({adder_1_out_2, adder_1_out}), .out(RDin), .sel(JAL));
  Multiplexer #(.select(2), .width(32), .disabled("Z"), .enable("false")) multiplexer_11 (
    .in0(next_PC), .in1(EPC_q), .in2(multiplexer_4_out), .out(in_PC), .sel({nor_1_out[1], ERET}));  // open: in3
  Counter #(.width(16), .max('hffff), .ongoal("wrap"), .trigger("rising"), .behavior("old")) counter_3 (
    .count(not_1_out), .Q(\总周期数 ), .clk(CLK));  // open: load, D, carry, clr, preset
  Multiplexer #(.select(1), .width(32), .disabled("Z"), .enable("false")) multiplexer_12 (
    .in0(MDin), .in1(multiplexer_9_out), .out(multiplexer_12_out), .sel(\单周期硬布线控制器_1_alu_src ));
  Comparator #(.width(32), .mode("twosComplement")) comparator_1 (
    .a(R1), .b(32'h32), .eq(comparator_1_eq));  // open: gt, lt
  MIPS_ALU mips_alu_1 (
    .X(R1), .Y(multiplexer_12_out), .AluOP(\单周期硬布线控制器_1_alu_op ), .Equal(mips_alu_1_equal),
    .Result(mips_alu_1_result), .shamt(IR[10:6]));  // open: Result_2
  Multiplexer #(.select(1), .width(32), .disabled("Z"), .enable("false")) multiplexer_13 (
    .in0(mips_alu_1_result), .in1(ram_1_data), .out(multiplexer_13_out), .sel(\单周期硬布线控制器_1_memtoreg ));
  and and_4 (Halt, comparator_1_eq, Syscall);
  and and_5 (and_5_out, ~comparator_1_eq, Syscall);  // AND_Gate
  and and_6 (and_6_out, mips_alu_1_equal, \单周期硬布线控制器_1_beq );
  or or_5 (or_5_out[0], and_6_out, and_7_out);
  and and_7 (and_7_out, ~mips_alu_1_equal, \单周期硬布线控制器_1_bne );  // AND_Gate
  Register #(.width(32), .trigger("rising"), .Select("low")) register_2 (
    .D(MDin), .en(and_5_out), .Q(LedData), .clk(CLK));  // open: clr
  RAM #(.addrWidth(10), .dataWidth(32), .bus("separate"), .Select("high")) ram_1 (
    .addr(mips_alu_1_result[11:2]), .din(MDin), .data(ram_1_data), .str(MemWrite), .clk(CLK));  // open: sel, ld, clr

  // Notes on the sheet:
  //   中断源
  //   中断等待指示
  //   总复位信号应将除ROM以外所有存储组件全部清零
  //   数码管输出
  //   数码管输出应该用寄存器锁存，否则显示数据只能一闪而过
  //   instr_index
  //   contents of rom_1 (hex, n*v repeats v):
  //   201d07d0 20100001 109fc0 139fc3 8021 2012000c 24160008 26100001 3210000f 20080008 20090001 139900
  //   2709825 132020 20020022 c 1094022 1500fff9 22100001 2018000f 2188024 108700 20080008 20090001 139902
  //   2709825 132021 20020022 c 1094022 1500fff9 108702 2c9b022 12c00001 8000c07 4020 1084027 84400
  //   3508ffff 82021 20020022 c 8000c01 afa20000 23bd0004 afa40000 23bd0004 afb00000 23bd0004 afb30000
  //   23bd0004 afb40000 23bd0004 afb50000 23bd0004 afb60000 23bd0004 20160001 20140003 20150001 168020
  //   108100 2149825 132020 20020022 c 1600fffa 295a022 1680fff7 23bdfffc 8fb60000 23bdfffc 8fb50000
  //   23bdfffc 8fb40000 23bdfffc 8fb30000 23bdfffc 8fb00000 23bdfffc 8fa40000 23bdfffc 8fa20000 42000018
  //   afa20000 23bd0004 afa40000 23bd0004 afb00000 23bd0004 afb30000 23bd0004 afb40000 23bd0004 afb50000
  //   23bd0004 afb60000 23bd0004 20160002 20140003 20150001 168020 108100 2149825 132020 20020022 c
  //   1600fffa 295a022 1680fff7 23bdfffc 8fb60000 23bdfffc 8fb50000 23bdfffc 8fb40000 23bdfffc 8fb30000
  //   23bdfffc 8fb00000 23bdfffc 8fa40000 23bdfffc 8fa20000 42000018 afa20000 23bd0004 afa40000 23bd0004
  //   afb00000 23bd0004 afb30000 23bd0004 afb40000 23bd0004 afb50000 23bd0004 afb60000 23bd0004 20160003
  //   20140003 20150001 168020 108100 2149825 132020 20020022 c 1600fffa 295a022 1680fff7 23bdfffc
  //   8fb60000 23bdfffc 8fb50000 23bdfffc 8fb40000 23bdfffc 8fb30000 23bdfffc 8fb00000 23bdfffc 8fa40000
  //   23bdfffc 8fa20000 42000018
  //   JMP
  //   JR
  //   OP
  //   Func
  //   rs
  //   rt
  //   rd
  //   imm
  //   sa
  //   Beq
  //   Bne
  //   AluOP
  //   AluSrcB
  //   RegWrite
  //   JAL
  //   RegDst
  //   Syscall
  //   v0
  //   a0
  //   MemToReg
  //   MemWrite
  //   为方便自动评测，需要输出PC，IR，寄存器堆写如数据RDin
  //   RAM写使能MemWrite、RAM写入数据MDin等信号
endmodule

// 单周期硬布线控制器
module \单周期硬布线控制器  (
  input  [5:0] OP,
  input  [5:0] Func,
  output [3:0] ALU_OP,
  output MemToReg,
  output MemWrite,
  output ALU_SRC,
  output RegWrite,
  output SysCALL,
  output SignedExt,
  output RegDst,
  output Beq,
  output Bne,
  output JR,
  output JMP,
  output JAL,
  output ERET
);

  \运算控制器自动生成  \u_运算控制器自动生成_1  (
    .OP0(OP[0]), .OP1(OP[1]), .OP2(OP[2]), .OP3(OP[3]), .OP4(OP[4]), .OP5(OP[5]), .F0(Func[0]), .F1(Func[1]),
    .F2(Func[2]), .F3(Func[3]), .F4(Func[4]), .F5(Func[5]), .S0(ALU_OP[0]), .S1(ALU_OP[1]), .S2(ALU_OP[2]),
    .S3(ALU_OP[3]));
  \控制信号自动生成  \u_控制信号自动生成_1  (
    .OP0(OP[0]), .OP1(OP[1]), .OP2(OP[2]), .OP3(OP[3]), .OP4(OP[4]), .OP5(OP[5]), .F0(Func[0]), .F1(Func[1]),
    .F2(Func[2]), .F3(Func[3]), .F4(Func[4]), .F5(Func[5]), .MemToReg(MemToReg), .MemWrite(MemWrite),
    .ALU_SRC(ALU_SRC), .RegWrite(RegWrite), .SysCALL(SysCALL), .SignedExt(SignedExt), .RegDst(RegDst),
    .BEQ(Beq), .BNE(Bne), .JR(JR), .JMP(JMP), .JAL(JAL), .ERET(ERET));

  // Other names for the same wires on the sheet: OP_CODE[5:0] = OP

  // Notes on the sheet:
  //   运算器控制器，根据指令生成运算器功能选择信号
  //   控制信号生成，产生数据通路需要的其他控制信号
endmodule

// 运算器控制器
module \运算控制器自动生成  (
  input  OP0,
  input  OP1,
  input  OP2,
  input  OP3,
  input  OP4,
  input  OP5,
  input  F0,
  input  F1,
  input  F2,
  input  F3,
  input  F4,
  input  F5,
  output S0,
  output S1,
  output S2,
  output S3
);

  wire and_1_out, and_2_out, and_3_out, and_4_out, and_5_out, and_6_out, and_7_out, and_8_out, and_9_out,
       and_10_out, and_11_out, and_12_out, and_13_out, and_14_out, and_15_out, and_16_out, and_17_out,
       and_18_out, and_19_out, and_20_out, and_21_out, and_22_out, and_23_out, and_24_out, and_25_out,
       and_26_out, and_27_out, and_28_out, and_29_out, and_30_out, and_31_out, and_32_out, and_33_out,
       and_34_out, and_35_out, and_36_out, and_37_out, and_38_out, and_39_out, and_40_out, not_1_out,
       not_2_out, not_3_out, not_4_out, not_5_out, not_6_out, not_7_out, not_8_out, not_9_out, not_10_out,
       not_11_out, not_12_out, not_13_out, not_14_out, not_15_out, not_16_out, not_17_out, not_18_out,
       not_19_out, not_20_out, not_21_out, not_22_out, not_23_out, not_24_out, not_25_out, not_26_out,
       not_27_out, not_28_out, not_29_out, not_30_out, not_31_out, not_32_out, not_33_out, not_34_out,
       not_35_out, not_36_out, not_37_out, not_38_out, not_39_out, not_40_out, not_41_out, not_42_out,
       not_43_out, not_44_out, not_45_out, not_46_out, not_47_out, not_48_out, not_49_out, not_50_out,
       not_51_out, not_52_out, not_53_out, not_54_out, not_55_out, not_56_out, not_57_out, not_58_out,
       not_59_out, not_60_out, not_61_out, not_62_out, not_63_out, not_64_out, not_65_out, not_66_out,
       not_67_out, not_68_out, not_69_out, not_70_out, not_71_out, not_72_out, not_73_out, not_74_out,
       not_75_out, not_76_out, not_77_out, not_78_out, not_79_out, not_80_out, not_81_out, not_82_out,
       not_83_out, not_84_out, not_85_out, not_86_out, not_87_out, not_88_out, not_89_out, not_90_out,
       not_91_out, not_92_out, not_93_out, not_94_out, not_95_out, not_96_out, not_97_out, not_98_out,
       not_99_out, not_100_out, not_101_out, not_102_out, not_103_out, not_104_out, not_105_out, not_106_out,
       not_107_out, not_108_out, not_109_out, not_110_out, not_111_out, not_112_out, not_113_out,
       not_114_out, not_115_out, not_116_out, not_117_out, not_118_out, not_119_out, not_120_out,
       not_121_out, not_122_out, not_123_out, not_124_out, not_125_out, not_126_out, not_127_out,
       not_128_out, not_129_out, not_130_out, not_131_out, not_132_out, not_133_out, not_134_out,
       not_135_out, not_136_out, not_137_out, not_138_out, not_139_out, not_140_out, not_141_out,
       not_142_out, not_143_out, not_144_out, not_145_out, not_146_out, not_147_out, not_148_out,
       not_149_out, not_150_out, not_151_out, not_152_out, not_153_out, not_154_out, not_155_out,
       not_156_out, not_157_out, not_158_out, not_159_out, not_160_out, not_161_out, not_162_out,
       not_163_out, not_164_out, not_165_out, not_166_out, not_167_out, not_168_out, not_169_out,
       not_170_out, not_171_out, not_172_out, not_173_out, not_174_out, not_175_out, not_176_out,
       not_177_out, not_178_out, not_179_out, not_180_out, not_181_out, not_182_out, not_183_out,
       not_184_out, not_185_out, not_186_out, not_187_out, not_188_out, not_189_out, not_190_out,
       not_191_out, not_192_out, not_193_out, not_194_out, not_195_out, not_196_out, not_197_out,
       not_198_out, not_199_out, not_200_out, not_201_out, not_202_out, not_203_out, not_204_out,
       not_205_out, not_206_out, not_207_out, not_208_out, not_209_out, not_210_out, not_211_out,
       not_212_out, not_213_out, not_214_out, not_215_out, not_216_out, not_217_out, not_218_out,
       not_219_out, not_220_out, not_221_out, not_222_out, not_223_out, not_224_out, not_225_out,
       not_226_out, not_227_out, not_228_out, not_229_out, not_230_out, not_231_out, not_232_out,
       not_233_out, not_234_out, not_235_out, not_236_out, not_237_out, not_238_out, not_239_out,
       not_240_out, not_241_out, not_242_out, not_243_out, not_244_out, not_245_out, not_246_out,
       not_247_out, not_248_out, not_249_out, not_250_out, not_251_out, not_252_out, not_253_out,
       not_254_out, not_255_out, not_256_out, not_257_out, not_258_out, not_259_out, not_260_out,
       not_261_out, not_262_out, not_263_out;

  not not_1 (not_1_out, OP5);
  not not_2 (not_2_out, OP4);
  not not_3 (not_3_out, OP3);
  not not_4 (not_4_out, OP2);
  not not_5 (not_5_out, OP1);
  not not_6 (not_6_out, OP0);
  not not_7 (not_7_out, F5);
  not not_8 (not_8_out, F4);
  not not_9 (not_9_out, F3);
  not not_10 (not_10_out, F2);
  not not_11 (not_11_out, OP5);
  not not_12 (not_12_out, OP4);
  not not_13 (not_13_out, OP3);
  not not_14 (not_14_out, OP2);
  not not_15 (not_15_out, OP1);
  not not_16 (not_16_out, OP0);
  not not_17 (not_17_out, F4);
  not not_18 (not_18_out, F3);
  not not_19 (not_19_out, F2);
  not not_20 (not_20_out, F1);
  not not_21 (not_21_out, F0);
  not not_22 (not_22_out, OP5);
  not not_23 (not_23_out, OP4);
  not not_24 (not_24_out, OP3);
  not not_25 (not_25_out, OP2);
  not not_26 (not_26_out, OP1);
  not not_27 (not_27_out, OP0);
  not not_28 (not_28_out, F4);
  not not_29 (not_29_out, F3);
  not not_30 (not_30_out, F2);
  not not_31 (not_31_out, F1);
  not not_32 (not_32_out, OP5);
  not not_33 (not_33_out, OP4);
  not not_34 (not_34_out, OP3);
  not not_35 (not_35_out, OP2);
  not not_36 (not_36_out, OP1);
  not not_37 (not_37_out, OP0);
  not not_38 (not_38_out, F4);
  not not_39 (not_39_out, F3);
  not not_40 (not_40_out, F1);
  not not_41 (not_41_out, F0);
  not not_42 (not_42_out, OP5);
  not not_43 (not_43_out, OP4);
  not not_44 (not_44_out, OP3);
  not not_45 (not_45_out, OP2);
  not not_46 (not_46_out, OP1);
  not not_47 (not_47_out, OP0);
  not not_48 (not_48_out, F4);
  not not_49 (not_49_out, F2);
  not not_50 (not_50_out, F0);
  not not_51 (not_51_out, OP5);
  not not_52 (not_52_out, OP4);
  not not_53 (not_53_out, OP3);
  not not_54 (not_54_out, OP1);
  not not_55 (not_55_out, OP0);
  not not_56 (not_56_out, OP5);
  not not_57 (not_57_out, OP4);
  not not_58 (not_58_out, OP3);
  not not_59 (not_59_out, OP1);
  not not_60 (not_60_out, OP5);
  not not_61 (not_61_out, OP4);
  not not_62 (not_62_out, OP2);
  not not_63 (not_63_out, OP1);
  not not_64 (not_64_out, OP0);
  not not_65 (not_65_out, OP5);
  not not_66 (not_66_out, OP4);
  not not_67 (not_67_out, OP1);
  not not_68 (not_68_out, OP0);
  not not_69 (not_69_out, OP5);
  not not_70 (not_70_out, OP4);
  not not_71 (not_71_out, OP2);
  not not_72 (not_72_out, OP1);
  not not_73 (not_73_out, OP5);
  not not_74 (not_74_out, OP4);
  not not_75 (not_75_out, OP2);
  not not_76 (not_76_out, OP0);
  not not_77 (not_77_out, OP4);
  not not_78 (not_78_out, OP3);
  not not_79 (not_79_out, OP2);
  not not_80 (not_80_out, OP4);
  not not_81 (not_81_out, OP2);
  not not_82 (not_82_out, OP5);
  not not_83 (not_83_out, OP4);
  not not_84 (not_84_out, OP3);
  not not_85 (not_85_out, OP2);
  not not_86 (not_86_out, OP1);
  not not_87 (not_87_out, OP0);
  not not_88 (not_88_out, F5);
  not not_89 (not_89_out, F4);
  not not_90 (not_90_out, F3);
  not not_91 (not_91_out, F2);
  not not_92 (not_92_out, F0);
  not not_93 (not_93_out, OP5);
  not not_94 (not_94_out, OP4);
  not not_95 (not_95_out, OP3);
  not not_96 (not_96_out, OP2);
  not not_97 (not_97_out, OP1);
  not not_98 (not_98_out, OP0);
  not not_99 (not_99_out, F4);
  not not_100 (not_100_out, F3);
  not not_101 (not_101_out, F2);
  not not_102 (not_102_out, F0);
  not not_103 (not_103_out, OP5);
  not not_104 (not_104_out, OP4);
  not not_105 (not_105_out, OP3);
  not not_106 (not_106_out, OP2);
  not not_107 (not_107_out, OP1);
  not not_108 (not_108_out, OP0);
  not not_109 (not_109_out, F4);
  not not_110 (not_110_out, F3);
  not not_111 (not_111_out, F1);
  not not_112 (not_112_out, F0);
  not not_113 (not_113_out, OP5);
  not not_114 (not_114_out, OP4);
  not not_115 (not_115_out, OP3);
  not not_116 (not_116_out, OP2);
  not not_117 (not_117_out, OP1);
  not not_118 (not_118_out, OP0);
  not not_119 (not_119_out, F4);
  not not_120 (not_120_out, F3);
  not not_121 (not_121_out, OP5);
  not not_122 (not_122_out, OP4);
  not not_123 (not_123_out, OP3);
  not not_124 (not_124_out, OP2);
  not not_125 (not_125_out, OP1);
  not not_126 (not_126_out, OP0);
  not not_127 (not_127_out, F4);
  not not_128 (not_128_out, F2);
  not not_129 (not_129_out, F0);
  not not_130 (not_130_out, OP5);
  not not_131 (not_131_out, OP4);
  not not_132 (not_132_out, OP3);
  not not_133 (not_133_out, OP1);
  not not_134 (not_134_out, OP0);
  not not_135 (not_135_out, OP5);
  not not_136 (not_136_out, OP4);
  not not_137 (not_137_out, OP3);
  not not_138 (not_138_out, OP1);
  not not_139 (not_139_out, OP5);
  not not_140 (not_140_out, OP4);
  not not_141 (not_141_out, OP1);
  not not_142 (not_142_out, OP0);
  not not_143 (not_143_out, OP5);
  not not_144 (not_144_out, OP4);
  not not_145 (not_145_out, OP2);
  not not_146 (not_146_out, OP0);
  not not_147 (not_147_out, OP5);
  not not_148 (not_148_out, OP4);
  not not_149 (not_149_out, OP3);
  not not_150 (not_150_out, OP2);
  not not_151 (not_151_out, OP1);
  not not_152 (not_152_out, OP0);
  not not_153 (not_153_out, F4);
  not not_154 (not_154_out, F3);
  not not_155 (not_155_out, F2);
  not not_156 (not_156_out, F1);
  not not_157 (not_157_out, F0);
  not not_158 (not_158_out, OP5);
  not not_159 (not_159_out, OP4);
  not not_160 (not_160_out, OP3);
  not not_161 (not_161_out, OP2);
  not not_162 (not_162_out, OP1);
  not not_163 (not_163_out, OP0);
  not not_164 (not_164_out, F4);
  not not_165 (not_165_out, F3);
  not not_166 (not_166_out, F2);
  not not_167 (not_167_out, F1);
  not not_168 (not_168_out, OP5);
  not not_169 (not_169_out, OP4);
  not not_170 (not_170_out, OP3);
  not not_171 (not_171_out, OP2);
  not not_172 (not_172_out, OP1);
  not not_173 (not_173_out, OP0);
  not not_174 (not_174_out, F4);
  not not_175 (not_175_out, F3);
  not not_176 (not_176_out, F2);
  not not_177 (not_177_out, F0);
  not not_178 (not_178_out, OP5);
  not not_179 (not_179_out, OP4);
  not not_180 (not_180_out, OP3);
  not not_181 (not_181_out, OP2);
  not not_182 (not_182_out, OP1);
  not not_183 (not_183_out, OP0);
  not not_184 (not_184_out, F4);
  not not_185 (not_185_out, F3);
  not not_186 (not_186_out, F1);
  not not_187 (not_187_out, F0);
  not not_188 (not_188_out, OP5);
  not not_189 (not_189_out, OP4);
  not not_190 (not_190_out, OP3);
  not not_191 (not_191_out, OP2);
  not not_192 (not_192_out, OP1);
  not not_193 (not_193_out, OP0);
  not not_194 (not_194_out, F4);
  not not_195 (not_195_out, F2);
  not not_196 (not_196_out, OP5);
  not not_197 (not_197_out, OP4);
  not not_198 (not_198_out, OP2);
  not not_199 (not_199_out, OP1);
  not not_200 (not_200_out, OP0);
  not not_201 (not_201_out, OP5);
  not not_202 (not_202_out, OP4);
  not not_203 (not_203_out, OP1);
  not not_204 (not_204_out, OP0);
  not not_205 (not_205_out, OP5);
  not not_206 (not_206_out, OP4);
  not not_207 (not_207_out, OP2);
  not not_208 (not_208_out, OP1);
  not not_209 (not_209_out, OP4);
  not not_210 (not_210_out, OP3);
  not not_211 (not_211_out, OP2);
  not not_212 (not_212_out, OP4);
  not not_213 (not_213_out, OP2);
  not not_214 (not_214_out, OP5);
  not not_215 (not_215_out, OP4);
  not not_216 (not_216_out, OP3);
  not not_217 (not_217_out, OP2);
  not not_218 (not_218_out, OP1);
  not not_219 (not_219_out, OP0);
  not not_220 (not_220_out, F4);
  not not_221 (not_221_out, F3);
  not not_222 (not_222_out, F1);
  not not_223 (not_223_out, OP5);
  not not_224 (not_224_out, OP4);
  not not_225 (not_225_out, OP3);
  not not_226 (not_226_out, OP2);
  not not_227 (not_227_out, OP1);
  not not_228 (not_228_out, OP0);
  not not_229 (not_229_out, F4);
  not not_230 (not_230_out, F3);
  not not_231 (not_231_out, OP5);
  not not_232 (not_232_out, OP4);
  not not_233 (not_233_out, OP3);
  not not_234 (not_234_out, OP2);
  not not_235 (not_235_out, OP1);
  not not_236 (not_236_out, OP0);
  not not_237 (not_237_out, F4);
  not not_238 (not_238_out, F2);
  not not_239 (not_239_out, F0);
  not not_240 (not_240_out, OP5);
  not not_241 (not_241_out, OP4);
  not not_242 (not_242_out, OP3);
  not not_243 (not_243_out, OP2);
  not not_244 (not_244_out, OP1);
  not not_245 (not_245_out, OP0);
  not not_246 (not_246_out, F4);
  not not_247 (not_247_out, F2);
  not not_248 (not_248_out, OP5);
  not not_249 (not_249_out, OP4);
  not not_250 (not_250_out, OP3);
  not not_251 (not_251_out, OP1);
  not not_252 (not_252_out, OP0);
  not not_253 (not_253_out, OP5);
  not not_254 (not_254_out, OP4);
  not not_255 (not_255_out, OP3);
  not not_256 (not_256_out, OP1);
  not not_257 (not_257_out, OP5);
  not not_258 (not_258_out, OP4);
  not not_259 (not_259_out, OP2);
  not not_260 (not_260_out, OP0);
  not not_261 (not_261_out, OP5);
  not not_262 (not_262_out, OP4);
  not not_263 (not_263_out, OP1);
  and and_1 (and_1_out, not_1_out, not_2_out, not_3_out, not_4_out, not_5_out, not_6_out, not_7_out, not_8_out, not_9_out, not_10_out, F1, F0);
  and and_2 (and_2_out, not_11_out, not_12_out, not_13_out, not_14_out, not_15_out, not_16_out, F5, not_17_out, not_18_out, not_19_out, not_20_out, not_21_out);
  and and_3 (and_3_out, not_22_out, not_23_out, not_24_out, not_25_out, not_26_out, not_27_out, F5, not_28_out, not_29_out, not_30_out, not_31_out, F0);
  and and_4 (and_4_out, not_32_out, not_33_out, not_34_out, not_35_out, not_36_out, not_37_out, F5, not_38_out, not_39_out, F2, not_40_out, not_41_out);
  and and_5 (and_5_out, not_42_out, not_43_out, not_44_out, not_45_out, not_46_out, not_47_out, F5, not_48_out, F3, not_49_out, F1, not_50_out);
  and and_6 (and_6_out, not_51_out, not_52_out, not_53_out, OP2, not_54_out, not_55_out);
  and and_7 (and_7_out, not_56_out, not_57_out, not_58_out, OP2, not_59_out, OP0);
  and and_8 (and_8_out, not_60_out, not_61_out, OP3, not_62_out, not_63_out, not_64_out);
  and and_9 (and_9_out, not_65_out, not_66_out, OP3, OP2, not_67_out, not_68_out);
  and and_10 (and_10_out, not_69_out, not_70_out, OP3, not_71_out, not_72_out, OP0);
  and and_11 (and_11_out, not_73_out, not_74_out, OP3, not_75_out, OP1, not_76_out);
  and and_12 (and_12_out, OP5, not_77_out, not_78_out, not_79_out, OP1, OP0);
  and and_13 (and_13_out, OP5, not_80_out, OP3, not_81_out, OP1, OP0);
  and and_14 (and_14_out, not_82_out, not_83_out, not_84_out, not_85_out, not_86_out, not_87_out, not_88_out, not_89_out, not_90_out, not_91_out, F1, not_92_out);
  and and_15 (and_15_out, not_93_out, not_94_out, not_95_out, not_96_out, not_97_out, not_98_out, F5, not_99_out, not_100_out, not_101_out, F1, not_102_out);
  and and_16 (and_16_out, not_103_out, not_104_out, not_105_out, not_106_out, not_107_out, not_108_out, F5, not_109_out, not_110_out, F2, not_111_out, not_112_out);
  and and_17 (and_17_out, not_113_out, not_114_out, not_115_out, not_116_out, not_117_out, not_118_out, F5, not_119_out, not_120_out, F2, F1, F0);
  and and_18 (and_18_out, not_121_out, not_122_out, not_123_out, not_124_out, not_125_out, not_126_out, F5, not_127_out, F3, not_128_out, F1, not_129_out);
  and and_19 (and_19_out, not_130_out, not_131_out, not_132_out, OP2, not_133_out, not_134_out);
  and and_20 (and_20_out, not_135_out, not_136_out, not_137_out, OP2, not_138_out, OP0);
  and and_21 (and_21_out, not_139_out, not_140_out, OP3, OP2, not_141_out, not_142_out);
  and and_22 (and_22_out, not_143_out, not_144_out, OP3, not_145_out, OP1, not_146_out);
  and and_23 (and_23_out, not_147_out, not_148_out, not_149_out, not_150_out, not_151_out, not_152_out, F5, not_153_out, not_154_out, not_155_out, not_156_out, not_157_out);
  and and_24 (and_24_out, not_158_out, not_159_out, not_160_out, not_161_out, not_162_out, not_163_out, F5, not_164_out, not_165_out, not_166_out, not_167_out, F0);
  and and_25 (and_25_out, not_168_out, not_169_out, not_170_out, not_171_out, not_172_out, not_173_out, F5, not_174_out, not_175_out, not_176_out, F1, not_177_out);
  and and_26 (and_26_out, not_178_out, not_179_out, not_180_out, not_181_out, not_182_out, not_183_out, F5, not_184_out, not_185_out, F2, not_186_out, not_187_out);
  and and_27 (and_27_out, not_188_out, not_189_out, not_190_out, not_191_out, not_192_out, not_193_out, F5, not_194_out, F3, not_195_out, F1, F0);
  and and_28 (and_28_out, not_196_out, not_197_out, OP3, not_198_out, not_199_out, not_200_out);
  and and_29 (and_29_out, not_201_out, not_202_out, OP3, OP2, not_203_out, not_204_out);
  and and_30 (and_30_out, not_205_out, not_206_out, OP3, not_207_out, not_208_out, OP0);
  and and_31 (and_31_out, OP5, not_209_out, not_210_out, not_211_out, OP1, OP0);
  and and_32 (and_32_out, OP5, not_212_out, OP3, not_213_out, OP1, OP0);
  and and_33 (and_33_out, not_214_out, not_215_out, not_216_out, not_217_out, not_218_out, not_219_out, F5, not_220_out, not_221_out, F2, not_222_out, F0);
  and and_34 (and_34_out, not_223_out, not_224_out, not_225_out, not_226_out, not_227_out, not_228_out, F5, not_229_out, not_230_out, F2, F1, F0);
  and and_35 (and_35_out, not_231_out, not_232_out, not_233_out, not_234_out, not_235_out, not_236_out, F5, not_237_out, F3, not_238_out, F1, not_239_out);
  and and_36 (and_36_out, not_240_out, not_241_out, not_242_out, not_243_out, not_244_out, not_245_out, F5, not_246_out, F3, not_247_out, F1, F0);
  and and_37 (and_37_out, not_248_out, not_249_out, not_250_out, OP2, not_251_out, not_252_out);
  and and_38 (and_38_out, not_253_out, not_254_out, not_255_out, OP2, not_256_out, OP0);
  and and_39 (and_39_out, not_257_out, not_258_out, OP3, not_259_out, OP1, not_260_out);
  and and_40 (and_40_out, not_261_out, not_262_out, OP3, OP2, not_263_out, OP0);
  or or_1 (S1, and_14_out, and_15_out, and_16_out, and_17_out, and_18_out, and_19_out, and_20_out, and_21_out, and_22_out);
  or or_2 (S2, and_23_out, and_24_out, and_25_out, and_26_out, and_27_out, and_28_out, and_29_out, and_30_out, and_31_out, and_32_out);
  or or_3 (S3, and_33_out, and_34_out, and_35_out, and_36_out, and_37_out, and_38_out, and_39_out, and_40_out);
  or or_4 (S0, and_1_out, and_2_out, and_3_out, and_4_out, and_5_out, and_6_out, and_7_out, and_8_out, and_9_out, and_10_out, and_11_out, and_12_out, and_13_out);
endmodule

// 控制信号生成
module \控制信号自动生成  (
  input  OP0,
  input  OP1,
  input  OP2,
  input  OP3,
  input  OP4,
  input  OP5,
  input  F0,
  input  F1,
  input  F2,
  input  F3,
  input  F4,
  input  F5,
  output MemToReg,
  output MemWrite,
  output ALU_SRC,
  output RegWrite,
  output SysCALL,
  output SignedExt,
  output RegDst,
  output BEQ,
  output BNE,
  output JR,
  output JMP,
  output JAL,
  output ERET
);

  wire and_3_out, and_4_out, and_5_out, and_6_out, and_7_out, and_8_out, and_9_out, and_10_out, and_11_out,
       and_12_out, and_13_out, and_15_out, and_16_out, and_17_out, and_18_out, and_19_out, and_20_out,
       and_21_out, and_25_out, and_26_out, not_1_out, not_2_out, not_3_out, not_4_out, not_5_out, not_6_out,
       not_7_out, not_8_out, not_9_out, not_10_out, not_11_out, not_12_out, not_13_out, not_14_out,
       not_15_out, not_16_out, not_17_out, not_18_out, not_19_out, not_20_out, not_21_out, not_22_out,
       not_23_out, not_24_out, not_25_out, not_26_out, not_27_out, not_28_out, not_29_out, not_30_out,
       not_31_out, not_32_out, not_33_out, not_34_out, not_35_out, not_36_out, not_37_out, not_38_out,
       not_39_out, not_40_out, not_41_out, not_42_out, not_43_out, not_44_out, not_45_out, not_46_out,
       not_47_out, not_48_out, not_49_out, not_50_out, not_51_out, not_52_out, not_53_out, not_54_out,
       not_55_out, not_56_out, not_57_out, not_58_out, not_59_out, not_60_out, not_61_out, not_62_out,
       not_63_out, not_64_out, not_65_out, not_66_out, not_67_out, not_68_out, not_69_out, not_70_out,
       not_71_out, not_72_out, not_73_out, not_74_out, not_75_out, not_76_out, not_77_out, not_78_out,
       not_79_out, not_80_out, not_81_out, not_82_out, not_83_out, not_84_out, not_85_out, not_86_out,
       not_87_out, not_88_out, not_89_out, not_90_out, not_91_out, not_92_out, not_93_out, not_94_out,
       not_95_out, not_96_out, not_97_out, not_98_out, not_99_out, not_100_out, not_101_out, not_102_out,
       not_103_out, not_104_out, not_105_out, not_106_out, not_107_out, not_108_out, not_109_out,
       not_110_out, not_111_out, not_112_out, not_113_out, not_114_out, not_115_out, not_116_out,
       not_117_out, not_118_out, not_119_out, not_120_out, not_121_out, not_122_out, not_123_out,
       not_124_out, not_125_out, not_126_out, not_127_out, not_128_out, not_129_out, not_130_out,
       not_131_out, not_132_out, not_133_out, not_134_out, not_135_out, not_136_out, not_137_out,
       not_138_out, not_139_out, not_140_out, not_141_out, not_142_out, not_143_out, not_144_out,
       not_145_out, not_146_out, not_147_out, not_148_out, not_149_out, not_150_out, not_151_out,
       not_152_out, not_153_out, not_154_out, not_155_out, not_156_out, not_157_out, not_158_out,
       not_159_out, not_160_out, not_161_out, not_162_out, not_163_out, not_164_out, not_165_out,
       not_166_out, not_167_out, not_168_out, not_169_out, not_170_out, not_171_out, not_172_out,
       not_173_out, not_174_out;

  not not_1 (not_1_out, OP2);
  not not_2 (not_2_out, OP3);
  not not_3 (not_3_out, OP4);
  not not_4 (not_4_out, OP2);
  not not_5 (not_5_out, OP4);
  not not_6 (not_6_out, OP0);
  not not_7 (not_7_out, OP2);
  not not_8 (not_8_out, OP4);
  not not_9 (not_9_out, OP5);
  not not_10 (not_10_out, OP1);
  not not_11 (not_11_out, OP4);
  not not_12 (not_12_out, OP5);
  not not_13 (not_13_out, OP2);
  not not_14 (not_14_out, OP4);
  not not_15 (not_15_out, OP0);
  not not_16 (not_16_out, OP1);
  not not_17 (not_17_out, OP2);
  not not_18 (not_18_out, OP4);
  not not_19 (not_19_out, OP5);
  not not_20 (not_20_out, F0);
  not not_21 (not_21_out, F2);
  not not_22 (not_22_out, F3);
  not not_23 (not_23_out, F4);
  not not_24 (not_24_out, OP0);
  not not_25 (not_25_out, OP1);
  not not_26 (not_26_out, OP2);
  not not_27 (not_27_out, OP4);
  not not_28 (not_28_out, OP5);
  not not_29 (not_29_out, F1);
  not not_30 (not_30_out, F3);
  not not_31 (not_31_out, F4);
  not not_32 (not_32_out, OP0);
  not not_33 (not_33_out, OP1);
  not not_34 (not_34_out, OP2);
  not not_35 (not_35_out, OP4);
  not not_36 (not_36_out, OP5);
  not not_37 (not_37_out, F2);
  not not_38 (not_38_out, F3);
  not not_39 (not_39_out, F4);
  not not_40 (not_40_out, F5);
  not not_41 (not_41_out, OP0);
  not not_42 (not_42_out, OP1);
  not not_43 (not_43_out, OP2);
  not not_44 (not_44_out, OP4);
  not not_45 (not_45_out, OP5);
  not not_46 (not_46_out, F2);
  not not_47 (not_47_out, F4);
  not not_48 (not_48_out, OP0);
  not not_49 (not_49_out, OP1);
  not not_50 (not_50_out, OP2);
  not not_51 (not_51_out, OP4);
  not not_52 (not_52_out, OP5);
  not not_53 (not_53_out, F3);
  not not_54 (not_54_out, F4);
  not not_55 (not_55_out, OP0);
  not not_56 (not_56_out, OP2);
  not not_57 (not_57_out, OP4);
  not not_58 (not_58_out, OP5);
  not not_59 (not_59_out, OP1);
  not not_60 (not_60_out, OP4);
  not not_61 (not_61_out, OP5);
  not not_62 (not_62_out, OP2);
  not not_63 (not_63_out, OP3);
  not not_64 (not_64_out, OP4);
  not not_65 (not_65_out, OP0);
  not not_66 (not_66_out, OP1);
  not not_67 (not_67_out, OP2);
  not not_68 (not_68_out, OP3);
  not not_69 (not_69_out, OP4);
  not not_70 (not_70_out, OP5);
  not not_71 (not_71_out, F0);
  not not_72 (not_72_out, F1);
  not not_73 (not_73_out, F4);
  not not_74 (not_74_out, F5);
  not not_75 (not_75_out, OP0);
  not not_76 (not_76_out, OP2);
  not not_77 (not_77_out, OP4);
  not not_78 (not_78_out, OP5);
  not not_79 (not_79_out, OP1);
  not not_80 (not_80_out, OP3);
  not not_81 (not_81_out, OP4);
  not not_82 (not_82_out, OP5);
  not not_83 (not_83_out, OP0);
  not not_84 (not_84_out, OP1);
  not not_85 (not_85_out, OP2);
  not not_86 (not_86_out, OP3);
  not not_87 (not_87_out, OP4);
  not not_88 (not_88_out, OP5);
  not not_89 (not_89_out, F0);
  not not_90 (not_90_out, F2);
  not not_91 (not_91_out, F3);
  not not_92 (not_92_out, F4);
  not not_93 (not_93_out, OP0);
  not not_94 (not_94_out, OP1);
  not not_95 (not_95_out, OP2);
  not not_96 (not_96_out, OP3);
  not not_97 (not_97_out, OP4);
  not not_98 (not_98_out, OP5);
  not not_99 (not_99_out, F1);
  not not_100 (not_100_out, F3);
  not not_101 (not_101_out, F4);
  not not_102 (not_102_out, OP0);
  not not_103 (not_103_out, OP1);
  not not_104 (not_104_out, OP2);
  not not_105 (not_105_out, OP3);
  not not_106 (not_106_out, OP4);
  not not_107 (not_107_out, OP5);
  not not_108 (not_108_out, F2);
  not not_109 (not_109_out, F3);
  not not_110 (not_110_out, F4);
  not not_111 (not_111_out, F5);
  not not_112 (not_112_out, OP0);
  not not_113 (not_113_out, OP1);
  not not_114 (not_114_out, OP2);
  not not_115 (not_115_out, OP3);
  not not_116 (not_116_out, OP4);
  not not_117 (not_117_out, OP5);
  not not_118 (not_118_out, F2);
  not not_119 (not_119_out, F4);
  not not_120 (not_120_out, OP0);
  not not_121 (not_121_out, OP1);
  not not_122 (not_122_out, OP2);
  not not_123 (not_123_out, OP3);
  not not_124 (not_124_out, OP4);
  not not_125 (not_125_out, OP5);
  not not_126 (not_126_out, F3);
  not not_127 (not_127_out, F4);
  not not_128 (not_128_out, OP0);
  not not_129 (not_129_out, OP1);
  not not_130 (not_130_out, OP3);
  not not_131 (not_131_out, OP4);
  not not_132 (not_132_out, OP5);
  not not_133 (not_133_out, OP1);
  not not_134 (not_134_out, OP3);
  not not_135 (not_135_out, OP4);
  not not_136 (not_136_out, OP5);
  not not_137 (not_137_out, OP0);
  not not_138 (not_138_out, OP1);
  not not_139 (not_139_out, OP2);
  not not_140 (not_140_out, OP3);
  not not_141 (not_141_out, OP4);
  not not_142 (not_142_out, OP5);
  not not_143 (not_143_out, F0);
  not not_144 (not_144_out, F1);
  not not_145 (not_145_out, F2);
  not not_146 (not_146_out, F4);
  not not_147 (not_147_out, F5);
  not not_148 (not_148_out, OP0);
  not not_149 (not_149_out, OP2);
  not not_150 (not_150_out, OP3);
  not not_151 (not_151_out, OP4);
  not not_152 (not_152_out, OP5);
  not not_153 (not_153_out, F0);
  not not_154 (not_154_out, F1);
  not not_155 (not_155_out, F2);
  not not_156 (not_156_out, F4);
  not not_157 (not_157_out, F5);
  not not_158 (not_158_out, OP2);
  not not_159 (not_159_out, OP3);
  not not_160 (not_160_out, OP4);
  not not_161 (not_161_out, OP5);
  not not_162 (not_162_out, OP2);
  not not_163 (not_163_out, OP3);
  not not_164 (not_164_out, OP4);
  not not_165 (not_165_out, OP5);
  not not_166 (not_166_out, OP5);
  not not_167 (not_167_out, OP3);
  not not_168 (not_168_out, OP2);
  not not_169 (not_169_out, OP1);
  not not_170 (not_170_out, OP0);
  not not_171 (not_171_out, F5);
  not not_172 (not_172_out, F2);
  not not_173 (not_173_out, F1);
  not not_174 (not_174_out, F0);
  and and_1 (MemToReg, OP0, OP1, not_1_out, not_2_out, not_3_out, OP5);
  and and_2 (MemWrite, OP0, OP1, not_4_out, OP3, not_5_out, OP5);
  and and_3 (and_3_out, not_6_out, not_7_out, OP3, not_8_out, not_9_out);
  and and_4 (and_4_out, not_10_out, OP3, not_11_out, not_12_out);
  or or_1 (ALU_SRC, and_3_out, and_4_out, and_5_out);
  and and_5 (and_5_out, OP0, OP1, not_13_out, not_14_out, OP5);
  and and_6 (and_6_out, not_15_out, not_16_out, not_17_out, not_18_out, not_19_out, not_20_out, not_21_out, not_22_out, not_23_out);
  and and_7 (and_7_out, not_24_out, not_25_out, not_26_out, not_27_out, not_28_out, not_29_out, not_30_out, not_31_out, F5);
  and and_8 (and_8_out, not_32_out, not_33_out, not_34_out, not_35_out, not_36_out, F1, not_37_out, not_38_out, not_39_out, not_40_out);
  and and_9 (and_9_out, not_41_out, not_42_out, not_43_out, not_44_out, not_45_out, F1, not_46_out, F3, not_47_out, F5);
  and and_10 (and_10_out, not_48_out, not_49_out, not_50_out, not_51_out, not_52_out, F0, F2, not_53_out, not_54_out, F5);
  and and_11 (and_11_out, not_55_out, not_56_out, OP3, not_57_out, not_58_out);
  and and_12 (and_12_out, not_59_out, OP3, not_60_out, not_61_out);
  and and_13 (and_13_out, OP0, OP1, not_62_out, not_63_out, not_64_out);
  and and_14 (SysCALL, not_65_out, not_66_out, not_67_out, not_68_out, not_69_out, not_70_out, not_71_out, not_72_out, F2, F3, not_73_out, not_74_out);
  and and_15 (and_15_out, not_75_out, not_76_out, OP3, not_77_out, not_78_out);
  or or_2 (SignedExt, and_15_out, and_16_out);
  and and_16 (and_16_out, not_79_out, OP2, not_80_out, not_81_out, not_82_out);
  and and_17 (and_17_out, not_83_out, not_84_out, not_85_out, not_86_out, not_87_out, not_88_out, not_89_out, not_90_out, not_91_out, not_92_out);
  and and_18 (and_18_out, not_93_out, not_94_out, not_95_out, not_96_out, not_97_out, not_98_out, not_99_out, not_100_out, not_101_out, F5);
  and and_19 (and_19_out, not_102_out, not_103_out, not_104_out, not_105_out, not_106_out, not_107_out, F1, not_108_out, not_109_out, not_110_out, not_111_out);
  and and_20 (and_20_out, not_112_out, not_113_out, not_114_out, not_115_out, not_116_out, not_117_out, F1, not_118_out, F3, not_119_out, F5);
  and and_21 (and_21_out, not_120_out, not_121_out, not_122_out, not_123_out, not_124_out, not_125_out, F0, F2, not_126_out, not_127_out, F5);
  and and_22 (BEQ, not_128_out, not_129_out, OP2, not_130_out, not_131_out, not_132_out);
  and and_23 (BNE, OP0, not_133_out, OP2, not_134_out, not_135_out, not_136_out);
  and and_24 (JR, not_137_out, not_138_out, not_139_out, not_140_out, not_141_out, not_142_out, not_143_out, not_144_out, not_145_out, F3, not_146_out, not_147_out);
  and and_25 (and_25_out, not_148_out, not_149_out, not_150_out, not_151_out, not_152_out, not_153_out, not_154_out, not_155_out, F3, not_156_out, not_157_out);
  and and_26 (and_26_out, OP1, not_158_out, not_159_out, not_160_out, not_161_out);
  and and_27 (JAL, OP0, OP1, not_162_out, not_163_out, not_164_out, not_165_out);
  and and_28 (ERET, not_166_out, OP4, not_167_out, not_168_out, not_169_out, not_170_out, not_171_out, F4, F3, not_172_out, not_173_out, not_174_out);
  or or_3 (RegWrite, and_6_out, and_7_out, and_8_out, and_9_out, and_10_out, and_11_out, and_12_out, and_13_out);
  or or_4 (RegDst, and_17_out, and_18_out, and_19_out, and_20_out, and_21_out);
  or or_5 (JMP, and_25_out, and_26_out);
endmodule

// ALU
module MIPS_ALU (
  input  [4:0] shamt,
  input  [31:0] X,
  input  [31:0] Y,
  input  [3:0] AluOP,
  output Equal,
  output [31:0] Result,
  output [31:0] Result_2
);

  wire [0:0] comparator_1_lt, comparator_2_lt;
  wire [31:0] adder_1_out, AND_out, divider_1_out, divider_1_rem, multiplier_1_cout, multiplier_1_out,
       NOR_out, OR_out, shifter_1_out, shifter_2_out, shifter_3_out, subtractor_1_out, XOR_out;

  assign AND_out = X & Y;  // AND_Gate AND, 32 bits wide
  assign OR_out = X | Y;  // OR_Gate OR, 32 bits wide
  Shifter #(.width(32), .shift("ll")) shifter_1 (.in(Y), .\dist (shamt), .out(shifter_1_out));
  Shifter #(.width(32), .shift("ar")) shifter_2 (.in(Y), .\dist (shamt), .out(shifter_2_out));
  Shifter #(.width(32), .shift("lr")) shifter_3 (.in(Y), .\dist (shamt), .out(shifter_3_out));
  Multiplier #(.width(32)) multiplier_1 (.a(X), .b(Y), .out(multiplier_1_out), .cout(multiplier_1_cout));  // open: cin
  Divider #(.width(32)) divider_1 (.a(X), .b(Y), .out(divider_1_out), .rem(divider_1_rem));  // open: upper
  Adder #(.width(32)) adder_1 (.a(X), .b(Y), .out(adder_1_out));  // open: cin, cout
  Subtractor #(.width(32)) subtractor_1 (.a(X), .b(Y), .out(subtractor_1_out));  // open: bin, bout
  assign XOR_out = X ^ Y;  // XOR_Gate XOR, 32 bits wide
  assign NOR_out = ~(X | Y);  // NOR_Gate NOR, 32 bits wide
  Comparator #(.width(32), .mode("twosComplement")) comparator_1 (
    .a(X), .b(Y), .eq(Equal), .lt(comparator_1_lt[0]));  // open: gt
  Comparator #(.width(32), .mode("unsigned")) comparator_2 (.a(X), .b(Y), .lt(comparator_2_lt[0]));  // open: gt, eq
  Multiplexer #(.select(4), .width(32), .disabled("Z"), .enable("false")) multiplexer_1 (
    .in0(shifter_1_out), .in1(shifter_2_out), .in2(shifter_3_out), .in3(multiplier_1_out),
    .in4(divider_1_out), .in5(adder_1_out), .in6(subtractor_1_out), .in7(AND_out), .in8(OR_out),
    .in9(XOR_out), .in10(NOR_out), .in11({{31{1'b0}}, comparator_1_lt[0]}),
    .in12({{31{1'b0}}, comparator_2_lt[0]}), .in13({32{1'b0}}), .in14({32{1'b0}}), .in15({32{1'b0}}),
    .out(Result), .sel(AluOP));
  Multiplexer #(.select(4), .width(32), .disabled("Z"), .enable("false")) multiplexer_2 (
    .in0({32{1'b0}}), .in1({32{1'b0}}), .in2({32{1'b0}}), .in3(multiplier_1_cout), .in4(divider_1_rem),
    .in5({32{1'b0}}), .in6({32{1'b0}}), .in7({32{1'b0}}), .in8({32{1'b0}}), .in9({32{1'b0}}),
    .in10({32{1'b0}}), .in11({32{1'b0}}), .in12({32{1'b0}}), .in13({32{1'b0}}), .in14({32{1'b0}}),
    .in15({32{1'b0}}), .out(Result_2), .sel(AluOP));

  // Other names for the same wires on the sheet: Result2[31:0] = Result_2; S[3:0] = AluOP

  // Notes on the sheet:
  //   不要改变此引脚区域内容，也不要改变ALU封装形式
  //   输入引脚
  //   输出引脚
endmodule

module MIPS_Regifile (
  input  [31:0] Din,
  input  Clk,
  input  WE,
  input  [4:0] R1_num,
  input  [4:0] W_num,
  input  [4:0] R2_num,
  output [31:0] R1,
  output [31:0] R2
);

  // RegisterFile registerfile_1: pin names not known; wires that end beside it: Din, Clk, WE, W_num, R1_num, R2_num, R1, R2
endmodule

module \理想流水线  (
  output RegWrite,
  output MemWrite,
  output [31:0] IF_PC,
  output [31:0] ID_PC,
  output [31:0] EX_PC,
  output [31:0] M_PC,
  output [31:0] WB_PC,
  output [31:0] RDin,
  output [31:0] MDin,
  output [31:0] LedData
);

  wire AluSrcB, and_1_out, and_2_out, Beq, Bne, CLK, comparator_1_eq, d_ff_1_q, ex_mem_1_halt_2,
       ex_mem_1_jal_2, ex_mem_1_memtoreg_2, ex_mem_1_regwrite_2, Go, Halt, id_ex_1_alusrcb_2, id_ex_1_jal_2,
       id_ex_1_memtoreg_2, id_ex_1_memwrite_2, id_ex_1_regwrite_2, ID_MemWrite, ID_RegWrite, IR1, IR2, IR3,
       JAL, JMP, JR, mem_wb_1_memtoreg_2, MemToReg, not_1_out, or_1_out, RST, SignedExt, Syscall, W1, W2, W3,
       \单周期硬布线控制器_1_regdst , \单周期硬布线控制器_1_syscall ;
  wire [3:0] AluOP, id_ex_1_aluop_2;
  wire [4:0] ex_mem_1_w_num_2, id_ex_1_ir_2_2, id_ex_1_w_num_2, multiplexer_1_out, multiplexer_2_out,
       multiplexer_3_out, W_num;
  wire [15:0] \LoadUse次数 , \总周期数 , \插入气泡数 , \无条件分支数 , \条件分支成功数 ;
  wire [31:0] adder_1_out, bit_extender_1_out, bit_extender_2_out, ex_mem_1_alu_2, ex_mem_1_ir_2,
       id_ex_1_imm_2, id_ex_1_ir_2, if_id_1_ir_2, mem_wb_1_alu_2, mem_wb_1_md_2, mips_alu_1_result,
       mips_regifile_1_r1, mips_regifile_1_r2, multiplexer_4_out, multiplexer_5_out, R1, R2, ram_1_data,
       rom_1_data;

  Button \u_总复位  (.out(RST));
  Button _1 (.out(IR1));
  Button _2 (.out(IR2));
  Button _3 (.out(IR3));
  // Probe on \总周期数 
  Button \u_继续运行  (.out(Go));
  LED #(.active("true")) led_1 (.in(W1));
  LED #(.active("true")) led_2 (.in(W2));
  LED #(.active("true")) led_3 (.in(W3));
  // Probe on IF_PC[11:0]
  Hex_Digit_Display hex_digit_display_1 (.value(LedData[31:28]));  // open: dp
  D_Flip_Flop #(.trigger("rising"), .Pre_Clr_Positions("LEGACY"), .NegatePresetClear("false"), .enable("true"), .NewFFLayout("false")) d_ff_1 (
    .clk(CLK), .D(1'b0), .Q(d_ff_1_q), .preset(Go));  // open: Qn, en, reset
  or or_1 (or_1_out, ~Halt, d_ff_1_q);  // OR_Gate
  Register #(.width(32), .trigger("rising"), .Select("low")) PC (
    .D(adder_1_out), .en(or_1_out), .Q(IF_PC), .clk(CLK));  // open: clr
  Hex_Digit_Display hex_digit_display_2 (.value(LedData[27:24]));  // open: dp
  Hex_Digit_Display hex_digit_display_3 (.value(LedData[23:20]));  // open: dp
  // Probe on ID_PC[11:0]
  Adder #(.width(32)) adder_1 (.a(IF_PC), .b(32'h4), .out(adder_1_out));  // open: cin, cout
  Hex_Digit_Display hex_digit_display_4 (.value(LedData[15:12]));  // open: dp
  Hex_Digit_Display hex_digit_display_5 (.value(LedData[19:16]));  // open: dp
  Hex_Digit_Display hex_digit_display_6 (.value(LedData[7:4]));  // open: dp
  Hex_Digit_Display hex_digit_display_7 (.value(LedData[11:8]));  // open: dp
  Clock #(.highDuration(1), .lowDuration(1)) clock_1 (.out(CLK));
  // Probe on EX_PC[11:0]
  ROM #(.addrWidth(10), .dataWidth(32), .Select("high")) rom_1 (.addr(IF_PC[11:2]), .data(rom_1_data));
  Hex_Digit_Display hex_digit_display_8 (.value(LedData[3:0]));  // open: dp
  IF_ID if_id_1 (.IR(rom_1_data), .PC(IF_PC), .IR_2(if_id_1_ir_2), .PC_2(ID_PC), .in_4(CLK), .in_3(or_1_out));
  // Probe on M_PC[11:0]
  Multiplexer #(.select(1), .width(5), .disabled("Z"), .enable("false")) multiplexer_1 (
    .in0(if_id_1_ir_2[25:21]), .in1(5'b00010), .out(multiplexer_1_out), .sel(\单周期硬布线控制器_1_syscall ));
  not not_1 (not_1_out, Halt);
  // Probe on \总周期数 
  // Probe on \无条件分支数 
  // Probe on \条件分支成功数 
  // Probe on \插入气泡数 
  // Probe on \LoadUse次数 
  \单周期硬布线控制器  \u_单周期硬布线控制器_1  (
    .Func(if_id_1_ir_2[5:0]), .OP(if_id_1_ir_2[31:26]), .ALU_OP(AluOP), .MemToReg(MemToReg),
    .MemWrite(ID_MemWrite), .ALU_SRC(AluSrcB), .RegWrite(ID_RegWrite), .SysCALL(\单周期硬布线控制器_1_syscall ),
    .SignedExt(SignedExt), .RegDst(\单周期硬布线控制器_1_regdst ), .JR(JR), .JMP(JMP), .Beq(Beq), .JAL(JAL), .Bne(Bne));  // open: ERET
  Multiplexer #(.select(1), .width(5), .disabled("Z"), .enable("false")) multiplexer_2 (
    .in0(if_id_1_ir_2[20:16]), .in1(5'b00100), .out(multiplexer_2_out), .sel(\单周期硬布线控制器_1_syscall ));
  assign bit_extender_1_out = {{16{1'b0}}, if_id_1_ir_2[15:0]};  // Bit_Extender bit_extender_1
  assign bit_extender_2_out = {{16{if_id_1_ir_2[15]}}, if_id_1_ir_2[15:0]};  // Bit_Extender bit_extender_2
  Counter #(.width(16), .max('hffff), .ongoal("wrap"), .trigger("rising"), .behavior("old")) counter_1 (
    .count(not_1_out), .Q(\总周期数 ), .clk(CLK));  // open: load, D, carry, clr, preset
  // Probe on IF_PC[11:0]
  // Probe on WB_PC[11:0]
  Multiplexer #(.select(1), .width(5), .disabled("Z"), .enable("false")) multiplexer_3 (
    .in0(if_id_1_ir_2[20:16]), .in1(if_id_1_ir_2[15:11]), .out(multiplexer_3_out), .sel(\单周期硬布线控制器_1_regdst ));
  MIPS_Regifile mips_regifile_1 (
    .Din(RDin), .Clk(CLK), .R1(mips_regifile_1_r1), .R2(mips_regifile_1_r2), .WE(RegWrite), .W_num(W_num),
    .R1_num(multiplexer_1_out), .R2_num(multiplexer_2_out));
  // Probe on ID_PC[11:0]
  // Probe on EX_PC[11:0]
  Multiplexer #(.select(1), .width(32), .disabled("Z"), .enable("false")) multiplexer_4 (
    .in0(bit_extender_1_out), .in1(bit_extender_2_out), .out(multiplexer_4_out), .sel(SignedExt));
  // Probe on M_PC[11:0]
  ID_EX id_ex_1 (
    .W_num(multiplexer_3_out), .MemToReg(MemToReg), .RegWrite(ID_RegWrite), .JAL(JAL),
    .MemWrite(ID_MemWrite), .AluOP(AluOP), .AluSrcB(AluSrcB), .Beq(Beq), .Bne(Bne), .JMP(JMP), .JR(JR),
    .IR(if_id_1_ir_2), .PC(ID_PC), .A(mips_regifile_1_r1), .B(mips_regifile_1_r2), .Imm(multiplexer_4_out),
    .W_num_2(id_ex_1_w_num_2), .MemToReg_2(id_ex_1_memtoreg_2), .RegWrite_2(id_ex_1_regwrite_2),
    .JAL_2(id_ex_1_jal_2), .MemWrite_2(id_ex_1_memwrite_2), .AluOP_2(id_ex_1_aluop_2),
    .AluSrcB_2(id_ex_1_alusrcb_2), .IR_2({id_ex_1_ir_2[31:11], id_ex_1_ir_2_2, id_ex_1_ir_2[5:0]}),
    .PC_2(EX_PC), .A_2(R1), .B_2(R2), .Imm_2(id_ex_1_imm_2), .in_19(CLK), .in_18(or_1_out),
    .Syscall(\单周期硬布线控制器_1_syscall ), .Syscall_2(Syscall));  // open: Beq_2, Bne_2, JMP_2, JR_2
  // Probe on WB_PC[11:0]
  Comparator #(.width(32), .mode("twosComplement")) comparator_1 (
    .a(R1), .b(32'h32), .eq(comparator_1_eq));  // open: gt, lt
  Multiplexer #(.select(1), .width(32), .disabled("Z"), .enable("false")) multiplexer_5 (
    .in0(R2), .in1(id_ex_1_imm_2), .out(multiplexer_5_out), .sel(id_ex_1_alusrcb_2));
  and and_1 (and_1_out, comparator_1_eq, Syscall);
  and and_2 (and_2_out, ~comparator_1_eq, Syscall);  // AND_Gate
  MIPS_ALU mips_alu_1 (
    .X(R1), .Y(multiplexer_5_out), .AluOP(id_ex_1_aluop_2), .Result(mips_alu_1_result), .shamt(id_ex_1_ir_2_2));  // open: Equal, Result_2
  Register #(.width(32), .trigger("rising"), .Select("low")) register_1 (
    .D(R2), .en(and_2_out), .Q(LedData), .clk(CLK));  // open: clr
  EX_MEM ex_mem_1 (
    .W_num(id_ex_1_w_num_2), .MemToReg(id_ex_1_memtoreg_2), .RegWrite(id_ex_1_regwrite_2),
    .JAL(id_ex_1_jal_2), .MemWrite(id_ex_1_memwrite_2),
    .IR({id_ex_1_ir_2[31:11], id_ex_1_ir_2_2, id_ex_1_ir_2[5:0]}), .PC(EX_PC), .ALU(mips_alu_1_result),
    .B(R2), .W_num_2(ex_mem_1_w_num_2), .MemToReg_2(ex_mem_1_memtoreg_2), .RegWrite_2(ex_mem_1_regwrite_2),
    .JAL_2(ex_mem_1_jal_2), .MemWrite_2(MemWrite), .IR_2(ex_mem_1_ir_2), .PC_2(M_PC), .ALU_2(ex_mem_1_alu_2),
    .B_2(MDin), .in_12(CLK), .in_11(or_1_out), .Halt(and_1_out), .Halt_2(ex_mem_1_halt_2));
  RAM #(.addrWidth(10), .dataWidth(32), .bus("separate"), .Select("high")) ram_1 (
    .addr(ex_mem_1_alu_2[11:2]), .din(MDin), .data(ram_1_data), .str(MemWrite), .clk(CLK));  // open: sel, ld, clr
  MEM_WB mem_wb_1 (
    .W_num(ex_mem_1_w_num_2), .MemToReg(ex_mem_1_memtoreg_2), .RegWrite(ex_mem_1_regwrite_2),
    .JAL(ex_mem_1_jal_2), .IR(ex_mem_1_ir_2), .PC(M_PC), .ALU(ex_mem_1_alu_2), .MD(ram_1_data),
    .W_num_2(W_num), .MemToReg_2(mem_wb_1_memtoreg_2), .RegWrite_2(RegWrite), .PC_2(WB_PC),
    .ALU_2(mem_wb_1_alu_2), .MD_2(mem_wb_1_md_2), .in_11(CLK), .in_10(or_1_out), .Halt(ex_mem_1_halt_2),
    .Halt_2(Halt));  // open: JAL_2, IR_2
  Multiplexer #(.select(1), .width(32), .disabled("Z"), .enable("false")) multiplexer_6 (
    .in0(mem_wb_1_alu_2), .in1(mem_wb_1_md_2), .out(RDin), .sel(mem_wb_1_memtoreg_2));

  // Other names for the same wires on the sheet: MEM_PC[31:0] = M_PC; WE = RegWrite

  // Notes on the sheet:
  //   中断源
  //   时空图监测，可删除
  //   中断等待指示
  //   数码管输出
  //   contents of rom_1 (hex, n*v repeats v):
  //   20100000 20110000 20120000 20130000 36100000 36310001 36520002 36730003 ae100000 ae110004 ae120008
  //   ae13000c 2002000a 0 0 0 c
  //   v0
  //   SignedExt
  //   Func
  //   rd
  //   rs
  //   rt
  //   a0
  //   imm
  //   Beq
  //   JMP
  //   JR
  //   Bne
  //   OP
  //   JAL
  //   MemToReg
  //   MemWrite
  //   AluOP
  //   AluSrcB
  //   RegWrite
  //   RegDst
  //   流水调试日志用
  //   sa
  //   为方便自动评测，需要输出流水线各段保存的PC值，注意是PC不是PC+4，另外ID段寄存器写入信息，Mem段内存写入信息也要输出
endmodule

module \气泡流水线  (
  output RegWrite,
  output MemWrite,
  output [31:0] IF_PC,
  output [31:0] ID_PC,
  output [31:0] EX_PC,
  output [31:0] M_PC,
  output [31:0] WB_PC,
  output [31:0] RDin,
  output [31:0] MDin,
  output [31:0] LedData
);

  wire AluSrcB, and_1_out, and_2_out, and_3_out, and_4_out, and_5_out, and_6_out, Beq, BLTZ, Bne, Branch,
       CLK, comparator_1_eq, d_ff_1_q, EX_AluEq, EX_Beq, EX_BLTZ, EX_Bne, EX_JMP, EX_JR, EX_RegWrite,
       EX_Syscall, Go, Halt, IR1, IR2, IR3, JAL, JMP, JR, LB, LUI, MEM_RegWrite, MemToReg, MemWrite_t,
       not_1_out, or_1_out, or_2_out, or_4_out, RegDst, regread_1_rsread, regread_1_rtread, RegWrite_t, RST,
       SignedExt, Stall, Syscall, W1, W2, W3, \扩展ex_mem_1_halt_2 , \扩展ex_mem_1_jal_2 , \扩展ex_mem_1_lb_2 ,
       \扩展ex_mem_1_lui_2 , \扩展ex_mem_1_memtoreg_2 , \扩展id_ex_1_alusrcb_2 , \扩展id_ex_1_jal_2 ,
       \扩展id_ex_1_lb_2 , \扩展id_ex_1_lui_2 , \扩展id_ex_1_memtoreg_2 , \扩展id_ex_1_memwrite_2 ,
       \扩展mem_wb_1_jal_2 , \扩展mem_wb_1_lb_2 , \扩展mem_wb_1_lui_2 , \扩展mem_wb_1_memtoreg_2 , \数据相关测试_1_hazard ,
       \数据相关测试_2_hazard ;
  wire [1:0] \扩展mem_wb_1_alu_2 ;
  wire [3:0] adder_2_out_2, AluOP, \扩展id_ex_1_aluop_2 ;
  wire [4:0] EX_rW, MEM_rW, multiplexer_2_out, multiplexer_3_out, multiplexer_4_out, multiplexer_5_out, WB_rW;
  wire [7:0] multiplexer_9_out;
  wire [15:0] \LoadUse次数 , \总周期数 , \插入气泡数 , \无条件分支数 , \条件分支成功数 ;
  wire [27:0] adder_2_out;
  wire [31:0] adder_1_out, adder_4_out, bit_extender_1_out, bit_extender_2_out, bit_extender_3_out, BranchPC,
       EX_A, EX_Alu, EX_B, EX_Imm, EX_IR, ID_IR, IF_IR, JmpPC, MEM_IR, multiplexer_1_out, multiplexer_6_out,
       multiplexer_7_out, multiplexer_8_out, multiplexer_11_out, multiplexer_12_out, multiplexer_13_out,
       ram_1_data, registerfile_1_p7, registerfile_1_p8, shifter_1_out, WB_IR, \扩展ex_mem_1_alu_2 ,
       \扩展ex_mem_1_imm_2 , \扩展mem_wb_1_imm_2 , \扩展mem_wb_1_md_2 ;
  wire [31:2] \扩展mem_wb_1_alu_2_2 ;

  Button \u_总复位  (.out(RST));
  Button _1 (.out(IR1));
  Button _2 (.out(IR2));
  Button _3 (.out(IR3));
  // Probe on \总周期数 
  Button \u_继续运行  (.out(Go));
  LED #(.active("true")) led_1 (.in(W1));
  LED #(.active("true")) led_2 (.in(W2));
  LED #(.active("true")) led_3 (.in(W3));
  // Probe on IF_PC
  Hex_Digit_Display hex_digit_display_1 (.value(LedData[31:28]));  // open: dp
  // Probe on IF_PC
  // Probe on ID_PC
  // Probe on EX_PC
  // Probe on M_PC
  // Probe on WB_PC
  Multiplexer #(.select(2), .width(32), .disabled("Z"), .enable("false")) multiplexer_1 (
    .in0(adder_1_out), .in1(JmpPC), .in2(BranchPC), .out(multiplexer_1_out), .sel({Branch, EX_JMP}));  // open: in3
  or or_1 (or_1_out, Branch, EX_JMP);
  Hex_Digit_Display hex_digit_display_2 (.value(LedData[23:20]));  // open: dp
  Hex_Digit_Display hex_digit_display_3 (.value(LedData[27:24]));  // open: dp
  // Probe on ID_PC
  or or_2 (or_2_out, ~Halt, d_ff_1_q);  // OR_Gate
  Register #(.width(32), .trigger("rising"), .Select("low")) PC (
    .D(multiplexer_1_out), .en(and_1_out), .Q(IF_PC), .clk(CLK));  // open: clr
  and and_1 (and_1_out, or_2_out, ~Stall);  // AND_Gate
  Hex_Digit_Display hex_digit_display_4 (.value(LedData[19:16]));  // open: dp
  Hex_Digit_Display hex_digit_display_5 (.value(LedData[15:12]));  // open: dp
  D_Flip_Flop #(.trigger("rising"), .Pre_Clr_Positions("LEGACY"), .NegatePresetClear("false"), .enable("true"), .NewFFLayout("false")) d_ff_1 (
    .clk(CLK), .D(1'b0), .Q(d_ff_1_q), .preset(Go));  // open: Qn, en, reset
  Adder #(.width(32)) adder_1 (.a(IF_PC), .b(32'h4), .out(adder_1_out));  // open: cin, cout
  Hex_Digit_Display hex_digit_display_6 (.value(LedData[7:4]));  // open: dp
  Hex_Digit_Display hex_digit_display_7 (.value(LedData[11:8]));  // open: dp
  Clock #(.highDuration(1), .lowDuration(1)) clock_1 (.out(CLK));
  // Probe on EX_PC
  // Probe on IF_IR
  // Probe on ID_IR
  // Probe on EX_IR
  // Probe on MEM_IR
  // Probe on WB_IR
  Hex_Digit_Display hex_digit_display_8 (.value(LedData[3:0]));  // open: dp
  ROM #(.addrWidth(10), .dataWidth(32), .Select("high")) rom_1 (.addr(IF_PC[11:2]), .data(IF_IR));
  RegRead regread_1 (
    .OP0(ID_IR[26]), .OP1(ID_IR[27]), .OP2(ID_IR[28]), .OP3(ID_IR[29]), .OP4(ID_IR[30]), .OP5(ID_IR[31]),
    .F0(ID_IR[0]), .F1(ID_IR[1]), .F2(ID_IR[2]), .F3(ID_IR[3]), .F4(ID_IR[4]), .F5(ID_IR[5]),
    .RsRead(regread_1_rsread), .RtRead(regread_1_rtread));
  // Probe on M_PC
  \扩展IF_ID  \u_扩展if_id_1  (
    .IR(IF_IR), .PC(IF_PC), .IR_2(ID_IR), .PC_2(ID_PC), .En(and_1_out), .Clk(CLK), .Clr(or_1_out));
  \数据相关测试  \u_数据相关测试_1  (
    .RsRead(regread_1_rsread), .Rs(ID_IR[25:21]), .RtRead(regread_1_rtread), .Rt(ID_IR[20:16]), .Rw(EX_rW),
    .RegWrite(EX_RegWrite), .Syscall(Syscall), .Hazard(\数据相关测试_1_hazard ));
  // Probe on \总周期数 
  // Probe on \无条件分支数 
  // Probe on \条件分支成功数 
  // Probe on \插入气泡数 
  // Probe on \LoadUse次数 
  \数据相关测试  \u_数据相关测试_2  (
    .RsRead(regread_1_rsread), .Rs(ID_IR[25:21]), .RtRead(regread_1_rtread), .Rt(ID_IR[20:16]), .Rw(MEM_rW),
    .RegWrite(MEM_RegWrite), .Syscall(Syscall), .Hazard(\数据相关测试_2_hazard ));
  // Probe on IF_PC[11:0]
  // Probe on WB_PC
  Multiplexer #(.select(1), .width(5), .disabled("Z"), .enable("false")) multiplexer_2 (
    .in0(ID_IR[20:16]), .in1(ID_IR[15:11]), .out(multiplexer_2_out), .sel(RegDst));
  or or_3 (Stall, \数据相关测试_2_hazard , \数据相关测试_1_hazard );
  // Probe on EX_PC[11:0]
  // Probe on ID_PC[11:0]
  \扩展单周期硬布线控制器  \u_扩展单周期硬布线控制器_1  (
    .OP(ID_IR[31:26]), .Func(ID_IR[5:0]), .ALU_OP(AluOP), .MemToReg(MemToReg), .MemWrite(MemWrite_t),
    .ALU_SRC(AluSrcB), .RegWrite(RegWrite_t), .SysCALL(Syscall), .SignedExt(SignedExt), .RegDst(RegDst),
    .Beq(Beq), .Bne(Bne), .JR(JR), .JMP(JMP), .JAL(JAL), .LUI(LUI), .LB(LB), .BLTZ(BLTZ));  // open: ERET
  Multiplexer #(.select(1), .width(5), .disabled("Z"), .enable("false")) multiplexer_3 (
    .in0(multiplexer_2_out), .in1({5{1'b1}}), .out(multiplexer_3_out), .sel(JAL));
  // Probe on M_PC[11:0]
  assign bit_extender_1_out = {{16{1'b0}}, ID_IR[15:0]};  // Bit_Extender bit_extender_1
  assign bit_extender_2_out = {{16{ID_IR[15]}}, ID_IR[15:0]};  // Bit_Extender bit_extender_2
  // Probe on WB_PC[11:0]
  Counter #(.width(16), .max('hffff), .ongoal("wrap"), .trigger("rising"), .behavior("old")) counter_1 (
    .count(not_1_out), .Q(\总周期数 ), .clk(CLK));  // open: load, D, carry, clr, preset
  not not_1 (not_1_out, Halt);
  Multiplexer #(.select(1), .width(5), .disabled("Z"), .enable("false")) multiplexer_4 (
    .in0(ID_IR[25:21]), .in1(5'b00010), .out(multiplexer_4_out), .sel(Syscall));
  Multiplexer #(.select(1), .width(5), .disabled("Z"), .enable("false")) multiplexer_5 (
    .in0(ID_IR[20:16]), .in1(5'b00100), .out(multiplexer_5_out), .sel(Syscall));
  Multiplexer #(.select(1), .width(32), .disabled("Z"), .enable("false")) multiplexer_6 (
    .in0(bit_extender_1_out), .in1(bit_extender_2_out), .out(multiplexer_6_out), .sel(SignedExt));
  Multiplexer #(.select(1), .width(32), .disabled("Z"), .enable("false")) multiplexer_7 (
    .in0(multiplexer_6_out), .in1({ID_IR[15:0], {16{1'b0}}}), .out(multiplexer_7_out), .sel(LUI));
  // RegisterFile registerfile_1: pin names not known; wires that end beside it: RDin, CLK, RegWrite, WB_rW, multiplexer_4_out, multiplexer_5_out, registerfile_1_p7, registerfile_1_p8
  and and_2 (and_2_out, comparator_1_eq, EX_Syscall);
  Comparator #(.width(32), .mode("twosComplement")) comparator_1 (
    .a(EX_A), .b(32'h32), .eq(comparator_1_eq));  // open: gt, lt
  \扩展ID_EX  \u_扩展id_ex_1  (
    .Syscall(Syscall), .W_num(multiplexer_3_out), .MemToReg(MemToReg), .RegWrite(RegWrite_t), .JAL(JAL),
    .LB(LB), .LUI(LUI), .MemWrite(MemWrite_t), .AluOP(AluOP), .AluSrcB(AluSrcB), .Beq(Beq), .Bne(Bne),
    .JMP(JMP), .JR(JR), .BLTZ(BLTZ), .IR(ID_IR), .PC(ID_PC), .A(registerfile_1_p7), .B(registerfile_1_p8),
    .Imm(multiplexer_7_out), .Syscall_2(EX_Syscall), .W_num_2(EX_rW), .MemToReg_2(\扩展id_ex_1_memtoreg_2 ),
    .RegWrite_2(EX_RegWrite), .JAL_2(\扩展id_ex_1_jal_2 ), .LB_2(\扩展id_ex_1_lb_2 ), .LUI_2(\扩展id_ex_1_lui_2 ),
    .MemWrite_2(\扩展id_ex_1_memwrite_2 ), .AluOP_2(\扩展id_ex_1_aluop_2 ), .AluSrcB_2(\扩展id_ex_1_alusrcb_2 ),
    .Beq_2(EX_Beq), .Bne_2(EX_Bne), .JMP_2(EX_JMP), .JR_2(EX_JR), .BLTZ_2(EX_BLTZ), .IR_2(EX_IR),
    .PC_2(EX_PC), .A_2(EX_A), .B_2(EX_B), .Imm_2(EX_Imm), .En(or_2_out), .Clk(CLK), .Clr(or_4_out));  // open: ERET, ERET_2
  or or_4 (or_4_out, or_1_out, Stall);
  and and_3 (and_3_out, ~comparator_1_eq, EX_Syscall);  // AND_Gate
  Register #(.width(32), .trigger("rising"), .Select("low")) register_1 (
    .D(EX_B), .en(and_3_out), .Q(LedData), .clk(CLK));  // open: clr
  Multiplexer #(.select(1), .width(32), .disabled("Z"), .enable("false")) multiplexer_8 (
    .in0(EX_B), .in1(EX_Imm), .out(multiplexer_8_out), .sel(\扩展id_ex_1_alusrcb_2 ));
  and and_4 (and_4_out, EX_AluEq, EX_Beq);
  and and_5 (and_5_out, ~EX_AluEq, EX_Bne);  // AND_Gate
  and and_6 (and_6_out, EX_Alu[0], BLTZ);
  MIPS_ALU mips_alu_1 (
    .X(EX_A), .Y(multiplexer_8_out), .AluOP(\扩展id_ex_1_aluop_2 ), .Equal(EX_AluEq), .Result(EX_Alu),
    .shamt(EX_IR[10:6]));  // open: Result_2
  or or_5 (Branch, and_4_out, and_5_out, and_6_out);
  \扩展EX_MEM  \u_扩展ex_mem_1  (
    .Halt(and_2_out), .Halt_2(\扩展ex_mem_1_halt_2 ), .W_num(EX_rW), .W_num_2(MEM_rW),
    .MemToReg(\扩展id_ex_1_memtoreg_2 ), .MemToReg_2(\扩展ex_mem_1_memtoreg_2 ), .RegWrite(EX_RegWrite),
    .RegWrite_2(MEM_RegWrite), .JAL(\扩展id_ex_1_jal_2 ), .JAL_2(\扩展ex_mem_1_jal_2 ), .LB(\扩展id_ex_1_lb_2 ),
    .LB_2(\扩展ex_mem_1_lb_2 ), .LUI(\扩展id_ex_1_lui_2 ), .LUI_2(\扩展ex_mem_1_lui_2 ),
    .MemWrite(\扩展id_ex_1_memwrite_2 ), .MemWrite_2(MemWrite), .IR(EX_IR), .IR_2(MEM_IR), .PC(EX_PC),
    .PC_2(M_PC), .ALU(EX_Alu), .ALU_2(\扩展ex_mem_1_alu_2 ), .B(EX_B), .B_2(MDin), .Imm(EX_Imm),
    .Imm_2(\扩展ex_mem_1_imm_2 ), .En(or_2_out), .Clk(CLK));  // open: Clr, ERET, ERET_2
  RAM #(.addrWidth(10), .dataWidth(32), .bus("separate"), .Select("high")) ram_1 (
    .addr(\扩展ex_mem_1_alu_2 [11:2]), .din(MDin), .data(ram_1_data), .str(MemWrite), .clk(CLK));  // open: sel, ld, clr
  Adder #(.width(32)) adder_2 (.a(EX_PC), .b(32'h4), .out({adder_2_out_2, adder_2_out}));  // open: cin, cout
  \扩展MEM_WB  \u_扩展mem_wb_1  (
    .Halt(\扩展ex_mem_1_halt_2 ), .Halt_2(Halt), .W_num(MEM_rW), .W_num_2(WB_rW),
    .MemToReg(\扩展ex_mem_1_memtoreg_2 ), .MemToReg_2(\扩展mem_wb_1_memtoreg_2 ), .RegWrite(MEM_RegWrite),
    .RegWrite_2(RegWrite), .JAL(\扩展ex_mem_1_jal_2 ), .JAL_2(\扩展mem_wb_1_jal_2 ), .LB(\扩展ex_mem_1_lb_2 ),
    .LB_2(\扩展mem_wb_1_lb_2 ), .LUI(\扩展ex_mem_1_lui_2 ), .LUI_2(\扩展mem_wb_1_lui_2 ), .IR(MEM_IR),
    .IR_2(WB_IR), .PC(M_PC), .PC_2(WB_PC), .ALU(\扩展ex_mem_1_alu_2 ),
    .ALU_2({\扩展mem_wb_1_alu_2_2 , \扩展mem_wb_1_alu_2 }), .MD(ram_1_data), .MD_2(\扩展mem_wb_1_md_2 ),
    .Imm(\扩展ex_mem_1_imm_2 ), .Imm_2(\扩展mem_wb_1_imm_2 ), .En(or_2_out), .Clk(CLK));  // open: Clr, ERET, ERET_2
  Shifter #(.width(32), .shift("ll")) shifter_1 (.in(EX_Imm), .\dist (5'b00010), .out(shifter_1_out));
  Multiplexer #(.select(2), .width(8), .disabled("Z"), .enable("false")) multiplexer_9 (
    .in0(\扩展mem_wb_1_md_2 [7:0]), .in1(\扩展mem_wb_1_md_2 [15:8]), .in2(\扩展mem_wb_1_md_2 [23:16]),
    .in3(\扩展mem_wb_1_md_2 [31:24]), .out(multiplexer_9_out), .sel(\扩展mem_wb_1_alu_2 ));
  Adder #(.width(32)) adder_3 (.a(shifter_1_out), .b({adder_2_out_2, adder_2_out}), .out(BranchPC));  // open: cin, cout
  Multiplexer #(.select(1), .width(32), .disabled("Z"), .enable("false")) multiplexer_10 (
    .in0({adder_2_out_2, EX_IR[25:0], 2'b00}), .in1(EX_A), .out(JmpPC), .sel(EX_JR));
  assign bit_extender_3_out = {{24{multiplexer_9_out[7]}}, multiplexer_9_out};  // Bit_Extender bit_extender_3
  Multiplexer #(.select(1), .width(32), .disabled("Z"), .enable("false")) multiplexer_11 (
    .in0({\扩展mem_wb_1_alu_2_2 , \扩展mem_wb_1_alu_2 }), .in1(multiplexer_12_out), .out(multiplexer_11_out),
    .sel(\扩展mem_wb_1_memtoreg_2 ));
  Multiplexer #(.select(1), .width(32), .disabled("Z"), .enable("false")) multiplexer_12 (
    .in0(\扩展mem_wb_1_md_2 ), .in1(bit_extender_3_out), .out(multiplexer_12_out), .sel(\扩展mem_wb_1_lb_2 ));
  Multiplexer #(.select(1), .width(32), .disabled("Z"), .enable("false")) multiplexer_13 (
    .in0(multiplexer_11_out), .in1(\扩展mem_wb_1_imm_2 ), .out(multiplexer_13_out), .sel(\扩展mem_wb_1_lui_2 ));
  Adder #(.width(32)) adder_4 (.a(WB_PC), .b(32'h4), .out(adder_4_out));  // open: cin, cout
  Multiplexer #(.select(1), .width(32), .disabled("Z"), .enable("false")) multiplexer_14 (
    .in0(multiplexer_13_out), .in1(adder_4_out), .out(RDin), .sel(\扩展mem_wb_1_jal_2 ));

  // Other names for the same wires on the sheet: IR[31:0] = IF_IR; MEM_MemWrite = MemWrite; MEM_PC[31:0] = M_PC;
  //   WB_RegWrite = RegWrite

  // Notes on the sheet:
  //   中断源
  //   时空图监测，可删除
  //   中断等待指示
  //   数码管输出
  //   OP
  //   Func
  //   rs
  //   rt
  //   contents of rom_1 (hex, n*v repeats v):
  //   20110001 8000c05 20110001 20120002 20130003 8000c09 20110001 20120002 20130003 8000c0d 20110001
  //   20120002 20130003 8000c11 20110001 20120002 20130003 c000cb8 20100001 20110001 118fc0 112020
  //   20020022 c 118882 12200001 8000c15 112020 20020022 c 20110001 118880 112020 20020022 c 12200001
  //   8000c1f 20110001 118fc0 112020 20020022 c 1188c3 112020 20020022 c 118903 112020 20020022 c 118903
  //   112020 20020022 c 118903 112020 20020022 c 118903 112020 20020022 c 118903 112020 20020022 c 118903
  //   112020 20020022 c 118903 112020 20020022 c 20100001 109fc0 139fc3 8021 2012000c 24160003 26100001
  //   3210000f 20080008 20090001 139900 2709825 132020 20020022 c 1094022 1500fff9 22100001 2018000f
  //   2188024 108700 20080008 20090001 139902 2709825 132021 20020022 c 1094022 1500fff9 108702 2c9b022
  //   12c00001 8000c50 4020 1084027 84400 3508ffff 82021 20020022 c 2010ffff 20110000 ae300000 22100001
  //   22310004 ae300000 22100001 22310004 ae300000 22100001 22310004 ae300000 22100001 22310004 ae300000
  //   22100001 22310004 ae300000 22100001 22310004 ae300000 22100001 22310004 ae300000 22100001 22310004
  //   ae300000 22100001 22310004 ae300000 22100001 22310004 ae300000 22100001 22310004 ae300000 22100001
  //   22310004 ae300000 22100001 22310004 ae300000 22100001 22310004 ae300000 22100001 22310004 ae300000
  //   22100001 22310004 22100001 8020 2011003c 8e130000 8e340000 274402a 11000002 ae330000 ae140000
  //   2231fffc 1611fff8 102020 20020022 c 22100004 2011003c 1611fff2 20020032 c 20100000 22100001 102020
  //   20020022 c 22100002 102020 20020022 c 22100003 102020 20020022 c 22100004 102020 20020022 c 22100005
  //   102020 20020022 c 22100006 102020 20020022 c 22100007 102020 20020022 c 22100008 102020 20020022
  //   20020022 c 3e00008
  //   OP
  //   Func
  //   rd
  //   rs
  //   rt
  //   imm
  //   流水调试日志用
  //   v0
  //   a0
  //   sa
  //   为方便自动评测，需要输出流水线各段保存的PC值，注意是PC不是PC+4，另外ID段寄存器写入信息，Mem段内存写入信息也要输出
  //   instr_index
endmodule

module \重定向流水线  (
  output RegWrite,
  output MemWrite,
  output [31:0] IF_PC,
  output [31:0] ID_PC,
  output [31:0] EX_PC,
  output [31:0] M_PC,
  output [31:0] WB_PC,
  output [31:0] RDin,
  output [31:0] MDin,
  output [31:0] LedData
);

  wire AluSrcB, and_1_out, and_3_out, and_4_out, and_5_out, and_6_out, and_7_out, Beq, BLTZ, Bne, Branch,
       CLK, comparator_1_eq, d_ff_1_q, EX_AluEq, EX_Beq, EX_BLTZ, EX_Bne, EX_JMP, EX_JR, EX_MemToReg,
       EX_RegWrite, EX_RsRead, EX_RtRead, EX_Syscall, Go, Halt, IR1, IR2, IR3, JAL, JMP, JR, LB, LoadUse,
       LUI, MEM_RegWrite, MemToReg, MemWrite_t, not_1_out, or_1_out, or_2_out, or_3_out, RegDst, RegWrite_t,
       RST, SignedExt, Syscall, W1, W2, W3, WB_MemToReg, \扩展ex_mem_1_halt_2 , \扩展ex_mem_1_jal_2 ,
       \扩展ex_mem_1_lb_2 , \扩展ex_mem_1_lui_2 , \扩展ex_mem_1_memtoreg_2 , \扩展id_ex_1_alusrcb_2 ,
       \扩展id_ex_1_jal_2 , \扩展id_ex_1_lb_2 , \扩展id_ex_1_lui_2 , \扩展id_ex_1_memwrite_2 , \扩展mem_wb_1_jal_2 ,
       \扩展mem_wb_1_lb_2 , \扩展mem_wb_1_lui_2 , \数据相关测试2_1_hazarda , \数据相关测试2_1_hazardb , \数据相关测试2_2_hazarda ,
       \数据相关测试2_2_hazardb , \数据相关测试_1_hazard ;
  wire [1:0] ForwardA, ForwardB, multiplexer_6_out, regread_1_rsread;
  wire [3:0] AluOP, \扩展id_ex_1_aluop_2 ;
  wire [4:0] EX_rW, MEM_rW, multiplexer_2_out, multiplexer_3_out, multiplexer_4_out, registerfile_1_p6, WB_rW;
  wire [7:0] multiplexer_13_out;
  wire [15:0] \LoadUse次数 , \总周期数 , \插入气泡数 , \无条件分支数 , \条件分支成功数 ;
  wire [31:0] adder_1_out, adder_2_out, adder_4_out, bit_extender_1_out, bit_extender_2_out,
       bit_extender_3_out, BranchPC, EX_A, EX_Alu, EX_B, EX_Imm, EX_IR, ID_IR, IF_IR, JmpPC, MEM_IR,
       multiplexer_1_out, multiplexer_5_out, multiplexer_8_out, multiplexer_11_out, multiplexer_14_out,
       multiplexer_15_out, multiplexer_16_out, ram_1_data, registerfile_1_p7, registerfile_1_p8,
       shifter_1_out, WB_IR, \扩展ex_mem_1_alu_2 , \扩展ex_mem_1_imm_2 , \扩展id_ex_1_a_2 , \扩展id_ex_1_b_2 ,
       \扩展mem_wb_1_alu_2 , \扩展mem_wb_1_imm_2 , \扩展mem_wb_1_md_2 ;

  Button \u_总复位  (.out(RST));
  Button _1 (.out(IR1));
  Button _2 (.out(IR2));
  Button _3 (.out(IR3));
  // Probe on \总周期数 
  Button \u_继续运行  (.out(Go));
  LED #(.active("true")) led_1 (.in(W1));
  LED #(.active("true")) led_2 (.in(W2));
  LED #(.active("true")) led_3 (.in(W3));
  // Probe on IF_PC
  Hex_Digit_Display hex_digit_display_1 (.value(LedData[31:28]));  // open: dp
  Multiplexer #(.select(2), .width(32), .disabled("Z"), .enable("false")) multiplexer_1 (
    .in0(adder_1_out), .in1(JmpPC), .in2(BranchPC), .out(multiplexer_1_out), .sel({Branch, EX_JMP}));  // open: in3
  or or_1 (or_1_out, Branch, EX_JMP);
  Hex_Digit_Display hex_digit_display_2 (.value(LedData[27:24]));  // open: dp
  Hex_Digit_Display hex_digit_display_3 (.value(LedData[23:20]));  // open: dp
  // Probe on ID_PC
  // Probe on IF_PC
  // Probe on ID_PC
  // Probe on EX_PC
  // Probe on M_PC
  // Probe on WB_PC
  or or_2 (or_2_out, ~Halt, d_ff_1_q);  // OR_Gate
  and and_1 (and_1_out, or_2_out, ~LoadUse);  // AND_Gate
  Hex_Digit_Display hex_digit_display_4 (.value(LedData[19:16]));  // open: dp
  Hex_Digit_Display hex_digit_display_5 (.value(LedData[15:12]));  // open: dp
  D_Flip_Flop #(.trigger("rising"), .Pre_Clr_Positions("LEGACY"), .NegatePresetClear("false"), .enable("true"), .NewFFLayout("false")) d_ff_1 (
    .clk(CLK), .D(1'b0), .Q(d_ff_1_q), .preset(Go));  // open: Qn, en, reset
  Register #(.width(32), .trigger("rising"), .Select("low")) PC (
    .D(multiplexer_1_out), .en(and_1_out), .Q(IF_PC), .clk(CLK));  // open: clr
  Hex_Digit_Display hex_digit_display_6 (.value(LedData[11:8]));  // open: dp
  Hex_Digit_Display hex_digit_display_7 (.value(LedData[7:4]));  // open: dp
  Clock #(.highDuration(1), .lowDuration(1)) clock_1 (.out(CLK));
  // Probe on EX_PC
  // Probe on IF_IR
  // Probe on ID_IR
  // Probe on EX_IR
  // Probe on MEM_IR
  // Probe on WB_IR
  Adder #(.width(32)) adder_1 (.a(IF_PC), .b(32'h4), .out(adder_1_out));  // open: cin, cout
  Hex_Digit_Display hex_digit_display_8 (.value(LedData[3:0]));  // open: dp
  ROM #(.addrWidth(10), .dataWidth(32), .Select("high")) rom_1 (.addr(IF_PC[11:2]), .data(IF_IR));
  RegRead regread_1 (
    .OP0(ID_IR[26]), .OP1(ID_IR[27]), .OP2(ID_IR[28]), .OP3(ID_IR[29]), .OP4(ID_IR[30]), .OP5(ID_IR[31]),
    .F0(ID_IR[0]), .F1(ID_IR[1]), .F2(ID_IR[2]), .F3(ID_IR[3]), .F4(ID_IR[4]), .F5(ID_IR[5]),
    .RsRead(regread_1_rsread[0]), .RtRead(regread_1_rsread[1]));
  // Probe on M_PC
  // Probe on \总周期数 
  // Probe on \无条件分支数 
  // Probe on \条件分支成功数 
  // Probe on \插入气泡数 
  // Probe on \LoadUse次数 
  \扩展IF_ID  \u_扩展if_id_1  (
    .IR(IF_IR), .PC(IF_PC), .IR_2(ID_IR), .PC_2(ID_PC), .En(and_1_out), .Clk(CLK), .Clr(or_1_out));
  \数据相关测试  \u_数据相关测试_1  (
    .RsRead(regread_1_rsread[0]), .Rs(ID_IR[25:21]), .RtRead(regread_1_rsread[1]), .Rt(ID_IR[20:16]),
    .Rw(EX_rW), .RegWrite(EX_RegWrite), .Syscall(Syscall), .Hazard(\数据相关测试_1_hazard ));
  // Probe on IF_PC[11:0]
  // Probe on WB_PC
  and and_2 (LoadUse, EX_MemToReg, \数据相关测试_1_hazard );
  // Probe on ID_PC[11:0]
  // Probe on EX_PC[11:0]
  \扩展单周期硬布线控制器  \u_扩展单周期硬布线控制器_1  (
    .OP(ID_IR[31:26]), .Func(ID_IR[5:0]), .ALU_OP(AluOP), .MemToReg(MemToReg), .MemWrite(MemWrite_t),
    .ALU_SRC(AluSrcB), .RegWrite(RegWrite_t), .SysCALL(Syscall), .SignedExt(SignedExt), .RegDst(RegDst),
    .Beq(Beq), .Bne(Bne), .JR(JR), .JMP(JMP), .JAL(JAL), .LUI(LUI), .LB(LB), .BLTZ(BLTZ));  // open: ERET
  Multiplexer #(.select(1), .width(5), .disabled("Z"), .enable("false")) multiplexer_2 (
    .in0(ID_IR[20:16]), .in1(ID_IR[15:11]), .out(multiplexer_2_out), .sel(RegDst));
  Multiplexer #(.select(1), .width(5), .disabled("Z"), .enable("false")) multiplexer_3 (
    .in0(multiplexer_2_out), .in1({5{1'b1}}), .out(multiplexer_3_out), .sel(JAL));
  // Probe on M_PC[11:0]
  assign bit_extender_1_out = {{16{1'b0}}, ID_IR[15:0]};  // Bit_Extender bit_extender_1
  assign bit_extender_2_out = {{16{ID_IR[15]}}, ID_IR[15:0]};  // Bit_Extender bit_extender_2
  // Probe on WB_PC[11:0]
  Counter #(.width(16), .max('hffff), .ongoal("wrap"), .trigger("rising"), .behavior("old")) counter_1 (
    .count(not_1_out), .Q(\总周期数 ), .clk(CLK));  // open: load, D, carry, clr, preset
  not not_1 (not_1_out, Halt);
  Multiplexer #(.select(1), .width(5), .disabled("Z"), .enable("false")) multiplexer_4 (
    .in0(ID_IR[25:21]), .in1(5'b00010), .out(multiplexer_4_out), .sel(Syscall));
  Multiplexer #(.select(1), .width(32), .disabled("Z"), .enable("false")) multiplexer_5 (
    .in0(bit_extender_1_out), .in1(bit_extender_2_out), .out(multiplexer_5_out), .sel(SignedExt));
  Multiplexer #(.select(1), .width(2), .disabled("Z"), .enable("false")) multiplexer_6 (
    .in0(regread_1_rsread), .in1(2'b00), .out(multiplexer_6_out), .sel(or_3_out));
  Register #(.width(2), .trigger("rising"), .Select("low")) register_1 (
    .D(multiplexer_6_out), .en(or_2_out), .Q({EX_RtRead, EX_RsRead}), .clk(CLK));  // open: clr
  // RegisterFile registerfile_1: pin names not known; wires that end beside it: RDin, CLK, RegWrite, WB_rW, multiplexer_4_out, registerfile_1_p6, registerfile_1_p7, registerfile_1_p8
  Multiplexer #(.select(1), .width(5), .disabled("Z"), .enable("false")) multiplexer_7 (
    .in0(ID_IR[20:16]), .in1(5'b00100), .out(registerfile_1_p6), .sel(Syscall));
  Multiplexer #(.select(1), .width(32), .disabled("Z"), .enable("false")) multiplexer_8 (
    .in0(multiplexer_5_out), .in1({ID_IR[15:0], {16{1'b0}}}), .out(multiplexer_8_out), .sel(LUI));
  \数据相关测试2  \u_数据相关测试2_1  (
    .RsRead(EX_RsRead), .Rs(EX_IR[25:21]), .RtRead(EX_RtRead), .Rt(EX_IR[20:16]), .Rw(MEM_rW),
    .RegWrite(MEM_RegWrite), .Syscall(EX_Syscall), .HazardA(\数据相关测试2_1_hazarda ),
    .HazardB(\数据相关测试2_1_hazardb ));
  \数据相关测试2  \u_数据相关测试2_2  (
    .RsRead(EX_RsRead), .Rs(EX_IR[25:21]), .RtRead(EX_RtRead), .Rt(EX_IR[20:16]), .Rw(WB_rW),
    .RegWrite(RegWrite), .Syscall(EX_Syscall), .HazardA(\数据相关测试2_2_hazarda ), .HazardB(\数据相关测试2_2_hazardb ));
  Forward forward_1 (
    .HazardA(\数据相关测试2_1_hazarda ), .HazardB(\数据相关测试2_2_hazarda ), .MemToReg(WB_MemToReg), .out_4(ForwardA));
  Forward forward_2 (
    .HazardA(\数据相关测试2_1_hazardb ), .HazardB(\数据相关测试2_2_hazardb ), .MemToReg(WB_MemToReg), .out_4(ForwardB));
  Comparator #(.width(32), .mode("twosComplement")) comparator_1 (
    .a(EX_A), .b(32'h32), .eq(comparator_1_eq));  // open: gt, lt
  \扩展ID_EX  \u_扩展id_ex_1  (
    .Syscall(Syscall), .W_num(multiplexer_3_out), .MemToReg(MemToReg), .RegWrite(RegWrite_t), .JAL(JAL),
    .LB(LB), .LUI(LUI), .MemWrite(MemWrite_t), .AluOP(AluOP), .AluSrcB(AluSrcB), .Beq(Beq), .Bne(Bne),
    .JMP(JMP), .JR(JR), .BLTZ(BLTZ), .IR(ID_IR), .PC(ID_PC), .A(registerfile_1_p7), .B(registerfile_1_p8),
    .Imm(multiplexer_8_out), .Syscall_2(EX_Syscall), .W_num_2(EX_rW), .MemToReg_2(EX_MemToReg),
    .RegWrite_2(EX_RegWrite), .JAL_2(\扩展id_ex_1_jal_2 ), .LB_2(\扩展id_ex_1_lb_2 ), .LUI_2(\扩展id_ex_1_lui_2 ),
    .MemWrite_2(\扩展id_ex_1_memwrite_2 ), .AluOP_2(\扩展id_ex_1_aluop_2 ), .AluSrcB_2(\扩展id_ex_1_alusrcb_2 ),
    .Beq_2(EX_Beq), .Bne_2(EX_Bne), .JMP_2(EX_JMP), .JR_2(EX_JR), .BLTZ_2(EX_BLTZ), .IR_2(EX_IR),
    .PC_2(EX_PC), .A_2(\扩展id_ex_1_a_2 ), .B_2(\扩展id_ex_1_b_2 ), .Imm_2(EX_Imm), .En(or_2_out), .Clk(CLK),
    .Clr(or_3_out));  // open: ERET, ERET_2
  or or_3 (or_3_out, or_1_out, LoadUse);
  and and_3 (and_3_out, comparator_1_eq, EX_Syscall);
  and and_4 (and_4_out, ~comparator_1_eq, EX_Syscall);  // AND_Gate
  Register #(.width(32), .trigger("rising"), .Select("low")) register_2 (
    .D(EX_B), .en(and_4_out), .Q(LedData), .clk(CLK));  // open: clr
  and and_5 (and_5_out, EX_AluEq, EX_Beq);
  and and_6 (and_6_out, ~EX_AluEq, EX_Bne);  // AND_Gate
  and and_7 (and_7_out, EX_Alu[0], EX_BLTZ);
  Multiplexer #(.select(2), .width(32), .disabled("Z"), .enable("false")) multiplexer_9 (
    .in0(\扩展id_ex_1_a_2 ), .in1(multiplexer_14_out), .in2(\扩展mem_wb_1_alu_2 ), .in3(\扩展ex_mem_1_alu_2 ),
    .out(EX_A), .sel(ForwardA));
  or or_4 (Branch, and_5_out, and_6_out, and_7_out);
  Multiplexer #(.select(2), .width(32), .disabled("Z"), .enable("false")) multiplexer_10 (
    .in0(\扩展id_ex_1_b_2 ), .in1(multiplexer_14_out), .in2(\扩展mem_wb_1_alu_2 ), .in3(\扩展ex_mem_1_alu_2 ),
    .out(EX_B), .sel(ForwardB));
  MIPS_ALU mips_alu_1 (
    .X(EX_A), .Y(multiplexer_11_out), .AluOP(\扩展id_ex_1_aluop_2 ), .Equal(EX_AluEq), .Result(EX_Alu),
    .shamt(EX_IR[10:6]));  // open: Result_2
  Multiplexer #(.select(1), .width(32), .disabled("Z"), .enable("false")) multiplexer_11 (
    .in0(EX_B), .in1(EX_Imm), .out(multiplexer_11_out), .sel(\扩展id_ex_1_alusrcb_2 ));
  Adder #(.width(32)) adder_2 (.a(EX_PC), .b(32'h4), .out(adder_2_out));  // open: cin, cout
  \扩展EX_MEM  \u_扩展ex_mem_1  (
    .Halt(and_3_out), .Halt_2(\扩展ex_mem_1_halt_2 ), .W_num(EX_rW), .W_num_2(MEM_rW), .MemToReg(EX_MemToReg),
    .MemToReg_2(\扩展ex_mem_1_memtoreg_2 ), .RegWrite(EX_RegWrite), .RegWrite_2(MEM_RegWrite),
    .JAL(\扩展id_ex_1_jal_2 ), .JAL_2(\扩展ex_mem_1_jal_2 ), .LB(\扩展id_ex_1_lb_2 ), .LB_2(\扩展ex_mem_1_lb_2 ),
    .LUI(\扩展id_ex_1_lui_2 ), .LUI_2(\扩展ex_mem_1_lui_2 ), .MemWrite(\扩展id_ex_1_memwrite_2 ),
    .MemWrite_2(MemWrite), .IR(EX_IR), .IR_2(MEM_IR), .PC(EX_PC), .PC_2(M_PC), .ALU(EX_Alu),
    .ALU_2(\扩展ex_mem_1_alu_2 ), .B(EX_B), .B_2(MDin), .Imm(EX_Imm), .Imm_2(\扩展ex_mem_1_imm_2 ),
    .En(or_2_out), .Clk(CLK));  // open: Clr, ERET, ERET_2
  Shifter #(.width(32), .shift("ll")) shifter_1 (.in(EX_Imm), .\dist (5'b00010), .out(shifter_1_out));
  Adder #(.width(32)) adder_3 (.a(shifter_1_out), .b(adder_2_out), .out(BranchPC));  // open: cin, cout
  Multiplexer #(.select(1), .width(32), .disabled("Z"), .enable("false")) multiplexer_12 (
    .in0({adder_2_out[31:28], EX_IR[25:0], 2'b00}), .in1(EX_A), .out(JmpPC), .sel(EX_JR));
  RAM #(.addrWidth(10), .dataWidth(32), .bus("separate"), .Select("high")) ram_1 (
    .addr(\扩展ex_mem_1_alu_2 [11:2]), .din(MDin), .data(ram_1_data), .str(MemWrite), .clk(CLK));  // open: sel, ld, clr
  \扩展MEM_WB  \u_扩展mem_wb_1  (
    .Halt(\扩展ex_mem_1_halt_2 ), .Halt_2(Halt), .W_num(MEM_rW), .W_num_2(WB_rW),
    .MemToReg(\扩展ex_mem_1_memtoreg_2 ), .MemToReg_2(WB_MemToReg), .RegWrite(MEM_RegWrite),
    .RegWrite_2(RegWrite), .JAL(\扩展ex_mem_1_jal_2 ), .JAL_2(\扩展mem_wb_1_jal_2 ), .LB(\扩展ex_mem_1_lb_2 ),
    .LB_2(\扩展mem_wb_1_lb_2 ), .LUI(\扩展ex_mem_1_lui_2 ), .LUI_2(\扩展mem_wb_1_lui_2 ), .IR(MEM_IR),
    .IR_2(WB_IR), .PC(M_PC), .PC_2(WB_PC), .ALU(\扩展ex_mem_1_alu_2 ), .ALU_2(\扩展mem_wb_1_alu_2 ),
    .MD(ram_1_data), .MD_2(\扩展mem_wb_1_md_2 ), .Imm(\扩展ex_mem_1_imm_2 ), .Imm_2(\扩展mem_wb_1_imm_2 ),
    .En(or_2_out), .Clk(CLK));  // open: Clr, ERET, ERET_2
  assign bit_extender_3_out = {{24{multiplexer_13_out[7]}}, multiplexer_13_out};  // Bit_Extender bit_extender_3
  Multiplexer #(.select(2), .width(8), .disabled("Z"), .enable("false")) multiplexer_13 (
    .in0(\扩展mem_wb_1_md_2 [7:0]), .in1(\扩展mem_wb_1_md_2 [15:8]), .in2(\扩展mem_wb_1_md_2 [23:16]),
    .in3(\扩展mem_wb_1_md_2 [31:24]), .out(multiplexer_13_out), .sel(\扩展mem_wb_1_alu_2 [1:0]));
  Multiplexer #(.select(1), .width(32), .disabled("Z"), .enable("false")) multiplexer_14 (
    .in0(\扩展mem_wb_1_md_2 ), .in1(bit_extender_3_out), .out(multiplexer_14_out), .sel(\扩展mem_wb_1_lb_2 ));
  Multiplexer #(.select(1), .width(32), .disabled("Z"), .enable("false")) multiplexer_15 (
    .in0(\扩展mem_wb_1_alu_2 ), .in1(multiplexer_14_out), .out(multiplexer_15_out), .sel(WB_MemToReg));
  Multiplexer #(.select(1), .width(32), .disabled("Z"), .enable("false")) multiplexer_16 (
    .in0(multiplexer_15_out), .in1(\扩展mem_wb_1_imm_2 ), .out(multiplexer_16_out), .sel(\扩展mem_wb_1_lui_2 ));
  Multiplexer #(.select(1), .width(32), .disabled("Z"), .enable("false")) multiplexer_17 (
    .in0(multiplexer_16_out), .in1(adder_4_out), .out(RDin), .sel(\扩展mem_wb_1_jal_2 ));
  Adder #(.width(32)) adder_4 (.a(WB_PC), .b(32'h4), .out(adder_4_out));  // open: cin, cout

  // Other names for the same wires on the sheet: IR[31:0] = IF_IR; MEM_MemWrite = MemWrite; MEM_PC[31:0] = M_PC;
  //   Stall = LoadUse; WB_RegWrite = RegWrite

  // Notes on the sheet:
  //   中断源
  //   时空图监测，可删除
  //   中断等待指示
  //   数码管输出
  //   OP
  //   Func
  //   rs
  //   rt
  //   contents of rom_1 (hex, n*v repeats v):
  //   20110001 8000c05 20110001 20120002 20130003 8000c09 20110001 20120002 20130003 8000c0d 20110001
  //   20120002 20130003 8000c11 20110001 20120002 20130003 c000cb8 20100001 20110001 118fc0 112020
  //   20020022 c 118882 12200001 8000c15 112020 20020022 c 20110001 118880 112020 20020022 c 12200001
  //   8000c1f 20110001 118fc0 112020 20020022 c 1188c3 112020 20020022 c 118903 112020 20020022 c 118903
  //   112020 20020022 c 118903 112020 20020022 c 118903 112020 20020022 c 118903 112020 20020022 c 118903
  //   112020 20020022 c 118903 112020 20020022 c 20100001 109fc0 139fc3 8021 2012000c 24160003 26100001
  //   3210000f 20080008 20090001 139900 2709825 132020 20020022 c 1094022 1500fff9 22100001 2018000f
  //   2188024 108700 20080008 20090001 139902 2709825 132021 20020022 c 1094022 1500fff9 108702 2c9b022
  //   12c00001 8000c50 4020 1084027 84400 3508ffff 82021 20020022 c 2010ffff 20110000 ae300000 22100001
  //   22310004 ae300000 22100001 22310004 ae300000 22100001 22310004 ae300000 22100001 22310004 ae300000
  //   22100001 22310004 ae300000 22100001 22310004 ae300000 22100001 22310004 ae300000 22100001 22310004
  //   ae300000 22100001 22310004 ae300000 22100001 22310004 ae300000 22100001 22310004 ae300000 22100001
  //   22310004 ae300000 22100001 22310004 ae300000 22100001 22310004 ae300000 22100001 22310004 ae300000
  //   22100001 22310004 22100001 8020 2011003c 8e130000 8e340000 274402a 11000002 ae330000 ae140000
  //   2231fffc 1611fff8 102020 20020022 c 22100004 2011003c 1611fff2 20020032 c 20100000 22100001 102020
  //   20020022 c 22100002 102020 20020022 c 22100003 102020 20020022 c 22100004 102020 20020022 c 22100005
  //   102020 20020022 c 22100006 102020 20020022 c 22100007 102020 20020022 c 22100008 102020 20020022
  //   20020022 c 3e00008
  //   OP
  //   Func
  //   rd
  //   rs
  //   rt
  //   imm
  //   rt
  //   流水调试日志用
  //   v0
  //   rs
  //   a0
  //   为方便自动评测，需要输出流水线各段保存的PC值，注意是PC不是PC+4，另外ID段寄存器写入信息，Mem段内存写入信息也要输出
  //   sa
  //   instr_index
endmodule

module \中断按键参考电路  (
  input  clk,
  input  IR,
  input  Clr,
  output IR_2,
  output W
);

  wire and_1_out, d_ff_1_q, or_2_out;

  or or_1 (W, IR_2, d_ff_1_q);
  D_Flip_Flop #(.trigger("rising"), .Pre_Clr_Positions("LEGACY"), .NegatePresetClear("false"), .enable("true"), .NewFFLayout("false")) d_ff_1 (
    .clk(IR), .D(1'b1), .Q(d_ff_1_q), .reset(IR_2));  // open: Qn, preset, en
  or or_2 (or_2_out, d_ff_1_q, IR_2);
  and and_1 (and_1_out, or_2_out, ~Clr);  // AND_Gate
  D_Flip_Flop #(.trigger("rising"), .Pre_Clr_Positions("LEGACY"), .NegatePresetClear("false"), .enable("true"), .NewFFLayout("false")) u_IR (
    .clk(clk), .D(and_1_out), .Q(IR_2));  // open: Qn, preset, en, reset

  // Notes on the sheet:
  //   中断信号采样参考电路
  //   Reset 
endmodule

module ID_EX (
  input  Syscall,
  input  [4:0] W_num,
  input  MemToReg,
  input  RegWrite,
  input  JAL,
  input  MemWrite,
  input  [3:0] AluOP,
  input  AluSrcB,
  input  Beq,
  input  Bne,
  input  JMP,
  input  JR,
  input  [31:0] IR,
  input  [31:0] PC,
  input  [31:0] A,
  input  [31:0] B,
  input  [31:0] Imm,
  input  in_18,
  input  in_19,
  output Syscall_2,
  output [4:0] W_num_2,
  output MemToReg_2,
  output RegWrite_2,
  output JAL_2,
  output MemWrite_2,
  output [3:0] AluOP_2,
  output AluSrcB_2,
  output Beq_2,
  output Bne_2,
  output JMP_2,
  output JR_2,
  output [31:0] IR_2,
  output [31:0] PC_2,
  output [31:0] A_2,
  output [31:0] B_2,
  output [31:0] Imm_2
);

  Register #(.width(1), .trigger("rising"), .Select("low")) u_Syscall (
    .D(Syscall), .en(in_18), .Q(Syscall_2), .clk(in_19));  // open: clr
  Register #(.width(8), .trigger("rising"), .Select("low")) WB (
    .D({JAL, RegWrite, MemToReg, W_num}), .en(in_18), .Q({JAL_2, RegWrite_2, MemToReg_2, W_num_2}),
    .clk(in_19));  // open: clr
  Register #(.width(1), .trigger("rising"), .Select("low")) MEM (
    .D(MemWrite), .en(in_18), .Q(MemWrite_2), .clk(in_19));  // open: clr
  Register #(.width(9), .trigger("rising"), .Select("low")) EX (
    .D({JR, JMP, Bne, Beq, AluSrcB, AluOP}), .en(in_18), .Q({JR_2, JMP_2, Bne_2, Beq_2, AluSrcB_2, AluOP_2}),
    .clk(in_19));  // open: clr
  Register #(.width(32), .trigger("rising"), .Select("low")) u_IR (
    .D(IR), .en(in_18), .Q(IR_2), .clk(in_19));  // open: clr
  Register #(.width(32), .trigger("rising"), .Select("low")) u_PC (.D(PC), .Q(PC_2), .clk(in_19));  // open: en, clr
  Register #(.width(32), .trigger("rising"), .Select("low")) u_A (
    .D(A), .en(in_18), .Q(A_2), .clk(in_19));  // open: clr
  Register #(.width(32), .trigger("rising"), .Select("low")) u_B (
    .D(B), .en(in_18), .Q(B_2), .clk(in_19));  // open: clr
  Register #(.width(32), .trigger("rising"), .Select("low")) u_Imm (
    .D(Imm), .en(in_18), .Q(Imm_2), .clk(in_19));  // open: clr
endmodule

module IF_ID (
  input  [31:0] IR,
  input  [31:0] PC,
  input  in_3,
  input  in_4,
  output [31:0] IR_2,
  output [31:0] PC_2
);

  Register #(.width(32), .trigger("rising"), .Select("low")) u_IR (
    .D(IR), .en(in_3), .Q(IR_2), .clk(in_4));  // open: clr
  Register #(.width(32), .trigger("rising"), .Select("low")) u_PC (
    .D(PC), .en(in_3), .Q(PC_2), .clk(in_4));  // open: clr
endmodule

module EX_MEM (
  input  Halt,
  input  [4:0] W_num,
  input  MemToReg,
  input  RegWrite,
  input  JAL,
  input  MemWrite,
  input  [31:0] IR,
  input  [31:0] PC,
  input  [31:0] ALU,
  input  [31:0] B,
  input  in_11,
  input  in_12,
  output Halt_2,
  output [4:0] W_num_2,
  output MemToReg_2,
  output RegWrite_2,
  output JAL_2,
  output MemWrite_2,
  output [31:0] IR_2,
  output [31:0] PC_2,
  output [31:0] ALU_2,
  output [31:0] B_2
);

  Register #(.width(1), .trigger("rising"), .Select("low")) u_Halt (
    .D(Halt), .en(in_11), .Q(Halt_2), .clk(in_12));  // open: clr
  Register #(.width(8), .trigger("rising"), .Select("low")) WB (
    .D({JAL, RegWrite, MemToReg, W_num}), .en(in_11), .Q({JAL_2, RegWrite_2, MemToReg_2, W_num_2}),
    .clk(in_12));  // open: clr
  Register #(.width(1), .trigger("rising"), .Select("low")) MEM (
    .D(MemWrite), .en(in_11), .Q(MemWrite_2), .clk(in_12));  // open: clr
  Register #(.width(32), .trigger("rising"), .Select("low")) u_IR (
    .D(IR), .en(in_11), .Q(IR_2), .clk(in_12));  // open: clr
  Register #(.width(32), .trigger("rising"), .Select("low")) u_PC (
    .D(PC), .en(in_11), .Q(PC_2), .clk(in_12));  // open: clr
  Register #(.width(32), .trigger("rising"), .Select("low")) u_ALU (
    .D(ALU), .en(in_11), .Q(ALU_2), .clk(in_12));  // open: clr
  Register #(.width(32), .trigger("rising"), .Select("low")) u_B (
    .D(B), .en(in_11), .Q(B_2), .clk(in_12));  // open: clr
endmodule

module MEM_WB (
  input  Halt,
  input  [4:0] W_num,
  input  MemToReg,
  input  RegWrite,
  input  JAL,
  input  [31:0] IR,
  input  [31:0] PC,
  input  [31:0] ALU,
  input  [31:0] MD,
  input  in_10,
  input  in_11,
  output Halt_2,
  output [4:0] W_num_2,
  output MemToReg_2,
  output RegWrite_2,
  output JAL_2,
  output [31:0] IR_2,
  output [31:0] PC_2,
  output [31:0] ALU_2,
  output [31:0] MD_2
);

  Register #(.width(1), .trigger("rising"), .Select("low")) register_1 (
    .D(Halt), .en(in_10), .Q(Halt_2), .clk(in_11));  // open: clr
  Register #(.width(8), .trigger("rising"), .Select("low")) WB (
    .D({JAL, RegWrite, MemToReg, W_num}), .en(in_10), .Q({JAL_2, RegWrite_2, MemToReg_2, W_num_2}),
    .clk(in_11));  // open: clr
  Register #(.width(32), .trigger("rising"), .Select("low")) u_IR (
    .D(IR), .en(in_10), .Q(IR_2), .clk(in_11));  // open: clr
  Register #(.width(32), .trigger("rising"), .Select("low")) u_PC (
    .D(PC), .en(in_10), .Q(PC_2), .clk(in_11));  // open: clr
  Register #(.width(32), .trigger("rising"), .Select("low")) u_ALU (
    .D(ALU), .en(in_10), .Q(ALU_2), .clk(in_11));  // open: clr
  Register #(.width(32), .trigger("rising"), .Select("low")) u_MD (
    .D(MD), .en(in_10), .Q(MD_2), .clk(in_11));  // open: clr
endmodule
module \扩展运算控制器  (
  input  OP0,
  input  OP1,
  input  OP2,
  input  OP3,
  input  OP4,
  input  OP5,
  input  F0,
  input  F1,
  input  F2,
  input  F3,
  input  F4,
  input  F5,
  output S0,
  output S1,
  output S2,
  output S3
);

  wire and_1_out, and_2_out, and_3_out, and_4_out, and_5_out, and_6_out, and_7_out, and_8_out, and_9_out,
       and_10_out, and_11_out, and_12_out, and_13_out, and_14_out, and_15_out, and_16_out, and_17_out,
       and_18_out, and_19_out, and_20_out, and_21_out, and_22_out, and_23_out, and_24_out, and_25_out,
       and_26_out, and_27_out, and_28_out, and_29_out, and_30_out, and_31_out, and_32_out, and_33_out,
       and_34_out, and_35_out, and_36_out, and_37_out, and_38_out, and_39_out, and_40_out, and_41_out,
       and_42_out, and_43_out, and_44_out, and_45_out, and_46_out, and_47_out, not_1_out, not_2_out,
       not_3_out, not_4_out, not_5_out, not_6_out, not_7_out, not_8_out, not_9_out, not_10_out, not_11_out,
       not_12_out, not_13_out, not_14_out, not_15_out, not_16_out, not_17_out, not_18_out, not_19_out,
       not_20_out, not_21_out, not_22_out, not_23_out, not_24_out, not_25_out, not_26_out, not_27_out,
       not_28_out, not_29_out, not_30_out, not_31_out, not_32_out, not_33_out, not_34_out, not_35_out,
       not_36_out, not_37_out, not_38_out, not_39_out, not_40_out, not_41_out, not_42_out, not_43_out,
       not_44_out, not_45_out, not_46_out, not_47_out, not_48_out, not_49_out, not_50_out, not_51_out,
       not_52_out, not_53_out, not_54_out, not_55_out, not_56_out, not_57_out, not_58_out, not_59_out,
       not_60_out, not_61_out, not_62_out, not_63_out, not_64_out, not_65_out, not_66_out, not_67_out,
       not_68_out, not_69_out, not_70_out, not_71_out, not_72_out, not_73_out, not_74_out, not_75_out,
       not_76_out, not_77_out, not_78_out, not_79_out, not_80_out, not_81_out, not_82_out, not_83_out,
       not_84_out, not_85_out, not_86_out, not_87_out, not_88_out, not_89_out, not_90_out, not_91_out,
       not_92_out, not_93_out, not_94_out, not_95_out, not_96_out, not_97_out, not_98_out, not_99_out,
       not_100_out, not_101_out, not_102_out, not_103_out, not_104_out, not_105_out, not_106_out,
       not_107_out, not_108_out, not_109_out, not_110_out, not_111_out, not_112_out, not_113_out,
       not_114_out, not_115_out, not_116_out, not_117_out, not_118_out, not_119_out, not_120_out,
       not_121_out, not_122_out, not_123_out, not_124_out, not_125_out, not_126_out, not_127_out,
       not_128_out, not_129_out, not_130_out, not_131_out, not_132_out, not_133_out, not_134_out,
       not_135_out, not_136_out, not_137_out, not_138_out, not_139_out, not_140_out, not_141_out,
       not_142_out, not_143_out, not_144_out, not_145_out, not_146_out, not_147_out, not_148_out,
       not_149_out, not_150_out, not_151_out, not_152_out, not_153_out, not_154_out, not_155_out,
       not_156_out, not_157_out, not_158_out, not_159_out, not_160_out, not_161_out, not_162_out,
       not_163_out, not_164_out, not_165_out, not_166_out, not_167_out, not_168_out, not_169_out,
       not_170_out, not_171_out, not_172_out, not_173_out, not_174_out, not_175_out, not_176_out,
       not_177_out, not_178_out, not_179_out, not_180_out, not_181_out, not_182_out, not_183_out,
       not_184_out, not_185_out, not_186_out, not_187_out, not_188_out, not_189_out, not_190_out,
       not_191_out, not_192_out, not_193_out, not_194_out, not_195_out, not_196_out, not_197_out,
       not_198_out, not_199_out, not_200_out, not_201_out, not_202_out, not_203_out, not_204_out,
       not_205_out, not_206_out, not_207_out, not_208_out, not_209_out, not_210_out, not_211_out,
       not_212_out, not_213_out, not_214_out, not_215_out, not_216_out, not_217_out, not_218_out,
       not_219_out, not_220_out, not_221_out, not_222_out, not_223_out, not_224_out, not_225_out,
       not_226_out, not_227_out, not_228_out, not_229_out, not_230_out, not_231_out, not_232_out,
       not_233_out, not_234_out, not_235_out, not_236_out, not_237_out, not_238_out, not_239_out,
       not_240_out, not_241_out, not_242_out, not_243_out, not_244_out, not_245_out, not_246_out,
       not_247_out, not_248_out, not_249_out, not_250_out, not_251_out, not_252_out, not_253_out,
       not_254_out, not_255_out, not_256_out, not_257_out, not_258_out, not_259_out, not_260_out,
       not_261_out, not_262_out, not_263_out, not_264_out, not_265_out, not_266_out, not_267_out,
       not_268_out, not_269_out, not_270_out, not_271_out, not_272_out, not_273_out, not_274_out,
       not_275_out, not_276_out, not_277_out, not_278_out, not_279_out, not_280_out, not_281_out,
       not_282_out, not_283_out, not_284_out, not_285_out, not_286_out, not_287_out, not_288_out,
       not_289_out, not_290_out, not_291_out, not_292_out, not_293_out, not_294_out, not_295_out,
       not_296_out, not_297_out, not_298_out, not_299_out, not_300_out, not_301_out, not_302_out,
       not_303_out, not_304_out, not_305_out, not_306_out;

  not not_1 (not_1_out, OP5);
  not not_2 (not_2_out, OP4);
  not not_3 (not_3_out, OP3);
  not not_4 (not_4_out, OP2);
  not not_5 (not_5_out, OP1);
  not not_6 (not_6_out, OP0);
  not not_7 (not_7_out, F5);
  not not_8 (not_8_out, F4);
  not not_9 (not_9_out, F3);
  not not_10 (not_10_out, F2);
  not not_11 (not_11_out, OP5);
  not not_12 (not_12_out, OP4);
  not not_13 (not_13_out, OP3);
  not not_14 (not_14_out, OP2);
  not not_15 (not_15_out, OP1);
  not not_16 (not_16_out, OP0);
  not not_17 (not_17_out, F4);
  not not_18 (not_18_out, F3);
  not not_19 (not_19_out, F2);
  not not_20 (not_20_out, F1);
  not not_21 (not_21_out, F0);
  not not_22 (not_22_out, OP5);
  not not_23 (not_23_out, OP4);
  not not_24 (not_24_out, OP3);
  not not_25 (not_25_out, OP2);
  not not_26 (not_26_out, OP1);
  not not_27 (not_27_out, OP0);
  not not_28 (not_28_out, F4);
  not not_29 (not_29_out, F3);
  not not_30 (not_30_out, F2);
  not not_31 (not_31_out, F1);
  not not_32 (not_32_out, OP5);
  not not_33 (not_33_out, OP4);
  not not_34 (not_34_out, OP3);
  not not_35 (not_35_out, OP2);
  not not_36 (not_36_out, OP1);
  not not_37 (not_37_out, OP0);
  not not_38 (not_38_out, F4);
  not not_39 (not_39_out, F3);
  not not_40 (not_40_out, F1);
  not not_41 (not_41_out, F0);
  not not_42 (not_42_out, OP5);
  not not_43 (not_43_out, OP4);
  not not_44 (not_44_out, OP3);
  not not_45 (not_45_out, OP2);
  not not_46 (not_46_out, OP1);
  not not_47 (not_47_out, OP0);
  not not_48 (not_48_out, F4);
  not not_49 (not_49_out, F2);
  not not_50 (not_50_out, F0);
  not not_51 (not_51_out, OP5);
  not not_52 (not_52_out, OP4);
  not not_53 (not_53_out, OP3);
  not not_54 (not_54_out, OP1);
  not not_55 (not_55_out, OP0);
  not not_56 (not_56_out, OP5);
  not not_57 (not_57_out, OP4);
  not not_58 (not_58_out, OP3);
  not not_59 (not_59_out, OP1);
  not not_60 (not_60_out, OP5);
  not not_61 (not_61_out, OP4);
  not not_62 (not_62_out, OP2);
  not not_63 (not_63_out, OP1);
  not not_64 (not_64_out, OP0);
  not not_65 (not_65_out, OP5);
  not not_66 (not_66_out, OP4);
  not not_67 (not_67_out, OP1);
  not not_68 (not_68_out, OP0);
  not not_69 (not_69_out, OP5);
  not not_70 (not_70_out, OP4);
  not not_71 (not_71_out, OP2);
  not not_72 (not_72_out, OP1);
  not not_73 (not_73_out, OP5);
  not not_74 (not_74_out, OP4);
  not not_75 (not_75_out, OP2);
  not not_76 (not_76_out, OP0);
  not not_77 (not_77_out, OP4);
  not not_78 (not_78_out, OP3);
  not not_79 (not_79_out, OP2);
  not not_80 (not_80_out, OP4);
  not not_81 (not_81_out, OP2);
  not not_82 (not_82_out, OP5);
  not not_83 (not_83_out, OP4);
  not not_84 (not_84_out, OP3);
  not not_85 (not_85_out, OP2);
  not not_86 (not_86_out, OP1);
  not not_87 (not_87_out, OP0);
  not not_88 (not_88_out, F4);
  not not_89 (not_89_out, F3);
  not not_90 (not_90_out, F0);
  not not_91 (not_91_out, OP4);
  not not_92 (not_92_out, OP3);
  not not_93 (not_93_out, OP2);
  not not_94 (not_94_out, OP1);
  not not_95 (not_95_out, OP0);
  not not_96 (not_96_out, OP5);
  not not_97 (not_97_out, OP4);
  not not_98 (not_98_out, OP3);
  not not_99 (not_99_out, OP2);
  not not_100 (not_100_out, OP1);
  not not_101 (not_101_out, OP5);
  not not_102 (not_102_out, OP4);
  not not_103 (not_103_out, OP3);
  not not_104 (not_104_out, OP2);
  not not_105 (not_105_out, OP1);
  not not_106 (not_106_out, OP0);
  not not_107 (not_107_out, F5);
  not not_108 (not_108_out, F4);
  not not_109 (not_109_out, F3);
  not not_110 (not_110_out, F2);
  not not_111 (not_111_out, F0);
  not not_112 (not_112_out, OP5);
  not not_113 (not_113_out, OP4);
  not not_114 (not_114_out, OP3);
  not not_115 (not_115_out, OP2);
  not not_116 (not_116_out, OP1);
  not not_117 (not_117_out, OP0);
  not not_118 (not_118_out, F4);
  not not_119 (not_119_out, F3);
  not not_120 (not_120_out, F2);
  not not_121 (not_121_out, F0);
  not not_122 (not_122_out, OP5);
  not not_123 (not_123_out, OP4);
  not not_124 (not_124_out, OP3);
  not not_125 (not_125_out, OP2);
  not not_126 (not_126_out, OP1);
  not not_127 (not_127_out, OP0);
  not not_128 (not_128_out, F4);
  not not_129 (not_129_out, F3);
  not not_130 (not_130_out, F1);
  not not_131 (not_131_out, F0);
  not not_132 (not_132_out, OP5);
  not not_133 (not_133_out, OP4);
  not not_134 (not_134_out, OP3);
  not not_135 (not_135_out, OP2);
  not not_136 (not_136_out, OP1);
  not not_137 (not_137_out, OP0);
  not not_138 (not_138_out, F4);
  not not_139 (not_139_out, F3);
  not not_140 (not_140_out, OP5);
  not not_141 (not_141_out, OP4);
  not not_142 (not_142_out, OP3);
  not not_143 (not_143_out, OP2);
  not not_144 (not_144_out, OP1);
  not not_145 (not_145_out, OP0);
  not not_146 (not_146_out, F4);
  not not_147 (not_147_out, F2);
  not not_148 (not_148_out, F0);
  not not_149 (not_149_out, OP5);
  not not_150 (not_150_out, OP4);
  not not_151 (not_151_out, OP3);
  not not_152 (not_152_out, OP1);
  not not_153 (not_153_out, OP0);
  not not_154 (not_154_out, OP5);
  not not_155 (not_155_out, OP4);
  not not_156 (not_156_out, OP3);
  not not_157 (not_157_out, OP1);
  not not_158 (not_158_out, OP5);
  not not_159 (not_159_out, OP4);
  not not_160 (not_160_out, OP1);
  not not_161 (not_161_out, OP0);
  not not_162 (not_162_out, OP5);
  not not_163 (not_163_out, OP4);
  not not_164 (not_164_out, OP2);
  not not_165 (not_165_out, OP0);
  not not_166 (not_166_out, OP5);
  not not_167 (not_167_out, OP4);
  not not_168 (not_168_out, OP3);
  not not_169 (not_169_out, OP2);
  not not_170 (not_170_out, OP1);
  not not_171 (not_171_out, OP5);
  not not_172 (not_172_out, OP4);
  not not_173 (not_173_out, OP3);
  not not_174 (not_174_out, OP2);
  not not_175 (not_175_out, OP1);
  not not_176 (not_176_out, OP0);
  not not_177 (not_177_out, F4);
  not not_178 (not_178_out, F3);
  not not_179 (not_179_out, F2);
  not not_180 (not_180_out, F1);
  not not_181 (not_181_out, F0);
  not not_182 (not_182_out, OP5);
  not not_183 (not_183_out, OP4);
  not not_184 (not_184_out, OP3);
  not not_185 (not_185_out, OP2);
  not not_186 (not_186_out, OP1);
  not not_187 (not_187_out, OP0);
  not not_188 (not_188_out, F4);
  not not_189 (not_189_out, F3);
  not not_190 (not_190_out, F2);
  not not_191 (not_191_out, F1);
  not not_192 (not_192_out, OP5);
  not not_193 (not_193_out, OP4);
  not not_194 (not_194_out, OP3);
  not not_195 (not_195_out, OP2);
  not not_196 (not_196_out, OP1);
  not not_197 (not_197_out, OP0);
  not not_198 (not_198_out, F4);
  not not_199 (not_199_out, F3);
  not not_200 (not_200_out, F2);
  not not_201 (not_201_out, F0);
  not not_202 (not_202_out, OP5);
  not not_203 (not_203_out, OP4);
  not not_204 (not_204_out, OP3);
  not not_205 (not_205_out, OP2);
  not not_206 (not_206_out, OP1);
  not not_207 (not_207_out, OP0);
  not not_208 (not_208_out, F4);
  not not_209 (not_209_out, F3);
  not not_210 (not_210_out, F1);
  not not_211 (not_211_out, F0);
  not not_212 (not_212_out, OP5);
  not not_213 (not_213_out, OP4);
  not not_214 (not_214_out, OP3);
  not not_215 (not_215_out, OP2);
  not not_216 (not_216_out, OP1);
  not not_217 (not_217_out, OP0);
  not not_218 (not_218_out, F4);
  not not_219 (not_219_out, F2);
  not not_220 (not_220_out, OP5);
  not not_221 (not_221_out, OP4);
  not not_222 (not_222_out, OP2);
  not not_223 (not_223_out, OP1);
  not not_224 (not_224_out, OP0);
  not not_225 (not_225_out, OP5);
  not not_226 (not_226_out, OP4);
  not not_227 (not_227_out, OP1);
  not not_228 (not_228_out, OP0);
  not not_229 (not_229_out, OP5);
  not not_230 (not_230_out, OP4);
  not not_231 (not_231_out, OP2);
  not not_232 (not_232_out, OP1);
  not not_233 (not_233_out, OP4);
  not not_234 (not_234_out, OP3);
  not not_235 (not_235_out, OP2);
  not not_236 (not_236_out, OP4);
  not not_237 (not_237_out, OP2);
  not not_238 (not_238_out, OP4);
  not not_239 (not_239_out, OP3);
  not not_240 (not_240_out, OP2);
  not not_241 (not_241_out, OP1);
  not not_242 (not_242_out, OP0);
  not not_243 (not_243_out, OP5);
  not not_244 (not_244_out, OP4);
  not not_245 (not_245_out, OP3);
  not not_246 (not_246_out, OP2);
  not not_247 (not_247_out, OP1);
  not not_248 (not_248_out, OP0);
  not not_249 (not_249_out, F4);
  not not_250 (not_250_out, F3);
  not not_251 (not_251_out, F1);
  not not_252 (not_252_out, OP5);
  not not_253 (not_253_out, OP4);
  not not_254 (not_254_out, OP3);
  not not_255 (not_255_out, OP2);
  not not_256 (not_256_out, OP1);
  not not_257 (not_257_out, OP0);
  not not_258 (not_258_out, F4);
  not not_259 (not_259_out, F3);
  not not_260 (not_260_out, OP5);
  not not_261 (not_261_out, OP4);
  not not_262 (not_262_out, OP3);
  not not_263 (not_263_out, OP2);
  not not_264 (not_264_out, OP1);
  not not_265 (not_265_out, OP0);
  not not_266 (not_266_out, F4);
  not not_267 (not_267_out, F2);
  not not_268 (not_268_out, F0);
  not not_269 (not_269_out, OP5);
  not not_270 (not_270_out, OP4);
  not not_271 (not_271_out, OP3);
  not not_272 (not_272_out, OP2);
  not not_273 (not_273_out, OP1);
  not not_274 (not_274_out, OP0);
  not not_275 (not_275_out, F4);
  not not_276 (not_276_out, F2);
  not not_277 (not_277_out, OP5);
  not not_278 (not_278_out, OP4);
  not not_279 (not_279_out, OP3);
  not not_280 (not_280_out, OP1);
  not not_281 (not_281_out, OP0);
  not not_282 (not_282_out, OP5);
  not not_283 (not_283_out, OP4);
  not not_284 (not_284_out, OP3);
  not not_285 (not_285_out, OP1);
  not not_286 (not_286_out, OP5);
  not not_287 (not_287_out, OP4);
  not not_288 (not_288_out, OP2);
  not not_289 (not_289_out, OP0);
  not not_290 (not_290_out, OP5);
  not not_291 (not_291_out, OP4);
  not not_292 (not_292_out, OP1);
  not not_293 (not_293_out, OP5);
  not not_294 (not_294_out, OP4);
  not not_295 (not_295_out, OP3);
  not not_296 (not_296_out, OP2);
  not not_297 (not_297_out, OP1);
  not not_298 (not_298_out, OP0);
  not not_299 (not_299_out, F4);
  not not_300 (not_300_out, F3);
  not not_301 (not_301_out, F0);
  not not_302 (not_302_out, OP5);
  not not_303 (not_303_out, OP4);
  not not_304 (not_304_out, OP3);
  not not_305 (not_305_out, OP2);
  not not_306 (not_306_out, OP1);
  and and_1 (and_1_out, not_1_out, not_2_out, not_3_out, not_4_out, not_5_out, not_6_out, not_7_out, not_8_out, not_9_out, not_10_out, F1, F0);
  and and_2 (and_2_out, not_11_out, not_12_out, not_13_out, not_14_out, not_15_out, not_16_out, F5, not_17_out, not_18_out, not_19_out, not_20_out, not_21_out);
  and and_3 (and_3_out, not_22_out, not_23_out, not_24_out, not_25_out, not_26_out, not_27_out, F5, not_28_out, not_29_out, not_30_out, not_31_out, F0);
  and and_4 (and_4_out, not_32_out, not_33_out, not_34_out, not_35_out, not_36_out, not_37_out, F5, not_38_out, not_39_out, F2, not_40_out, not_41_out);
  and and_5 (and_5_out, not_42_out, not_43_out, not_44_out, not_45_out, not_46_out, not_47_out, F5, not_48_out, F3, not_49_out, F1, not_50_out);
  and and_6 (and_6_out, not_51_out, not_52_out, not_53_out, OP2, not_54_out, not_55_out);
  and and_7 (and_7_out, not_56_out, not_57_out, not_58_out, OP2, not_59_out, OP0);
  and and_8 (and_8_out, not_60_out, not_61_out, OP3, not_62_out, not_63_out, not_64_out);
  and and_9 (and_9_out, not_65_out, not_66_out, OP3, OP2, not_67_out, not_68_out);
  and and_10 (and_10_out, not_69_out, not_70_out, OP3, not_71_out, not_72_out, OP0);
  and and_11 (and_11_out, not_73_out, not_74_out, OP3, not_75_out, OP1, not_76_out);
  and and_12 (and_12_out, OP5, not_77_out, not_78_out, not_79_out, OP1, OP0);
  and and_13 (and_13_out, OP5, not_80_out, OP3, not_81_out, OP1, OP0);
  and and_14 (and_14_out, not_82_out, not_83_out, not_84_out, not_85_out, not_86_out, not_87_out, F5, not_88_out, not_89_out, F2, F1, not_90_out);
  and and_15 (and_15_out, OP5, not_91_out, not_92_out, not_93_out, not_94_out, not_95_out);
  and and_16 (and_16_out, not_96_out, not_97_out, not_98_out, not_99_out, not_100_out, OP0);
  and and_17 (and_17_out, not_101_out, not_102_out, not_103_out, not_104_out, not_105_out, not_106_out, not_107_out, not_108_out, not_109_out, not_110_out, F1, not_111_out);
  and and_18 (and_18_out, not_112_out, not_113_out, not_114_out, not_115_out, not_116_out, not_117_out, F5, not_118_out, not_119_out, not_120_out, F1, not_121_out);
  and and_19 (and_19_out, not_122_out, not_123_out, not_124_out, not_125_out, not_126_out, not_127_out, F5, not_128_out, not_129_out, F2, not_130_out, not_131_out);
  and and_20 (and_20_out, not_132_out, not_133_out, not_134_out, not_135_out, not_136_out, not_137_out, F5, not_138_out, not_139_out, F2, F1, F0);
  and and_21 (and_21_out, not_140_out, not_141_out, not_142_out, not_143_out, not_144_out, not_145_out, F5, not_146_out, F3, not_147_out, F1, not_148_out);
  and and_22 (and_22_out, not_149_out, not_150_out, not_151_out, OP2, not_152_out, not_153_out);
  and and_23 (and_23_out, not_154_out, not_155_out, not_156_out, OP2, not_157_out, OP0);
  and and_24 (and_24_out, not_158_out, not_159_out, OP3, OP2, not_160_out, not_161_out);
  and and_25 (and_25_out, not_162_out, not_163_out, OP3, not_164_out, OP1, not_165_out);
  and and_26 (and_26_out, not_166_out, not_167_out, not_168_out, not_169_out, not_170_out, OP0);
  and and_27 (and_27_out, not_171_out, not_172_out, not_173_out, not_174_out, not_175_out, not_176_out, F5, not_177_out, not_178_out, not_179_out, not_180_out, not_181_out);
  and and_28 (and_28_out, not_182_out, not_183_out, not_184_out, not_185_out, not_186_out, not_187_out, F5, not_188_out, not_189_out, not_190_out, not_191_out, F0);
  and and_29 (and_29_out, not_192_out, not_193_out, not_194_out, not_195_out, not_196_out, not_197_out, F5, not_198_out, not_199_out, not_200_out, F1, not_201_out);
  and and_30 (and_30_out, not_202_out, not_203_out, not_204_out, not_205_out, not_206_out, not_207_out, F5, not_208_out, not_209_out, F2, not_210_out, not_211_out);
  and and_31 (and_31_out, not_212_out, not_213_out, not_214_out, not_215_out, not_216_out, not_217_out, F5, not_218_out, F3, not_219_out, F1, F0);
  and and_32 (and_32_out, not_220_out, not_221_out, OP3, not_222_out, not_223_out, not_224_out);
  and and_33 (and_33_out, not_225_out, not_226_out, OP3, OP2, not_227_out, not_228_out);
  and and_34 (and_34_out, not_229_out, not_230_out, OP3, not_231_out, not_232_out, OP0);
  and and_35 (and_35_out, OP5, not_233_out, not_234_out, not_235_out, OP1, OP0);
  and and_36 (and_36_out, OP5, not_236_out, OP3, not_237_out, OP1, OP0);
  and and_37 (and_37_out, OP5, not_238_out, not_239_out, not_240_out, not_241_out, not_242_out);
  and and_38 (and_38_out, not_243_out, not_244_out, not_245_out, not_246_out, not_247_out, not_248_out, F5, not_249_out, not_250_out, F2, not_251_out, F0);
  and and_39 (and_39_out, not_252_out, not_253_out, not_254_out, not_255_out, not_256_out, not_257_out, F5, not_258_out, not_259_out, F2, F1, F0);
  and and_40 (and_40_out, not_260_out, not_261_out, not_262_out, not_263_out, not_264_out, not_265_out, F5, not_266_out, F3, not_267_out, F1, not_268_out);
  and and_41 (and_41_out, not_269_out, not_270_out, not_271_out, not_272_out, not_273_out, not_274_out, F5, not_275_out, F3, not_276_out, F1, F0);
  and and_42 (and_42_out, not_277_out, not_278_out, not_279_out, OP2, not_280_out, not_281_out);
  and and_43 (and_43_out, not_282_out, not_283_out, not_284_out, OP2, not_285_out, OP0);
  and and_44 (and_44_out, not_286_out, not_287_out, OP3, not_288_out, OP1, not_289_out);
  and and_45 (and_45_out, not_290_out, not_291_out, OP3, OP2, not_292_out, OP0);
  and and_46 (and_46_out, not_293_out, not_294_out, not_295_out, not_296_out, not_297_out, not_298_out, F5, not_299_out, not_300_out, F2, F1, not_301_out);
  and and_47 (and_47_out, not_302_out, not_303_out, not_304_out, not_305_out, not_306_out, OP0);
  or or_1 (S1, and_17_out, and_18_out, and_19_out, and_20_out, and_21_out, and_22_out, and_23_out, and_24_out, and_25_out, and_26_out);
  or or_2 (S2, and_27_out, and_28_out, and_29_out, and_30_out, and_31_out, and_32_out, and_33_out, and_34_out, and_35_out, and_36_out, and_37_out);
  or or_3 (S3, and_38_out, and_39_out, and_40_out, and_41_out, and_42_out, and_43_out, and_44_out, and_45_out, and_46_out, and_47_out);
  or or_4 (S0, and_1_out, and_2_out, and_3_out, and_4_out, and_5_out, and_6_out, and_7_out, and_8_out, and_9_out, and_10_out, and_11_out, and_12_out, and_13_out, and_14_out, and_15_out, and_16_out);
endmodule

module \扩展控制信号  (
  input  OP0,
  input  OP1,
  input  OP2,
  input  OP3,
  input  OP4,
  input  OP5,
  input  F0,
  input  F1,
  input  F2,
  input  F3,
  input  F4,
  input  F5,
  output MemToReg,
  output MemWrite,
  output ALU_SRC,
  output RegWrite,
  output SysCALL,
  output SignedExt,
  output RegDst,
  output BEQ,
  output BNE,
  output JR,
  output JMP,
  output JAL,
  output LUI,
  output LB,
  output BLTZ,
  output ERET
);

  wire and_1_out, and_2_out, and_4_out, and_5_out, and_6_out, and_7_out, and_8_out, and_9_out, and_10_out,
       and_11_out, and_12_out, and_13_out, and_14_out, and_15_out, and_16_out, and_17_out, and_19_out,
       and_20_out, and_21_out, and_22_out, and_23_out, and_24_out, and_25_out, and_26_out, and_30_out,
       and_31_out, not_1_out, not_2_out, not_3_out, not_4_out, not_5_out, not_6_out, not_7_out, not_8_out,
       not_9_out, not_10_out, not_11_out, not_12_out, not_13_out, not_14_out, not_15_out, not_16_out,
       not_17_out, not_18_out, not_19_out, not_20_out, not_21_out, not_22_out, not_23_out, not_24_out,
       not_25_out, not_26_out, not_27_out, not_28_out, not_29_out, not_30_out, not_31_out, not_32_out,
       not_33_out, not_34_out, not_35_out, not_36_out, not_37_out, not_38_out, not_39_out, not_40_out,
       not_41_out, not_42_out, not_43_out, not_44_out, not_45_out, not_46_out, not_47_out, not_48_out,
       not_49_out, not_50_out, not_51_out, not_52_out, not_53_out, not_54_out, not_55_out, not_56_out,
       not_57_out, not_58_out, not_59_out, not_60_out, not_61_out, not_62_out, not_63_out, not_64_out,
       not_65_out, not_66_out, not_67_out, not_68_out, not_69_out, not_70_out, not_71_out, not_72_out,
       not_73_out, not_74_out, not_75_out, not_76_out, not_77_out, not_78_out, not_79_out, not_80_out,
       not_81_out, not_82_out, not_83_out, not_84_out, not_85_out, not_86_out, not_87_out, not_88_out,
       not_89_out, not_90_out, not_91_out, not_92_out, not_93_out, not_94_out, not_95_out, not_96_out,
       not_97_out, not_98_out, not_99_out, not_100_out, not_101_out, not_102_out, not_103_out, not_104_out,
       not_105_out, not_106_out, not_107_out, not_108_out, not_109_out, not_110_out, not_111_out,
       not_112_out, not_113_out, not_114_out, not_115_out, not_116_out, not_117_out, not_118_out,
       not_119_out, not_120_out, not_121_out, not_122_out, not_123_out, not_124_out, not_125_out,
       not_126_out, not_127_out, not_128_out, not_129_out, not_130_out, not_131_out, not_132_out,
       not_133_out, not_134_out, not_135_out, not_136_out, not_137_out, not_138_out, not_139_out,
       not_140_out, not_141_out, not_142_out, not_143_out, not_144_out, not_145_out, not_146_out,
       not_147_out, not_148_out, not_149_out, not_150_out, not_151_out, not_152_out, not_153_out,
       not_154_out, not_155_out, not_156_out, not_157_out, not_158_out, not_159_out, not_160_out,
       not_161_out, not_162_out, not_163_out, not_164_out, not_165_out, not_166_out, not_167_out,
       not_168_out, not_169_out, not_170_out, not_171_out, not_172_out, not_173_out, not_174_out,
       not_175_out, not_176_out, not_177_out, not_178_out, not_179_out, not_180_out, not_181_out,
       not_182_out, not_183_out, not_184_out, not_185_out, not_186_out, not_187_out, not_188_out,
       not_189_out, not_190_out, not_191_out, not_192_out, not_193_out, not_194_out, not_195_out,
       not_196_out, not_197_out, not_198_out, not_199_out, not_200_out, not_201_out, not_202_out,
       not_203_out, not_204_out, not_205_out, not_206_out, not_207_out;

  not not_1 (not_1_out, OP0);
  not not_2 (not_2_out, OP1);
  not not_3 (not_3_out, OP2);
  not not_4 (not_4_out, OP3);
  not not_5 (not_5_out, OP4);
  not not_6 (not_6_out, OP2);
  not not_7 (not_7_out, OP3);
  not not_8 (not_8_out, OP4);
  not not_9 (not_9_out, OP2);
  not not_10 (not_10_out, OP4);
  not not_11 (not_11_out, OP0);
  not not_12 (not_12_out, OP1);
  not not_13 (not_13_out, OP2);
  not not_14 (not_14_out, OP3);
  not not_15 (not_15_out, OP4);
  not not_16 (not_16_out, OP0);
  not not_17 (not_17_out, OP2);
  not not_18 (not_18_out, OP4);
  not not_19 (not_19_out, OP5);
  not not_20 (not_20_out, OP1);
  not not_21 (not_21_out, OP4);
  not not_22 (not_22_out, OP5);
  not not_23 (not_23_out, OP2);
  not not_24 (not_24_out, OP4);
  not not_25 (not_25_out, OP0);
  not not_26 (not_26_out, OP1);
  not not_27 (not_27_out, OP2);
  not not_28 (not_28_out, OP3);
  not not_29 (not_29_out, OP4);
  not not_30 (not_30_out, F0);
  not not_31 (not_31_out, F2);
  not not_32 (not_32_out, F3);
  not not_33 (not_33_out, F4);
  not not_34 (not_34_out, OP0);
  not not_35 (not_35_out, OP1);
  not not_36 (not_36_out, OP2);
  not not_37 (not_37_out, OP3);
  not not_38 (not_38_out, OP4);
  not not_39 (not_39_out, F1);
  not not_40 (not_40_out, F3);
  not not_41 (not_41_out, F4);
  not not_42 (not_42_out, OP0);
  not not_43 (not_43_out, OP1);
  not not_44 (not_44_out, OP2);
  not not_45 (not_45_out, OP3);
  not not_46 (not_46_out, OP4);
  not not_47 (not_47_out, F3);
  not not_48 (not_48_out, F4);
  not not_49 (not_49_out, OP0);
  not not_50 (not_50_out, OP1);
  not not_51 (not_51_out, OP2);
  not not_52 (not_52_out, OP3);
  not not_53 (not_53_out, OP4);
  not not_54 (not_54_out, F2);
  not not_55 (not_55_out, F3);
  not not_56 (not_56_out, F4);
  not not_57 (not_57_out, F5);
  not not_58 (not_58_out, OP0);
  not not_59 (not_59_out, OP1);
  not not_60 (not_60_out, OP2);
  not not_61 (not_61_out, OP3);
  not not_62 (not_62_out, OP4);
  not not_63 (not_63_out, F2);
  not not_64 (not_64_out, F4);
  not not_65 (not_65_out, OP0);
  not not_66 (not_66_out, OP1);
  not not_67 (not_67_out, OP2);
  not not_68 (not_68_out, OP3);
  not not_69 (not_69_out, OP4);
  not not_70 (not_70_out, OP0);
  not not_71 (not_71_out, OP2);
  not not_72 (not_72_out, OP4);
  not not_73 (not_73_out, OP5);
  not not_74 (not_74_out, OP1);
  not not_75 (not_75_out, OP4);
  not not_76 (not_76_out, OP5);
  not not_77 (not_77_out, OP4);
  not not_78 (not_78_out, OP5);
  not not_79 (not_79_out, OP2);
  not not_80 (not_80_out, OP3);
  not not_81 (not_81_out, OP4);
  not not_82 (not_82_out, OP0);
  not not_83 (not_83_out, OP1);
  not not_84 (not_84_out, OP2);
  not not_85 (not_85_out, OP3);
  not not_86 (not_86_out, OP4);
  not not_87 (not_87_out, OP5);
  not not_88 (not_88_out, F0);
  not not_89 (not_89_out, F1);
  not not_90 (not_90_out, F4);
  not not_91 (not_91_out, F5);
  not not_92 (not_92_out, OP0);
  not not_93 (not_93_out, OP2);
  not not_94 (not_94_out, OP4);
  not not_95 (not_95_out, OP5);
  not not_96 (not_96_out, OP1);
  not not_97 (not_97_out, OP3);
  not not_98 (not_98_out, OP4);
  not not_99 (not_99_out, OP5);
  not not_100 (not_100_out, OP1);
  not not_101 (not_101_out, OP3);
  not not_102 (not_102_out, OP4);
  not not_103 (not_103_out, OP5);
  not not_104 (not_104_out, OP0);
  not not_105 (not_105_out, OP1);
  not not_106 (not_106_out, OP2);
  not not_107 (not_107_out, OP3);
  not not_108 (not_108_out, OP4);
  not not_109 (not_109_out, OP5);
  not not_110 (not_110_out, F0);
  not not_111 (not_111_out, F2);
  not not_112 (not_112_out, F3);
  not not_113 (not_113_out, F4);
  not not_114 (not_114_out, OP0);
  not not_115 (not_115_out, OP1);
  not not_116 (not_116_out, OP2);
  not not_117 (not_117_out, OP3);
  not not_118 (not_118_out, OP4);
  not not_119 (not_119_out, OP5);
  not not_120 (not_120_out, F1);
  not not_121 (not_121_out, F3);
  not not_122 (not_122_out, F4);
  not not_123 (not_123_out, OP0);
  not not_124 (not_124_out, OP1);
  not not_125 (not_125_out, OP2);
  not not_126 (not_126_out, OP3);
  not not_127 (not_127_out, OP4);
  not not_128 (not_128_out, OP5);
  not not_129 (not_129_out, F3);
  not not_130 (not_130_out, F4);
  not not_131 (not_131_out, OP0);
  not not_132 (not_132_out, OP1);
  not not_133 (not_133_out, OP2);
  not not_134 (not_134_out, OP3);
  not not_135 (not_135_out, OP4);
  not not_136 (not_136_out, OP5);
  not not_137 (not_137_out, F2);
  not not_138 (not_138_out, F3);
  not not_139 (not_139_out, F4);
  not not_140 (not_140_out, F5);
  not not_141 (not_141_out, OP0);
  not not_142 (not_142_out, OP1);
  not not_143 (not_143_out, OP2);
  not not_144 (not_144_out, OP3);
  not not_145 (not_145_out, OP4);
  not not_146 (not_146_out, OP5);
  not not_147 (not_147_out, F2);
  not not_148 (not_148_out, F4);
  not not_149 (not_149_out, OP0);
  not not_150 (not_150_out, OP1);
  not not_151 (not_151_out, OP3);
  not not_152 (not_152_out, OP4);
  not not_153 (not_153_out, OP5);
  not not_154 (not_154_out, OP1);
  not not_155 (not_155_out, OP3);
  not not_156 (not_156_out, OP4);
  not not_157 (not_157_out, OP5);
  not not_158 (not_158_out, OP0);
  not not_159 (not_159_out, OP1);
  not not_160 (not_160_out, OP2);
  not not_161 (not_161_out, OP3);
  not not_162 (not_162_out, OP4);
  not not_163 (not_163_out, OP5);
  not not_164 (not_164_out, F0);
  not not_165 (not_165_out, F1);
  not not_166 (not_166_out, F2);
  not not_167 (not_167_out, F4);
  not not_168 (not_168_out, F5);
  not not_169 (not_169_out, OP0);
  not not_170 (not_170_out, OP2);
  not not_171 (not_171_out, OP3);
  not not_172 (not_172_out, OP4);
  not not_173 (not_173_out, OP5);
  not not_174 (not_174_out, F0);
  not not_175 (not_175_out, F1);
  not not_176 (not_176_out, F2);
  not not_177 (not_177_out, F4);
  not not_178 (not_178_out, F5);
  not not_179 (not_179_out, OP2);
  not not_180 (not_180_out, OP3);
  not not_181 (not_181_out, OP4);
  not not_182 (not_182_out, OP5);
  not not_183 (not_183_out, OP2);
  not not_184 (not_184_out, OP3);
  not not_185 (not_185_out, OP4);
  not not_186 (not_186_out, OP5);
  not not_187 (not_187_out, OP4);
  not not_188 (not_188_out, OP5);
  not not_189 (not_189_out, OP0);
  not not_190 (not_190_out, OP1);
  not not_191 (not_191_out, OP2);
  not not_192 (not_192_out, OP3);
  not not_193 (not_193_out, OP4);
  not not_194 (not_194_out, OP1);
  not not_195 (not_195_out, OP2);
  not not_196 (not_196_out, OP3);
  not not_197 (not_197_out, OP4);
  not not_198 (not_198_out, OP5);
  not not_199 (not_199_out, OP5);
  not not_200 (not_200_out, OP3);
  not not_201 (not_201_out, OP2);
  not not_202 (not_202_out, OP1);
  not not_203 (not_203_out, OP0);
  not not_204 (not_204_out, F5);
  not not_205 (not_205_out, F2);
  not not_206 (not_206_out, F1);
  not not_207 (not_207_out, F0);
  and and_1 (and_1_out, not_1_out, not_2_out, not_3_out, not_4_out, not_5_out, OP5);
  and and_2 (and_2_out, OP0, OP1, not_6_out, not_7_out, not_8_out, OP5);
  and and_3 (MemWrite, OP0, OP1, not_9_out, OP3, not_10_out, OP5);
  and and_4 (and_4_out, not_11_out, not_12_out, not_13_out, not_14_out, not_15_out, OP5);
  and and_5 (and_5_out, not_16_out, not_17_out, OP3, not_18_out, not_19_out);
  and and_6 (and_6_out, not_20_out, OP3, not_21_out, not_22_out);
  and and_7 (and_7_out, OP0, OP1, not_23_out, not_24_out, OP5);
  and and_8 (and_8_out, not_25_out, not_26_out, not_27_out, not_28_out, not_29_out, not_30_out, not_31_out, not_32_out, not_33_out);
  and and_9 (and_9_out, not_34_out, not_35_out, not_36_out, not_37_out, not_38_out, not_39_out, not_40_out, not_41_out, F5);
  and and_10 (and_10_out, not_42_out, not_43_out, not_44_out, not_45_out, not_46_out, F2, not_47_out, not_48_out, F5);
  and and_11 (and_11_out, not_49_out, not_50_out, not_51_out, not_52_out, not_53_out, F1, not_54_out, not_55_out, not_56_out, not_57_out);
  and and_12 (and_12_out, not_58_out, not_59_out, not_60_out, not_61_out, not_62_out, F1, not_63_out, F3, not_64_out, F5);
  and and_13 (and_13_out, not_65_out, not_66_out, not_67_out, not_68_out, not_69_out, OP5);
  and and_14 (and_14_out, not_70_out, not_71_out, OP3, not_72_out, not_73_out);
  and and_15 (and_15_out, not_74_out, OP3, not_75_out, not_76_out);
  and and_16 (and_16_out, OP0, OP2, OP3, not_77_out, not_78_out);
  and and_17 (and_17_out, OP0, OP1, not_79_out, not_80_out, not_81_out);
  and and_18 (SysCALL, not_82_out, not_83_out, not_84_out, not_85_out, not_86_out, not_87_out, not_88_out, not_89_out, F2, F3, not_90_out, not_91_out);
  and and_19 (and_19_out, not_92_out, not_93_out, OP3, not_94_out, not_95_out);
  and and_20 (and_20_out, not_96_out, OP2, not_97_out, not_98_out, not_99_out);
  or or_1 (SignedExt, and_19_out, and_20_out, and_21_out);
  and and_21 (and_21_out, OP0, not_100_out, not_101_out, not_102_out, not_103_out);
  and and_22 (and_22_out, not_104_out, not_105_out, not_106_out, not_107_out, not_108_out, not_109_out, not_110_out, not_111_out, not_112_out, not_113_out);
  and and_23 (and_23_out, not_114_out, not_115_out, not_116_out, not_117_out, not_118_out, not_119_out, not_120_out, not_121_out, not_122_out, F5);
  and and_24 (and_24_out, not_123_out, not_124_out, not_125_out, not_126_out, not_127_out, not_128_out, F2, not_129_out, not_130_out, F5);
  and and_25 (and_25_out, not_131_out, not_132_out, not_133_out, not_134_out, not_135_out, not_136_out, F1, not_137_out, not_138_out, not_139_out, not_140_out);
  and and_26 (and_26_out, not_141_out, not_142_out, not_143_out, not_144_out, not_145_out, not_146_out, F1, not_147_out, F3, not_148_out, F5);
  and and_27 (BEQ, not_149_out, not_150_out, OP2, not_151_out, not_152_out, not_153_out);
  and and_28 (BNE, OP0, not_154_out, OP2, not_155_out, not_156_out, not_157_out);
  and and_29 (JR, not_158_out, not_159_out, not_160_out, not_161_out, not_162_out, not_163_out, not_164_out, not_165_out, not_166_out, F3, not_167_out, not_168_out);
  and and_30 (and_30_out, not_169_out, not_170_out, not_171_out, not_172_out, not_173_out, not_174_out, not_175_out, not_176_out, F3, not_177_out, not_178_out);
  and and_31 (and_31_out, OP1, not_179_out, not_180_out, not_181_out, not_182_out);
  and and_32 (JAL, OP0, OP1, not_183_out, not_184_out, not_185_out, not_186_out);
  and and_33 (LUI, OP0, OP1, OP2, OP3, not_187_out, not_188_out);
  and and_34 (LB, not_189_out, not_190_out, not_191_out, not_192_out, not_193_out, OP5);
  and and_35 (BLTZ, OP0, not_194_out, not_195_out, not_196_out, not_197_out, not_198_out);
  and and_36 (ERET, not_199_out, OP4, not_200_out, not_201_out, not_202_out, not_203_out, not_204_out, F4, F3, not_205_out, not_206_out, not_207_out);
  or or_2 (MemToReg, and_1_out, and_2_out);
  or or_3 (ALU_SRC, and_4_out, and_5_out, and_6_out, and_7_out);
  or or_4 (RegWrite, and_8_out, and_9_out, and_10_out, and_11_out, and_12_out, and_13_out, and_14_out, and_15_out, and_16_out, and_17_out);
  or or_5 (RegDst, and_22_out, and_23_out, and_24_out, and_25_out, and_26_out);
  or or_6 (JMP, and_30_out, and_31_out);
endmodule

module \扩展单周期硬布线控制器  (
  input  [5:0] OP,
  input  [5:0] Func,
  output [3:0] ALU_OP,
  output MemToReg,
  output MemWrite,
  output ALU_SRC,
  output RegWrite,
  output SysCALL,
  output SignedExt,
  output RegDst,
  output Beq,
  output Bne,
  output JR,
  output JMP,
  output JAL,
  output LUI,
  output LB,
  output BLTZ,
  output ERET
);

  \扩展运算控制器  \u_扩展运算控制器_1  (
    .OP0(OP[0]), .OP1(OP[1]), .OP2(OP[2]), .OP3(OP[3]), .OP4(OP[4]), .OP5(OP[5]), .F0(Func[0]), .F1(Func[1]),
    .F2(Func[2]), .F3(Func[3]), .F4(Func[4]), .F5(Func[5]), .S0(ALU_OP[0]), .S1(ALU_OP[1]), .S2(ALU_OP[2]),
    .S3(ALU_OP[3]));
  \扩展控制信号  \u_扩展控制信号_1  (
    .OP0(OP[0]), .OP1(OP[1]), .OP2(OP[2]), .OP3(OP[3]), .OP4(OP[4]), .OP5(OP[5]), .F0(Func[0]), .F1(Func[1]),
    .F2(Func[2]), .F3(Func[3]), .F4(Func[4]), .F5(Func[5]), .MemToReg(MemToReg), .MemWrite(MemWrite),
    .ALU_SRC(ALU_SRC), .RegWrite(RegWrite), .SysCALL(SysCALL), .SignedExt(SignedExt), .RegDst(RegDst),
    .BEQ(Beq), .BNE(Bne), .JR(JR), .JMP(JMP), .JAL(JAL), .LUI(LUI), .LB(LB), .BLTZ(BLTZ), .ERET(ERET));

  // Other names for the same wires on the sheet: OP_CODE[5:0] = OP

  // Notes on the sheet:
  //   运算器控制器，根据指令生成运算器功能选择信号
  //   控制信号生成，产生数据通路需要的其他控制信号
endmodule

module \扩展单周期MIPS  (
  output RegWrite,
  output MemWrite,
  output [31:0] PC,
  output [31:0] IR,
  output [31:0] RDin,
  output [31:0] MDin
);

  wire and_2_out, and_3_out, and_4_out, and_5_out, Beq, BLTZ, Bne, CLK, comparator_1_eq, d_ff_1_q, Go, Halt,
       IR1, IR2, IR3, JAL, JR, LB, LUI, mips_alu_1_equal, not_1_out, or_1_out, RST, SignedExt, Syscall, W1,
       W2, W3, \扩展单周期硬布线控制器_1_alu_src , \扩展单周期硬布线控制器_1_memtoreg , \扩展单周期硬布线控制器_1_regdst ;
  wire [1:0] mips_alu_1_result, or_2_out;
  wire [3:0] \扩展单周期硬布线控制器_1_alu_op ;
  wire [4:0] multiplexer_3_out, multiplexer_4_out, multiplexer_5_out, multiplexer_6_out;
  wire [7:0] multiplexer_13_out, ram_1_data, ram_1_data_2, ram_1_data_3, ram_1_data_4;
  wire [9:0] mips_alu_1_result_2;
  wire [15:0] \总周期数 , \无条件分支数 , \条件分支成功数 ;
  wire [27:0] adder_1_out;
  wire [31:0] adder_2_out, bit_extender_1_out, bit_extender_2_out, bit_extender_3_out, LedData,
       multiplexer_1_out, multiplexer_2_out, multiplexer_7_out, multiplexer_9_out, multiplexer_10_out,
       multiplexer_11_out, multiplexer_12_out, R1, shifter_1_out;
  wire [31:12] mips_alu_1_result_3;
  wire [31:28] adder_1_out_2;

  Clock #(.highDuration(1), .lowDuration(1)) clock_1 (.out(CLK));
  Button _1 (.out(IR1));
  Button _2 (.out(IR2));
  Button _3 (.out(IR3));
  Button button_1 (.out(RST));
  Button \u_继续运行  (.out(Go));
  LED #(.active("true")) led_1 (.in(W1));
  LED #(.active("true")) led_2 (.in(W2));
  LED #(.active("true")) led_3 (.in(W3));
  or or_1 (or_1_out, ~Halt, d_ff_1_q);  // OR_Gate
  Multiplexer #(.select(2), .width(32), .disabled("Z"), .enable("false")) multiplexer_1 (
    .in0({adder_1_out_2, adder_1_out}), .in1(adder_2_out), .in2(multiplexer_2_out), .out(multiplexer_1_out),
    .sel(or_2_out));  // open: in3
  Multiplexer #(.select(1), .width(32), .disabled("Z"), .enable("false")) multiplexer_2 (
    .in0({adder_1_out_2, IR[25:0], 2'b00}), .in1(R1), .out(multiplexer_2_out), .sel(JR));
  Hex_Digit_Display hex_digit_display_1 (.value(LedData[31:28]));  // open: dp
  Counter #(.width(16), .max('hffff), .ongoal("wrap"), .trigger("rising"), .behavior("old")) counter_1 (
    .count(or_2_out[0]), .Q(\条件分支成功数 ), .clk(CLK), .clr(RST));  // open: load, D, carry, preset
  Counter #(.width(16), .max('hffff), .ongoal("wrap"), .trigger("rising"), .behavior("old")) counter_2 (
    .count(or_2_out[1]), .Q(\无条件分支数 ), .clk(CLK), .clr(RST));  // open: load, D, carry, preset
  Register #(.width(32), .trigger("rising"), .Select("low")) u_PC (
    .D(multiplexer_1_out), .en(or_1_out), .Q(PC), .clk(CLK), .clr(RST));
  Hex_Digit_Display hex_digit_display_2 (.value(LedData[27:24]));  // open: dp
  Hex_Digit_Display hex_digit_display_3 (.value(LedData[23:20]));  // open: dp
  D_Flip_Flop #(.trigger("rising"), .Pre_Clr_Positions("LEGACY"), .NegatePresetClear("false"), .enable("true"), .NewFFLayout("false")) d_ff_1 (
    .clk(CLK), .D(1'b0), .Q(d_ff_1_q), .preset(Go), .reset(RST));  // open: Qn, en
  Adder #(.width(32)) adder_1 (.a(PC), .b(32'h4), .out({adder_1_out_2, adder_1_out}));  // open: cin, cout
  Hex_Digit_Display hex_digit_display_4 (.value(LedData[15:12]));  // open: dp
  Hex_Digit_Display hex_digit_display_5 (.value(LedData[19:16]));  // open: dp
  ROM #(.addrWidth(10), .dataWidth(32), .Select("high")) rom_1 (.addr(PC[11:2]), .data(IR));
  Hex_Digit_Display hex_digit_display_6 (.value(LedData[11:8]));  // open: dp
  Hex_Digit_Display hex_digit_display_7 (.value(LedData[7:4]));  // open: dp
  // Probe on \总周期数 
  Adder #(.width(32)) adder_2 (
    .a({adder_1_out_2, adder_1_out}), .b(shifter_1_out), .out(adder_2_out));  // open: cin, cout
  Hex_Digit_Display hex_digit_display_8 (.value(LedData[3:0]));  // open: dp
  \扩展单周期硬布线控制器  \u_扩展单周期硬布线控制器_1  (
    .OP(IR[31:26]), .Func(IR[5:0]), .ALU_OP(\扩展单周期硬布线控制器_1_alu_op ), .MemToReg(\扩展单周期硬布线控制器_1_memtoreg ),
    .MemWrite(MemWrite), .ALU_SRC(\扩展单周期硬布线控制器_1_alu_src ), .RegWrite(RegWrite), .SysCALL(Syscall),
    .SignedExt(SignedExt), .RegDst(\扩展单周期硬布线控制器_1_regdst ), .Beq(Beq), .Bne(Bne), .JR(JR), .JMP(or_2_out[1]),
    .JAL(JAL), .LUI(LUI), .LB(LB), .BLTZ(BLTZ));  // open: ERET
  Multiplexer #(.select(1), .width(5), .disabled("Z"), .enable("false")) multiplexer_3 (
    .in0(IR[20:16]), .in1(IR[15:11]), .out(multiplexer_3_out), .sel(\扩展单周期硬布线控制器_1_regdst ));
  assign bit_extender_1_out = {{16{1'b0}}, IR[15:0]};  // Bit_Extender bit_extender_1
  assign bit_extender_2_out = {{16{IR[15]}}, IR[15:0]};  // Bit_Extender bit_extender_2
  Multiplexer #(.select(1), .width(5), .disabled("Z"), .enable("false")) multiplexer_4 (
    .in0(IR[25:21]), .in1(5'b00010), .out(multiplexer_4_out), .sel(Syscall));
  Multiplexer #(.select(1), .width(5), .disabled("Z"), .enable("false")) multiplexer_5 (
    .in0(IR[20:16]), .in1(5'b00100), .out(multiplexer_5_out), .sel(Syscall));
  Multiplexer #(.select(1), .width(5), .disabled("Z"), .enable("false")) multiplexer_6 (
    .in0(multiplexer_3_out), .in1({5{1'b1}}), .out(multiplexer_6_out), .sel(JAL));
  Shifter #(.width(32), .shift("ll")) shifter_1 (.in(bit_extender_2_out), .\dist (5'b00010), .out(shifter_1_out));
  Multiplexer #(.select(1), .width(32), .disabled("Z"), .enable("false")) multiplexer_7 (
    .in0(bit_extender_1_out), .in1(bit_extender_2_out), .out(multiplexer_7_out), .sel(SignedExt));
  Multiplexer #(.select(1), .width(32), .disabled("Z"), .enable("false")) multiplexer_8 (
    .in0(multiplexer_9_out), .in1({IR[15:0], {16{1'b0}}}), .out(RDin), .sel(LUI));
  Counter #(.width(16), .max('hffff), .ongoal("wrap"), .trigger("rising"), .behavior("old")) counter_3 (
    .count(not_1_out), .Q(\总周期数 ), .clk(CLK), .clr(RST));  // open: load, D, carry, preset
  not not_1 (not_1_out, Halt);
  MIPS_Regifile mips_regifile_1 (
    .Din(RDin), .Clk(CLK), .R1(R1), .R2(MDin), .WE(RegWrite), .W_num(multiplexer_6_out),
    .R1_num(multiplexer_4_out), .R2_num(multiplexer_5_out));
  Multiplexer #(.select(1), .width(32), .disabled("Z"), .enable("false")) multiplexer_9 (
    .in0(multiplexer_11_out), .in1({adder_1_out_2, adder_1_out}), .out(multiplexer_9_out), .sel(JAL));
  Multiplexer #(.select(1), .width(32), .disabled("Z"), .enable("false")) multiplexer_10 (
    .in0(MDin), .in1(multiplexer_7_out), .out(multiplexer_10_out), .sel(\扩展单周期硬布线控制器_1_alu_src ));
  Comparator #(.width(32), .mode("twosComplement")) comparator_1 (
    .a(R1), .b(32'ha), .eq(comparator_1_eq));  // open: gt, lt
  MIPS_ALU mips_alu_1 (
    .X(R1), .Y(multiplexer_10_out), .AluOP(\扩展单周期硬布线控制器_1_alu_op ), .Equal(mips_alu_1_equal),
    .Result({mips_alu_1_result_3, mips_alu_1_result_2, mips_alu_1_result}), .shamt(IR[10:6]));  // open: Result_2
  Multiplexer #(.select(1), .width(32), .disabled("Z"), .enable("false")) multiplexer_11 (
    .in0({mips_alu_1_result_3, mips_alu_1_result_2, mips_alu_1_result}), .in1(multiplexer_12_out),
    .out(multiplexer_11_out), .sel(\扩展单周期硬布线控制器_1_memtoreg ));
  and and_1 (Halt, comparator_1_eq, Syscall);
  and and_2 (and_2_out, ~comparator_1_eq, Syscall);  // AND_Gate
  Register #(.width(32), .trigger("rising"), .Select("low")) register_1 (
    .D(MDin), .en(and_2_out), .Q(LedData), .clk(CLK), .clr(RST));
  Multiplexer #(.select(1), .width(32), .disabled("Z"), .enable("false")) multiplexer_12 (
    .in0({ram_1_data_4, ram_1_data_3, ram_1_data_2, ram_1_data}), .in1(bit_extender_3_out),
    .out(multiplexer_12_out), .sel(LB));
  and and_3 (and_3_out, mips_alu_1_equal, Beq);
  and and_4 (and_4_out, ~mips_alu_1_equal, Bne);  // AND_Gate
  and and_5 (and_5_out, mips_alu_1_result[0], BLTZ);
  Multiplexer #(.select(2), .width(8), .disabled("Z"), .enable("false")) multiplexer_13 (
    .in0(ram_1_data), .in1(ram_1_data_2), .in2(ram_1_data_3), .in3(ram_1_data_4), .out(multiplexer_13_out),
    .sel(mips_alu_1_result));
  assign bit_extender_3_out = {{24{multiplexer_13_out[7]}}, multiplexer_13_out};  // Bit_Extender bit_extender_3
  or or_2 (or_2_out[0], and_3_out, and_4_out, and_5_out);
  RAM #(.addrWidth(10), .dataWidth(32), .bus("separate"), .Select("high")) ram_1 (
    .addr(mips_alu_1_result_2), .din(MDin), .data({ram_1_data_4, ram_1_data_3, ram_1_data_2, ram_1_data}),
    .str(MemWrite), .clk(CLK), .clr(RST));  // open: sel, ld

  // Other names for the same wires on the sheet: R2[31:0] = MDin

  // Notes on the sheet:
  //   中断源
  //   中断等待指示
  //   总复位信号应将除ROM以外所有存储组件全部清零
  //   指令存储器
  //   数码管输出
  //   contents of rom_1 (hex, n*v repeats v):
  //   3c011001 34210000 14820 200b0010 34118483 20120404 118c00 129400 36318281 22520404 ad310000 2328820
  //   21290004 216bffff 1560fffb 200b0020 3c011001 34210000 14820 81310000 112020 20020022 c 21290001
  //   216bffff 1560fff9 20020032 c
  //   instr_index
  //   数码管输出应该用寄存器锁存，否则显示数据只能一闪而过
  //   rs
  //   指令字
  //   rt
  //   rd
  //   imm
  //   sa
  //   JMP
  //   JR
  //   OP
  //   JAL
  //   Func
  //   Syscall
  //   v0
  //   a0
  //   MemToReg
  //   MemWrite
  //   AluOP
  //   AluSrcB
  //   RegWrite
  //   RegDst
  //   为方便自动评测，需要输出PC，IR，寄存器文件写入端口RDin，内存写入端口MDin等信号
endmodule

module \扩展ID_EX  (
  input  ERET,
  input  Syscall,
  input  [4:0] W_num,
  input  MemToReg,
  input  RegWrite,
  input  JAL,
  input  LB,
  input  LUI,
  input  MemWrite,
  input  [3:0] AluOP,
  input  AluSrcB,
  input  Beq,
  input  Bne,
  input  JMP,
  input  JR,
  input  BLTZ,
  input  [31:0] IR,
  input  [31:0] PC,
  input  [31:0] A,
  input  [31:0] B,
  input  [31:0] Imm,
  input  Clr,
  input  En,
  input  Clk,
  output ERET_2,
  output Syscall_2,
  output [4:0] W_num_2,
  output MemToReg_2,
  output RegWrite_2,
  output JAL_2,
  output LB_2,
  output LUI_2,
  output MemWrite_2,
  output [3:0] AluOP_2,
  output AluSrcB_2,
  output Beq_2,
  output Bne_2,
  output JMP_2,
  output JR_2,
  output BLTZ_2,
  output [31:0] IR_2,
  output [31:0] PC_2,
  output [31:0] A_2,
  output [31:0] B_2,
  output [31:0] Imm_2
);

  wire multiplexer_1_out, multiplexer_2_out, multiplexer_4_out;
  wire [9:0] multiplexer_3_out, multiplexer_5_out;
  wire [31:0] multiplexer_6_out, multiplexer_7_out, multiplexer_8_out, multiplexer_9_out, multiplexer_10_out;

  Pull_Resistor #(.pull(0)) pull_resistor_1 (.node(Clr));
  Multiplexer #(.select(1), .width(1), .disabled("Z"), .enable("false")) multiplexer_1 (
    .in0(ERET), .in1(1'b0), .out(multiplexer_1_out), .sel(Clr));
  Multiplexer #(.select(1), .width(1), .disabled("Z"), .enable("false")) multiplexer_2 (
    .in0(Syscall), .in1(1'b0), .out(multiplexer_2_out), .sel(Clr));
  Multiplexer #(.select(1), .width(10), .disabled("Z"), .enable("false")) multiplexer_3 (
    .in0({LUI, LB, JAL, RegWrite, MemToReg, W_num}), .in1({10{1'b0}}), .out(multiplexer_3_out), .sel(Clr));
  Multiplexer #(.select(1), .width(1), .disabled("Z"), .enable("false")) multiplexer_4 (
    .in0(MemWrite), .in1(1'b0), .out(multiplexer_4_out), .sel(Clr));
  Multiplexer #(.select(1), .width(10), .disabled("Z"), .enable("false")) multiplexer_5 (
    .in0({BLTZ, JR, JMP, Bne, Beq, AluSrcB, AluOP}), .in1({10{1'b0}}), .out(multiplexer_5_out), .sel(Clr));
  Multiplexer #(.select(1), .width(32), .disabled("Z"), .enable("false")) multiplexer_6 (
    .in0(IR), .in1({32{1'b0}}), .out(multiplexer_6_out), .sel(Clr));
  Multiplexer #(.select(1), .width(32), .disabled("Z"), .enable("false")) multiplexer_7 (
    .in0(PC), .in1({32{1'b0}}), .out(multiplexer_7_out), .sel(Clr));
  Multiplexer #(.select(1), .width(32), .disabled("Z"), .enable("false")) multiplexer_8 (
    .in0(A), .in1({32{1'b0}}), .out(multiplexer_8_out), .sel(Clr));
  Multiplexer #(.select(1), .width(32), .disabled("Z"), .enable("false")) multiplexer_9 (
    .in0(B), .in1({32{1'b0}}), .out(multiplexer_9_out), .sel(Clr));
  Multiplexer #(.select(1), .width(32), .disabled("Z"), .enable("false")) multiplexer_10 (
    .in0(Imm), .in1({32{1'b0}}), .out(multiplexer_10_out), .sel(Clr));
  Register #(.width(1), .trigger("rising"), .Select("low")) u_ERET (
    .D(multiplexer_1_out), .en(En), .Q(ERET_2), .clk(Clk));  // open: clr
  Register #(.width(1), .trigger("rising"), .Select("low")) u_Syscall (
    .D(multiplexer_2_out), .en(En), .Q(Syscall_2), .clk(Clk));  // open: clr
  Register #(.width(10), .trigger("rising"), .Select("low")) WB (
    .D(multiplexer_3_out), .en(En), .Q({LUI_2, LB_2, JAL_2, RegWrite_2, MemToReg_2, W_num_2}), .clk(Clk));  // open: clr
  Register #(.width(1), .trigger("rising"), .Select("low")) MEM (
    .D(multiplexer_4_out), .en(En), .Q(MemWrite_2), .clk(Clk));  // open: clr
  Register #(.width(10), .trigger("rising"), .Select("low")) EX (
    .D(multiplexer_5_out), .en(En), .Q({BLTZ_2, JR_2, JMP_2, Bne_2, Beq_2, AluSrcB_2, AluOP_2}), .clk(Clk));  // open: clr
  Register #(.width(32), .trigger("rising"), .Select("low")) u_IR (
    .D(multiplexer_6_out), .en(En), .Q(IR_2), .clk(Clk));  // open: clr
  Register #(.width(32), .trigger("rising"), .Select("low")) u_PC (
    .D(multiplexer_7_out), .en(En), .Q(PC_2), .clk(Clk));  // open: clr
  Register #(.width(32), .trigger("rising"), .Select("low")) u_A (
    .D(multiplexer_8_out), .en(En), .Q(A_2), .clk(Clk));  // open: clr
  Register #(.width(32), .trigger("rising"), .Select("low")) u_B (
    .D(multiplexer_9_out), .en(En), .Q(B_2), .clk(Clk));  // open: clr
  Register #(.width(32), .trigger("rising"), .Select("low")) u_Imm (
    .D(multiplexer_10_out), .en(En), .Q(Imm_2), .clk(Clk));  // open: clr
endmodule

module \扩展IF_ID  (
  input  [31:0] IR,
  input  [31:0] PC,
  input  Clr,
  input  En,
  input  Clk,
  output [31:0] IR_2,
  output [31:0] PC_2
);

  wire [31:0] multiplexer_1_out, multiplexer_2_out;

  Pull_Resistor #(.pull(0)) pull_resistor_1 (.node(Clr));
  Multiplexer #(.select(1), .width(32), .disabled("Z"), .enable("false")) multiplexer_1 (
    .in0(IR), .in1({32{1'b0}}), .out(multiplexer_1_out), .sel(Clr));
  Multiplexer #(.select(1), .width(32), .disabled("Z"), .enable("false")) multiplexer_2 (
    .in0(PC), .in1({32{1'b0}}), .out(multiplexer_2_out), .sel(Clr));
  Register #(.width(32), .trigger("rising"), .Select("low")) u_IR (
    .D(multiplexer_1_out), .en(En), .Q(IR_2), .clk(Clk));  // open: clr
  Register #(.width(32), .trigger("rising"), .Select("low")) u_PC (
    .D(multiplexer_2_out), .en(En), .Q(PC_2), .clk(Clk));  // open: clr
endmodule

module \扩展EX_MEM  (
  input  ERET,
  input  Halt,
  input  [4:0] W_num,
  input  MemToReg,
  input  RegWrite,
  input  JAL,
  input  LB,
  input  LUI,
  input  MemWrite,
  input  [31:0] IR,
  input  [31:0] PC,
  input  [31:0] ALU,
  input  [31:0] B,
  input  [31:0] Imm,
  input  Clr,
  input  En,
  input  Clk,
  output ERET_2,
  output Halt_2,
  output [4:0] W_num_2,
  output MemToReg_2,
  output RegWrite_2,
  output JAL_2,
  output LB_2,
  output LUI_2,
  output MemWrite_2,
  output [31:0] IR_2,
  output [31:0] PC_2,
  output [31:0] ALU_2,
  output [31:0] B_2,
  output [31:0] Imm_2
);

  wire multiplexer_1_out, multiplexer_2_out, multiplexer_4_out;
  wire [9:0] multiplexer_3_out;
  wire [31:0] multiplexer_5_out, multiplexer_6_out, multiplexer_7_out, multiplexer_8_out, multiplexer_9_out;

  Pull_Resistor #(.pull(0)) pull_resistor_1 (.node(Clr));
  Multiplexer #(.select(1), .width(1), .disabled("Z"), .enable("false")) multiplexer_1 (
    .in0(ERET), .in1(1'b0), .out(multiplexer_1_out), .sel(Clr));
  Multiplexer #(.select(1), .width(1), .disabled("Z"), .enable("false")) multiplexer_2 (
    .in0(Halt), .in1(1'b0), .out(multiplexer_2_out), .sel(Clr));
  Multiplexer #(.select(1), .width(10), .disabled("Z"), .enable("false")) multiplexer_3 (
    .in0({LUI, LB, JAL, RegWrite, MemToReg, W_num}), .in1({10{1'b0}}), .out(multiplexer_3_out), .sel(Clr));
  Multiplexer #(.select(1), .width(1), .disabled("Z"), .enable("false")) multiplexer_4 (
    .in0(MemWrite), .in1(1'b0), .out(multiplexer_4_out), .sel(Clr));
  Multiplexer #(.select(1), .width(32), .disabled("Z"), .enable("false")) multiplexer_5 (
    .in0(IR), .in1({32{1'b0}}), .out(multiplexer_5_out), .sel(Clr));
  Multiplexer #(.select(1), .width(32), .disabled("Z"), .enable("false")) multiplexer_6 (
    .in0(PC), .in1({32{1'b0}}), .out(multiplexer_6_out), .sel(Clr));
  Multiplexer #(.select(1), .width(32), .disabled("Z"), .enable("false")) multiplexer_7 (
    .in0(ALU), .in1({32{1'b0}}), .out(multiplexer_7_out), .sel(Clr));
  Multiplexer #(.select(1), .width(32), .disabled("Z"), .enable("false")) multiplexer_8 (
    .in0(B), .in1({32{1'b0}}), .out(multiplexer_8_out), .sel(Clr));
  Multiplexer #(.select(1), .width(32), .disabled("Z"), .enable("false")) multiplexer_9 (
    .in0(Imm), .in1({32{1'b0}}), .out(multiplexer_9_out), .sel(Clr));
  Register #(.width(1), .trigger("rising"), .Select("low")) u_ERET (
    .D(multiplexer_1_out), .en(En), .Q(ERET_2), .clk(Clk));  // open: clr
  Register #(.width(1), .trigger("rising"), .Select("low")) u_Halt (
    .D(multiplexer_2_out), .en(En), .Q(Halt_2), .clk(Clk));  // open: clr
  Register #(.width(10), .trigger("rising"), .Select("low")) WB (
    .D(multiplexer_3_out), .en(En), .Q({LUI_2, LB_2, JAL_2, RegWrite_2, MemToReg_2, W_num_2}), .clk(Clk));  // open: clr
  Register #(.width(1), .trigger("rising"), .Select("low")) MEM (
    .D(multiplexer_4_out), .en(En), .Q(MemWrite_2), .clk(Clk));  // open: clr
  Register #(.width(32), .trigger("rising"), .Select("low")) u_IR (
    .D(multiplexer_5_out), .en(En), .Q(IR_2), .clk(Clk));  // open: clr
  Register #(.width(32), .trigger("rising"), .Select("low")) u_PC (
    .D(multiplexer_6_out), .en(En), .Q(PC_2), .clk(Clk));  // open: clr
  Register #(.width(32), .trigger("rising"), .Select("low")) u_ALU (
    .D(multiplexer_7_out), .en(En), .Q(ALU_2), .clk(Clk));  // open: clr
  Register #(.width(32), .trigger("rising"), .Select("low")) u_B (
    .D(multiplexer_8_out), .en(En), .Q(B_2), .clk(Clk));  // open: clr
  Register #(.width(32), .trigger("rising"), .Select("low")) u_Imm (
    .D(multiplexer_9_out), .en(En), .Q(Imm_2), .clk(Clk));  // open: clr
endmodule

module \扩展MEM_WB  (
  input  ERET,
  input  Halt,
  input  [4:0] W_num,
  input  MemToReg,
  input  RegWrite,
  input  JAL,
  input  LB,
  input  LUI,
  input  [31:0] IR,
  input  [31:0] PC,
  input  [31:0] ALU,
  input  [31:0] MD,
  input  [31:0] Imm,
  input  Clr,
  input  En,
  input  Clk,
  output ERET_2,
  output Halt_2,
  output [4:0] W_num_2,
  output MemToReg_2,
  output RegWrite_2,
  output JAL_2,
  output LB_2,
  output LUI_2,
  output [31:0] IR_2,
  output [31:0] PC_2,
  output [31:0] ALU_2,
  output [31:0] MD_2,
  output [31:0] Imm_2
);

  wire multiplexer_1_out, multiplexer_2_out;
  wire [9:0] multiplexer_3_out;
  wire [31:0] multiplexer_4_out, multiplexer_5_out, multiplexer_6_out, multiplexer_7_out, multiplexer_8_out;

  Pull_Resistor #(.pull(0)) pull_resistor_1 (.node(Clr));
  Multiplexer #(.select(1), .width(1), .disabled("Z"), .enable("false")) multiplexer_1 (
    .in0(ERET), .in1(1'b0), .out(multiplexer_1_out), .sel(Clr));
  Multiplexer #(.select(1), .width(1), .disabled("Z"), .enable("false")) multiplexer_2 (
    .in0(Halt), .in1(1'b0), .out(multiplexer_2_out), .sel(Clr));
  Multiplexer #(.select(1), .width(10), .disabled("Z"), .enable("false")) multiplexer_3 (
    .in0({LUI, LB, JAL, RegWrite, MemToReg, W_num}), .in1({10{1'b0}}), .out(multiplexer_3_out), .sel(Clr));
  Multiplexer #(.select(1), .width(32), .disabled("Z"), .enable("false")) multiplexer_4 (
    .in0(IR), .in1({32{1'b0}}), .out(multiplexer_4_out), .sel(Clr));
  Multiplexer #(.select(1), .width(32), .disabled("Z"), .enable("false")) multiplexer_5 (
    .in0(PC), .in1({32{1'b0}}), .out(multiplexer_5_out), .sel(Clr));
  Multiplexer #(.select(1), .width(32), .disabled("Z"), .enable("false")) multiplexer_6 (
    .in0(ALU), .in1({32{1'b0}}), .out(multiplexer_6_out), .sel(Clr));
  Multiplexer #(.select(1), .width(32), .disabled("Z"), .enable("false")) multiplexer_7 (
    .in0(MD), .in1({32{1'b0}}), .out(multiplexer_7_out), .sel(Clr));
  Multiplexer #(.select(1), .width(32), .disabled("Z"), .enable("false")) multiplexer_8 (
    .in0(Imm), .in1({32{1'b0}}), .out(multiplexer_8_out), .sel(Clr));
  Register #(.width(1), .trigger("rising"), .Select("low")) u_ERET (
    .D(multiplexer_1_out), .en(En), .Q(ERET_2), .clk(Clk));  // open: clr
  Register #(.width(1), .trigger("rising"), .Select("low")) u_Halt (
    .D(multiplexer_2_out), .en(En), .Q(Halt_2), .clk(Clk));  // open: clr
  Register #(.width(10), .trigger("rising"), .Select("low")) WB (
    .D(multiplexer_3_out), .en(En), .Q({LUI_2, LB_2, JAL_2, RegWrite_2, MemToReg_2, W_num_2}), .clk(Clk));  // open: clr
  Register #(.width(32), .trigger("rising"), .Select("low")) u_IR (
    .D(multiplexer_4_out), .en(En), .Q(IR_2), .clk(Clk));  // open: clr
  Register #(.width(32), .trigger("rising"), .Select("low")) u_PC (
    .D(multiplexer_5_out), .en(En), .Q(PC_2), .clk(Clk));  // open: clr
  Register #(.width(32), .trigger("rising"), .Select("low")) u_ALU (
    .D(multiplexer_6_out), .en(En), .Q(ALU_2), .clk(Clk));  // open: clr
  Register #(.width(32), .trigger("rising"), .Select("low")) u_MD (
    .D(multiplexer_7_out), .en(En), .Q(MD_2), .clk(Clk));  // open: clr
  Register #(.width(32), .trigger("rising"), .Select("low")) u_Imm (
    .D(multiplexer_8_out), .en(En), .Q(Imm_2), .clk(Clk));  // open: clr
endmodule

module \数据相关测试  (
  input  RsRead,
  input  [4:0] Rs,
  input  RtRead,
  input  [4:0] Rt,
  input  [4:0] Rw,
  input  RegWrite,
  input  Syscall,
  output Hazard
);

  wire and_1_out, and_2_out, and_3_out, and_4_out, comparator_1_eq, comparator_2_eq, comparator_3_eq,
       comparator_4_eq, comparator_5_eq, or_1_out;

  Comparator #(.width(5), .mode("twosComplement")) comparator_1 (.a(Rs), .b(Rw), .eq(comparator_1_eq));  // open: gt, lt
  Comparator #(.width(5), .mode("twosComplement")) comparator_2 (.a(Rt), .b(Rw), .eq(comparator_2_eq));  // open: gt, lt
  Comparator #(.width(5), .mode("twosComplement")) comparator_3 (
    .a(Rw), .b(5'b00010), .eq(comparator_3_eq));  // open: gt, lt
  Comparator #(.width(5), .mode("twosComplement")) comparator_4 (
    .a(Rw), .b(5'b00100), .eq(comparator_4_eq));  // open: gt, lt
  Comparator #(.width(5), .mode("twosComplement")) comparator_5 (
    .a(Rw), .b({5{1'b0}}), .eq(comparator_5_eq));  // open: gt, lt
  and and_1 (and_1_out, RsRead, comparator_1_eq, RegWrite);
  and and_2 (and_2_out, RtRead, comparator_2_eq, RegWrite);
  and and_3 (and_3_out, RegWrite, Syscall, comparator_3_eq);
  and and_4 (and_4_out, RegWrite, Syscall, comparator_4_eq);
  or or_1 (or_1_out, and_1_out, and_2_out, and_3_out, and_4_out);
  and and_5 (Hazard, or_1_out, ~comparator_5_eq);  // AND_Gate
endmodule

module RegRead (
  input  OP0,
  input  OP1,
  input  OP2,
  input  OP3,
  input  OP4,
  input  OP5,
  input  F0,
  input  F1,
  input  F2,
  input  F3,
  input  F4,
  input  F5,
  output RsRead,
  output RtRead
);

  wire and_1_out, and_2_out, and_3_out, and_4_out, and_5_out, and_6_out, and_7_out, and_8_out, and_9_out,
       and_10_out, and_11_out, and_12_out, and_13_out, and_14_out, and_15_out, and_16_out, and_17_out,
       and_18_out, and_19_out, and_20_out, and_21_out, and_22_out, and_23_out, and_24_out, and_25_out,
       and_26_out, and_27_out, and_28_out, and_29_out, and_30_out, and_31_out, and_32_out, and_33_out,
       and_34_out, and_35_out, and_36_out, not_1_out, not_2_out, not_3_out, not_4_out, not_5_out, not_6_out,
       not_7_out, not_8_out, not_9_out, not_10_out, not_11_out, not_12_out, not_13_out, not_14_out,
       not_15_out, not_16_out, not_17_out, not_18_out, not_19_out, not_20_out, not_21_out, not_22_out,
       not_23_out, not_24_out, not_25_out, not_26_out, not_27_out, not_28_out, not_29_out, not_30_out,
       not_31_out, not_32_out, not_33_out, not_34_out, not_35_out, not_36_out, not_37_out, not_38_out,
       not_39_out, not_40_out, not_41_out, not_42_out, not_43_out, not_44_out, not_45_out, not_46_out,
       not_47_out, not_48_out, not_49_out, not_50_out, not_51_out, not_52_out, not_53_out, not_54_out,
       not_55_out, not_56_out, not_57_out, not_58_out, not_59_out, not_60_out, not_61_out, not_62_out,
       not_63_out, not_64_out, not_65_out, not_66_out, not_67_out, not_68_out, not_69_out, not_70_out,
       not_71_out, not_72_out, not_73_out, not_74_out, not_75_out, not_76_out, not_77_out, not_78_out,
       not_79_out, not_80_out, not_81_out, not_82_out, not_83_out, not_84_out, not_85_out, not_86_out,
       not_87_out, not_88_out, not_89_out, not_90_out, not_91_out, not_92_out, not_93_out, not_94_out,
       not_95_out, not_96_out, not_97_out, not_98_out, not_99_out, not_100_out, not_101_out, not_102_out,
       not_103_out, not_104_out, not_105_out, not_106_out, not_107_out, not_108_out, not_109_out,
       not_110_out, not_111_out, not_112_out, not_113_out, not_114_out, not_115_out, not_116_out,
       not_117_out, not_118_out, not_119_out, not_120_out, not_121_out, not_122_out, not_123_out,
       not_124_out, not_125_out, not_126_out, not_127_out, not_128_out, not_129_out, not_130_out,
       not_131_out, not_132_out, not_133_out, not_134_out, not_135_out, not_136_out, not_137_out,
       not_138_out, not_139_out, not_140_out, not_141_out, not_142_out, not_143_out, not_144_out,
       not_145_out, not_146_out, not_147_out, not_148_out, not_149_out, not_150_out, not_151_out,
       not_152_out, not_153_out, not_154_out, not_155_out, not_156_out, not_157_out, not_158_out,
       not_159_out, not_160_out, not_161_out, not_162_out, not_163_out, not_164_out, not_165_out,
       not_166_out, not_167_out, not_168_out, not_169_out, not_170_out, not_171_out, not_172_out,
       not_173_out, not_174_out, not_175_out, not_176_out, not_177_out, not_178_out, not_179_out,
       not_180_out, not_181_out, not_182_out, not_183_out, not_184_out, not_185_out, not_186_out,
       not_187_out, not_188_out, not_189_out, not_190_out, not_191_out, not_192_out, not_193_out,
       not_194_out, not_195_out, not_196_out, not_197_out, not_198_out, not_199_out, not_200_out,
       not_201_out, not_202_out, not_203_out, not_204_out, not_205_out, not_206_out, not_207_out,
       not_208_out, not_209_out, not_210_out, not_211_out, not_212_out, not_213_out, not_214_out,
       not_215_out, not_216_out, not_217_out, not_218_out, not_219_out, not_220_out, not_221_out,
       not_222_out, not_223_out, not_224_out, not_225_out, not_226_out, not_227_out, not_228_out,
       not_229_out, not_230_out, not_231_out, not_232_out, not_233_out, not_234_out, not_235_out,
       not_236_out, not_237_out, not_238_out, not_239_out, not_240_out, not_241_out, not_242_out,
       not_243_out, not_244_out, not_245_out, not_246_out, not_247_out, not_248_out, not_249_out,
       not_250_out, not_251_out, not_252_out, not_253_out, not_254_out, not_255_out, not_256_out,
       not_257_out, not_258_out, not_259_out, not_260_out, not_261_out, not_262_out, not_263_out,
       not_264_out, not_265_out, not_266_out, not_267_out;

  not not_1 (not_1_out, OP5);
  not not_2 (not_2_out, OP4);
  not not_3 (not_3_out, OP3);
  not not_4 (not_4_out, OP2);
  not not_5 (not_5_out, OP1);
  not not_6 (not_6_out, OP0);
  not not_7 (not_7_out, F4);
  not not_8 (not_8_out, F3);
  not not_9 (not_9_out, F2);
  not not_10 (not_10_out, F1);
  not not_11 (not_11_out, F0);
  not not_12 (not_12_out, OP5);
  not not_13 (not_13_out, OP4);
  not not_14 (not_14_out, OP3);
  not not_15 (not_15_out, OP2);
  not not_16 (not_16_out, OP1);
  not not_17 (not_17_out, OP0);
  not not_18 (not_18_out, F4);
  not not_19 (not_19_out, F3);
  not not_20 (not_20_out, F2);
  not not_21 (not_21_out, F1);
  not not_22 (not_22_out, OP5);
  not not_23 (not_23_out, OP4);
  not not_24 (not_24_out, OP3);
  not not_25 (not_25_out, OP2);
  not not_26 (not_26_out, OP1);
  not not_27 (not_27_out, OP0);
  not not_28 (not_28_out, F4);
  not not_29 (not_29_out, F3);
  not not_30 (not_30_out, F2);
  not not_31 (not_31_out, F0);
  not not_32 (not_32_out, OP5);
  not not_33 (not_33_out, OP4);
  not not_34 (not_34_out, OP3);
  not not_35 (not_35_out, OP2);
  not not_36 (not_36_out, OP1);
  not not_37 (not_37_out, OP0);
  not not_38 (not_38_out, F4);
  not not_39 (not_39_out, F3);
  not not_40 (not_40_out, F1);
  not not_41 (not_41_out, F0);
  not not_42 (not_42_out, OP5);
  not not_43 (not_43_out, OP4);
  not not_44 (not_44_out, OP3);
  not not_45 (not_45_out, OP2);
  not not_46 (not_46_out, OP1);
  not not_47 (not_47_out, OP0);
  not not_48 (not_48_out, F4);
  not not_49 (not_49_out, F3);
  not not_50 (not_50_out, F1);
  not not_51 (not_51_out, OP5);
  not not_52 (not_52_out, OP4);
  not not_53 (not_53_out, OP3);
  not not_54 (not_54_out, OP2);
  not not_55 (not_55_out, OP1);
  not not_56 (not_56_out, OP0);
  not not_57 (not_57_out, F4);
  not not_58 (not_58_out, F3);
  not not_59 (not_59_out, OP5);
  not not_60 (not_60_out, OP4);
  not not_61 (not_61_out, OP3);
  not not_62 (not_62_out, OP2);
  not not_63 (not_63_out, OP1);
  not not_64 (not_64_out, OP0);
  not not_65 (not_65_out, F4);
  not not_66 (not_66_out, F2);
  not not_67 (not_67_out, F0);
  not not_68 (not_68_out, OP5);
  not not_69 (not_69_out, OP4);
  not not_70 (not_70_out, OP3);
  not not_71 (not_71_out, OP2);
  not not_72 (not_72_out, OP1);
  not not_73 (not_73_out, OP0);
  not not_74 (not_74_out, F4);
  not not_75 (not_75_out, F2);
  not not_76 (not_76_out, OP5);
  not not_77 (not_77_out, OP4);
  not not_78 (not_78_out, OP3);
  not not_79 (not_79_out, OP2);
  not not_80 (not_80_out, OP1);
  not not_81 (not_81_out, OP0);
  not not_82 (not_82_out, F5);
  not not_83 (not_83_out, F4);
  not not_84 (not_84_out, F2);
  not not_85 (not_85_out, F1);
  not not_86 (not_86_out, F0);
  not not_87 (not_87_out, OP5);
  not not_88 (not_88_out, OP4);
  not not_89 (not_89_out, OP3);
  not not_90 (not_90_out, OP1);
  not not_91 (not_91_out, OP0);
  not not_92 (not_92_out, OP5);
  not not_93 (not_93_out, OP4);
  not not_94 (not_94_out, OP3);
  not not_95 (not_95_out, OP1);
  not not_96 (not_96_out, OP5);
  not not_97 (not_97_out, OP4);
  not not_98 (not_98_out, OP2);
  not not_99 (not_99_out, OP1);
  not not_100 (not_100_out, OP0);
  not not_101 (not_101_out, OP5);
  not not_102 (not_102_out, OP4);
  not not_103 (not_103_out, OP1);
  not not_104 (not_104_out, OP0);
  not not_105 (not_105_out, OP5);
  not not_106 (not_106_out, OP4);
  not not_107 (not_107_out, OP2);
  not not_108 (not_108_out, OP1);
  not not_109 (not_109_out, OP5);
  not not_110 (not_110_out, OP4);
  not not_111 (not_111_out, OP2);
  not not_112 (not_112_out, OP0);
  not not_113 (not_113_out, OP5);
  not not_114 (not_114_out, OP4);
  not not_115 (not_115_out, OP1);
  not not_116 (not_116_out, OP4);
  not not_117 (not_117_out, OP3);
  not not_118 (not_118_out, OP2);
  not not_119 (not_119_out, OP4);
  not not_120 (not_120_out, OP2);
  not not_121 (not_121_out, OP5);
  not not_122 (not_122_out, OP4);
  not not_123 (not_123_out, OP3);
  not not_124 (not_124_out, OP2);
  not not_125 (not_125_out, OP1);
  not not_126 (not_126_out, OP0);
  not not_127 (not_127_out, F4);
  not not_128 (not_128_out, F3);
  not not_129 (not_129_out, F0);
  not not_130 (not_130_out, OP4);
  not not_131 (not_131_out, OP3);
  not not_132 (not_132_out, OP2);
  not not_133 (not_133_out, OP1);
  not not_134 (not_134_out, OP0);
  not not_135 (not_135_out, OP5);
  not not_136 (not_136_out, OP4);
  not not_137 (not_137_out, OP3);
  not not_138 (not_138_out, OP2);
  not not_139 (not_139_out, OP1);
  not not_140 (not_140_out, OP5);
  not not_141 (not_141_out, OP4);
  not not_142 (not_142_out, OP3);
  not not_143 (not_143_out, OP2);
  not not_144 (not_144_out, OP1);
  not not_145 (not_145_out, OP0);
  not not_146 (not_146_out, F5);
  not not_147 (not_147_out, F4);
  not not_148 (not_148_out, F3);
  not not_149 (not_149_out, F2);
  not not_150 (not_150_out, F1);
  not not_151 (not_151_out, F0);
  not not_152 (not_152_out, OP5);
  not not_153 (not_153_out, OP4);
  not not_154 (not_154_out, OP3);
  not not_155 (not_155_out, OP2);
  not not_156 (not_156_out, OP1);
  not not_157 (not_157_out, OP0);
  not not_158 (not_158_out, F5);
  not not_159 (not_159_out, F4);
  not not_160 (not_160_out, F3);
  not not_161 (not_161_out, F2);
  not not_162 (not_162_out, OP5);
  not not_163 (not_163_out, OP4);
  not not_164 (not_164_out, OP3);
  not not_165 (not_165_out, OP2);
  not not_166 (not_166_out, OP1);
  not not_167 (not_167_out, OP0);
  not not_168 (not_168_out, F5);
  not not_169 (not_169_out, F4);
  not not_170 (not_170_out, F3);
  not not_171 (not_171_out, F2);
  not not_172 (not_172_out, F0);
  not not_173 (not_173_out, OP5);
  not not_174 (not_174_out, OP4);
  not not_175 (not_175_out, OP3);
  not not_176 (not_176_out, OP2);
  not not_177 (not_177_out, OP1);
  not not_178 (not_178_out, OP0);
  not not_179 (not_179_out, F4);
  not not_180 (not_180_out, F3);
  not not_181 (not_181_out, F2);
  not not_182 (not_182_out, F1);
  not not_183 (not_183_out, F0);
  not not_184 (not_184_out, OP5);
  not not_185 (not_185_out, OP4);
  not not_186 (not_186_out, OP3);
  not not_187 (not_187_out, OP2);
  not not_188 (not_188_out, OP1);
  not not_189 (not_189_out, OP0);
  not not_190 (not_190_out, F4);
  not not_191 (not_191_out, F3);
  not not_192 (not_192_out, F2);
  not not_193 (not_193_out, F1);
  not not_194 (not_194_out, OP5);
  not not_195 (not_195_out, OP4);
  not not_196 (not_196_out, OP3);
  not not_197 (not_197_out, OP2);
  not not_198 (not_198_out, OP1);
  not not_199 (not_199_out, OP0);
  not not_200 (not_200_out, F4);
  not not_201 (not_201_out, F3);
  not not_202 (not_202_out, F2);
  not not_203 (not_203_out, F0);
  not not_204 (not_204_out, OP5);
  not not_205 (not_205_out, OP4);
  not not_206 (not_206_out, OP3);
  not not_207 (not_207_out, OP2);
  not not_208 (not_208_out, OP1);
  not not_209 (not_209_out, OP0);
  not not_210 (not_210_out, F4);
  not not_211 (not_211_out, F3);
  not not_212 (not_212_out, F1);
  not not_213 (not_213_out, F0);
  not not_214 (not_214_out, OP5);
  not not_215 (not_215_out, OP4);
  not not_216 (not_216_out, OP3);
  not not_217 (not_217_out, OP2);
  not not_218 (not_218_out, OP1);
  not not_219 (not_219_out, OP0);
  not not_220 (not_220_out, F4);
  not not_221 (not_221_out, F3);
  not not_222 (not_222_out, F1);
  not not_223 (not_223_out, OP5);
  not not_224 (not_224_out, OP4);
  not not_225 (not_225_out, OP3);
  not not_226 (not_226_out, OP2);
  not not_227 (not_227_out, OP1);
  not not_228 (not_228_out, OP0);
  not not_229 (not_229_out, F4);
  not not_230 (not_230_out, F3);
  not not_231 (not_231_out, OP5);
  not not_232 (not_232_out, OP4);
  not not_233 (not_233_out, OP3);
  not not_234 (not_234_out, OP2);
  not not_235 (not_235_out, OP1);
  not not_236 (not_236_out, OP0);
  not not_237 (not_237_out, F4);
  not not_238 (not_238_out, F2);
  not not_239 (not_239_out, F0);
  not not_240 (not_240_out, OP5);
  not not_241 (not_241_out, OP4);
  not not_242 (not_242_out, OP3);
  not not_243 (not_243_out, OP2);
  not not_244 (not_244_out, OP1);
  not not_245 (not_245_out, OP0);
  not not_246 (not_246_out, F4);
  not not_247 (not_247_out, F2);
  not not_248 (not_248_out, OP5);
  not not_249 (not_249_out, OP4);
  not not_250 (not_250_out, OP3);
  not not_251 (not_251_out, OP1);
  not not_252 (not_252_out, OP0);
  not not_253 (not_253_out, OP5);
  not not_254 (not_254_out, OP4);
  not not_255 (not_255_out, OP3);
  not not_256 (not_256_out, OP1);
  not not_257 (not_257_out, OP4);
  not not_258 (not_258_out, OP2);
  not not_259 (not_259_out, OP5);
  not not_260 (not_260_out, OP4);
  not not_261 (not_261_out, OP3);
  not not_262 (not_262_out, OP2);
  not not_263 (not_263_out, OP1);
  not not_264 (not_264_out, OP0);
  not not_265 (not_265_out, F4);
  not not_266 (not_266_out, F3);
  not not_267 (not_267_out, F0);
  and and_1 (and_1_out, not_1_out, not_2_out, not_3_out, not_4_out, not_5_out, not_6_out, F5, not_7_out, not_8_out, not_9_out, not_10_out, not_11_out);
  and and_2 (and_2_out, not_12_out, not_13_out, not_14_out, not_15_out, not_16_out, not_17_out, F5, not_18_out, not_19_out, not_20_out, not_21_out, F0);
  and and_3 (and_3_out, not_22_out, not_23_out, not_24_out, not_25_out, not_26_out, not_27_out, F5, not_28_out, not_29_out, not_30_out, F1, not_31_out);
  and and_4 (and_4_out, not_32_out, not_33_out, not_34_out, not_35_out, not_36_out, not_37_out, F5, not_38_out, not_39_out, F2, not_40_out, not_41_out);
  and and_5 (and_5_out, not_42_out, not_43_out, not_44_out, not_45_out, not_46_out, not_47_out, F5, not_48_out, not_49_out, F2, not_50_out, F0);
  and and_6 (and_6_out, not_51_out, not_52_out, not_53_out, not_54_out, not_55_out, not_56_out, F5, not_57_out, not_58_out, F2, F1, F0);
  and and_7 (and_7_out, not_59_out, not_60_out, not_61_out, not_62_out, not_63_out, not_64_out, F5, not_65_out, F3, not_66_out, F1, not_67_out);
  and and_8 (and_8_out, not_68_out, not_69_out, not_70_out, not_71_out, not_72_out, not_73_out, F5, not_74_out, F3, not_75_out, F1, F0);
  and and_9 (and_9_out, not_76_out, not_77_out, not_78_out, not_79_out, not_80_out, not_81_out, not_82_out, not_83_out, F3, not_84_out, not_85_out, not_86_out);
  and and_10 (and_10_out, not_87_out, not_88_out, not_89_out, OP2, not_90_out, not_91_out);
  and and_11 (and_11_out, not_92_out, not_93_out, not_94_out, OP2, not_95_out, OP0);
  and and_12 (and_12_out, not_96_out, not_97_out, OP3, not_98_out, not_99_out, not_100_out);
  and and_13 (and_13_out, not_101_out, not_102_out, OP3, OP2, not_103_out, not_104_out);
  and and_14 (and_14_out, not_105_out, not_106_out, OP3, not_107_out, not_108_out, OP0);
  and and_15 (and_15_out, not_109_out, not_110_out, OP3, not_111_out, OP1, not_112_out);
  and and_16 (and_16_out, not_113_out, not_114_out, OP3, OP2, not_115_out, OP0);
  and and_17 (and_17_out, OP5, not_116_out, not_117_out, not_118_out, OP1, OP0);
  and and_18 (and_18_out, OP5, not_119_out, OP3, not_120_out, OP1, OP0);
  and and_19 (and_19_out, not_121_out, not_122_out, not_123_out, not_124_out, not_125_out, not_126_out, F5, not_127_out, not_128_out, F2, F1, not_129_out);
  and and_20 (and_20_out, OP5, not_130_out, not_131_out, not_132_out, not_133_out, not_134_out);
  and and_21 (and_21_out, not_135_out, not_136_out, not_137_out, not_138_out, not_139_out, OP0);
  and and_22 (and_22_out, not_140_out, not_141_out, not_142_out, not_143_out, not_144_out, not_145_out, not_146_out, not_147_out, not_148_out, not_149_out, not_150_out, not_151_out);
  and and_23 (and_23_out, not_152_out, not_153_out, not_154_out, not_155_out, not_156_out, not_157_out, not_158_out, not_159_out, not_160_out, not_161_out, F1, F0);
  and and_24 (and_24_out, not_162_out, not_163_out, not_164_out, not_165_out, not_166_out, not_167_out, not_168_out, not_169_out, not_170_out, not_171_out, F1, not_172_out);
  and and_25 (and_25_out, not_173_out, not_174_out, not_175_out, not_176_out, not_177_out, not_178_out, F5, not_179_out, not_180_out, not_181_out, not_182_out, not_183_out);
  and and_26 (and_26_out, not_184_out, not_185_out, not_186_out, not_187_out, not_188_out, not_189_out, F5, not_190_out, not_191_out, not_192_out, not_193_out, F0);
  and and_27 (and_27_out, not_194_out, not_195_out, not_196_out, not_197_out, not_198_out, not_199_out, F5, not_200_out, not_201_out, not_202_out, F1, not_203_out);
  and and_28 (and_28_out, not_204_out, not_205_out, not_206_out, not_207_out, not_208_out, not_209_out, F5, not_210_out, not_211_out, F2, not_212_out, not_213_out);
  and and_29 (and_29_out, not_214_out, not_215_out, not_216_out, not_217_out, not_218_out, not_219_out, F5, not_220_out, not_221_out, F2, not_222_out, F0);
  and and_30 (and_30_out, not_223_out, not_224_out, not_225_out, not_226_out, not_227_out, not_228_out, F5, not_229_out, not_230_out, F2, F1, F0);
  and and_31 (and_31_out, not_231_out, not_232_out, not_233_out, not_234_out, not_235_out, not_236_out, F5, not_237_out, F3, not_238_out, F1, not_239_out);
  and and_32 (and_32_out, not_240_out, not_241_out, not_242_out, not_243_out, not_244_out, not_245_out, F5, not_246_out, F3, not_247_out, F1, F0);
  and and_33 (and_33_out, not_248_out, not_249_out, not_250_out, OP2, not_251_out, not_252_out);
  and and_34 (and_34_out, not_253_out, not_254_out, not_255_out, OP2, not_256_out, OP0);
  and and_35 (and_35_out, OP5, not_257_out, OP3, not_258_out, OP1, OP0);
  and and_36 (and_36_out, not_259_out, not_260_out, not_261_out, not_262_out, not_263_out, not_264_out, F5, not_265_out, not_266_out, F2, F1, not_267_out);
  or or_1 (RsRead, and_1_out, and_2_out, and_3_out, and_4_out, and_5_out, and_6_out, and_7_out, and_8_out, and_9_out, and_10_out, and_11_out, and_12_out, and_13_out, and_14_out, and_15_out, and_16_out, and_17_out, and_18_out, and_19_out, and_20_out, and_21_out);
  or or_2 (RtRead, and_22_out, and_23_out, and_24_out, and_25_out, and_26_out, and_27_out, and_28_out, and_29_out, and_30_out, and_31_out, and_32_out, and_33_out, and_34_out, and_35_out, and_36_out);
endmodule

module \数据相关测试2  (
  input  RsRead,
  input  [4:0] Rs,
  input  RtRead,
  input  [4:0] Rt,
  input  [4:0] Rw,
  input  RegWrite,
  input  Syscall,
  output HazardA,
  output HazardB
);

  wire and_1_out, and_2_out, and_3_out, and_4_out, comparator_1_eq, comparator_2_eq, comparator_3_eq,
       comparator_4_eq, comparator_5_eq, or_1_out, or_2_out;

  Comparator #(.width(5), .mode("twosComplement")) comparator_1 (.a(Rs), .b(Rw), .eq(comparator_1_eq));  // open: gt, lt
  Comparator #(.width(5), .mode("twosComplement")) comparator_2 (.a(Rt), .b(Rw), .eq(comparator_2_eq));  // open: gt, lt
  Comparator #(.width(5), .mode("twosComplement")) comparator_3 (
    .a(Rw), .b(5'b00010), .eq(comparator_3_eq));  // open: gt, lt
  Comparator #(.width(5), .mode("twosComplement")) comparator_4 (
    .a(Rw), .b(5'b00100), .eq(comparator_4_eq));  // open: gt, lt
  Comparator #(.width(5), .mode("twosComplement")) comparator_5 (
    .a(Rw), .b({5{1'b0}}), .eq(comparator_5_eq));  // open: gt, lt
  and and_1 (and_1_out, RsRead, comparator_1_eq, RegWrite);
  and and_2 (and_2_out, RtRead, comparator_2_eq, RegWrite);
  and and_3 (and_3_out, RegWrite, Syscall, comparator_3_eq);
  and and_4 (and_4_out, RegWrite, Syscall, comparator_4_eq);
  or or_1 (or_1_out, and_1_out, and_3_out);
  and and_5 (HazardA, or_1_out, ~comparator_5_eq);  // AND_Gate
  or or_2 (or_2_out, and_2_out, and_4_out);
  and and_6 (HazardB, or_2_out, ~comparator_5_eq);  // AND_Gate
endmodule

module Forward (
  input  HazardA,
  input  HazardB,
  input  MemToReg,
  output [1:0] out_4
);

  wire and_1_out, and_2_out;

  and and_1 (and_1_out, HazardB, MemToReg);
  and and_2 (and_2_out, HazardB, ~MemToReg);  // AND_Gate
  or or_1 (out_4[0], HazardA, and_1_out);
  or or_2 (out_4[1], HazardA, and_2_out);
endmodule

module \单周期MIPS  (
  input  IR1,
  input  IR2,
  input  IR3,
  output RegWrite,
  output MemWrite,
  output [31:0] PC,
  output [31:0] IR,
  output [31:0] RDin,
  output [31:0] MDin,
  output [31:0] LedData
);

  wire and_2_out, and_3_out, and_4_out, and_5_out, Beq, BLTZ, Bne, CLK, comparator_1_eq, d_ff_1_q, Go, Halt,
       IR1_t, IR2_t, IR3_t, IRA, IRB, IRC, JAL, JR, LB, LUI, mips_alu_1_equal, not_1_out, or_1_out,
       SignedExt, Syscall, W1, W2, W3, \扩展单周期硬布线控制器_1_alu_src , \扩展单周期硬布线控制器_1_memtoreg ,
       \扩展单周期硬布线控制器_1_regdst ;
  wire [1:0] mips_alu_1_result, or_5_out;
  wire [3:0] \扩展单周期硬布线控制器_1_alu_op ;
  wire [4:0] multiplexer_3_out, multiplexer_4_out, multiplexer_5_out, multiplexer_6_out;
  wire [7:0] multiplexer_13_out, ram_1_data, ram_1_data_2, ram_1_data_3, ram_1_data_4;
  wire [9:0] mips_alu_1_result_2;
  wire [15:0] \总周期数 , \无条件分支数 , \条件分支成功数 ;
  wire [27:0] adder_1_out;
  wire [31:0] adder_2_out, bit_extender_1_out, bit_extender_2_out, bit_extender_3_out, multiplexer_1_out,
       multiplexer_2_out, multiplexer_7_out, multiplexer_9_out, multiplexer_10_out, multiplexer_11_out,
       multiplexer_12_out, R1, shifter_1_out;
  wire [31:12] mips_alu_1_result_3;
  wire [31:28] adder_1_out_2;

  Clock #(.highDuration(1), .lowDuration(1)) clock_1 (.out(CLK));
  Button _1 (.out(IRA));
  Button _2 (.out(IRB));
  Button _3 (.out(IRC));
  Button \u_继续运行  (.out(Go));
  LED #(.active("true")) led_1 (.in(W1));
  LED #(.active("true")) led_2 (.in(W2));
  LED #(.active("true")) led_3 (.in(W3));
  or or_1 (or_1_out, ~Halt, d_ff_1_q);  // OR_Gate
  Multiplexer #(.select(2), .width(32), .disabled("Z"), .enable("false")) multiplexer_1 (
    .in0({adder_1_out_2, adder_1_out}), .in1(adder_2_out), .in2(multiplexer_2_out), .out(multiplexer_1_out),
    .sel(or_5_out));  // open: in3
  Multiplexer #(.select(1), .width(32), .disabled("Z"), .enable("false")) multiplexer_2 (
    .in0({adder_1_out_2, IR[25:0], 2'b00}), .in1(R1), .out(multiplexer_2_out), .sel(JR));
  Hex_Digit_Display hex_digit_display_1 (.value(LedData[31:28]));  // open: dp
  Counter #(.width(16), .max('hffff), .ongoal("wrap"), .trigger("rising"), .behavior("old")) counter_1 (
    .count(or_5_out[0]), .Q(\条件分支成功数 ), .clk(CLK));  // open: load, D, carry, clr, preset
  Counter #(.width(16), .max('hffff), .ongoal("wrap"), .trigger("rising"), .behavior("old")) counter_2 (
    .count(or_5_out[1]), .Q(\无条件分支数 ), .clk(CLK));  // open: load, D, carry, clr, preset
  Register #(.width(32), .trigger("rising"), .Select("low")) u_PC (
    .D(multiplexer_1_out), .en(or_1_out), .Q(PC), .clk(CLK));  // open: clr
  Hex_Digit_Display hex_digit_display_2 (.value(LedData[23:20]));  // open: dp
  Hex_Digit_Display hex_digit_display_3 (.value(LedData[27:24]));  // open: dp
  D_Flip_Flop #(.trigger("rising"), .Pre_Clr_Positions("LEGACY"), .NegatePresetClear("false"), .enable("true"), .NewFFLayout("false")) d_ff_1 (
    .clk(CLK), .D(1'b0), .Q(d_ff_1_q), .preset(Go));  // open: Qn, en, reset
  Adder #(.width(32)) adder_1 (.a(PC), .b(32'h4), .out({adder_1_out_2, adder_1_out}));  // open: cin, cout
  Hex_Digit_Display hex_digit_display_4 (.value(LedData[19:16]));  // open: dp
  Hex_Digit_Display hex_digit_display_5 (.value(LedData[15:12]));  // open: dp
  ROM #(.addrWidth(10), .dataWidth(32), .Select("high")) rom_1 (.addr(PC[11:2]), .data(IR));
  Hex_Digit_Display hex_digit_display_6 (.value(LedData[11:8]));  // open: dp
  Hex_Digit_Display hex_digit_display_7 (.value(LedData[7:4]));  // open: dp
  // Probe on \总周期数 
  Adder #(.width(32)) adder_2 (
    .a({adder_1_out_2, adder_1_out}), .b(shifter_1_out), .out(adder_2_out));  // open: cin, cout
  Hex_Digit_Display hex_digit_display_8 (.value(LedData[3:0]));  // open: dp
  \扩展单周期硬布线控制器  \u_扩展单周期硬布线控制器_1  (
    .OP(IR[31:26]), .Func(IR[5:0]), .ALU_OP(\扩展单周期硬布线控制器_1_alu_op ), .MemToReg(\扩展单周期硬布线控制器_1_memtoreg ),
    .MemWrite(MemWrite), .ALU_SRC(\扩展单周期硬布线控制器_1_alu_src ), .RegWrite(RegWrite), .SysCALL(Syscall),
    .SignedExt(SignedExt), .RegDst(\扩展单周期硬布线控制器_1_regdst ), .Beq(Beq), .Bne(Bne), .JR(JR), .JMP(or_5_out[1]),
    .JAL(JAL), .LUI(LUI), .LB(LB), .BLTZ(BLTZ));  // open: ERET
  Multiplexer #(.select(1), .width(5), .disabled("Z"), .enable("false")) multiplexer_3 (
    .in0(IR[20:16]), .in1(IR[15:11]), .out(multiplexer_3_out), .sel(\扩展单周期硬布线控制器_1_regdst ));
  assign bit_extender_1_out = {{16{1'b0}}, IR[15:0]};  // Bit_Extender bit_extender_1
  assign bit_extender_2_out = {{16{IR[15]}}, IR[15:0]};  // Bit_Extender bit_extender_2
  Multiplexer #(.select(1), .width(5), .disabled("Z"), .enable("false")) multiplexer_4 (
    .in0(IR[25:21]), .in1(5'b00010), .out(multiplexer_4_out), .sel(Syscall));
  Multiplexer #(.select(1), .width(5), .disabled("Z"), .enable("false")) multiplexer_5 (
    .in0(IR[20:16]), .in1(5'b00100), .out(multiplexer_5_out), .sel(Syscall));
  Multiplexer #(.select(1), .width(5), .disabled("Z"), .enable("false")) multiplexer_6 (
    .in0(multiplexer_3_out), .in1({5{1'b1}}), .out(multiplexer_6_out), .sel(JAL));
  Shifter #(.width(32), .shift("ll")) shifter_1 (.in(bit_extender_2_out), .\dist (5'b00010), .out(shifter_1_out));
  or or_2 (IR1_t, IR1, IRA);
  Multiplexer #(.select(1), .width(32), .disabled("Z"), .enable("false")) multiplexer_7 (
    .in0(bit_extender_1_out), .in1(bit_extender_2_out), .out(multiplexer_7_out), .sel(SignedExt));
  Multiplexer #(.select(1), .width(32), .disabled("Z"), .enable("false")) multiplexer_8 (
    .in0(multiplexer_9_out), .in1({IR[15:0], {16{1'b0}}}), .out(RDin), .sel(LUI));
  or or_3 (IR2_t, IR2, IRB);
  Counter #(.width(16), .max('hffff), .ongoal("wrap"), .trigger("rising"), .behavior("old")) counter_3 (
    .count(not_1_out), .Q(\总周期数 ), .clk(CLK));  // open: load, D, carry, clr, preset
  not not_1 (not_1_out, Halt);
  MIPS_Regifile mips_regifile_1 (
    .Din(RDin), .Clk(CLK), .R1(R1), .R2(MDin), .WE(RegWrite), .W_num(multiplexer_6_out),
    .R1_num(multiplexer_4_out), .R2_num(multiplexer_5_out));
  Multiplexer #(.select(1), .width(32), .disabled("Z"), .enable("false")) multiplexer_9 (
    .in0(multiplexer_11_out), .in1({adder_1_out_2, adder_1_out}), .out(multiplexer_9_out), .sel(JAL));
  Multiplexer #(.select(1), .width(32), .disabled("Z"), .enable("false")) multiplexer_10 (
    .in0(MDin), .in1(multiplexer_7_out), .out(multiplexer_10_out), .sel(\扩展单周期硬布线控制器_1_alu_src ));
  Comparator #(.width(32), .mode("twosComplement")) comparator_1 (
    .a(R1), .b(32'h32), .eq(comparator_1_eq));  // open: gt, lt
  or or_4 (IR3_t, IR3, IRC);
  MIPS_ALU mips_alu_1 (
    .X(R1), .Y(multiplexer_10_out), .AluOP(\扩展单周期硬布线控制器_1_alu_op ), .Equal(mips_alu_1_equal),
    .Result({mips_alu_1_result_3, mips_alu_1_result_2, mips_alu_1_result}), .shamt(IR[10:6]));  // open: Result_2
  Multiplexer #(.select(1), .width(32), .disabled("Z"), .enable("false")) multiplexer_11 (
    .in0({mips_alu_1_result_3, mips_alu_1_result_2, mips_alu_1_result}), .in1(multiplexer_12_out),
    .out(multiplexer_11_out), .sel(\扩展单周期硬布线控制器_1_memtoreg ));
  and and_1 (Halt, comparator_1_eq, Syscall);
  and and_2 (and_2_out, ~comparator_1_eq, Syscall);  // AND_Gate
  Register #(.width(32), .trigger("rising"), .Select("low")) register_1 (
    .D(MDin), .en(and_2_out), .Q(LedData), .clk(CLK));  // open: clr
  Multiplexer #(.select(1), .width(32), .disabled("Z"), .enable("false")) multiplexer_12 (
    .in0({ram_1_data_4, ram_1_data_3, ram_1_data_2, ram_1_data}), .in1(bit_extender_3_out),
    .out(multiplexer_12_out), .sel(LB));
  and and_3 (and_3_out, mips_alu_1_equal, Beq);
  and and_4 (and_4_out, ~mips_alu_1_equal, Bne);  // AND_Gate
  and and_5 (and_5_out, mips_alu_1_result[0], BLTZ);
  Multiplexer #(.select(2), .width(8), .disabled("Z"), .enable("false")) multiplexer_13 (
    .in0(ram_1_data), .in1(ram_1_data_2), .in2(ram_1_data_3), .in3(ram_1_data_4), .out(multiplexer_13_out),
    .sel(mips_alu_1_result));
  assign bit_extender_3_out = {{24{multiplexer_13_out[7]}}, multiplexer_13_out};  // Bit_Extender bit_extender_3
  or or_5 (or_5_out[0], and_3_out, and_4_out, and_5_out);
  RAM #(.addrWidth(10), .dataWidth(32), .bus("separate"), .Select("high")) ram_1 (
    .addr(mips_alu_1_result_2), .din(MDin), .data({ram_1_data_4, ram_1_data_3, ram_1_data_2, ram_1_data}),
    .str(MemWrite), .clk(CLK));  // open: sel, ld, clr

  // Other names for the same wires on the sheet: R2[31:0] = MDin

  // Notes on the sheet:
  //   中断源
  //   中断等待指示
  //   总复位信号应将除ROM以外所有存储组件全部清零
  //   指令存储器
  //   数码管输出
  //   contents of rom_1 (hex, n*v repeats v):
  //   20110001 8000c05 20110001 20120002 20130003 8000c09 20110001 20120002 20130003 8000c0d 20110001
  //   20120002 20130003 8000c11 20110001 20120002 20130003 c000cb8 20100001 20110001 118fc0 112020
  //   20020022 c 118882 12200001 8000c15 112020 20020022 c 20110001 118880 112020 20020022 c 12200001
  //   8000c1f 20110001 118fc0 112020 20020022 c 1188c3 112020 20020022 c 118903 112020 20020022 c 118903
  //   112020 20020022 c 118903 112020 20020022 c 118903 112020 20020022 c 118903 112020 20020022 c 118903
  //   112020 20020022 c 118903 112020 20020022 c 20100001 109fc0 139fc3 8021 2012000c 24160003 26100001
  //   3210000f 20080008 20090001 139900 2709825 132020 20020022 c 1094022 1500fff9 22100001 2018000f
  //   2188024 108700 20080008 20090001 139902 2709825 132021 20020022 c 1094022 1500fff9 108702 2c9b022
  //   12c00001 8000c50 4020 1084027 84400 3508ffff 82021 20020022 c 2010ffff 20110000 ae300000 22100001
  //   22310004 ae300000 22100001 22310004 ae300000 22100001 22310004 ae300000 22100001 22310004 ae300000
  //   22100001 22310004 ae300000 22100001 22310004 ae300000 22100001 22310004 ae300000 22100001 22310004
  //   ae300000 22100001 22310004 ae300000 22100001 22310004 ae300000 22100001 22310004 ae300000 22100001
  //   22310004 ae300000 22100001 22310004 ae300000 22100001 22310004 ae300000 22100001 22310004 ae300000
  //   22100001 22310004 22100001 8020 2011003c 8e130000 8e340000 274402a 11000002 ae330000 ae140000
  //   2231fffc 1611fff8 102020 20020022 c 22100004 2011003c 1611fff2 20020032 c 20100000 22100001 102020
  //   20020022 c 22100002 102020 20020022 c 22100003 102020 20020022 c 22100004 102020 20020022 c 22100005
  //   102020 20020022 c 22100006 102020 20020022 c 22100007 102020 20020022 c 22100008 102020 20020022
  //   20020022 c 3e00008
  //   instr_index
  //   数码管输出应该用寄存器锁存，否则显示数据只能一闪而过
  //   rs
  //   指令字
  //   rt
  //   rd
  //   imm
  //   sa
  //   JMP
  //   JR
  //   OP
  //   JAL
  //   Func
  //   Syscall
  //   v0
  //   a0
  //   MemToReg
  //   MemWrite
  //   AluOP
  //   AluSrcB
  //   RegWrite
  //   RegDst
  //   为方便自动评测，需要输出PC，IR，寄存器堆写如数据RDin
  //   RAM写使能MemWrite、RAM写入数据MDin等信号
endmodule

module MFC_MTC (
  input  [10:0] in_1,
  output MFC,
  output MTC
);

  Comparator #(.width(11), .mode("twosComplement")) comparator_1 (.a(in_1), .b(11'h200), .eq(MFC));  // open: gt, lt
  Comparator #(.width(11), .mode("twosComplement")) comparator_2 (.a(in_1), .b(11'h204), .eq(MTC));  // open: gt, lt
endmodule
module \单周期MIPS_多级中断  (
  input  IR1,
  input  IR2,
  input  IR3,
  output RegWrite,
  output MemWrite,
  output [31:0] PC,
  output [31:0] IR,
  output [31:0] RDin,
  output [31:0] MDin,
  output [31:0] LedData
);

  wire and_1_out, and_2_out, and_3_out, and_6_out, and_7_out, and_8_out, CLK, comparator_1_gt,
       comparator_2_eq, d_ff_1_q, decoder_1_out1, decoder_1_out2, decoder_1_out3, ERET, Exception, Go, Halt,
       IR1_t, IR2_t, IR3_t, IRA, IRB, IRC, JAL, JR, MFC, mips_alu_1_equal, MTC, multiplexer_12_out, nIE_q,
       not_1_out, or_1_out, or_2_out, or_5_out, or_6_out, or_8_out, SignedExt, Syscall, W1, W2, W3,
       \中断按键参考电路_1_ir_2 , \中断按键参考电路_2_ir_2 , \中断按键参考电路_3_ir_2 , \单周期硬布线控制器_1_alu_src , \单周期硬布线控制器_1_beq ,
       \单周期硬布线控制器_1_bne , \单周期硬布线控制器_1_memtoreg , \单周期硬布线控制器_1_regdst ;
  wire [1:0] ExcepType, Execp2_q, Execp3_q, multiplexer_1_out, multiplexer_2_out, multiplexer_5_out,
       or_9_out, Pri;
  wire [3:0] \单周期硬布线控制器_1_alu_op ;
  wire [4:0] multiplexer_6_out, multiplexer_8_out, multiplexer_9_out, multiplexer_10_out;
  wire [15:0] \总周期数 , \无条件分支数 , \条件分支成功数 ;
  wire [27:0] adder_1_out;
  wire [31:0] adder_2_out, bit_extender_1_out, bit_extender_2_out, EPC1_q, EPC2_q, EPC3_q, in_PC,
       mips_alu_1_result, multiplexer_4_out, multiplexer_7_out, multiplexer_11_out, multiplexer_14_out,
       multiplexer_15_out, multiplexer_17_out, multiplexer_18_out, next_PC, R1, ram_1_data, shifter_1_out;
  wire [31:28] adder_1_out_2;

  Clock #(.highDuration(1), .lowDuration(1)) clock_1 (.out(CLK));
  Button _1 (.out(IRA));
  Button _2 (.out(IRB));
  Button _3 (.out(IRC));
  Button \u_继续运行  (.out(Go));
  LED #(.active("true")) led_1 (.in(W1));
  LED #(.active("true")) led_2 (.in(W2));
  LED #(.active("true")) led_3 (.in(W3));
  Multiplexer #(.select(1), .width(2), .disabled("Z"), .enable("false")) multiplexer_1 (
    .in0(Pri), .in1(Execp2_q), .out(multiplexer_1_out), .sel(ERET));
  Register #(.width(2), .trigger("rising"), .Select("low")) Excep1 (
    .D(multiplexer_1_out), .en(or_1_out), .Q(ExcepType), .clk(CLK));  // open: clr
  or or_1 (or_1_out, ERET, Exception);
  Hex_Digit_Display hex_digit_display_1 (.value(LedData[31:28]));  // open: dp
  Multiplexer #(.select(1), .width(2), .disabled("Z"), .enable("false")) multiplexer_2 (
    .in0(ExcepType), .in1(Execp3_q), .out(multiplexer_2_out), .sel(ERET));
  Hex_Digit_Display hex_digit_display_2 (.value(LedData[23:20]));  // open: dp
  Hex_Digit_Display hex_digit_display_3 (.value(LedData[27:24]));  // open: dp
  or or_2 (or_2_out, ~Halt, d_ff_1_q);  // OR_Gate
  Multiplexer #(.select(2), .width(32), .disabled("Z"), .enable("false")) multiplexer_3 (
    .in0({adder_1_out_2, adder_1_out}), .in1(adder_2_out), .in2(multiplexer_4_out), .out(next_PC),
    .sel(or_9_out));  // open: in3
  Multiplexer #(.select(1), .width(32), .disabled("Z"), .enable("false")) multiplexer_4 (
    .in0({adder_1_out_2, IR[25:0], 2'b00}), .in1(R1), .out(multiplexer_4_out), .sel(JR));
  Register #(.width(2), .trigger("rising"), .Select("low")) Execp2 (
    .D(multiplexer_2_out), .en(or_1_out), .Q(Execp2_q), .clk(CLK));  // open: clr
  Hex_Digit_Display hex_digit_display_4 (.value(LedData[15:12]));  // open: dp
  Hex_Digit_Display hex_digit_display_5 (.value(LedData[19:16]));  // open: dp
  Counter #(.width(16), .max('hffff), .ongoal("wrap"), .trigger("rising"), .behavior("old")) counter_1 (
    .count(or_9_out[0]), .Q(\条件分支成功数 ), .clk(CLK));  // open: load, D, carry, clr, preset
  Counter #(.width(16), .max('hffff), .ongoal("wrap"), .trigger("rising"), .behavior("old")) counter_2 (
    .count(or_9_out[1]), .Q(\无条件分支数 ), .clk(CLK));  // open: load, D, carry, clr, preset
  Register #(.width(32), .trigger("rising"), .Select("low")) u_PC (
    .D(in_PC), .en(or_2_out), .Q(PC), .clk(CLK));  // open: clr
  Multiplexer #(.select(1), .width(2), .disabled("Z"), .enable("false")) multiplexer_5 (
    .in0(Execp2_q), .in1(2'b00), .out(multiplexer_5_out), .sel(ERET));
  Decoder #(.select(2), .tristate("false"), .disabled("Z"), .enable("false")) decoder_1 (
    .out1(decoder_1_out1), .out2(decoder_1_out2), .out3(decoder_1_out3), .sel(ExcepType));  // open: out0
  Hex_Digit_Display hex_digit_display_6 (.value(LedData[11:8]));  // open: dp
  Hex_Digit_Display hex_digit_display_7 (.value(LedData[7:4]));  // open: dp
  // Probe on \总周期数 
  D_Flip_Flop #(.trigger("rising"), .Pre_Clr_Positions("LEGACY"), .NegatePresetClear("false"), .enable("true"), .NewFFLayout("false")) d_ff_1 (
    .clk(CLK), .D(1'b0), .Q(d_ff_1_q), .preset(Go));  // open: Qn, en, reset
  Adder #(.width(32)) adder_1 (.a(PC), .b(32'h4), .out({adder_1_out_2, adder_1_out}));  // open: cin, cout
  Register #(.width(2), .trigger("rising"), .Select("low")) Execp3 (
    .D(multiplexer_5_out), .en(or_1_out), .Q(Execp3_q), .clk(CLK));  // open: clr
  and and_1 (and_1_out, ERET, decoder_1_out1);
  and and_2 (and_2_out, ERET, decoder_1_out2);
  and and_3 (and_3_out, ERET, decoder_1_out3);
  Hex_Digit_Display hex_digit_display_8 (.value(LedData[3:0]));  // open: dp
  Adder #(.width(32)) adder_2 (
    .a({adder_1_out_2, adder_1_out}), .b(shifter_1_out), .out(adder_2_out));  // open: cin, cout
  \中断按键参考电路  \u_中断按键参考电路_1  (.IR_2(\中断按键参考电路_1_ir_2 ), .Clr(and_1_out), .clk(CLK), .W(W1), .IR(IR1_t));
  \中断按键参考电路  \u_中断按键参考电路_2  (.IR_2(\中断按键参考电路_2_ir_2 ), .Clr(and_2_out), .clk(CLK), .W(W2), .IR(IR2_t));
  \中断按键参考电路  \u_中断按键参考电路_3  (.IR_2(\中断按键参考电路_3_ir_2 ), .Clr(and_3_out), .clk(CLK), .W(W3), .IR(IR3_t));
  ROM #(.addrWidth(10), .dataWidth(32), .Select("high")) rom_1 (.addr(PC[11:2]), .data(IR));
  or or_3 (IR1_t, IR1, IRA);
  Priority_Encoder #(.select(2), .disabled("Z")) priority_encoder_1 (
    .in1(\中断按键参考电路_1_ir_2 ), .in2(\中断按键参考电路_2_ir_2 ), .in3(\中断按键参考电路_3_ir_2 ), .out(Pri), .en_in(1'b1));  // open: in0, gs, en_out
  or or_4 (IR2_t, IR2, IRB);
  \单周期硬布线控制器  \u_单周期硬布线控制器_1  (
    .Func(IR[5:0]), .OP(IR[31:26]), .ALU_OP(\单周期硬布线控制器_1_alu_op ), .MemToReg(\单周期硬布线控制器_1_memtoreg ),
    .MemWrite(MemWrite), .ALU_SRC(\单周期硬布线控制器_1_alu_src ), .RegWrite(RegWrite), .SysCALL(Syscall),
    .SignedExt(SignedExt), .RegDst(\单周期硬布线控制器_1_regdst ), .JR(JR), .JMP(or_9_out[1]),
    .Beq(\单周期硬布线控制器_1_beq ), .JAL(JAL), .Bne(\单周期硬布线控制器_1_bne ), .ERET(ERET));
  Multiplexer #(.select(1), .width(5), .disabled("Z"), .enable("false")) multiplexer_6 (
    .in0(IR[20:16]), .in1(IR[15:11]), .out(multiplexer_6_out), .sel(\单周期硬布线控制器_1_regdst ));
  assign bit_extender_1_out = {{16{1'b0}}, IR[15:0]};  // Bit_Extender bit_extender_1
  assign bit_extender_2_out = {{16{IR[15]}}, IR[15:0]};  // Bit_Extender bit_extender_2
  MFC_MTC mfc_mtc_1 (.in_1(IR[31:21]), .MFC(MFC), .MTC(MTC));
  or or_5 (or_5_out, MTC, Exception);
  or or_6 (or_6_out, Exception, ERET, MFC, MTC);
  Pull_Resistor #(.pull(0)) pull_resistor_1 (.node(Pri));
  Multiplexer #(.select(2), .width(32), .disabled("Z"), .enable("false")) multiplexer_7 (
    .in0({32{1'b0}}), .in1(32'h30ac), .in2(32'h3158), .in3(32'h3204), .out(multiplexer_7_out), .sel(Pri));
  Multiplexer #(.select(1), .width(5), .disabled("Z"), .enable("false")) multiplexer_8 (
    .in0(IR[25:21]), .in1(5'b00010), .out(multiplexer_8_out), .sel(Syscall));
  Multiplexer #(.select(1), .width(5), .disabled("Z"), .enable("false")) multiplexer_9 (
    .in0(IR[20:16]), .in1(5'b00100), .out(multiplexer_9_out), .sel(Syscall));
  Multiplexer #(.select(1), .width(5), .disabled("Z"), .enable("false")) multiplexer_10 (
    .in0(multiplexer_6_out), .in1({5{1'b1}}), .out(multiplexer_10_out), .sel(JAL));
  Multiplexer #(.select(1), .width(32), .disabled("Z"), .enable("false")) multiplexer_11 (
    .in0(bit_extender_1_out), .in1(bit_extender_2_out), .out(multiplexer_11_out), .sel(SignedExt));
  Shifter #(.width(32), .shift("ll")) shifter_1 (.in(bit_extender_2_out), .\dist (5'b00010), .out(shifter_1_out));
  Multiplexer #(.select(1), .width(1), .disabled("Z"), .enable("false")) multiplexer_12 (
    .in0(1'b0), .in1(1'b1), .out(multiplexer_12_out), .sel(or_5_out));
  Register #(.width(1), .trigger("rising"), .Select("low")) nIE (
    .D(multiplexer_12_out), .en(or_6_out), .Q(nIE_q), .clk(CLK));  // open: clr
  or or_7 (IR3_t, IR3, IRC);
  not not_1 (not_1_out, Halt);
  MIPS_Regifile mips_regifile_1 (
    .Din(RDin), .Clk(CLK), .R1(R1), .R2(MDin), .WE(RegWrite), .W_num(multiplexer_10_out),
    .R1_num(multiplexer_8_out), .R2_num(multiplexer_9_out));
  Multiplexer #(.select(1), .width(32), .disabled("Z"), .enable("false")) multiplexer_13 (
    .in0(multiplexer_17_out), .in1({adder_1_out_2, adder_1_out}), .out(RDin), .sel(JAL));
  Comparator #(.width(2), .mode("unsigned")) comparator_1 (
    .a(Pri), .b(ExcepType), .gt(comparator_1_gt));  // open: eq, lt
  Counter #(.width(16), .max('hffff), .ongoal("wrap"), .trigger("rising"), .behavior("old")) counter_3 (
    .count(not_1_out), .Q(\总周期数 ), .clk(CLK));  // open: load, D, carry, clr, preset
  and and_4 (Exception, ~nIE_q, comparator_1_gt);  // AND_Gate
  Multiplexer #(.select(1), .width(32), .disabled("Z"), .enable("false")) multiplexer_14 (
    .in0(MDin), .in1(multiplexer_11_out), .out(multiplexer_14_out), .sel(\单周期硬布线控制器_1_alu_src ));
  Comparator #(.width(32), .mode("twosComplement")) comparator_2 (
    .a(R1), .b(32'h32), .eq(comparator_2_eq));  // open: gt, lt
  Multiplexer #(.select(1), .width(32), .disabled("Z"), .enable("false")) multiplexer_15 (
    .in0(next_PC), .in1(EPC2_q), .out(multiplexer_15_out), .sel(ERET));
  or or_8 (or_8_out, ERET, Exception);
  Multiplexer #(.select(2), .width(32), .disabled("Z"), .enable("false")) multiplexer_16 (
    .in0(next_PC), .in1(multiplexer_7_out), .in2(EPC1_q), .out(in_PC), .sel({ERET, Exception}));  // open: in3
  MIPS_ALU mips_alu_1 (
    .X(R1), .Y(multiplexer_14_out), .AluOP(\单周期硬布线控制器_1_alu_op ), .Equal(mips_alu_1_equal),
    .Result(mips_alu_1_result), .shamt(IR[10:6]));  // open: Result_2
  Multiplexer #(.select(1), .width(32), .disabled("Z"), .enable("false")) multiplexer_17 (
    .in0(mips_alu_1_result), .in1(ram_1_data), .out(multiplexer_17_out), .sel(\单周期硬布线控制器_1_memtoreg ));
  and and_5 (Halt, comparator_2_eq, Syscall);
  and and_6 (and_6_out, ~comparator_2_eq, Syscall);  // AND_Gate
  Register #(.width(32), .trigger("rising"), .Select("low")) EPC1 (
    .D(multiplexer_15_out), .en(or_8_out), .Q(EPC1_q), .clk(CLK));  // open: clr
  and and_7 (and_7_out, mips_alu_1_equal, \单周期硬布线控制器_1_beq );
  or or_9 (or_9_out[0], and_7_out, and_8_out);
  and and_8 (and_8_out, ~mips_alu_1_equal, \单周期硬布线控制器_1_bne );  // AND_Gate
  Register #(.width(32), .trigger("rising"), .Select("low")) register_1 (
    .D(MDin), .en(and_6_out), .Q(LedData), .clk(CLK));  // open: clr
  Multiplexer #(.select(1), .width(32), .disabled("Z"), .enable("false")) multiplexer_18 (
    .in0(EPC1_q), .in1(EPC3_q), .out(multiplexer_18_out), .sel(ERET));
  Register #(.width(32), .trigger("rising"), .Select("low")) EPC2 (
    .D(multiplexer_18_out), .en(or_8_out), .Q(EPC2_q), .clk(CLK));  // open: clr
  RAM #(.addrWidth(10), .dataWidth(32), .bus("separate"), .Select("high")) ram_1 (
    .addr(mips_alu_1_result[11:2]), .din(MDin), .data(ram_1_data), .str(MemWrite), .clk(CLK));  // open: sel, ld, clr
  Register #(.width(32), .trigger("rising"), .Select("low")) EPC3 (
    .D(EPC2_q), .en(Exception), .Q(EPC3_q), .clk(CLK));  // open: clr

  // Notes on the sheet:
  //   中断源
  //   中断等待指示
  //   总复位信号应将除ROM以外所有存储组件全部清零
  //   数码管输出
  //   数码管输出应该用寄存器锁存，否则显示数据只能一闪而过
  //   instr_index
  //   contents of rom_1 (hex, n*v repeats v):
  //   201d07d0 20100001 109fc0 139fc3 8021 2012000c 24160008 26100001 3210000f 20080008 20090001 139900
  //   2709825 132020 20020022 c 1094022 1500fff9 22100001 2018000f 2188024 108700 20080008 20090001 139902
  //   2709825 132021 20020022 c 1094022 1500fff9 108702 2c9b022 12c00001 8000c07 4020 1084027 84400
  //   3508ffff 82021 20020022 c 8000c01 afa20000 23bd0004 afa40000 23bd0004 afb00000 23bd0004 afb30000
  //   23bd0004 afb40000 23bd0004 afb50000 23bd0004 afb60000 23bd0004 40000000 20160001 20140003 20150001
  //   168020 108100 2149825 132020 20020022 c 1600fffa 295a022 1680fff7 40800000 23bdfffc 8fb60000
  //   23bdfffc 8fb50000 23bdfffc 8fb40000 23bdfffc 8fb30000 23bdfffc 8fb00000 23bdfffc 8fa40000 23bdfffc
  //   8fa20000 42000018 afa20000 23bd0004 afa40000 23bd0004 afb00000 23bd0004 afb30000 23bd0004 afb40000
  //   23bd0004 afb50000 23bd0004 afb60000 23bd0004 40000000 20160002 20140003 20150001 168020 108100
  //   2149825 132020 20020022 c 1600fffa 295a022 1680fff7 40800000 23bdfffc 8fb60000 23bdfffc 8fb50000
  //   23bdfffc 8fb40000 23bdfffc 8fb30000 23bdfffc 8fb00000 23bdfffc 8fa40000 23bdfffc 8fa20000 42000018
  //   afa20000 23bd0004 afa40000 23bd0004 afb00000 23bd0004 afb30000 23bd0004 afb40000 23bd0004 afb50000
  //   23bd0004 afb60000 23bd0004 40000000 20160003 20140003 20150001 168020 108100 2149825 132020 20020022
  //   c 1600fffa 295a022 1680fff7 40800000 23bdfffc 8fb60000 23bdfffc 8fb50000 23bdfffc 8fb40000 23bdfffc
  //   8fb30000 23bdfffc 8fb00000 23bdfffc 8fa40000 23bdfffc 8fa20000 42000018
  //   JMP
  //   JR
  //   OP
  //   Func
  //   rs
  //   rt
  //   rd
  //   imm
  //   sa
  //   Beq
  //   Bne
  //   AluOP
  //   AluSrcB
  //   RegWrite
  //   JAL
  //   RegDst
  //   Syscall
  //   v0
  //   a0
  //   MemToReg
  //   MemWrite
  //   为方便自动评测，需要输出PC，IR，寄存器堆写如数据RDin
  //   RAM写使能MemWrite、RAM写入数据MDin等信号
endmodule

module \重定向流水线_单级中断  (
  output RegWrite,
  output MemWrite,
  output [31:0] IF_PC,
  output [31:0] ID_PC,
  output [31:0] EX_PC,
  output [31:0] M_PC,
  output [31:0] WB_PC,
  output [31:0] RDin,
  output [31:0] MDin,
  output [31:0] LedData
);

  wire AluSrcB, and_1_out, and_2_out, and_3_out, and_4_out, and_6_out, and_7_out, and_8_out, and_9_out,
       and_10_out, Beq, BLTZ, Bne, Branch, CLK, comparator_1_eq, d_ff_1_q, decoder_1_out0, decoder_1_out1,
       decoder_1_out2, ERET, EX_AluEq, EX_Beq, EX_BLTZ, EX_Bne, EX_JMP, EX_JR, EX_MemToReg, EX_RegWrite,
       EX_RsRead, EX_RtRead, EX_Syscall, Exception, Go, Halt, IR1, IR2, IR3, JAL, JMP, JR, LB, LoadUse, LUI,
       MEM_RegWrite, MemToReg, MemWrite_t, multiplexer_2_out, nIE_q, not_1_out, or_1_out, or_2_out, or_3_out,
       or_4_out, priority_encoder_1_en_out, priority_encoder_1_gs, RegDst, RegWrite_t, RST, SignedExt,
       Syscall, W1, W2, W3, WB_ERET, WB_MemToReg, \中断按键参考电路_1_ir_2 , \中断按键参考电路_2_ir_2 , \中断按键参考电路_3_ir_2 ,
       \扩展ex_mem_1_eret_2 , \扩展ex_mem_1_halt_2 , \扩展ex_mem_1_jal_2 , \扩展ex_mem_1_lb_2 , \扩展ex_mem_1_lui_2 ,
       \扩展ex_mem_1_memtoreg_2 , \扩展id_ex_1_alusrcb_2 , \扩展id_ex_1_eret_2 , \扩展id_ex_1_jal_2 ,
       \扩展id_ex_1_lb_2 , \扩展id_ex_1_lui_2 , \扩展id_ex_1_memwrite_2 , \扩展mem_wb_1_jal_2 , \扩展mem_wb_1_lb_2 ,
       \扩展mem_wb_1_lui_2 , \数据相关测试2_1_hazarda , \数据相关测试2_1_hazardb , \数据相关测试2_2_hazarda ,
       \数据相关测试2_2_hazardb , \数据相关测试_1_hazard ;
  wire [1:0] comparator_2_gt, ForwardA, ForwardB, multiplexer_9_out, priority_encoder_1_out, register_1_q,
       regread_1_rsread, \扩展mem_wb_1_alu_2 ;
  wire [3:0] adder_2_out_2, AluOP, \扩展id_ex_1_aluop_2 ;
  wire [4:0] EX_rW, MEM_rW, multiplexer_4_out, multiplexer_5_out, multiplexer_7_out, registerfile_1_p6, WB_rW;
  wire [7:0] multiplexer_17_out, \扩展mem_wb_1_md_2 , \扩展mem_wb_1_md_2_2 , \扩展mem_wb_1_md_2_3 ,
       \扩展mem_wb_1_md_2_4 ;
  wire [15:0] \LoadUse次数 , \总周期数 , \插入气泡数 , \无条件分支数 , \条件分支成功数 ;
  wire [27:0] adder_2_out;
  wire [31:0] adder_1_out, adder_4_out, bit_extender_1_out, bit_extender_2_out, bit_extender_3_out, BranchPC,
       EPC, EPC_q, EX_A, EX_Alu, EX_B, EX_Imm, EX_IR, ID_IR, IF_IR, in_PC, JmpPC, MEM_IR, multiplexer_3_out,
       multiplexer_8_out, multiplexer_11_out, multiplexer_14_out, multiplexer_18_out, multiplexer_19_out,
       multiplexer_20_out, next_PC, ram_1_data, registerfile_1_p7, registerfile_1_p8, shifter_1_out, WB_IR,
       \扩展ex_mem_1_alu_2 , \扩展ex_mem_1_imm_2 , \扩展id_ex_1_a_2 , \扩展id_ex_1_b_2 , \扩展mem_wb_1_imm_2 ;
  wire [31:2] \扩展mem_wb_1_alu_2_2 ;

  Button \u_总复位  (.out(RST));
  Button _1 (.out(IR1));
  Button _2 (.out(IR2));
  Button _3 (.out(IR3));
  // Probe on \总周期数 
  Button \u_继续运行  (.out(Go));
  LED #(.active("true")) led_1 (.in(W1));
  LED #(.active("true")) led_2 (.in(W2));
  LED #(.active("true")) led_3 (.in(W3));
  // Probe on IF_PC
  Hex_Digit_Display hex_digit_display_1 (.value(LedData[31:28]));  // open: dp
  Multiplexer #(.select(2), .width(32), .disabled("Z"), .enable("false")) multiplexer_1 (
    .in0(adder_1_out), .in1(JmpPC), .in2(BranchPC), .out(next_PC), .sel({Branch, EX_JMP}));  // open: in3
  or or_1 (or_1_out, Branch, EX_JMP, Exception);
  Decoder #(.select(2), .tristate("false"), .disabled("Z"), .enable("false")) decoder_1 (
    .out0(decoder_1_out0), .out1(decoder_1_out1), .out2(decoder_1_out2), .sel(register_1_q));  // open: out3
  Hex_Digit_Display hex_digit_display_2 (.value(LedData[23:20]));  // open: dp
  Hex_Digit_Display hex_digit_display_3 (.value(LedData[27:24]));  // open: dp
  // Probe on ID_PC
  // Probe on IF_PC
  // Probe on ID_PC
  // Probe on EX_PC
  // Probe on M_PC
  // Probe on WB_PC
  or or_2 (or_2_out, ~Halt, d_ff_1_q);  // OR_Gate
  and and_1 (and_1_out, or_2_out, ~LoadUse);  // AND_Gate
  and and_2 (and_2_out, WB_ERET, decoder_1_out0);
  and and_3 (and_3_out, WB_ERET, decoder_1_out1);
  and and_4 (and_4_out, WB_ERET, decoder_1_out2);
  Hex_Digit_Display hex_digit_display_4 (.value(LedData[19:16]));  // open: dp
  Hex_Digit_Display hex_digit_display_5 (.value(LedData[15:12]));  // open: dp
  D_Flip_Flop #(.trigger("rising"), .Pre_Clr_Positions("LEGACY"), .NegatePresetClear("false"), .enable("true"), .NewFFLayout("false")) d_ff_1 (
    .clk(CLK), .D(1'b0), .Q(d_ff_1_q), .preset(Go));  // open: Qn, en, reset
  Register #(.width(32), .trigger("rising"), .Select("low")) PC (
    .D(in_PC), .en(and_1_out), .Q(IF_PC), .clk(CLK));  // open: clr
  \中断按键参考电路  \u_中断按键参考电路_1  (.IR_2(\中断按键参考电路_1_ir_2 ), .Clr(and_2_out), .clk(CLK), .W(W1), .IR(IR1));
  \中断按键参考电路  \u_中断按键参考电路_2  (.IR_2(\中断按键参考电路_2_ir_2 ), .Clr(and_3_out), .clk(CLK), .W(W2), .IR(IR2));
  \中断按键参考电路  \u_中断按键参考电路_3  (.IR_2(\中断按键参考电路_3_ir_2 ), .Clr(and_4_out), .clk(CLK), .W(W3), .IR(IR3));
  Hex_Digit_Display hex_digit_display_6 (.value(LedData[7:4]));  // open: dp
  Hex_Digit_Display hex_digit_display_7 (.value(LedData[11:8]));  // open: dp
  Clock #(.highDuration(1), .lowDuration(1)) clock_1 (.out(CLK));
  // Probe on EX_PC
  Adder #(.width(32)) adder_1 (.a(IF_PC), .b(32'h4), .out(adder_1_out));  // open: cin, cout
  Hex_Digit_Display hex_digit_display_8 (.value(LedData[3:0]));  // open: dp
  // Probe on IF_IR
  // Probe on ID_IR
  // Probe on EX_IR
  // Probe on MEM_IR
  // Probe on WB_IR
  ROM #(.addrWidth(10), .dataWidth(32), .Select("high")) rom_1 (.addr(IF_PC[11:2]), .data(IF_IR));
  RegRead regread_1 (
    .OP0(ID_IR[26]), .OP1(ID_IR[27]), .OP2(ID_IR[28]), .OP3(ID_IR[29]), .OP4(ID_IR[30]), .OP5(ID_IR[31]),
    .F0(ID_IR[0]), .F1(ID_IR[1]), .F2(ID_IR[2]), .F3(ID_IR[3]), .F4(ID_IR[4]), .F5(ID_IR[5]),
    .RsRead(regread_1_rsread[0]), .RtRead(regread_1_rsread[1]));
  Multiplexer #(.select(1), .width(1), .disabled("Z"), .enable("false")) multiplexer_2 (
    .in0(priority_encoder_1_gs), .in1(1'b0), .out(multiplexer_2_out), .sel(WB_ERET));
  Register #(.width(1), .trigger("rising"), .Select("low")) nIE (
    .D(multiplexer_2_out), .Q(nIE_q), .clk(CLK));  // open: en, clr
  // Probe on M_PC
  nor nor_1 (Exception, nIE_q, priority_encoder_1_en_out);
  Priority_Encoder #(.select(2), .disabled("Z")) priority_encoder_1 (
    .in0(\中断按键参考电路_1_ir_2 ), .in1(\中断按键参考电路_2_ir_2 ), .in2(\中断按键参考电路_3_ir_2 ), .in3(1'b0),
    .out(priority_encoder_1_out), .gs(priority_encoder_1_gs), .en_out(priority_encoder_1_en_out), .en_in(1'b1));
  Multiplexer #(.select(2), .width(32), .disabled("Z"), .enable("false")) multiplexer_3 (
    .in0(32'h30ac), .in1(32'h3150), .in2(32'h31f4), .out(multiplexer_3_out), .sel(priority_encoder_1_out));  // open: in3
  // Probe on \总周期数 
  // Probe on \无条件分支数 
  // Probe on \条件分支成功数 
  // Probe on \插入气泡数 
  // Probe on \LoadUse次数 
  \扩展IF_ID  \u_扩展if_id_1  (
    .IR(IF_IR), .PC(IF_PC), .IR_2(ID_IR), .PC_2(ID_PC), .En(and_1_out), .Clk(CLK), .Clr(or_3_out));
  or or_3 (or_3_out, ERET, or_1_out);
  \数据相关测试  \u_数据相关测试_1  (
    .RsRead(regread_1_rsread[0]), .Rs(ID_IR[25:21]), .RtRead(regread_1_rsread[1]), .Rt(ID_IR[20:16]),
    .Rw(EX_rW), .RegWrite(EX_RegWrite), .Syscall(Syscall), .Hazard(\数据相关测试_1_hazard ));
  Register #(.width(2), .trigger("rising"), .Select("low")) register_1 (
    .D(priority_encoder_1_out), .en(Exception), .Q(register_1_q), .clk(CLK));  // open: clr
  // Probe on IF_PC[11:0]
  // Probe on WB_PC
  and and_5 (LoadUse, EX_MemToReg, \数据相关测试_1_hazard );
  Register #(.width(32), .trigger("rising"), .Select("low")) u_EPC (
    .D(EPC), .en(Exception), .Q(EPC_q), .clk(CLK));  // open: clr
  // Probe on EX_PC[11:0]
  // Probe on ID_PC[11:0]
  \扩展单周期硬布线控制器  \u_扩展单周期硬布线控制器_1  (
    .OP(ID_IR[31:26]), .Func(ID_IR[5:0]), .ALU_OP(AluOP), .MemToReg(MemToReg), .MemWrite(MemWrite_t),
    .ALU_SRC(AluSrcB), .RegWrite(RegWrite_t), .SysCALL(Syscall), .SignedExt(SignedExt), .RegDst(RegDst),
    .Beq(Beq), .Bne(Bne), .JR(JR), .JMP(JMP), .JAL(JAL), .LUI(LUI), .LB(LB), .BLTZ(BLTZ), .ERET(ERET));
  Multiplexer #(.select(1), .width(5), .disabled("Z"), .enable("false")) multiplexer_4 (
    .in0(ID_IR[20:16]), .in1(ID_IR[15:11]), .out(multiplexer_4_out), .sel(RegDst));
  Multiplexer #(.select(1), .width(5), .disabled("Z"), .enable("false")) multiplexer_5 (
    .in0(multiplexer_4_out), .in1({5{1'b1}}), .out(multiplexer_5_out), .sel(JAL));
  Multiplexer #(.select(2), .width(32), .disabled("Z"), .enable("false")) multiplexer_6 (
    .in0(next_PC), .in1(EPC_q), .in2(multiplexer_3_out), .out(in_PC), .sel({Exception, ERET}));  // open: in3
  // Probe on M_PC[11:0]
  assign bit_extender_1_out = {{16{1'b0}}, ID_IR[15:0]};  // Bit_Extender bit_extender_1
  assign bit_extender_2_out = {{16{ID_IR[15]}}, ID_IR[15:0]};  // Bit_Extender bit_extender_2
  // Probe on WB_PC[11:0]
  Counter #(.width(16), .max('hffff), .ongoal("wrap"), .trigger("rising"), .behavior("old")) counter_1 (
    .count(not_1_out), .Q(\总周期数 ), .clk(CLK));  // open: load, D, carry, clr, preset
  not not_1 (not_1_out, Halt);
  Multiplexer #(.select(1), .width(5), .disabled("Z"), .enable("false")) multiplexer_7 (
    .in0(ID_IR[25:21]), .in1(5'b00010), .out(multiplexer_7_out), .sel(Syscall));
  Multiplexer #(.select(1), .width(32), .disabled("Z"), .enable("false")) multiplexer_8 (
    .in0(bit_extender_1_out), .in1(bit_extender_2_out), .out(multiplexer_8_out), .sel(SignedExt));
  Multiplexer #(.select(1), .width(2), .disabled("Z"), .enable("false")) multiplexer_9 (
    .in0(regread_1_rsread), .in1(2'b00), .out(multiplexer_9_out), .sel(or_4_out));
  // RegisterFile registerfile_1: pin names not known; wires that end beside it: RDin, CLK, RegWrite, WB_rW, multiplexer_7_out, registerfile_1_p6, registerfile_1_p7, registerfile_1_p8
  Multiplexer #(.select(1), .width(5), .disabled("Z"), .enable("false")) multiplexer_10 (
    .in0(ID_IR[20:16]), .in1(5'b00100), .out(registerfile_1_p6), .sel(Syscall));
  Multiplexer #(.select(1), .width(32), .disabled("Z"), .enable("false")) multiplexer_11 (
    .in0(multiplexer_8_out), .in1({ID_IR[15:0], {16{1'b0}}}), .out(multiplexer_11_out), .sel(LUI));
  Register #(.width(2), .trigger("rising"), .Select("low")) register_2 (
    .D(multiplexer_9_out), .en(or_2_out), .Q({EX_RtRead, EX_RsRead}), .clk(CLK));  // open: clr
  \数据相关测试2  \u_数据相关测试2_1  (
    .RsRead(EX_RsRead), .Rs(EX_IR[25:21]), .RtRead(EX_RtRead), .Rt(EX_IR[20:16]), .Rw(MEM_rW),
    .RegWrite(MEM_RegWrite), .Syscall(EX_Syscall), .HazardA(\数据相关测试2_1_hazarda ),
    .HazardB(\数据相关测试2_1_hazardb ));
  \数据相关测试2  \u_数据相关测试2_2  (
    .RsRead(EX_RsRead), .Rs(EX_IR[25:21]), .RtRead(EX_RtRead), .Rt(EX_IR[20:16]), .Rw(WB_rW),
    .RegWrite(RegWrite), .Syscall(EX_Syscall), .HazardA(\数据相关测试2_2_hazarda ), .HazardB(\数据相关测试2_2_hazardb ));
  Comparator #(.width(32), .mode("twosComplement")) comparator_1 (
    .a(EX_A), .b(32'h32), .eq(comparator_1_eq));  // open: gt, lt
  \扩展ID_EX  \u_扩展id_ex_1  (
    .Syscall(Syscall), .W_num(multiplexer_5_out), .MemToReg(MemToReg), .RegWrite(RegWrite_t), .JAL(JAL),
    .LB(LB), .LUI(LUI), .MemWrite(MemWrite_t), .AluOP(AluOP), .AluSrcB(AluSrcB), .Beq(Beq), .Bne(Bne),
    .JMP(JMP), .JR(JR), .BLTZ(BLTZ), .IR(ID_IR), .PC(ID_PC), .A(registerfile_1_p7), .B(registerfile_1_p8),
    .Imm(multiplexer_11_out), .Syscall_2(EX_Syscall), .W_num_2(EX_rW), .MemToReg_2(EX_MemToReg),
    .RegWrite_2(EX_RegWrite), .JAL_2(\扩展id_ex_1_jal_2 ), .LB_2(\扩展id_ex_1_lb_2 ), .LUI_2(\扩展id_ex_1_lui_2 ),
    .MemWrite_2(\扩展id_ex_1_memwrite_2 ), .AluOP_2(\扩展id_ex_1_aluop_2 ), .AluSrcB_2(\扩展id_ex_1_alusrcb_2 ),
    .Beq_2(EX_Beq), .Bne_2(EX_Bne), .JMP_2(EX_JMP), .JR_2(EX_JR), .BLTZ_2(EX_BLTZ), .IR_2(EX_IR),
    .PC_2(EX_PC), .A_2(\扩展id_ex_1_a_2 ), .B_2(\扩展id_ex_1_b_2 ), .Imm_2(EX_Imm), .En(or_2_out), .Clk(CLK),
    .Clr(or_4_out), .ERET(ERET), .ERET_2(\扩展id_ex_1_eret_2 ));
  or or_4 (or_4_out, or_1_out, LoadUse);
  Forward forward_1 (
    .HazardA(\数据相关测试2_1_hazarda ), .HazardB(\数据相关测试2_2_hazarda ), .MemToReg(WB_MemToReg), .out_4(ForwardA));
  Forward forward_2 (
    .HazardA(\数据相关测试2_1_hazardb ), .HazardB(\数据相关测试2_2_hazardb ), .MemToReg(WB_MemToReg), .out_4(ForwardB));
  and and_6 (and_6_out, comparator_1_eq, EX_Syscall);
  and and_7 (and_7_out, ~comparator_1_eq, EX_Syscall);  // AND_Gate
  Register #(.width(32), .trigger("rising"), .Select("low")) register_3 (
    .D(EX_B), .en(and_7_out), .Q(LedData), .clk(CLK));  // open: clr
  Multiplexer #(.select(2), .width(32), .disabled("Z"), .enable("false")) multiplexer_12 (
    .in0(\扩展id_ex_1_a_2 ), .in1(multiplexer_18_out), .in2({\扩展mem_wb_1_alu_2_2 , \扩展mem_wb_1_alu_2 }),
    .in3(\扩展ex_mem_1_alu_2 ), .out(EX_A), .sel(ForwardA));
  and and_8 (and_8_out, EX_AluEq, EX_Beq);
  and and_9 (and_9_out, ~EX_AluEq, EX_Bne);  // AND_Gate
  or or_5 (Branch, and_8_out, and_9_out, and_10_out);
  and and_10 (and_10_out, EX_Alu[0], BLTZ);
  Comparator #(.width(32), .mode("unsigned")) comparator_2 (
    .a(ID_PC), .b({32{1'b0}}), .gt(comparator_2_gt[0]));  // open: eq, lt
  Comparator #(.width(32), .mode("unsigned")) comparator_3 (
    .a(EX_PC), .b({32{1'b0}}), .gt(comparator_2_gt[1]));  // open: eq, lt
  Multiplexer #(.select(2), .width(32), .disabled("Z"), .enable("false")) multiplexer_13 (
    .in0(\扩展id_ex_1_b_2 ), .in1(multiplexer_18_out), .in2({\扩展mem_wb_1_alu_2_2 , \扩展mem_wb_1_alu_2 }),
    .in3(\扩展ex_mem_1_alu_2 ), .out(EX_B), .sel(ForwardB));
  Multiplexer #(.select(1), .width(32), .disabled("Z"), .enable("false")) multiplexer_14 (
    .in0(EX_B), .in1(EX_Imm), .out(multiplexer_14_out), .sel(\扩展id_ex_1_alusrcb_2 ));
  Multiplexer #(.select(2), .width(32), .disabled("Z"), .enable("false")) multiplexer_15 (
    .in0(IF_PC), .in1(ID_PC), .in2(EX_PC), .in3(EX_PC), .out(EPC), .sel(comparator_2_gt));
  MIPS_ALU mips_alu_1 (
    .X(EX_A), .Y(multiplexer_14_out), .AluOP(\扩展id_ex_1_aluop_2 ), .Equal(EX_AluEq), .Result(EX_Alu),
    .shamt(EX_IR[10:6]));  // open: Result_2
  Adder #(.width(32)) adder_2 (.a(EX_PC), .b(32'h4), .out({adder_2_out_2, adder_2_out}));  // open: cin, cout
  \扩展EX_MEM  \u_扩展ex_mem_1  (
    .Halt(and_6_out), .Halt_2(\扩展ex_mem_1_halt_2 ), .W_num(EX_rW), .W_num_2(MEM_rW), .MemToReg(EX_MemToReg),
    .MemToReg_2(\扩展ex_mem_1_memtoreg_2 ), .RegWrite(EX_RegWrite), .RegWrite_2(MEM_RegWrite),
    .JAL(\扩展id_ex_1_jal_2 ), .JAL_2(\扩展ex_mem_1_jal_2 ), .LB(\扩展id_ex_1_lb_2 ), .LB_2(\扩展ex_mem_1_lb_2 ),
    .LUI(\扩展id_ex_1_lui_2 ), .LUI_2(\扩展ex_mem_1_lui_2 ), .MemWrite(\扩展id_ex_1_memwrite_2 ),
    .MemWrite_2(MemWrite), .IR(EX_IR), .IR_2(MEM_IR), .PC(EX_PC), .PC_2(M_PC), .ALU(EX_Alu),
    .ALU_2(\扩展ex_mem_1_alu_2 ), .B(EX_B), .B_2(MDin), .Imm(EX_Imm), .Imm_2(\扩展ex_mem_1_imm_2 ),
    .Clr(Exception), .En(or_2_out), .Clk(CLK), .ERET(\扩展id_ex_1_eret_2 ), .ERET_2(\扩展ex_mem_1_eret_2 ));
  Shifter #(.width(32), .shift("ll")) shifter_1 (.in(EX_Imm), .\dist (5'b00010), .out(shifter_1_out));
  Adder #(.width(32)) adder_3 (.a(shifter_1_out), .b({adder_2_out_2, adder_2_out}), .out(BranchPC));  // open: cin, cout
  Multiplexer #(.select(1), .width(32), .disabled("Z"), .enable("false")) multiplexer_16 (
    .in0({adder_2_out_2, EX_IR[25:0], 2'b00}), .in1(EX_A), .out(JmpPC), .sel(EX_JR));
  RAM #(.addrWidth(10), .dataWidth(32), .bus("separate"), .Select("high")) ram_1 (
    .addr(\扩展ex_mem_1_alu_2 [11:2]), .din(MDin), .data(ram_1_data), .str(MemWrite), .clk(CLK));  // open: sel, ld, clr
  \扩展MEM_WB  \u_扩展mem_wb_1  (
    .Halt(\扩展ex_mem_1_halt_2 ), .Halt_2(Halt), .W_num(MEM_rW), .W_num_2(WB_rW),
    .MemToReg(\扩展ex_mem_1_memtoreg_2 ), .MemToReg_2(WB_MemToReg), .RegWrite(MEM_RegWrite),
    .RegWrite_2(RegWrite), .JAL(\扩展ex_mem_1_jal_2 ), .JAL_2(\扩展mem_wb_1_jal_2 ), .LB(\扩展ex_mem_1_lb_2 ),
    .LB_2(\扩展mem_wb_1_lb_2 ), .LUI(\扩展ex_mem_1_lui_2 ), .LUI_2(\扩展mem_wb_1_lui_2 ), .IR(MEM_IR),
    .IR_2(WB_IR), .PC(M_PC), .PC_2(WB_PC), .ALU(\扩展ex_mem_1_alu_2 ),
    .ALU_2({\扩展mem_wb_1_alu_2_2 , \扩展mem_wb_1_alu_2 }), .MD(ram_1_data),
    .MD_2({\扩展mem_wb_1_md_2_4 , \扩展mem_wb_1_md_2_3 , \扩展mem_wb_1_md_2_2 , \扩展mem_wb_1_md_2 }),
    .Imm(\扩展ex_mem_1_imm_2 ), .Imm_2(\扩展mem_wb_1_imm_2 ), .En(or_2_out), .Clk(CLK),
    .ERET(\扩展ex_mem_1_eret_2 ), .ERET_2(WB_ERET));  // open: Clr
  Multiplexer #(.select(2), .width(8), .disabled("Z"), .enable("false")) multiplexer_17 (
    .in0(\扩展mem_wb_1_md_2 ), .in1(\扩展mem_wb_1_md_2_2 ), .in2(\扩展mem_wb_1_md_2_3 ), .in3(\扩展mem_wb_1_md_2_4 ),
    .out(multiplexer_17_out), .sel(\扩展mem_wb_1_alu_2 ));
  Multiplexer #(.select(1), .width(32), .disabled("Z"), .enable("false")) multiplexer_18 (
    .in0({\扩展mem_wb_1_md_2_4 , \扩展mem_wb_1_md_2_3 , \扩展mem_wb_1_md_2_2 , \扩展mem_wb_1_md_2 }),
    .in1(bit_extender_3_out), .out(multiplexer_18_out), .sel(\扩展mem_wb_1_lb_2 ));
  assign bit_extender_3_out = {{24{multiplexer_17_out[7]}}, multiplexer_17_out};  // Bit_Extender bit_extender_3
  Multiplexer #(.select(1), .width(32), .disabled("Z"), .enable("false")) multiplexer_19 (
    .in0({\扩展mem_wb_1_alu_2_2 , \扩展mem_wb_1_alu_2 }), .in1(multiplexer_18_out), .out(multiplexer_19_out),
    .sel(WB_MemToReg));
  Multiplexer #(.select(1), .width(32), .disabled("Z"), .enable("false")) multiplexer_20 (
    .in0(multiplexer_19_out), .in1(\扩展mem_wb_1_imm_2 ), .out(multiplexer_20_out), .sel(\扩展mem_wb_1_lui_2 ));
  Multiplexer #(.select(1), .width(32), .disabled("Z"), .enable("false")) multiplexer_21 (
    .in0(multiplexer_20_out), .in1(adder_4_out), .out(RDin), .sel(\扩展mem_wb_1_jal_2 ));
  Adder #(.width(32)) adder_4 (.a(WB_PC), .b(32'h4), .out(adder_4_out));  // open: cin, cout

  // Other names for the same wires on the sheet: IR[31:0] = IF_IR; MEM_MemWrite = MemWrite; MEM_PC[31:0] = M_PC;
  //   Stall = LoadUse; WB_RegWrite = RegWrite

  // Notes on the sheet:
  //   中断源
  //   时空图监测，可删除
  //   中断等待指示
  //   数码管输出
  //   rt
  //   OP
  //   Func
  //   rs
  //   contents of rom_1 (hex, n*v repeats v):
  //   201d07d0 20100001 109fc0 139fc3 8021 2012000c 24160008 26100001 3210000f 20080008 20090001 139900
  //   2709825 132020 20020022 c 1094022 1500fff9 22100001 2018000f 2188024 108700 20080008 20090001 139902
  //   2709825 132021 20020022 c 1094022 1500fff9 108702 2c9b022 12c00001 8000c07 4020 1084027 84400
  //   3508ffff 82021 20020022 c 8000c01 afa20000 23bd0004 afa40000 23bd0004 afb00000 23bd0004 afb30000
  //   23bd0004 afb40000 23bd0004 afb50000 23bd0004 afb60000 23bd0004 20160001 20140003 20150001 168020
  //   108100 2149825 132020 20020022 c 1600fffa 295a022 1680fff7 23bdfffc 8fb60000 23bdfffc 8fb50000
  //   23bdfffc 8fb40000 23bdfffc 8fb30000 23bdfffc 8fb00000 23bdfffc 8fa40000 23bdfffc 8fa20000 42000018
  //   afa20000 23bd0004 afa40000 23bd0004 afb00000 23bd0004 afb30000 23bd0004 afb40000 23bd0004 afb50000
  //   23bd0004 afb60000 23bd0004 20160002 20140003 20150001 168020 108100 2149825 132020 20020022 c
  //   1600fffa 295a022 1680fff7 23bdfffc 8fb60000 23bdfffc 8fb50000 23bdfffc 8fb40000 23bdfffc 8fb30000
  //   23bdfffc 8fb00000 23bdfffc 8fa40000 23bdfffc 8fa20000 42000018 afa20000 23bd0004 afa40000 23bd0004
  //   afb00000 23bd0004 afb30000 23bd0004 afb40000 23bd0004 afb50000 23bd0004 afb60000 23bd0004 20160003
  //   20140003 20150001 168020 108100 2149825 132020 20020022 c 1600fffa 295a022 1680fff7 23bdfffc
  //   8fb60000 23bdfffc 8fb50000 23bdfffc 8fb40000 23bdfffc 8fb30000 23bdfffc 8fb00000 23bdfffc 8fa40000
  //   23bdfffc 8fa20000 42000018
  //   OP
  //   Func
  //   rd
  //   rs
  //   rt
  //   imm
  //   流水调试日志用
  //   v0
  //   rs
  //   rt
  //   a0
  //   为方便自动评测，需要输出流水线各段保存的PC值，注意是PC不是PC+4，另外ID段寄存器写入信息，Mem段内存写入信息也要输出
  //   sa
  //   instr_index
endmodule

module \重定向流水线_动态分支预测  (
  output RegWrite,
  output MemWrite,
  output [31:0] IF_PC,
  output [31:0] ID_PC,
  output [31:0] EX_PC,
  output [31:0] M_PC,
  output [31:0] WB_PC,
  output [31:0] RDin,
  output [31:0] MDin,
  output [31:0] LedData
);

  wire AluSrcB, and_1_out, and_2_out, and_4_out, and_7_out, and_8_out, and_9_out, and_11_out, and_12_out,
       and_13_out, and_14_out, and_15_out, Beq, BLTZ, Bne, BranchSuccess, CLK, Clr, comparator_1_eq,
       comparator_2_eq, d_ff_1_q, EX_AluEq, EX_Beq, EX_BLTZ, EX_Bne, EX_Branch, EX_Hit, EX_JMP, EX_JR,
       EX_MemToReg, EX_RegWrite, EX_RsRead, EX_RtRead, EX_Syscall, Go, Halt, Hit, IF_ID_q, IF_Run, IR1, IR2,
       IR3, JAL, JMP, JR, LB, LoadUse, LUI, MEM_RegWrite, MemToReg, MemWrite_t, multiplexer_5_out,
       multiplexer_6_out, not_1_out, or_2_out, or_3_out, or_6_out, or_7_out, or_8_out, or_9_out, RegDst,
       RegWrite_t, RST, Run, SignedExt, Syscall, W1, W2, W3, WB_MemToReg, Wrong, \扩展ex_mem_1_halt_2 ,
       \扩展ex_mem_1_jal_2 , \扩展ex_mem_1_lb_2 , \扩展ex_mem_1_lui_2 , \扩展ex_mem_1_memtoreg_2 ,
       \扩展id_ex_1_alusrcb_2 , \扩展id_ex_1_jal_2 , \扩展id_ex_1_lb_2 , \扩展id_ex_1_lui_2 , \扩展id_ex_1_memwrite_2 ,
       \扩展mem_wb_1_jal_2 , \扩展mem_wb_1_lb_2 , \扩展mem_wb_1_lui_2 , \数据相关测试2_1_hazarda , \数据相关测试2_1_hazardb ,
       \数据相关测试2_2_hazarda , \数据相关测试2_2_hazardb , \数据相关测试_1_hazard ;
  wire [1:0] and_3_out, ForwardA, ForwardB, multiplexer_9_out, regread_1_rsread;
  wire [3:0] adder_3_out_2, AluOP, \扩展id_ex_1_aluop_2 ;
  wire [4:0] EX_rW, MEM_rW, multiplexer_7_out, multiplexer_8_out, multiplexer_10_out, multiplexer_11_out,
       WB_rW;
  wire [7:0] multiplexer_18_out;
  wire [15:0] \LoadUse次数 , \总周期数 , \插入气泡数 , \无条件分支数 , \条件分支成功数 ;
  wire [27:0] adder_3_out;
  wire [31:0] adder_1_out, adder_2_out, adder_5_out, bit_extender_1_out, bit_extender_2_out,
       bit_extender_3_out, BranchPC, EX_A, EX_Alu, EX_B, EX_Imm, EX_IR, ID_IR, IF_IR, JmpPC, MEM_IR,
       multiplexer_1_out, multiplexer_2_out, multiplexer_3_out, multiplexer_4_out, multiplexer_12_out,
       multiplexer_13_out, multiplexer_16_out, multiplexer_19_out, multiplexer_20_out, multiplexer_21_out,
       PredictPC, ram_1_data, registerfile_1_p7, registerfile_1_p8, shifter_1_out, WB_IR, \扩展ex_mem_1_alu_2 ,
       \扩展ex_mem_1_imm_2 , \扩展id_ex_1_a_2 , \扩展id_ex_1_b_2 , \扩展mem_wb_1_alu_2 , \扩展mem_wb_1_imm_2 ,
       \扩展mem_wb_1_md_2 ;

  Button \u_总复位  (.out(RST));
  Button _1 (.out(IR1));
  Button _2 (.out(IR2));
  Button _3 (.out(IR3));
  // Probe on \总周期数 
  Button \u_继续运行  (.out(Go));
  LED #(.active("true")) led_1 (.in(W1));
  LED #(.active("true")) led_2 (.in(W2));
  LED #(.active("true")) led_3 (.in(W3));
  // Probe on IF_PC
  Hex_Digit_Display hex_digit_display_1 (.value(LedData[31:28]));  // open: dp
  Hex_Digit_Display hex_digit_display_2 (.value(LedData[27:24]));  // open: dp
  Hex_Digit_Display hex_digit_display_3 (.value(LedData[23:20]));  // open: dp
  // Probe on ID_PC
  Hex_Digit_Display hex_digit_display_4 (.value(LedData[15:12]));  // open: dp
  Hex_Digit_Display hex_digit_display_5 (.value(LedData[19:16]));  // open: dp
  Hex_Digit_Display hex_digit_display_6 (.value(LedData[7:4]));  // open: dp
  Hex_Digit_Display hex_digit_display_7 (.value(LedData[11:8]));  // open: dp
  Clock #(.highDuration(1), .lowDuration(1)) clock_1 (.out(CLK));
  // Probe on EX_PC
  Multiplexer #(.select(1), .width(32), .disabled("Z"), .enable("false")) multiplexer_1 (
    .in0(BranchPC), .in1(JmpPC), .out(multiplexer_1_out), .sel(EX_JMP));
  Hex_Digit_Display hex_digit_display_8 (.value(LedData[3:0]));  // open: dp
  Multiplexer #(.select(1), .width(32), .disabled("Z"), .enable("false")) multiplexer_2 (
    .in0(adder_2_out), .in1(PredictPC), .out(multiplexer_2_out), .sel(Hit));
  Adder #(.width(32)) adder_1 (.a(EX_PC), .b(32'h4), .out(adder_1_out));  // open: cin, cout
  // Probe on M_PC
  and and_1 (and_1_out, Wrong, EX_Branch);
  or or_1 (and_3_out[1], and_1_out, and_2_out);
  and and_2 (and_2_out, ~EX_Hit, BranchSuccess);  // AND_Gate
  or or_2 (or_2_out, Wrong, ~EX_Hit);  // OR_Gate
  and and_3 (and_3_out[0], or_2_out, EX_JMP);
  Multiplexer #(.select(1), .width(32), .disabled("Z"), .enable("false")) multiplexer_3 (
    .in0(BranchPC), .in1(adder_1_out), .out(multiplexer_3_out), .sel(Wrong));
  or or_3 (or_3_out, EX_JMP, BranchSuccess);
  BTB btb_1 (
    .IndexPC(IF_PC), .UpdatePC(EX_PC), .inData(multiplexer_1_out), .Delete(Wrong), .Write(and_7_out),
    .Clk(CLK), .Data(PredictPC), .Hit(Hit));
  // Probe on \总周期数 
  // Probe on \无条件分支数 
  // Probe on \条件分支成功数 
  // Probe on \插入气泡数 
  // Probe on \LoadUse次数 
  // Probe on IF_PC
  // Probe on ID_PC
  // Probe on EX_PC
  // Probe on M_PC
  // Probe on WB_PC
  Multiplexer #(.select(2), .width(32), .disabled("Z"), .enable("false")) multiplexer_4 (
    .in0(multiplexer_2_out), .in1(JmpPC), .in2(multiplexer_3_out), .out(multiplexer_4_out), .sel(and_3_out));  // open: in3
  or or_4 (Clr, Wrong, and_4_out);
  and and_4 (and_4_out, ~EX_Hit, or_3_out);  // AND_Gate
  // Probe on IF_PC[11:0]
  // Probe on WB_PC
  D_Flip_Flop #(.trigger("rising"), .Pre_Clr_Positions("LEGACY"), .NegatePresetClear("false"), .enable("true"), .NewFFLayout("false")) d_ff_1 (
    .clk(CLK), .D(1'b0), .Q(d_ff_1_q), .preset(Go));  // open: Qn, en, reset
  or or_5 (Run, ~Halt, d_ff_1_q);  // OR_Gate
  Register #(.width(32), .trigger("rising"), .Select("low")) PC (
    .D(multiplexer_4_out), .en(IF_Run), .Q(IF_PC), .clk(CLK));  // open: clr
  and and_5 (IF_Run, Run, ~LoadUse);  // AND_Gate
  Multiplexer #(.select(1), .width(1), .disabled("Z"), .enable("false")) multiplexer_5 (
    .in0(Hit), .in1(1'b0), .out(multiplexer_5_out), .sel(Clr));
  // Probe on ID_PC[11:0]
  // Probe on EX_PC[11:0]
  Adder #(.width(32)) adder_2 (.a(IF_PC), .b(32'h4), .out(adder_2_out));  // open: cin, cout
  Register #(.width(1), .trigger("rising"), .Select("low")) IF_ID (
    .D(multiplexer_5_out), .en(IF_Run), .Q(IF_ID_q), .clk(CLK));  // open: clr
  // Probe on M_PC[11:0]
  // Probe on IF_IR
  // Probe on ID_IR
  // Probe on EX_IR
  // Probe on MEM_IR
  // Probe on WB_IR
  or or_6 (or_6_out, Clr, LoadUse);
  // Probe on WB_PC[11:0]
  ROM #(.addrWidth(10), .dataWidth(32), .Select("high")) rom_1 (.addr(IF_PC[11:2]), .data(IF_IR));
  RegRead regread_1 (
    .OP0(ID_IR[26]), .OP1(ID_IR[27]), .OP2(ID_IR[28]), .OP3(ID_IR[29]), .OP4(ID_IR[30]), .OP5(ID_IR[31]),
    .F0(ID_IR[0]), .F1(ID_IR[1]), .F2(ID_IR[2]), .F3(ID_IR[3]), .F4(ID_IR[4]), .F5(ID_IR[5]),
    .RsRead(regread_1_rsread[0]), .RtRead(regread_1_rsread[1]));
  Multiplexer #(.select(1), .width(1), .disabled("Z"), .enable("false")) multiplexer_6 (
    .in0(IF_ID_q), .in1(1'b0), .out(multiplexer_6_out), .sel(or_6_out));
  \扩展IF_ID  \u_扩展if_id_1  (.IR(IF_IR), .PC(IF_PC), .IR_2(ID_IR), .PC_2(ID_PC), .En(IF_Run), .Clk(CLK), .Clr(Clr));
  Register #(.width(1), .trigger("rising"), .Select("low")) ID_EX (
    .D(multiplexer_6_out), .en(Run), .Q(EX_Hit), .clk(CLK));  // open: clr
  \数据相关测试  \u_数据相关测试_1  (
    .RsRead(regread_1_rsread[0]), .Rs(ID_IR[25:21]), .RtRead(regread_1_rsread[1]), .Rt(ID_IR[20:16]),
    .Rw(EX_rW), .RegWrite(EX_RegWrite), .Syscall(Syscall), .Hazard(\数据相关测试_1_hazard ));
  Comparator #(.width(32), .mode("unsigned")) comparator_1 (
    .a(JmpPC), .b(ID_PC), .eq(comparator_1_eq));  // open: gt, lt
  \扩展单周期硬布线控制器  \u_扩展单周期硬布线控制器_1  (
    .OP(ID_IR[31:26]), .Func(ID_IR[5:0]), .ALU_OP(AluOP), .MemToReg(MemToReg), .MemWrite(MemWrite_t),
    .ALU_SRC(AluSrcB), .RegWrite(RegWrite_t), .SysCALL(Syscall), .SignedExt(SignedExt), .RegDst(RegDst),
    .Beq(Beq), .Bne(Bne), .JR(JR), .JMP(JMP), .JAL(JAL), .LUI(LUI), .LB(LB), .BLTZ(BLTZ));  // open: ERET
  Multiplexer #(.select(1), .width(5), .disabled("Z"), .enable("false")) multiplexer_7 (
    .in0(ID_IR[20:16]), .in1(ID_IR[15:11]), .out(multiplexer_7_out), .sel(RegDst));
  and and_6 (LoadUse, EX_MemToReg, \数据相关测试_1_hazard );
  and and_7 (and_7_out, ~EX_Hit, or_7_out);  // AND_Gate
  or or_7 (or_7_out, BranchSuccess, EX_JMP);
  and and_8 (and_8_out, ~comparator_1_eq, EX_JMP);  // AND_Gate
  and and_9 (and_9_out, ~BranchSuccess, EX_Branch);  // AND_Gate
  Multiplexer #(.select(1), .width(5), .disabled("Z"), .enable("false")) multiplexer_8 (
    .in0(multiplexer_7_out), .in1({5{1'b1}}), .out(multiplexer_8_out), .sel(JAL));
  and and_10 (Wrong, EX_Hit, or_8_out);
  or or_8 (or_8_out, and_8_out, and_9_out);
  not not_1 (not_1_out, Halt);
  assign bit_extender_1_out = {{16{1'b0}}, ID_IR[15:0]};  // Bit_Extender bit_extender_1
  assign bit_extender_2_out = {{16{ID_IR[15]}}, ID_IR[15:0]};  // Bit_Extender bit_extender_2
  Multiplexer #(.select(1), .width(2), .disabled("Z"), .enable("false")) multiplexer_9 (
    .in0(regread_1_rsread), .in1(2'b00), .out(multiplexer_9_out), .sel(or_9_out));
  Counter #(.width(16), .max('hffff), .ongoal("wrap"), .trigger("rising"), .behavior("old")) counter_1 (
    .count(not_1_out), .Q(\总周期数 ), .clk(CLK));  // open: load, D, carry, clr, preset
  Multiplexer #(.select(1), .width(5), .disabled("Z"), .enable("false")) multiplexer_10 (
    .in0(ID_IR[25:21]), .in1(5'b00010), .out(multiplexer_10_out), .sel(Syscall));
  Multiplexer #(.select(1), .width(5), .disabled("Z"), .enable("false")) multiplexer_11 (
    .in0(ID_IR[20:16]), .in1(5'b00100), .out(multiplexer_11_out), .sel(Syscall));
  Multiplexer #(.select(1), .width(32), .disabled("Z"), .enable("false")) multiplexer_12 (
    .in0(bit_extender_1_out), .in1(bit_extender_2_out), .out(multiplexer_12_out), .sel(SignedExt));
  Multiplexer #(.select(1), .width(32), .disabled("Z"), .enable("false")) multiplexer_13 (
    .in0(multiplexer_12_out), .in1({ID_IR[15:0], {16{1'b0}}}), .out(multiplexer_13_out), .sel(LUI));
  Register #(.width(2), .trigger("rising"), .Select("low")) ID_EX_2 (
    .D(multiplexer_9_out), .en(Run), .Q({EX_RtRead, EX_RsRead}), .clk(CLK));  // open: clr
  // RegisterFile registerfile_1: pin names not known; wires that end beside it: RDin, CLK, RegWrite, WB_rW, multiplexer_10_out, multiplexer_11_out, registerfile_1_p7, registerfile_1_p8
  \数据相关测试2  \u_数据相关测试2_1  (
    .RsRead(EX_RsRead), .Rs(EX_IR[25:21]), .RtRead(EX_RtRead), .Rt(EX_IR[20:16]), .Rw(MEM_rW),
    .RegWrite(MEM_RegWrite), .Syscall(EX_Syscall), .HazardA(\数据相关测试2_1_hazarda ),
    .HazardB(\数据相关测试2_1_hazardb ));
  \数据相关测试2  \u_数据相关测试2_2  (
    .RsRead(EX_RsRead), .Rs(EX_IR[25:21]), .RtRead(EX_RtRead), .Rt(EX_IR[20:16]), .Rw(WB_rW),
    .RegWrite(RegWrite), .Syscall(EX_Syscall), .HazardA(\数据相关测试2_2_hazarda ), .HazardB(\数据相关测试2_2_hazardb ));
  Comparator #(.width(32), .mode("twosComplement")) comparator_2 (
    .a(EX_A), .b(32'h32), .eq(comparator_2_eq));  // open: gt, lt
  Forward forward_1 (
    .HazardA(\数据相关测试2_1_hazarda ), .HazardB(\数据相关测试2_2_hazarda ), .MemToReg(WB_MemToReg), .out_4(ForwardA));
  Forward forward_2 (
    .HazardA(\数据相关测试2_1_hazardb ), .HazardB(\数据相关测试2_2_hazardb ), .MemToReg(WB_MemToReg), .out_4(ForwardB));
  and and_11 (and_11_out, comparator_2_eq, EX_Syscall);
  \扩展ID_EX  \u_扩展id_ex_1  (
    .Syscall(Syscall), .W_num(multiplexer_8_out), .MemToReg(MemToReg), .RegWrite(RegWrite_t), .JAL(JAL),
    .LB(LB), .LUI(LUI), .MemWrite(MemWrite_t), .AluOP(AluOP), .AluSrcB(AluSrcB), .Beq(Beq), .Bne(Bne),
    .JMP(JMP), .JR(JR), .BLTZ(BLTZ), .IR(ID_IR), .PC(ID_PC), .A(registerfile_1_p7), .B(registerfile_1_p8),
    .Imm(multiplexer_13_out), .Syscall_2(EX_Syscall), .W_num_2(EX_rW), .MemToReg_2(EX_MemToReg),
    .RegWrite_2(EX_RegWrite), .JAL_2(\扩展id_ex_1_jal_2 ), .LB_2(\扩展id_ex_1_lb_2 ), .LUI_2(\扩展id_ex_1_lui_2 ),
    .MemWrite_2(\扩展id_ex_1_memwrite_2 ), .AluOP_2(\扩展id_ex_1_aluop_2 ), .AluSrcB_2(\扩展id_ex_1_alusrcb_2 ),
    .Beq_2(EX_Beq), .Bne_2(EX_Bne), .JMP_2(EX_JMP), .JR_2(EX_JR), .BLTZ_2(EX_BLTZ), .IR_2(EX_IR),
    .PC_2(EX_PC), .A_2(\扩展id_ex_1_a_2 ), .B_2(\扩展id_ex_1_b_2 ), .Imm_2(EX_Imm), .En(Run), .Clk(CLK),
    .Clr(or_9_out));  // open: ERET, ERET_2
  or or_9 (or_9_out, Clr, LoadUse);
  and and_12 (and_12_out, ~comparator_2_eq, EX_Syscall);  // AND_Gate
  Register #(.width(32), .trigger("rising"), .Select("low")) register_1 (
    .D(EX_B), .en(and_12_out), .Q(LedData), .clk(CLK));  // open: clr
  Multiplexer #(.select(2), .width(32), .disabled("Z"), .enable("false")) multiplexer_14 (
    .in0(\扩展id_ex_1_a_2 ), .in1(multiplexer_20_out), .in2(\扩展mem_wb_1_alu_2 ), .in3(\扩展ex_mem_1_alu_2 ),
    .out(EX_A), .sel(ForwardA));
  and and_13 (and_13_out, EX_AluEq, EX_Beq);
  and and_14 (and_14_out, ~EX_AluEq, EX_Bne);  // AND_Gate
  and and_15 (and_15_out, EX_Alu[0], EX_BLTZ);
  Multiplexer #(.select(2), .width(32), .disabled("Z"), .enable("false")) multiplexer_15 (
    .in0(\扩展id_ex_1_b_2 ), .in1(multiplexer_20_out), .in2(\扩展mem_wb_1_alu_2 ), .in3(\扩展ex_mem_1_alu_2 ),
    .out(EX_B), .sel(ForwardB));
  or or_10 (BranchSuccess, and_13_out, and_14_out, and_15_out);
  or or_11 (EX_Branch, EX_Bne, EX_Beq, EX_BLTZ);
  Multiplexer #(.select(1), .width(32), .disabled("Z"), .enable("false")) multiplexer_16 (
    .in0(EX_B), .in1(EX_Imm), .out(multiplexer_16_out), .sel(\扩展id_ex_1_alusrcb_2 ));
  MIPS_ALU mips_alu_1 (
    .X(EX_A), .Y(multiplexer_16_out), .AluOP(\扩展id_ex_1_aluop_2 ), .Equal(EX_AluEq), .Result(EX_Alu),
    .shamt(EX_IR[10:6]));  // open: Result_2
  \扩展EX_MEM  \u_扩展ex_mem_1  (
    .Halt(and_11_out), .Halt_2(\扩展ex_mem_1_halt_2 ), .W_num(EX_rW), .W_num_2(MEM_rW), .MemToReg(EX_MemToReg),
    .MemToReg_2(\扩展ex_mem_1_memtoreg_2 ), .RegWrite(EX_RegWrite), .RegWrite_2(MEM_RegWrite),
    .JAL(\扩展id_ex_1_jal_2 ), .JAL_2(\扩展ex_mem_1_jal_2 ), .LB(\扩展id_ex_1_lb_2 ), .LB_2(\扩展ex_mem_1_lb_2 ),
    .LUI(\扩展id_ex_1_lui_2 ), .LUI_2(\扩展ex_mem_1_lui_2 ), .MemWrite(\扩展id_ex_1_memwrite_2 ),
    .MemWrite_2(MemWrite), .IR(EX_IR), .IR_2(MEM_IR), .PC(EX_PC), .PC_2(M_PC), .ALU(EX_Alu),
    .ALU_2(\扩展ex_mem_1_alu_2 ), .B(EX_B), .B_2(MDin), .Imm(EX_Imm), .Imm_2(\扩展ex_mem_1_imm_2 ), .En(Run),
    .Clk(CLK));  // open: Clr, ERET, ERET_2
  Adder #(.width(32)) adder_3 (.a(EX_PC), .b(32'h4), .out({adder_3_out_2, adder_3_out}));  // open: cin, cout
  Shifter #(.width(32), .shift("ll")) shifter_1 (.in(EX_Imm), .\dist (5'b00010), .out(shifter_1_out));
  Adder #(.width(32)) adder_4 (.a(shifter_1_out), .b({adder_3_out_2, adder_3_out}), .out(BranchPC));  // open: cin, cout
  Multiplexer #(.select(1), .width(32), .disabled("Z"), .enable("false")) multiplexer_17 (
    .in0({adder_3_out_2, EX_IR[25:0], 2'b00}), .in1(EX_A), .out(JmpPC), .sel(EX_JR));
  RAM #(.addrWidth(10), .dataWidth(32), .bus("separate"), .Select("high")) ram_1 (
    .addr(\扩展ex_mem_1_alu_2 [11:2]), .din(MDin), .data(ram_1_data), .str(MemWrite), .clk(CLK));  // open: sel, ld, clr
  \扩展MEM_WB  \u_扩展mem_wb_1  (
    .Halt(\扩展ex_mem_1_halt_2 ), .Halt_2(Halt), .W_num(MEM_rW), .W_num_2(WB_rW),
    .MemToReg(\扩展ex_mem_1_memtoreg_2 ), .MemToReg_2(WB_MemToReg), .RegWrite(MEM_RegWrite),
    .RegWrite_2(RegWrite), .JAL(\扩展ex_mem_1_jal_2 ), .JAL_2(\扩展mem_wb_1_jal_2 ), .LB(\扩展ex_mem_1_lb_2 ),
    .LB_2(\扩展mem_wb_1_lb_2 ), .LUI(\扩展ex_mem_1_lui_2 ), .LUI_2(\扩展mem_wb_1_lui_2 ), .IR(MEM_IR),
    .IR_2(WB_IR), .PC(M_PC), .PC_2(WB_PC), .ALU(\扩展ex_mem_1_alu_2 ), .ALU_2(\扩展mem_wb_1_alu_2 ),
    .MD(ram_1_data), .MD_2(\扩展mem_wb_1_md_2 ), .Imm(\扩展ex_mem_1_imm_2 ), .Imm_2(\扩展mem_wb_1_imm_2 ),
    .En(Run), .Clk(CLK));  // open: Clr, ERET, ERET_2
  Multiplexer #(.select(2), .width(8), .disabled("Z"), .enable("false")) multiplexer_18 (
    .in0(\扩展mem_wb_1_md_2 [7:0]), .in1(\扩展mem_wb_1_md_2 [15:8]), .in2(\扩展mem_wb_1_md_2 [23:16]),
    .in3(\扩展mem_wb_1_md_2 [31:24]), .out(multiplexer_18_out), .sel(\扩展mem_wb_1_alu_2 [1:0]));
  assign bit_extender_3_out = {{24{multiplexer_18_out[7]}}, multiplexer_18_out};  // Bit_Extender bit_extender_3
  Multiplexer #(.select(1), .width(32), .disabled("Z"), .enable("false")) multiplexer_19 (
    .in0(\扩展mem_wb_1_alu_2 ), .in1(multiplexer_20_out), .out(multiplexer_19_out), .sel(WB_MemToReg));
  Multiplexer #(.select(1), .width(32), .disabled("Z"), .enable("false")) multiplexer_20 (
    .in0(\扩展mem_wb_1_md_2 ), .in1(bit_extender_3_out), .out(multiplexer_20_out), .sel(\扩展mem_wb_1_lb_2 ));
  Multiplexer #(.select(1), .width(32), .disabled("Z"), .enable("false")) multiplexer_21 (
    .in0(multiplexer_19_out), .in1(\扩展mem_wb_1_imm_2 ), .out(multiplexer_21_out), .sel(\扩展mem_wb_1_lui_2 ));
  Adder #(.width(32)) adder_5 (.a(WB_PC), .b(32'h4), .out(adder_5_out));  // open: cin, cout
  Multiplexer #(.select(1), .width(32), .disabled("Z"), .enable("false")) multiplexer_22 (
    .in0(multiplexer_21_out), .in1(adder_5_out), .out(RDin), .sel(\扩展mem_wb_1_jal_2 ));

  // Other names for the same wires on the sheet: IR[31:0] = IF_IR; MEM_MemWrite = MemWrite; MEM_PC[31:0] = M_PC;
  //   Stall = LoadUse; WB_RegWrite = RegWrite

  // Notes on the sheet:
  //   中断源
  //   时空图监测，可删除
  //   中断等待指示
  //   数码管输出
  //   OP
  //   Func
  //   rs
  //   rt
  //   流水调试日志用
  //   contents of rom_1 (hex, n*v repeats v):
  //   20110001 8000c05 20110001 20120002 20130003 8000c09 20110001 20120002 20130003 8000c0d 20110001
  //   20120002 20130003 8000c11 20110001 20120002 20130003 c000cb8 20100001 20110001 118fc0 112020
  //   20020022 c 118882 12200001 8000c15 112020 20020022 c 20110001 118880 112020 20020022 c 12200001
  //   8000c1f 20110001 118fc0 112020 20020022 c 1188c3 112020 20020022 c 118903 112020 20020022 c 118903
  //   112020 20020022 c 118903 112020 20020022 c 118903 112020 20020022 c 118903 112020 20020022 c 118903
  //   112020 20020022 c 118903 112020 20020022 c 20100001 109fc0 139fc3 8021 2012000c 24160003 26100001
  //   3210000f 20080008 20090001 139900 2709825 132020 20020022 c 1094022 1500fff9 22100001 2018000f
  //   2188024 108700 20080008 20090001 139902 2709825 132021 20020022 c 1094022 1500fff9 108702 2c9b022
  //   12c00001 8000c50 4020 1084027 84400 3508ffff 82021 20020022 c 2010ffff 20110000 ae300000 22100001
  //   22310004 ae300000 22100001 22310004 ae300000 22100001 22310004 ae300000 22100001 22310004 ae300000
  //   22100001 22310004 ae300000 22100001 22310004 ae300000 22100001 22310004 ae300000 22100001 22310004
  //   ae300000 22100001 22310004 ae300000 22100001 22310004 ae300000 22100001 22310004 ae300000 22100001
  //   22310004 ae300000 22100001 22310004 ae300000 22100001 22310004 ae300000 22100001 22310004 ae300000
  //   22100001 22310004 22100001 8020 2011003c 8e130000 8e340000 274402a 11000002 ae330000 ae140000
  //   2231fffc 1611fff8 102020 20020022 c 22100004 2011003c 1611fff2 20020032 c 20100000 22100001 102020
  //   20020022 c 22100002 102020 20020022 c 22100003 102020 20020022 c 22100004 102020 20020022 c 22100005
  //   102020 20020022 c 22100006 102020 20020022 c 22100007 102020 20020022 c 22100008 102020 20020022
  //   20020022 c 3e00008
  //   OP
  //   Func
  //   rd
  //   rs
  //   rt
  //   imm
  //   rs
  //   rt
  //   v0
  //   a0
  //   为方便自动评测，需要输出流水线各段保存的PC值，注意是PC不是PC+4，另外ID段寄存器写入信息，Mem段内存写入信息也要输出
  //   sa
  //   instr_index
endmodule

module BTB (
  input  [31:0] IndexPC,
  input  [31:0] UpdatePC,
  input  [31:0] inData,
  input  Delete,
  input  Write,
  input  Clk,
  output [31:0] Data,
  output Hit
);

  wire comparator_1_eq, comparator_2_eq, comparator_3_eq, comparator_4_eq, comparator_5_eq, comparator_6_eq,
       comparator_7_eq, comparator_8_eq, decoder_1_out0, decoder_1_out1, decoder_1_out2, decoder_1_out3,
       DWire0, DWire1, DWire2, DWire3, L0, L1, L2, L3, multiplexer_1_out, multiplexer_2_out,
       multiplexer_3_out, multiplexer_4_out, not_1_out, not_2_out, not_3_out, not_4_out, not_5_out,
       not_6_out, not_7_out, not_8_out, or_2_out, or_3_out, or_4_out, or_5_out, priority_encoder_1_en_out,
       V0, V1, V2, V3, Wire0, Wire1, Wire2, Wire3, WWire0, WWire1, WWire2, WWire3;
  wire [1:0] max2_1_max_num, max2_2_max_num, max2_3_max_num, multiplexer_5_out, priority_encoder_1_out;
  wire [15:0] Count0, Count1, Count2, Count3, max2_1_max, max2_2_max;
  wire [31:0] Data_2_q, Data_3_q, Data_4_q, Data_q, Index0, Index1, Index2, Index3;

  Multiplexer #(.select(1), .width(1), .disabled("Z"), .enable("false")) multiplexer_1 (
    .in0(1'b1), .in1(1'b0), .out(multiplexer_1_out), .sel(Delete));
  Multiplexer #(.select(1), .width(1), .disabled("Z"), .enable("false")) multiplexer_2 (
    .in0(1'b1), .in1(1'b0), .out(multiplexer_2_out), .sel(Delete));
  Multiplexer #(.select(1), .width(1), .disabled("Z"), .enable("false")) multiplexer_3 (
    .in0(1'b1), .in1(1'b0), .out(multiplexer_3_out), .sel(Delete));
  Multiplexer #(.select(1), .width(1), .disabled("Z"), .enable("false")) multiplexer_4 (
    .in0(1'b1), .in1(1'b0), .out(multiplexer_4_out), .sel(Delete));
  Register #(.width(1), .trigger("rising"), .Select("low")) Valid (
    .D(multiplexer_1_out), .en(Wire0), .Q(V0), .clk(Clk));  // open: clr
  Register #(.width(1), .trigger("rising"), .Select("low")) Valid_2 (
    .D(multiplexer_2_out), .en(Wire1), .Q(V1), .clk(Clk));  // open: clr
  Register #(.width(1), .trigger("rising"), .Select("low")) Valid_3 (
    .D(multiplexer_3_out), .en(Wire2), .Q(V2), .clk(Clk));  // open: clr
  Register #(.width(1), .trigger("rising"), .Select("low")) Valid_4 (
    .D(multiplexer_4_out), .en(Wire3), .Q(V3), .clk(Clk));  // open: clr
  and and_1 (L0, V0, comparator_1_eq);
  Comparator #(.width(32), .mode("unsigned")) comparator_1 (
    .a(IndexPC), .b(Index0), .eq(comparator_1_eq));  // open: gt, lt
  and and_2 (L1, V1, comparator_2_eq);
  Comparator #(.width(32), .mode("unsigned")) comparator_2 (
    .a(IndexPC), .b(Index1), .eq(comparator_2_eq));  // open: gt, lt
  and and_3 (L2, V2, comparator_3_eq);
  Comparator #(.width(32), .mode("unsigned")) comparator_3 (
    .a(IndexPC), .b(Index2), .eq(comparator_3_eq));  // open: gt, lt
  and and_4 (L3, V3, comparator_4_eq);
  Comparator #(.width(32), .mode("unsigned")) comparator_4 (
    .a(IndexPC), .b(Index3), .eq(comparator_4_eq));  // open: gt, lt
  Register #(.width(32), .trigger("rising"), .Select("low")) Index (
    .D(UpdatePC), .en(Wire0), .Q(Index0), .clk(Clk));  // open: clr
  Register #(.width(32), .trigger("rising"), .Select("low")) Index_2 (
    .D(UpdatePC), .en(Wire1), .Q(Index1), .clk(Clk));  // open: clr
  Register #(.width(32), .trigger("rising"), .Select("low")) Index_3 (
    .D(UpdatePC), .en(Wire2), .Q(Index2), .clk(Clk));  // open: clr
  Register #(.width(32), .trigger("rising"), .Select("low")) Index_4 (
    .D(UpdatePC), .en(Wire3), .Q(Index3), .clk(Clk));  // open: clr
  or or_1 (Hit, L0, L1, L2, L3);
  Register #(.width(32), .trigger("rising"), .Select("low")) u_Data (
    .D(inData), .en(Wire0), .Q(Data_q), .clk(Clk));  // open: clr
  assign Data = L0 ? Data_q : 32'bz;  // Controlled_Buffer controlled_buffer_1
  assign Data = L1 ? Data_2_q : 32'bz;  // Controlled_Buffer controlled_buffer_2
  Register #(.width(32), .trigger("rising"), .Select("low")) Data_2 (
    .D(inData), .en(Wire1), .Q(Data_2_q), .clk(Clk));  // open: clr
  assign Data = L2 ? Data_3_q : 32'bz;  // Controlled_Buffer controlled_buffer_3
  Register #(.width(32), .trigger("rising"), .Select("low")) Data_3 (
    .D(inData), .en(Wire2), .Q(Data_3_q), .clk(Clk));  // open: clr
  assign Data = L3 ? Data_4_q : 32'bz;  // Controlled_Buffer controlled_buffer_4
  Register #(.width(32), .trigger("rising"), .Select("low")) Data_4 (
    .D(inData), .en(Wire3), .Q(Data_4_q), .clk(Clk));  // open: clr
  or or_2 (or_2_out, L0, Wire0);
  or or_3 (or_3_out, L1, Wire1);
  or or_4 (or_4_out, L2, Wire2);
  or or_5 (or_5_out, L3, Wire3);
  not not_1 (not_1_out, or_2_out);
  not not_2 (not_2_out, or_3_out);
  not not_3 (not_3_out, or_4_out);
  not not_4 (not_4_out, or_5_out);
  not not_5 (not_5_out, V0);
  not not_6 (not_6_out, V1);
  not not_7 (not_7_out, V2);
  not not_8 (not_8_out, V3);
  Counter #(.width(16), .max('hffff), .ongoal("stay"), .trigger("rising"), .behavior("old")) Count (
    .load(or_2_out), .D({16{1'b0}}), .count(not_1_out), .Q(Count0), .clk(Clk));  // open: carry, clr, preset
  Counter #(.width(16), .max('hffff), .ongoal("stay"), .trigger("rising"), .behavior("old")) Count_2 (
    .load(or_3_out), .D({16{1'b0}}), .count(not_2_out), .Q(Count1), .clk(Clk));  // open: carry, clr, preset
  Counter #(.width(16), .max('hffff), .ongoal("stay"), .trigger("rising"), .behavior("old")) Count_3 (
    .load(or_4_out), .D({16{1'b0}}), .count(not_3_out), .Q(Count2), .clk(Clk));  // open: carry, clr, preset
  Counter #(.width(16), .max('hffff), .ongoal("stay"), .trigger("rising"), .behavior("old")) Count_4 (
    .load(or_5_out), .D({16{1'b0}}), .count(not_4_out), .Q(Count3), .clk(Clk));  // open: carry, clr, preset
  Priority_Encoder #(.select(2), .disabled("Z")) priority_encoder_1 (
    .in0(not_5_out), .in1(not_6_out), .in2(not_7_out), .in3(not_8_out), .out(priority_encoder_1_out),
    .en_out(priority_encoder_1_en_out));  // open: gs, en_in
  Max2 max2_1 (.Y(Count0), .X(Count1), .Y_num(2'b00), .X_num(2'b01), .MAX(max2_1_max), .MAX_num(max2_1_max_num));
  Max2 max2_2 (.Y(Count2), .X(Count3), .Y_num(2'b10), .X_num(2'b11), .MAX(max2_2_max), .MAX_num(max2_2_max_num));
  Comparator #(.width(32), .mode("unsigned")) comparator_5 (
    .a(UpdatePC), .b(Index0), .eq(comparator_5_eq));  // open: gt, lt
  Comparator #(.width(32), .mode("unsigned")) comparator_6 (
    .a(UpdatePC), .b(Index1), .eq(comparator_6_eq));  // open: gt, lt
  Comparator #(.width(32), .mode("unsigned")) comparator_7 (
    .a(UpdatePC), .b(Index2), .eq(comparator_7_eq));  // open: gt, lt
  Comparator #(.width(32), .mode("unsigned")) comparator_8 (
    .a(UpdatePC), .b(Index3), .eq(comparator_8_eq));  // open: gt, lt
  Max2 max2_3 (
    .Y(max2_1_max), .X(max2_2_max), .Y_num(max2_1_max_num), .X_num(max2_2_max_num), .MAX_num(max2_3_max_num));  // open: MAX
  and and_5 (DWire0, Delete, comparator_5_eq);
  and and_6 (DWire1, Delete, comparator_6_eq);
  and and_7 (DWire2, Delete, comparator_7_eq);
  and and_8 (DWire3, Delete, comparator_8_eq);
  Decoder #(.select(2), .tristate("false"), .disabled("Z"), .enable("false")) decoder_1 (
    .out0(decoder_1_out0), .out1(decoder_1_out1), .out2(decoder_1_out2), .out3(decoder_1_out3),
    .sel(multiplexer_5_out));
  Multiplexer #(.select(1), .width(2), .disabled("Z"), .enable("false")) multiplexer_5 (
    .in0(priority_encoder_1_out), .in1(max2_3_max_num), .out(multiplexer_5_out),
    .sel(priority_encoder_1_en_out));
  and and_9 (WWire3, Write, decoder_1_out3);
  and and_10 (WWire2, Write, decoder_1_out2);
  and and_11 (WWire1, Write, decoder_1_out1);
  and and_12 (WWire0, Write, decoder_1_out0);
  or or_6 (Wire0, DWire0, WWire0);
  or or_7 (Wire1, DWire1, WWire1);
  or or_8 (Wire2, DWire2, WWire2);
  or or_9 (Wire3, DWire3, WWire3);
endmodule

module Max2 (
  input  [15:0] Y,
  input  [15:0] X,
  input  [1:0] Y_num,
  input  [1:0] X_num,
  output [15:0] MAX,
  output [1:0] MAX_num
);

  wire comparator_1_eq, comparator_1_gt, or_1_out;

  Multiplexer #(.select(1), .width(16), .disabled("Z"), .enable("true")) multiplexer_1 (
    .in0(Y), .in1(X), .out(MAX), .sel(or_1_out), .en(1'b1));
  Comparator #(.width(16), .mode("unsigned")) comparator_1 (
    .a(X), .b(Y), .gt(comparator_1_gt), .eq(comparator_1_eq));  // open: lt
  or or_1 (or_1_out, comparator_1_gt, comparator_1_eq);
  Multiplexer #(.select(1), .width(2), .disabled("Z"), .enable("false")) multiplexer_2 (
    .in0(Y_num), .in1(X_num), .out(MAX_num), .sel(or_1_out));

  // Notes on the sheet:
  //   输出两个输入中的较大值，并输出较大值的2位编号
endmodule

module demo (
  input  in_1,
  input  \中断源 ,
  input  RST,
  output out_4,
  output out_5,
  output out_6,
  output enable,
  output [6:0] X,
  output CLK,
  output [6:0] Y,
  output RST_2,
  output [15:0] clolor
);

  wire ALU_SRC, and_1_out, and_2_out, and_3_out, and_4_out, and_5_out, and_6_out, and_7_out, and_9_out,
       and_10_out, and_12_out, and_14_out, Beq, Bne, comparator_3_gt, comparator_4_eq, comparator_5_eq,
       comparator_6_eq, d_ff_1_q, decoder_1_out1, decoder_1_out2, decoder_1_out3, down, Equal, ERET,
       Exception, Go, Halt, JAL, JMP, JR, left, MemToReg, MemWrite, MFC, MTC, multiplexer_13_out, nIE_q,
       not_1_out, or_1_out, or_2_out, or_3_out, or_4_out, or_5_out, or_7_out, RegDst, RegWrite, right,
       SignedExt, SysCALL, up, \中断按键参考电路_1_ir_2 , \中断按键参考电路_2_ir_2 , \中断按键参考电路_3_ir_2 , \中断按键参考电路_4_ir_2 ,
       \中断按键参考电路_5_ir_2 , \中断按键参考电路_6_ir_2 , \中断按键参考电路_7_ir_2 ;
  wire [0:0] comparator_7_lt, comparator_8_lt, or_6_out;
  wire [1:0] ExcepType, Execp2_q, Execp3_q, MDin, multiplexer_1_out, multiplexer_4_out, multiplexer_5_out,
       Pri, priority_encoder_1_out;
  wire [3:0] ALU_OP;
  wire [4:0] multiplexer_6_out, R1_num, R2_num, w_num;
  wire [5:0] FUNC;
  wire [15:0] \总周期数 , \无条件分支数 , \条件分支成功数 ;
  wire [27:0] adder_1_out;
  wire [31:0] adder_2_out, adder_3_out, AND_15_out, bit_extender_1_out, bit_extender_2_out, Din,
       divider_1_out, divider_1_rem, EPC1_q, EPC2_q, EPC3_q, in_PC, LedData, multiplexer_3_out,
       multiplexer_10_out, multiplexer_12_out, multiplexer_14_out, multiplexer_16_out, multiplexer_17_out,
       multiplexer_19_out, multiplier_1_cout, multiplier_1_out, next_PC, NOR_out, OR_9_out, PC, R1,
       ram_1_data, Result, Result2, shifter_1_out, shifter_2_out, shifter_3_out, shifter_4_out,
       subtractor_1_out, XOR_out, Y_t;
  wire [31:6] IR;
  wire [31:28] adder_1_out_2;

  Clock #(.highDuration(1), .lowDuration(1)) clock_1 (.out(CLK));
  Button \u_继续运行  (.out(Go));
  LED #(.active("true")) led_1 (.in(out_4));
  LED #(.active("true")) led_2 (.in(out_5));
  LED #(.active("true")) led_3 (.in(out_6));
  Hex_Digit_Display hex_digit_display_1 (.value(LedData[31:28]));  // open: dp
  Multiplexer #(.select(1), .width(2), .disabled("Z"), .enable("false")) multiplexer_1 (
    .in0(Pri), .in1(Execp2_q), .out(multiplexer_1_out), .sel(ERET));
  or or_1 (or_1_out, ERET, Exception);
  Hex_Digit_Display hex_digit_display_2 (.value(LedData[27:24]));  // open: dp
  Hex_Digit_Display hex_digit_display_3 (.value(LedData[23:20]));  // open: dp
  or or_2 (or_2_out, ~Halt, d_ff_1_q);  // OR_Gate
  Multiplexer #(.select(2), .width(32), .disabled("Z"), .enable("false")) multiplexer_2 (
    .in0({adder_1_out_2, adder_1_out}), .in1(adder_2_out), .in2(multiplexer_3_out), .out(next_PC),
    .sel({JMP, or_6_out[0]}));  // open: in3
  Multiplexer #(.select(1), .width(32), .disabled("Z"), .enable("false")) multiplexer_3 (
    .in0({adder_1_out_2, IR[25:6], FUNC, 2'b00}), .in1(R1), .out(multiplexer_3_out), .sel(JR));
  Register #(.width(2), .trigger("rising"), .Select("low")) Excep1 (
    .D(multiplexer_1_out), .en(or_1_out), .Q(ExcepType), .clk(CLK));  // open: clr
  Hex_Digit_Display hex_digit_display_4 (.value(LedData[15:12]));  // open: dp
  Hex_Digit_Display hex_digit_display_5 (.value(LedData[19:16]));  // open: dp
  Counter #(.width(16), .max('hffff), .ongoal("wrap"), .trigger("rising"), .behavior("old")) counter_1 (
    .count(or_6_out[0]), .Q(\条件分支成功数 ), .clk(CLK), .clr(RST));  // open: load, D, carry, preset
  Counter #(.width(16), .max('hffff), .ongoal("wrap"), .trigger("rising"), .behavior("old")) counter_2 (
    .count(JMP), .Q(\无条件分支数 ), .clk(CLK), .clr(RST));  // open: load, D, carry, preset
  Register #(.width(32), .trigger("rising"), .Select("low")) u_PC (
    .D(in_PC), .en(or_2_out), .Q(PC), .clk(CLK), .clr(RST));
  Multiplexer #(.select(1), .width(2), .disabled("Z"), .enable("false")) multiplexer_4 (
    .in0(ExcepType), .in1(Execp3_q), .out(multiplexer_4_out), .sel(ERET));
  Register #(.width(2), .trigger("rising"), .Select("low")) Execp2 (
    .D(multiplexer_4_out), .en(or_1_out), .Q(Execp2_q), .clk(CLK));  // open: clr
  Hex_Digit_Display hex_digit_display_6 (.value(LedData[7:4]));  // open: dp
  Hex_Digit_Display hex_digit_display_7 (.value(LedData[11:8]));  // open: dp
  D_Flip_Flop #(.trigger("rising"), .Pre_Clr_Positions("LEGACY"), .NegatePresetClear("false"), .enable("true"), .NewFFLayout("false")) d_ff_1 (
    .clk(CLK), .D(1'b0), .Q(d_ff_1_q), .preset(Go), .reset(RST));  // open: Qn, en
  Adder #(.width(32)) adder_1 (.a(PC), .b(32'h4), .out({adder_1_out_2, adder_1_out}));  // open: cin, cout
  \运算控制器自动生成  \u_运算控制器自动生成_1  (
    .OP0(IR[26]), .OP1(IR[27]), .OP2(IR[28]), .OP3(IR[29]), .OP4(IR[30]), .OP5(IR[31]), .F0(FUNC[0]),
    .F1(FUNC[1]), .F2(FUNC[2]), .F3(FUNC[3]), .F4(FUNC[4]), .F5(FUNC[5]), .S0(ALU_OP[0]), .S1(ALU_OP[1]),
    .S2(ALU_OP[2]), .S3(ALU_OP[3]));
  \控制信号自动生成  \u_控制信号自动生成_1  (
    .OP0(IR[26]), .OP1(IR[27]), .OP2(IR[28]), .OP3(IR[29]), .OP4(IR[30]), .OP5(IR[31]), .F0(FUNC[0]),
    .F1(FUNC[1]), .F2(FUNC[2]), .F3(FUNC[3]), .F4(FUNC[4]), .F5(FUNC[5]), .MemToReg(MemToReg),
    .MemWrite(MemWrite), .ALU_SRC(ALU_SRC), .RegWrite(RegWrite), .SysCALL(SysCALL), .SignedExt(SignedExt),
    .RegDst(RegDst), .BEQ(Beq), .BNE(Bne), .JR(JR), .JMP(JMP), .JAL(JAL), .ERET(ERET));
  Multiplexer #(.select(1), .width(2), .disabled("Z"), .enable("false")) multiplexer_5 (
    .in0(Execp2_q), .in1(2'b00), .out(multiplexer_5_out), .sel(ERET));
  Decoder #(.select(2), .tristate("false"), .disabled("Z"), .enable("false")) decoder_1 (
    .out1(decoder_1_out1), .out2(decoder_1_out2), .out3(decoder_1_out3), .sel(ExcepType));  // open: out0
  Hex_Digit_Display hex_digit_display_8 (.value(LedData[3:0]));  // open: dp
  // Probe on \总周期数 
  Adder #(.width(32)) adder_2 (
    .a({adder_1_out_2, adder_1_out}), .b(shifter_1_out), .out(adder_2_out));  // open: cin, cout
  Register #(.width(2), .trigger("rising"), .Select("low")) Execp3 (
    .D(multiplexer_5_out), .en(or_1_out), .Q(Execp3_q), .clk(CLK));  // open: clr
  and and_1 (and_1_out, ERET, decoder_1_out1);
  and and_2 (and_2_out, ERET, decoder_1_out2);
  and and_3 (and_3_out, ERET, decoder_1_out3);
  ROM #(.addrWidth(11), .dataWidth(32), .Select("high")) rom_1 (.addr(PC[12:2]), .data({IR, FUNC}));
  or or_3 (or_3_out, up, down, left, right);
  and and_4 (and_4_out, up, ~out_4);  // AND_Gate
  and and_5 (and_5_out, down, ~out_4);  // AND_Gate
  and and_6 (and_6_out, left, ~out_4);  // AND_Gate
  and and_7 (and_7_out, right, ~out_4);  // AND_Gate
  \中断按键参考电路  \u_中断按键参考电路_1  (.IR_2(\中断按键参考电路_1_ir_2 ), .Clr(and_1_out), .clk(CLK), .W(out_4), .IR(or_3_out));
  \中断按键参考电路  \u_中断按键参考电路_2  (.IR_2(\中断按键参考电路_2_ir_2 ), .Clr(and_2_out), .clk(CLK), .W(out_5), .IR(in_1));
  \中断按键参考电路  \u_中断按键参考电路_3  (.IR_2(\中断按键参考电路_3_ir_2 ), .Clr(and_3_out), .clk(CLK), .W(out_6), .IR(\中断源 ));
  \中断按键参考电路  \u_中断按键参考电路_4  (.IR_2(\中断按键参考电路_4_ir_2 ), .Clr(and_1_out), .clk(CLK), .IR(and_4_out));  // open: W
  \中断按键参考电路  \u_中断按键参考电路_5  (.IR_2(\中断按键参考电路_5_ir_2 ), .Clr(and_1_out), .clk(CLK), .IR(and_5_out));  // open: W
  \中断按键参考电路  \u_中断按键参考电路_6  (.IR_2(\中断按键参考电路_6_ir_2 ), .Clr(and_1_out), .clk(CLK), .IR(and_6_out));  // open: W
  \中断按键参考电路  \u_中断按键参考电路_7  (.IR_2(\中断按键参考电路_7_ir_2 ), .Clr(and_1_out), .clk(CLK), .IR(and_7_out));  // open: W
  Multiplexer #(.select(1), .width(5), .disabled("Z"), .enable("false")) multiplexer_6 (
    .in0(IR[20:16]), .in1(IR[15:11]), .out(multiplexer_6_out), .sel(RegDst));
  assign bit_extender_1_out = {{16{1'b0}}, {IR[15:6], FUNC}};  // Bit_Extender bit_extender_1
  assign bit_extender_2_out = {{16{IR[15]}}, {IR[15:6], FUNC}};  // Bit_Extender bit_extender_2
  Priority_Encoder #(.select(2), .disabled("Z")) priority_encoder_1 (
    .in0(\中断按键参考电路_4_ir_2 ), .in1(\中断按键参考电路_5_ir_2 ), .in2(\中断按键参考电路_6_ir_2 ), .in3(\中断按键参考电路_7_ir_2 ),
    .out(priority_encoder_1_out));  // open: gs, en_out, en_in
  Multiplexer #(.select(1), .width(5), .disabled("Z"), .enable("false")) multiplexer_7 (
    .in0(IR[25:21]), .in1(5'b00010), .out(R1_num), .sel(SysCALL));
  Multiplexer #(.select(1), .width(5), .disabled("Z"), .enable("false")) multiplexer_8 (
    .in0(IR[20:16]), .in1(5'b00100), .out(R2_num), .sel(SysCALL));
  Multiplexer #(.select(1), .width(5), .disabled("Z"), .enable("false")) multiplexer_9 (
    .in0(multiplexer_6_out), .in1({5{1'b1}}), .out(w_num), .sel(JAL));
  Shifter #(.width(32), .shift("ll")) shifter_1 (.in(bit_extender_2_out), .\dist (5'b00010), .out(shifter_1_out));
  Comparator #(.width(11), .mode("twosComplement")) comparator_1 (
    .a(IR[31:21]), .b(11'h200), .eq(MFC));  // open: gt, lt
  Comparator #(.width(11), .mode("twosComplement")) comparator_2 (
    .a(IR[31:21]), .b(11'h204), .eq(MTC));  // open: gt, lt
  or or_4 (or_4_out, Exception, ERET, MFC, MTC);
  Pull_Resistor #(.pull(0)) pull_resistor_1 (.node(Pri));
  Priority_Encoder #(.select(2), .disabled("Z")) priority_encoder_2 (
    .in1(\中断按键参考电路_1_ir_2 ), .in2(\中断按键参考电路_2_ir_2 ), .in3(\中断按键参考电路_3_ir_2 ), .out(Pri), .en_in(1'b1));  // open: in0, gs, en_out
  Multiplexer #(.select(2), .width(32), .disabled("Z"), .enable("false")) multiplexer_10 (
    .in0(32'h16c), .in1(32'h3f4), .in2(32'h67c), .in3(32'h904), .out(multiplexer_10_out),
    .sel(priority_encoder_1_out));
  Multiplexer #(.select(1), .width(32), .disabled("Z"), .enable("false")) multiplexer_11 (
    .in0(multiplexer_16_out), .in1({adder_1_out_2, adder_1_out}), .out(Din), .sel(JAL));
  Multiplexer #(.select(1), .width(32), .disabled("Z"), .enable("false")) multiplexer_12 (
    .in0(bit_extender_1_out), .in1(bit_extender_2_out), .out(multiplexer_12_out), .sel(SignedExt));
  or or_5 (or_5_out, MTC, Exception);
  Multiplexer #(.select(1), .width(1), .disabled("Z"), .enable("false")) multiplexer_13 (
    .in0(1'b0), .in1(1'b1), .out(multiplexer_13_out), .sel(or_5_out));
  Register #(.width(1), .trigger("rising"), .Select("low")) nIE (
    .D(multiplexer_13_out), .en(or_4_out), .Q(nIE_q), .clk(CLK));  // open: clr
  Multiplexer #(.select(2), .width(32), .disabled("Z"), .enable("false")) multiplexer_14 (
    .in0({32{1'b0}}), .in1(multiplexer_10_out), .in2({32{1'b0}}), .in3({32{1'b0}}), .out(multiplexer_14_out),
    .sel(Pri));
  Counter #(.width(16), .max('hffff), .ongoal("wrap"), .trigger("rising"), .behavior("old")) counter_3 (
    .count(not_1_out), .Q(\总周期数 ), .clk(CLK), .clr(RST));  // open: load, D, carry, preset
  not not_1 (not_1_out, Halt);
  Comparator #(.width(2), .mode("unsigned")) comparator_3 (
    .a(Pri), .b(ExcepType), .gt(comparator_3_gt));  // open: eq, lt
  Multiplexer #(.select(1), .width(32), .disabled("Z"), .enable("false")) multiplexer_15 (
    .in0({X, Y, clolor, MDin}), .in1(multiplexer_12_out), .out(Y_t), .sel(ALU_SRC));
  and and_8 (Exception, ~nIE_q, comparator_3_gt);  // AND_Gate
  Multiplexer #(.select(1), .width(32), .disabled("Z"), .enable("false")) multiplexer_16 (
    .in0(Result), .in1(ram_1_data), .out(multiplexer_16_out), .sel(MemToReg));
  Multiplexer #(.select(1), .width(32), .disabled("Z"), .enable("false")) multiplexer_17 (
    .in0(next_PC), .in1(EPC2_q), .out(multiplexer_17_out), .sel(ERET));
  Multiplexer #(.select(2), .width(32), .disabled("Z"), .enable("false")) multiplexer_18 (
    .in0(next_PC), .in1(multiplexer_14_out), .in2(EPC1_q), .out(in_PC), .sel({ERET, Exception}));  // open: in3
  and and_9 (and_9_out, Equal, Beq);
  or or_6 (or_6_out[0], and_9_out, and_10_out);
  and and_10 (and_10_out, ~Equal, Bne);  // AND_Gate
  Register #(.width(32), .trigger("rising"), .Select("low")) EPC1 (
    .D(multiplexer_17_out), .en(or_7_out), .Q(EPC1_q), .clk(CLK));  // open: clr
  or or_7 (or_7_out, ERET, Exception);
  Multiplexer #(.select(1), .width(32), .disabled("Z"), .enable("false")) multiplexer_19 (
    .in0(EPC1_q), .in1(EPC3_q), .out(multiplexer_19_out), .sel(ERET));
  RAM #(.addrWidth(24), .dataWidth(32), .bus("separate"), .Select("high")) ram_1 (
    .addr(Result[25:2]), .din({X, Y, clolor, MDin}), .data(ram_1_data), .str(MemWrite), .clk(CLK));  // open: sel, ld, clr
  Register #(.width(32), .trigger("rising"), .Select("low")) EPC2 (
    .D(multiplexer_19_out), .en(or_7_out), .Q(EPC2_q), .clk(CLK));  // open: clr
  Register #(.width(32), .trigger("rising"), .Select("low")) EPC3 (
    .D(EPC2_q), .en(Exception), .Q(EPC3_q), .clk(CLK));  // open: clr
  Comparator #(.width(32), .mode("twosComplement")) comparator_4 (
    .a(R1), .b(32'h32), .eq(comparator_4_eq));  // open: gt, lt
  Comparator #(.width(32), .mode("twosComplement")) comparator_5 (
    .a(R1), .b(32'h22), .eq(comparator_5_eq));  // open: gt, lt
  Comparator #(.width(32), .mode("twosComplement")) comparator_6 (
    .a(R1), .b(32'h147), .eq(comparator_6_eq));  // open: gt, lt
  Button button_1 (.out(up));
  Button button_2 (.out(left));
  Button button_3 (.out(down));
  and and_11 (Halt, comparator_4_eq, SysCALL);
  and and_12 (and_12_out, comparator_5_eq, SysCALL);
  and and_13 (enable, comparator_6_eq, SysCALL);
  Button button_4 (.out(right));
  Register #(.width(32), .trigger("rising"), .Select("low")) register_1 (
    .D({X, Y, clolor, MDin}), .en(and_12_out), .Q(LedData), .clk(CLK), .clr(RST));
  // RegisterFile registerfile_1: pin names not known; wires that end beside it: Din, CLK, RegWrite, w_num, R1_num, R2_num, R1, {X, Y, clolor, MDin}
  or or_8 (RST_2, RST, and_14_out);
  and and_14 (and_14_out, enable, MDin[1]);
  // LCD_Video lcd_video_1: pin names not known; wires that end beside it: RST_2, CLK, enable, X, Y, clolor
  Shifter #(.width(32), .shift("ll")) shifter_2 (.in(Y_t), .\dist (IR[10:6]), .out(shifter_2_out));
  Shifter #(.width(32), .shift("ar")) shifter_3 (.in(Y_t), .\dist (IR[10:6]), .out(shifter_3_out));
  Shifter #(.width(32), .shift("lr")) shifter_4 (.in(Y_t), .\dist (IR[10:6]), .out(shifter_4_out));
  Multiplier #(.width(32)) multiplier_1 (
    .a(R1), .b(Y_t), .out(multiplier_1_out), .cout(multiplier_1_cout));  // open: cin
  Divider #(.width(32)) divider_1 (.a(R1), .b(Y_t), .out(divider_1_out), .rem(divider_1_rem));  // open: upper
  Adder #(.width(32)) adder_3 (.a(R1), .b(Y_t), .out(adder_3_out));  // open: cin, cout
  Subtractor #(.width(32)) subtractor_1 (.a(R1), .b(Y_t), .out(subtractor_1_out));  // open: bin, bout
  assign AND_15_out = R1 & Y_t;  // AND_Gate AND_15, 32 bits wide
  assign OR_9_out = R1 | Y_t;  // OR_Gate OR_9, 32 bits wide
  assign XOR_out = R1 ^ Y_t;  // XOR_Gate XOR, 32 bits wide
  assign NOR_out = ~(R1 | Y_t);  // NOR_Gate NOR, 32 bits wide
  Comparator #(.width(32), .mode("twosComplement")) comparator_7 (
    .a(R1), .b(Y_t), .eq(Equal), .lt(comparator_7_lt[0]));  // open: gt
  Comparator #(.width(32), .mode("unsigned")) comparator_8 (.a(R1), .b(Y_t), .lt(comparator_8_lt[0]));  // open: gt, eq
  Multiplexer #(.select(4), .width(32), .disabled("Z"), .enable("false")) multiplexer_20 (
    .in0(shifter_2_out), .in1(shifter_3_out), .in2(shifter_4_out), .in3(multiplier_1_out),
    .in4(divider_1_out), .in5(adder_3_out), .in6(subtractor_1_out), .in7(AND_15_out), .in8(OR_9_out),
    .in9(XOR_out), .in10(NOR_out), .in11({{31{1'b0}}, comparator_7_lt[0]}),
    .in12({{31{1'b0}}, comparator_8_lt[0]}), .in13({32{1'b0}}), .in14({32{1'b0}}), .in15({32{1'b0}}),
    .out(Result), .sel(ALU_OP));
  Multiplexer #(.select(4), .width(32), .disabled("Z"), .enable("false")) multiplexer_21 (
    .in0({32{1'b0}}), .in1({32{1'b0}}), .in2({32{1'b0}}), .in3(multiplier_1_cout), .in4(divider_1_rem),
    .in5({32{1'b0}}), .in6({32{1'b0}}), .in7({32{1'b0}}), .in8({32{1'b0}}), .in9({32{1'b0}}),
    .in10({32{1'b0}}), .in11({32{1'b0}}), .in12({32{1'b0}}), .in13({32{1'b0}}), .in14({32{1'b0}}),
    .in15({32{1'b0}}), .out(Result2), .sel(ALU_OP));

  // Other names for the same wires on the sheet: IR[5:0] = FUNC; shamt[4:0] = IR[10:6]; OP_CODE[5:0] = IR[31:26];
  //   IR2 = in_1; IR3 = \中断源 ; R2[31:0] = {X, Y, clolor, MDin}; MDin[31:2] = {X, Y, clolor}; RDin[31:0] = Din;
  //   S[3:0] = ALU_OP; W1 = out_4; W2 = out_5; W3 = out_6; WE = RegWrite; X_t[31:0] = R1

  // Notes on the sheet:
  //   中断等待指示
  //   总复位信号应将除ROM以外所有存储组件全部清零
  //   单周期硬布线控制器
  //   中断相应逻辑
  //   数码管输出
  //   数码管输出应该用寄存器锁存，否则显示数据只能一闪而过
  //   instr_index
  //   contents of rom_1 (hex, n*v repeats v):
  //   201c1800 201d3ffc af800008 201a0000 201b0000 1a4100 11b4020 84080 8d060000 10c00008 20080003
  //   14c80003 8f880008 20080001 af880008 1a2020 1b2820 c00001b 237b0001 20080010 1768fff0 235a0001
  //   20080010 1748ffec 8000018 20020032 c 23bd0018 afa80000 afb0fffc afb1fff8 afb2fff4 afb3fff0 afb4ffec
  //   10c0000f 20080001 10c8000f 20080002 10c80010 20080003 10c80013 20080004 10c80014 20080005 10c80015
  //   20080006 10c80008 8fa80000 23bdffe8 3e00008 20100000 8000044 2010739f 108080 8000044 af840000
  //   af850004 20106c47 108080 8000044 20107f40 108080 8000044 2010239a 108080 8000044 201057e5 108080
  //   488c0 22320008 598c0 22740008 102020 114480 882020 134640 882020 20020147 c 22730001 1674fff7
  //   22310001 1632fff3 8fa80000 8fb0fffc 8fb1fff8 8fb2fff4 8fb3fff0 8fb4ffec 23bdffe8 3e00008 23bd002c
  //   afa80000 afa9fffc afaafff8 afb0fff4 afb1fff0 afb2ffec afb3ffe8 afb4ffe4 afa4ffe0 afa5ffdc afa6ffd8
  //   8f900000 8f910004 104100 1114020 84080 8d120000 2209ffff 94100 1114020 84080 8d130000 12600008
  //   20080001 1268007b 20080003 12680006 20080004 12680028 20080005 12680028 200a0002 80000c6 2209fffe
  //   94100 1114020 84080 8d140000 12800003 20080004 1288000d 80000f0 200a0003 2209fffe 94100 1114020
  //   84080 ad0a0000 92020 112820 a3020 c00001b 200a0002 80000c6 8f880008 2008ffff af880008 200a0005
  //   2209fffe 94100 1114020 84080 ad0a0000 92020 112820 a3020 c00001b 200a0002 80000c6 200a0006 80000c6
  //   2209fffe 94100 1114020 84080 8d140000 12800003 20080004 12880010 80000f0 8f880008 20080001 af880008
  //   200a0003 2209fffe 94100 1114020 84080 ad0a0000 92020 112820 a3020 c00001b 200a0006 80000c6 200a0005
  //   2209fffe 94100 1114020 84080 ad0a0000 92020 112820 a3020 c00001b 200a0006 2209ffff 94100 1114020
  //   84080 ad0a0000 92020 112820 a3020 c00001b 20080006 12480016 200a0000 104100 1114020 84080 ad0a0000
  //   102020 112820 a3020 c00001b 8fa80000 8fa9fffc 8faafff8 8fb0fff4 8fb1fff0 8fb2ffec 8fb3ffe8 8fb4ffe4
  //   8fa4ffe0 8fa5ffdc 8fa6ffd8 23bdffd4 42000018 200a0004 104100 1114020 84080 ad0a0000 102020 112820
  //   a3020 c00001b 8fa80000 8fa9fffc 8faafff8 8fb0fff4 8fb1fff0 8fb2ffec 8fb3ffe8 8fb4ffe4 8fa4ffe0
  //   8fa5ffdc 8fa6ffd8 23bdffd4 42000018 23bd002c afa80000 afa9fffc afaafff8 afb0fff4 afb1fff0 afb2ffec
  //   afb3ffe8 afb4ffe4 afa4ffe0 afa5ffdc afa6ffd8 8f900000 8f910004 104100 1114020 84080 8d120000
  //   22090001 94100 1114020 84080 8d130000 12600008 20080001 1268007b 20080003 12680006 20080004 12680028
  //   20080005 12680028 200a0002 8000168 22090002 94100 1114020 84080 8d140000 12800003 20080004 1288000d
  //   8000192 200a0003 22090002 94100 1114020 84080 ad0a0000 92020 112820 a3020 c00001b 200a0002 8000168
  //   8f880008 2008ffff af880008 200a0005 22090002 94100 1114020 84080 ad0a0000 92020 112820 a3020 c00001b
  //   200a0002 8000168 200a0006 8000168 22090002 94100 1114020 84080 8d140000 12800003 20080004 12880010
  //   8000192 8f880008 20080001 af880008 200a0003 22090002 94100 1114020 84080 ad0a0000 92020 112820 a3020
  //   c00001b 200a0006 8000168 200a0005 22090002 94100 1114020 84080 ad0a0000 92020 112820 a3020 c00001b
  //   200a0006 22090001 94100 1114020 84080 ad0a0000 92020 112820 a3020 c00001b 20080006 12480016 200a0000
  //   104100 1114020 84080 ad0a0000 102020 112820 a3020 c00001b 8fa80000 8fa9fffc 8faafff8 8fb0fff4
  //   8fb1fff0 8fb2ffec 8fb3ffe8 8fb4ffe4 8fa4ffe0 8fa5ffdc 8fa6ffd8 23bdffd4 42000018 200a0004 104100
  //   1114020 84080 ad0a0000 102020 112820 a3020 c00001b 8fa80000 8fa9fffc 8faafff8 8fb0fff4 8fb1fff0
  //   8fb2ffec 8fb3ffe8 8fb4ffe4 8fa4ffe0 8fa5ffdc 8fa6ffd8 23bdffd4 42000018 23bd002c afa80000 afa9fffc
  //   afaafff8 afb0fff4 afb1fff0 afb2ffec afb3ffe8 afb4ffe4 afa4ffe0 afa5ffdc afa6ffd8 8f900000 8f910004
  //   104100 1114020 84080 8d120000 104100 2229ffff 1094020 84080 8d130000 12600008 20080001 1268007b
  //   20080003 12680006 20080004 12680028 20080005 12680028 200a0002 800020a 104100 2229fffe 1094020 84080
  //   8d140000 12800003 20080004 1288000d 8000234 200a0003 104100 2229fffe 1094020 84080 ad0a0000 102020
  //   92820 a3020 c00001b 200a0002 800020a 8f880008 2008ffff af880008 200a0005 104100 2229fffe 1094020
  //   84080 ad0a0000 102020 92820 a3020 c00001b 200a0002 800020a 200a0006 800020a 104100 2229ff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
  //   运算器控制器，根据指令生成运算器功能选择信号
  //   rs
  //   rt
  //   rd
  //   imm
  //   sa
  //   Syscall
  //   v0
  //   a0
  //   Beq
  //   Bne
  //   MemToReg
  //   MemWrite
  //   AluOP
  //   AluSrcB
  //   显像逻辑
  //   Regfile
  //   ALU
endmodule
