// Logisim project TeamWork_v2.0.circ as structural Verilog: 5 circuits, main circuit ◇运算控制器自动生成
// 运算器控制器
module \运算控制器自动生成  (
  input  OP0,
  input  OP1,
  input  OP2,
  input  OP3,
  input  OP4,
  input  OP5,
  input  F0,
  input  F1,
  input  F2,
  input  F3,
  input  F4,
  input  F5,
  output S0,
  output S1,
  output S2,
  output S3
);

  wire and_1_out, and_2_out, and_3_out, and_4_out, and_5_out, and_6_out, and_7_out, and_8_out, and_9_out,
       and_10_out, and_11_out, and_12_out, and_13_out, and_14_out, and_15_out, and_16_out, and_17_out,
       and_18_out, and_19_out, and_20_out, and_21_out, and_22_out, and_23_out, and_24_out, and_25_out,
       and_26_out, and_27_out, and_28_out, and_29_out, and_30_out, and_31_out, and_32_out, and_33_out,
       and_34_out, and_35_out, and_36_out, and_37_out, and_38_out, and_39_out, and_40_out, not_1_out,
       not_2_out, not_3_out, not_4_out, not_5_out, not_6_out, not_7_out, not_8_out, not_9_out, not_10_out,
       not_11_out, not_12_out, not_13_out, not_14_out, not_15_out, not_16_out, not_17_out, not_18_out,
       not_19_out, not_20_out, not_21_out, not_22_out, not_23_out, not_24_out, not_25_out, not_26_out,
       not_27_out, not_28_out, not_29_out, not_30_out, not_31_out, not_32_out, not_33_out, not_34_out,
       not_35_out, not_36_out, not_37_out, not_38_out, not_39_out, not_40_out, not_41_out, not_42_out,
       not_43_out, not_44_out, not_45_out, not_46_out, not_47_out, not_48_out, not_49_out, not_50_out,
       not_51_out, not_52_out, not_53_out, not_54_out, not_55_out, not_56_out, not_57_out, not_58_out,
       not_59_out, not_60_out, not_61_out, not_62_out, not_63_out, not_64_out, not_65_out, not_66_out,
       not_67_out, not_68_out, not_69_out, not_70_out, not_71_out, not_72_out, not_73_out, not_74_out,
       not_75_out, not_76_out, not_77_out, not_78_out, not_79_out, not_80_out, not_81_out, not_82_out,
       not_83_out, not_84_out, not_85_out, not_86_out, not_87_out, not_88_out, not_89_out, not_90_out,
       not_91_out, not_92_out, not_93_out, not_94_out, not_95_out, not_96_out, not_97_out, not_98_out,
       not_99_out, not_100_out, not_101_out, not_102_out, not_103_out, not_104_out, not_105_out, not_106_out,
       not_107_out, not_108_out, not_109_out, not_110_out, not_111_out, not_112_out, not_113_out,
       not_114_out, not_115_out, not_116_out, not_117_out, not_118_out, not_119_out, not_120_out,
       not_121_out, not_122_out, not_123_out, not_124_out, not_125_out, not_126_out, not_127_out,
       not_128_out, not_129_out, not_130_out, not_131_out, not_132_out, not_133_out, not_134_out,
       not_135_out, not_136_out, not_137_out, not_138_out, not_139_out, not_140_out, not_141_out,
       not_142_out, not_143_out, not_144_out, not_145_out, not_146_out, not_147_out, not_148_out,
       not_149_out, not_150_out, not_151_out, not_152_out, not_153_out, not_154_out, not_155_out,
       not_156_out, not_157_out, not_158_out, not_159_out, not_160_out, not_161_out, not_162_out,
       not_163_out, not_164_out, not_165_out, not_166_out, not_167_out, not_168_out, not_169_out,
       not_170_out, not_171_out, not_172_out, not_173_out, not_174_out, not_175_out, not_176_out,
       not_177_out, not_178_out, not_179_out, not_180_out, not_181_out, not_182_out, not_183_out,
       not_184_out, not_185_out, not_186_out, not_187_out, not_188_out, not_189_out, not_190_out,
       not_191_out, not_192_out, not_193_out, not_194_out, not_195_out, not_196_out, not_197_out,
       not_198_out, not_199_out, not_200_out, not_201_out, not_202_out, not_203_out, not_204_out,
       not_205_out, not_206_out, not_207_out, not_208_out, not_209_out, not_210_out, not_211_out,
       not_212_out, not_213_out, not_214_out, not_215_out, not_216_out, not_217_out, not_218_out,
       not_219_out, not_220_out, not_221_out, not_222_out, not_223_out, not_224_out, not_225_out,
       not_226_out, not_227_out, not_228_out, not_229_out, not_230_out, not_231_out, not_232_out,
       not_233_out, not_234_out, not_235_out, not_236_out, not_237_out, not_238_out, not_239_out,
       not_240_out, not_241_out, not_242_out, not_243_out, not_244_out, not_245_out, not_246_out,
       not_247_out, not_248_out, not_249_out, not_250_out, not_251_out, not_252_out, not_253_out,
       not_254_out, not_255_out, not_256_out, not_257_out, not_258_out, not_259_out, not_260_out,
       not_261_out, not_262_out, not_263_out;

  not not_1 (not_1_out, OP5);
  not not_2 (not_2_out, OP4);
  not not_3 (not_3_out, OP3);
  not not_4 (not_4_out, OP2);
  not not_5 (not_5_out, OP1);
  not not_6 (not_6_out, OP0);
  not not_7 (not_7_out, F5);
  not not_8 (not_8_out, F4);
  not not_9 (not_9_out, F3);
  not not_10 (not_10_out, F2);
  not not_11 (not_11_out, OP5);
  not not_12 (not_12_out, OP4);
  not not_13 (not_13_out, OP3);
  not not_14 (not_14_out, OP2);
  not not_15 (not_15_out, OP1);
  not not_16 (not_16_out, OP0);
  not not_17 (not_17_out, F4);
  not not_18 (not_18_out, F3);
  not not_19 (not_19_out, F2);
  not not_20 (not_20_out, F1);
  not not_21 (not_21_out, F0);
  not not_22 (not_22_out, OP5);
  not not_23 (not_23_out, OP4);
  not not_24 (not_24_out, OP3);
  not not_25 (not_25_out, OP2);
  not not_26 (not_26_out, OP1);
  not not_27 (not_27_out, OP0);
  not not_28 (not_28_out, F4);
  not not_29 (not_29_out, F3);
  not not_30 (not_30_out, F2);
  not not_31 (not_31_out, F1);
  not not_32 (not_32_out, OP5);
  not not_33 (not_33_out, OP4);
  not not_34 (not_34_out, OP3);
  not not_35 (not_35_out, OP2);
  not not_36 (not_36_out, OP1);
  not not_37 (not_37_out, OP0);
  not not_38 (not_38_out, F4);
  not not_39 (not_39_out, F3);
  not not_40 (not_40_out, F1);
  not not_41 (not_41_out, F0);
  not not_42 (not_42_out, OP5);
  not not_43 (not_43_out, OP4);
  not not_44 (not_44_out, OP3);
  not not_45 (not_45_out, OP2);
  not not_46 (not_46_out, OP1);
  not not_47 (not_47_out, OP0);
  not not_48 (not_48_out, F4);
  not not_49 (not_49_out, F2);
  not not_50 (not_50_out, F0);
  not not_51 (not_51_out, OP5);
  not not_52 (not_52_out, OP4);
  not not_53 (not_53_out, OP3);
  not not_54 (not_54_out, OP1);
  not not_55 (not_55_out, OP0);
  not not_56 (not_56_out, OP5);
  not not_57 (not_57_out, OP4);
  not not_58 (not_58_out, OP3);
  not not_59 (not_59_out, OP1);
  not not_60 (not_60_out, OP5);
  not not_61 (not_61_out, OP4);
  not not_62 (not_62_out, OP2);
  not not_63 (not_63_out, OP1);
  not not_64 (not_64_out, OP0);
  not not_65 (not_65_out, OP5);
  not not_66 (not_66_out, OP4);
  not not_67 (not_67_out, OP1);
  not not_68 (not_68_out, OP0);
  not not_69 (not_69_out, OP5);
  not not_70 (not_70_out, OP4);
  not not_71 (not_71_out, OP2);
  not not_72 (not_72_out, OP1);
  not not_73 (not_73_out, OP5);
  not not_74 (not_74_out, OP4);
  not not_75 (not_75_out, OP2);
  not not_76 (not_76_out, OP0);
  not not_77 (not_77_out, OP4);
  not not_78 (not_78_out, OP3);
  not not_79 (not_79_out, OP2);
  not not_80 (not_80_out, OP4);
  not not_81 (not_81_out, OP2);
  not not_82 (not_82_out, OP5);
  not not_83 (not_83_out, OP4);
  not not_84 (not_84_out, OP3);
  not not_85 (not_85_out, OP2);
  not not_86 (not_86_out, OP1);
  not not_87 (not_87_out, OP0);
  not not_88 (not_88_out, F5);
  not not_89 (not_89_out, F4);
  not not_90 (not_90_out, F3);
  not not_91 (not_91_out, F2);
  not not_92 (not_92_out, F0);
  not not_93 (not_93_out, OP5);
  not not_94 (not_94_out, OP4);
  not not_95 (not_95_out, OP3);
  not not_96 (not_96_out, OP2);
  not not_97 (not_97_out, OP1);
  not not_98 (not_98_out, OP0);
  not not_99 (not_99_out, F4);
  not not_100 (not_100_out, F3);
  not not_101 (not_101_out, F2);
  not not_102 (not_102_out, F0);
  not not_103 (not_103_out, OP5);
  not not_104 (not_104_out, OP4);
  not not_105 (not_105_out, OP3);
  not not_106 (not_106_out, OP2);
  not not_107 (not_107_out, OP1);
  not not_108 (not_108_out, OP0);
  not not_109 (not_109_out, F4);
  not not_110 (not_110_out, F3);
  not not_111 (not_111_out, F1);
  not not_112 (not_112_out, F0);
  not not_113 (not_113_out, OP5);
  not not_114 (not_114_out, OP4);
  not not_115 (not_115_out, OP3);
  not not_116 (not_116_out, OP2);
  not not_117 (not_117_out, OP1);
  not not_118 (not_118_out, OP0);
  not not_119 (not_119_out, F4);
  not not_120 (not_120_out, F3);
  not not_121 (not_121_out, OP5);
  not not_122 (not_122_out, OP4);
  not not_123 (not_123_out, OP3);
  not not_124 (not_124_out, OP2);
  not not_125 (not_125_out, OP1);
  not not_126 (not_126_out, OP0);
  not not_127 (not_127_out, F4);
  not not_128 (not_128_out, F2);
  not not_129 (not_129_out, F0);
  not not_130 (not_130_out, OP5);
  not not_131 (not_131_out, OP4);
  not not_132 (not_132_out, OP3);
  not not_133 (not_133_out, OP1);
  not not_134 (not_134_out, OP0);
  not not_135 (not_135_out, OP5);
  not not_136 (not_136_out, OP4);
  not not_137 (not_137_out, OP3);
  not not_138 (not_138_out, OP1);
  not not_139 (not_139_out, OP5);
  not not_140 (not_140_out, OP4);
  not not_141 (not_141_out, OP1);
  not not_142 (not_142_out, OP0);
  not not_143 (not_143_out, OP5);
  not not_144 (not_144_out, OP4);
  not not_145 (not_145_out, OP2);
  not not_146 (not_146_out, OP0);
  not not_147 (not_147_out, OP5);
  not not_148 (not_148_out, OP4);
  not not_149 (not_149_out, OP3);
  not not_150 (not_150_out, OP2);
  not not_151 (not_151_out, OP1);
  not not_152 (not_152_out, OP0);
  not not_153 (not_153_out, F4);
  not not_154 (not_154_out, F3);
  not not_155 (not_155_out, F2);
  not not_156 (not_156_out, F1);
  not not_157 (not_157_out, F0);
  not not_158 (not_158_out, OP5);
  not not_159 (not_159_out, OP4);
  not not_160 (not_160_out, OP3);
  not not_161 (not_161_out, OP2);
  not not_162 (not_162_out, OP1);
  not not_163 (not_163_out, OP0);
  not not_164 (not_164_out, F4);
  not not_165 (not_165_out, F3);
  not not_166 (not_166_out, F2);
  not not_167 (not_167_out, F1);
  not not_168 (not_168_out, OP5);
  not not_169 (not_169_out, OP4);
  not not_170 (not_170_out, OP3);
  not not_171 (not_171_out, OP2);
  not not_172 (not_172_out, OP1);
  not not_173 (not_173_out, OP0);
  not not_174 (not_174_out, F4);
  not not_175 (not_175_out, F3);
  not not_176 (not_176_out, F2);
  not not_177 (not_177_out, F0);
  not not_178 (not_178_out, OP5);
  not not_179 (not_179_out, OP4);
  not not_180 (not_180_out, OP3);
  not not_181 (not_181_out, OP2);
  not not_182 (not_182_out, OP1);
  not not_183 (not_183_out, OP0);
  not not_184 (not_184_out, F4);
  not not_185 (not_185_out, F3);
  not not_186 (not_186_out, F1);
  not not_187 (not_187_out, F0);
  not not_188 (not_188_out, OP5);
  not not_189 (not_189_out, OP4);
  not not_190 (not_190_out, OP3);
  not not_191 (not_191_out, OP2);
  not not_192 (not_192_out, OP1);
  not not_193 (not_193_out, OP0);
  not not_194 (not_194_out, F4);
  not not_195 (not_195_out, F2);
  not not_196 (not_196_out, OP5);
  not not_197 (not_197_out, OP4);
  not not_198 (not_198_out, OP2);
  not not_199 (not_199_out, OP1);
  not not_200 (not_200_out, OP0);
  not not_201 (not_201_out, OP5);
  not not_202 (not_202_out, OP4);
  not not_203 (not_203_out, OP1);
  not not_204 (not_204_out, OP0);
  not not_205 (not_205_out, OP5);
  not not_206 (not_206_out, OP4);
  not not_207 (not_207_out, OP2);
  not not_208 (not_208_out, OP1);
  not not_209 (not_209_out, OP4);
  not not_210 (not_210_out, OP3);
  not not_211 (not_211_out, OP2);
  not not_212 (not_212_out, OP4);
  not not_213 (not_213_out, OP2);
  not not_214 (not_214_out, OP5);
  not not_215 (not_215_out, OP4);
  not not_216 (not_216_out, OP3);
  not not_217 (not_217_out, OP2);
  not not_218 (not_218_out, OP1);
  not not_219 (not_219_out, OP0);
  not not_220 (not_220_out, F4);
  not not_221 (not_221_out, F3);
  not not_222 (not_222_out, F1);
  not not_223 (not_223_out, OP5);
  not not_224 (not_224_out, OP4);
  not not_225 (not_225_out, OP3);
  not not_226 (not_226_out, OP2);
  not not_227 (not_227_out, OP1);
  not not_228 (not_228_out, OP0);
  not not_229 (not_229_out, F4);
  not not_230 (not_230_out, F3);
  not not_231 (not_231_out, OP5);
  not not_232 (not_232_out, OP4);
  not not_233 (not_233_out, OP3);
  not not_234 (not_234_out, OP2);
  not not_235 (not_235_out, OP1);
  not not_236 (not_236_out, OP0);
  not not_237 (not_237_out, F4);
  not not_238 (not_238_out, F2);
  not not_239 (not_239_out, F0);
  not not_240 (not_240_out, OP5);
  not not_241 (not_241_out, OP4);
  not not_242 (not_242_out, OP3);
  not not_243 (not_243_out, OP2);
  not not_244 (not_244_out, OP1);
  not not_245 (not_245_out, OP0);
  not not_246 (not_246_out, F4);
  not not_247 (not_247_out, F2);
  not not_248 (not_248_out, OP5);
  not not_249 (not_249_out, OP4);
  not not_250 (not_250_out, OP3);
  not not_251 (not_251_out, OP1);
  not not_252 (not_252_out, OP0);
  not not_253 (not_253_out, OP5);
  not not_254 (not_254_out, OP4);
  not not_255 (not_255_out, OP3);
  not not_256 (not_256_out, OP1);
  not not_257 (not_257_out, OP5);
  not not_258 (not_258_out, OP4);
  not not_259 (not_259_out, OP2);
  not not_260 (not_260_out, OP0);
  not not_261 (not_261_out, OP5);
  not not_262 (not_262_out, OP4);
  not not_263 (not_263_out, OP1);
  and and_1 (and_1_out, not_1_out, not_2_out, not_3_out, not_4_out, not_5_out, not_6_out, not_7_out, not_8_out, not_9_out, not_10_out, F1, F0);
  and and_2 (and_2_out, not_11_out, not_12_out, not_13_out, not_14_out, not_15_out, not_16_out, F5, not_17_out, not_18_out, not_19_out, not_20_out, not_21_out);
  and and_3 (and_3_out, not_22_out, not_23_out, not_24_out, not_25_out, not_26_out, not_27_out, F5, not_28_out, not_29_out, not_30_out, not_31_out, F0);
  and and_4 (and_4_out, not_32_out, not_33_out, not_34_out, not_35_out, not_36_out, not_37_out, F5, not_38_out, not_39_out, F2, not_40_out, not_41_out);
  and and_5 (and_5_out, not_42_out, not_43_out, not_44_out, not_45_out, not_46_out, not_47_out, F5, not_48_out, F3, not_49_out, F1, not_50_out);
  and and_6 (and_6_out, not_51_out, not_52_out, not_53_out, OP2, not_54_out, not_55_out);
  and and_7 (and_7_out, not_56_out, not_57_out, not_58_out, OP2, not_59_out, OP0);
  and and_8 (and_8_out, not_60_out, not_61_out, OP3, not_62_out, not_63_out, not_64_out);
  and and_9 (and_9_out, not_65_out, not_66_out, OP3, OP2, not_67_out, not_68_out);
  and and_10 (and_10_out, not_69_out, not_70_out, OP3, not_71_out, not_72_out, OP0);
  and and_11 (and_11_out, not_73_out, not_74_out, OP3, not_75_out, OP1, not_76_out);
  and and_12 (and_12_out, OP5, not_77_out, not_78_out, not_79_out, OP1, OP0);
  and and_13 (and_13_out, OP5, not_80_out, OP3, not_81_out, OP1, OP0);
  and and_14 (and_14_out, not_82_out, not_83_out, not_84_out, not_85_out, not_86_out, not_87_out, not_88_out, not_89_out, not_90_out, not_91_out, F1, not_92_out);
  and and_15 (and_15_out, not_93_out, not_94_out, not_95_out, not_96_out, not_97_out, not_98_out, F5, not_99_out, not_100_out, not_101_out, F1, not_102_out);
  and and_16 (and_16_out, not_103_out, not_104_out, not_105_out, not_106_out, not_107_out, not_108_out, F5, not_109_out, not_110_out, F2, not_111_out, not_112_out);
  and and_17 (and_17_out, not_113_out, not_114_out, not_115_out, not_116_out, not_117_out, not_118_out, F5, not_119_out, not_120_out, F2, F1, F0);
  and and_18 (and_18_out, not_121_out, not_122_out, not_123_out, not_124_out, not_125_out, not_126_out, F5, not_127_out, F3, not_128_out, F1, not_129_out);
  and and_19 (and_19_out, not_130_out, not_131_out, not_132_out, OP2, not_133_out, not_134_out);
  and and_20 (and_20_out, not_135_out, not_136_out, not_137_out, OP2, not_138_out, OP0);
  and and_21 (and_21_out, not_139_out, not_140_out, OP3, OP2, not_141_out, not_142_out);
  and and_22 (and_22_out, not_143_out, not_144_out, OP3, not_145_out, OP1, not_146_out);
  and and_23 (and_23_out, not_147_out, not_148_out, not_149_out, not_150_out, not_151_out, not_152_out, F5, not_153_out, not_154_out, not_155_out, not_156_out, not_157_out);
  and and_24 (and_24_out, not_158_out, not_159_out, not_160_out, not_161_out, not_162_out, not_163_out, F5, not_164_out, not_165_out, not_166_out, not_167_out, F0);
  and and_25 (and_25_out, not_168_out, not_169_out, not_170_out, not_171_out, not_172_out, not_173_out, F5, not_174_out, not_175_out, not_176_out, F1, not_177_out);
  and and_26 (and_26_out, not_178_out, not_179_out, not_180_out, not_181_out, not_182_out, not_183_out, F5, not_184_out, not_185_out, F2, not_186_out, not_187_out);
  and and_27 (and_27_out, not_188_out, not_189_out, not_190_out, not_191_out, not_192_out, not_193_out, F5, not_194_out, F3, not_195_out, F1, F0);
  and and_28 (and_28_out, not_196_out, not_197_out, OP3, not_198_out, not_199_out, not_200_out);
  and and_29 (and_29_out, not_201_out, not_202_out, OP3, OP2, not_203_out, not_204_out);
  and and_30 (and_30_out, not_205_out, not_206_out, OP3, not_207_out, not_208_out, OP0);
  and and_31 (and_31_out, OP5, not_209_out, not_210_out, not_211_out, OP1, OP0);
  and and_32 (and_32_out, OP5, not_212_out, OP3, not_213_out, OP1, OP0);
  and and_33 (and_33_out, not_214_out, not_215_out, not_216_out, not_217_out, not_218_out, not_219_out, F5, not_220_out, not_221_out, F2, not_222_out, F0);
  and and_34 (and_34_out, not_223_out, not_224_out, not_225_out, not_226_out, not_227_out, not_228_out, F5, not_229_out, not_230_out, F2, F1, F0);
  and and_35 (and_35_out, not_231_out, not_232_out, not_233_out, not_234_out, not_235_out, not_236_out, F5, not_237_out, F3, not_238_out, F1, not_239_out);
  and and_36 (and_36_out, not_240_out, not_241_out, not_242_out, not_243_out, not_244_out, not_245_out, F5, not_246_out, F3, not_247_out, F1, F0);
  and and_37 (and_37_out, not_248_out, not_249_out, not_250_out, OP2, not_251_out, not_252_out);
  and and_38 (and_38_out, not_253_out, not_254_out, not_255_out, OP2, not_256_out, OP0);
  and and_39 (and_39_out, not_257_out, not_258_out, OP3, not_259_out, OP1, not_260_out);
  and and_40 (and_40_out, not_261_out, not_262_out, OP3, OP2, not_263_out, OP0);
  or or_1 (S1, and_14_out, and_15_out, and_16_out, and_17_out, and_18_out, and_19_out, and_20_out, and_21_out, and_22_out);
  or or_2 (S2, and_23_out, and_24_out, and_25_out, and_26_out, and_27_out, and_28_out, and_29_out, and_30_out, and_31_out, and_32_out);
  or or_3 (S3, and_33_out, and_34_out, and_35_out, and_36_out, and_37_out, and_38_out, and_39_out, and_40_out);
  or or_4 (S0, and_1_out, and_2_out, and_3_out, and_4_out, and_5_out, and_6_out, and_7_out, and_8_out, and_9_out, and_10_out, and_11_out, and_12_out, and_13_out);
endmodule

// 控制信号生成
module \控制信号自动生成  (
  input  OP0,
  input  OP1,
  input  OP2,
  input  OP3,
  input  OP4,
  input  OP5,
  input  F0,
  input  F1,
  input  F2,
  input  F3,
  input  F4,
  input  F5,
  output MemToReg,
  output MemWrite,
  output ALU_SRC,
  output RegWrite,
  output SysCALL,
  output SignedExt,
  output RegDst,
  output BEQ,
  output BNE,
  output JR,
  output JMP,
  output JAL,
  output ERET
);

  wire and_3_out, and_4_out, and_5_out, and_6_out, and_7_out, and_8_out, and_9_out, and_10_out, and_11_out,
       and_12_out, and_13_out, and_15_out, and_16_out, and_17_out, and_18_out, and_19_out, and_20_out,
       and_21_out, and_25_out, and_26_out, not_1_out, not_2_out, not_3_out, not_4_out, not_5_out, not_6_out,
       not_7_out, not_8_out, not_9_out, not_10_out, not_11_out, not_12_out, not_13_out, not_14_out,
       not_15_out, not_16_out, not_17_out, not_18_out, not_19_out, not_20_out, not_21_out, not_22_out,
       not_23_out, not_24_out, not_25_out, not_26_out, not_27_out, not_28_out, not_29_out, not_30_out,
       not_31_out, not_32_out, not_33_out, not_34_out, not_35_out, not_36_out, not_37_out, not_38_out,
       not_39_out, not_40_out, not_41_out, not_42_out, not_43_out, not_44_out, not_45_out, not_46_out,
       not_47_out, not_48_out, not_49_out, not_50_out, not_51_out, not_52_out, not_53_out, not_54_out,
       not_55_out, not_56_out, not_57_out, not_58_out, not_59_out, not_60_out, not_61_out, not_62_out,
       not_63_out, not_64_out, not_65_out, not_66_out, not_67_out, not_68_out, not_69_out, not_70_out,
       not_71_out, not_72_out, not_73_out, not_74_out, not_75_out, not_76_out, not_77_out, not_78_out,
       not_79_out, not_80_out, not_81_out, not_82_out, not_83_out, not_84_out, not_85_out, not_86_out,
       not_87_out, not_88_out, not_89_out, not_90_out, not_91_out, not_92_out, not_93_out, not_94_out,
       not_95_out, not_96_out, not_97_out, not_98_out, not_99_out, not_100_out, not_101_out, not_102_out,
       not_103_out, not_104_out, not_105_out, not_106_out, not_107_out, not_108_out, not_109_out,
       not_110_out, not_111_out, not_112_out, not_113_out, not_114_out, not_115_out, not_116_out,
       not_117_out, not_118_out, not_119_out, not_120_out, not_121_out, not_122_out, not_123_out,
       not_124_out, not_125_out, not_126_out, not_127_out, not_128_out, not_129_out, not_130_out,
       not_131_out, not_132_out, not_133_out, not_134_out, not_135_out, not_136_out, not_137_out,
       not_138_out, not_139_out, not_140_out, not_141_out, not_142_out, not_143_out, not_144_out,
       not_145_out, not_146_out, not_147_out, not_148_out, not_149_out, not_150_out, not_151_out,
       not_152_out, not_153_out, not_154_out, not_155_out, not_156_out, not_157_out, not_158_out,
       not_159_out, not_160_out, not_161_out, not_162_out, not_163_out, not_164_out, not_165_out,
       not_166_out, not_167_out, not_168_out, not_169_out, not_170_out, not_171_out, not_172_out,
       not_173_out, not_174_out;

  not not_1 (not_1_out, OP2);
  not not_2 (not_2_out, OP3);
  not not_3 (not_3_out, OP4);
  not not_4 (not_4_out, OP2);
  not not_5 (not_5_out, OP4);
  not not_6 (not_6_out, OP0);
  not not_7 (not_7_out, OP2);
  not not_8 (not_8_out, OP4);
  not not_9 (not_9_out, OP5);
  not not_10 (not_10_out, OP1);
  not not_11 (not_11_out, OP4);
  not not_12 (not_12_out, OP5);
  not not_13 (not_13_out, OP2);
  not not_14 (not_14_out, OP4);
  not not_15 (not_15_out, OP0);
  not not_16 (not_16_out, OP1);
  not not_17 (not_17_out, OP2);
  not not_18 (not_18_out, OP4);
  not not_19 (not_19_out, OP5);
  not not_20 (not_20_out, F0);
  not not_21 (not_21_out, F2);
  not not_22 (not_22_out, F3);
  not not_23 (not_23_out, F4);
  not not_24 (not_24_out, OP0);
  not not_25 (not_25_out, OP1);
  not not_26 (not_26_out, OP2);
  not not_27 (not_27_out, OP4);
  not not_28 (not_28_out, OP5);
  not not_29 (not_29_out, F1);
  not not_30 (not_30_out, F3);
  not not_31 (not_31_out, F4);
  not not_32 (not_32_out, OP0);
  not not_33 (not_33_out, OP1);
  not not_34 (not_34_out, OP2);
  not not_35 (not_35_out, OP4);
  not not_36 (not_36_out, OP5);
  not not_37 (not_37_out, F2);
  not not_38 (not_38_out, F3);
  not not_39 (not_39_out, F4);
  not not_40 (not_40_out, F5);
  not not_41 (not_41_out, OP0);
  not not_42 (not_42_out, OP1);
  not not_43 (not_43_out, OP2);
  not not_44 (not_44_out, OP4);
  not not_45 (not_45_out, OP5);
  not not_46 (not_46_out, F2);
  not not_47 (not_47_out, F4);
  not not_48 (not_48_out, OP0);
  not not_49 (not_49_out, OP1);
  not not_50 (not_50_out, OP2);
  not not_51 (not_51_out, OP4);
  not not_52 (not_52_out, OP5);
  not not_53 (not_53_out, F3);
  not not_54 (not_54_out, F4);
  not not_55 (not_55_out, OP0);
  not not_56 (not_56_out, OP2);
  not not_57 (not_57_out, OP4);
  not not_58 (not_58_out, OP5);
  not not_59 (not_59_out, OP1);
  not not_60 (not_60_out, OP4);
  not not_61 (not_61_out, OP5);
  not not_62 (not_62_out, OP2);
  not not_63 (not_63_out, OP3);
  not not_64 (not_64_out, OP4);
  not not_65 (not_65_out, OP0);
  not not_66 (not_66_out, OP1);
  not not_67 (not_67_out, OP2);
  not not_68 (not_68_out, OP3);
  not not_69 (not_69_out, OP4);
  not not_70 (not_70_out, OP5);
  not not_71 (not_71_out, F0);
  not not_72 (not_72_out, F1);
  not not_73 (not_73_out, F4);
  not not_74 (not_74_out, F5);
  not not_75 (not_75_out, OP0);
  not not_76 (not_76_out, OP2);
  not not_77 (not_77_out, OP4);
  not not_78 (not_78_out, OP5);
  not not_79 (not_79_out, OP1);
  not not_80 (not_80_out, OP3);
  not not_81 (not_81_out, OP4);
  not not_82 (not_82_out, OP5);
  not not_83 (not_83_out, OP0);
  not not_84 (not_84_out, OP1);
  not not_85 (not_85_out, OP2);
  not not_86 (not_86_out, OP3);
  not not_87 (not_87_out, OP4);
  not not_88 (not_88_out, OP5);
  not not_89 (not_89_out, F0);
  not not_90 (not_90_out, F2);
  not not_91 (not_91_out, F3);
  not not_92 (not_92_out, F4);
  not not_93 (not_93_out, OP0);
  not not_94 (not_94_out, OP1);
  not not_95 (not_95_out, OP2);
  not not_96 (not_96_out, OP3);
  not not_97 (not_97_out, OP4);
  not not_98 (not_98_out, OP5);
  not not_99 (not_99_out, F1);
  not not_100 (not_100_out, F3);
  not not_101 (not_101_out, F4);
  not not_102 (not_102_out, OP0);
  not not_103 (not_103_out, OP1);
  not not_104 (not_104_out, OP2);
  not not_105 (not_105_out, OP3);
  not not_106 (not_106_out, OP4);
  not not_107 (not_107_out, OP5);
  not not_108 (not_108_out, F2);
  not not_109 (not_109_out, F3);
  not not_110 (not_110_out, F4);
  not not_111 (not_111_out, F5);
  not not_112 (not_112_out, OP0);
  not not_113 (not_113_out, OP1);
  not not_114 (not_114_out, OP2);
  not not_115 (not_115_out, OP3);
  not not_116 (not_116_out, OP4);
  not not_117 (not_117_out, OP5);
  not not_118 (not_118_out, F2);
  not not_119 (not_119_out, F4);
  not not_120 (not_120_out, OP0);
  not not_121 (not_121_out, OP1);
  not not_122 (not_122_out, OP2);
  not not_123 (not_123_out, OP3);
  not not_124 (not_124_out, OP4);
  not not_125 (not_125_out, OP5);
  not not_126 (not_126_out, F3);
  not not_127 (not_127_out, F4);
  not not_128 (not_128_out, OP0);
  not not_129 (not_129_out, OP1);
  not not_130 (not_130_out, OP3);
  not not_131 (not_131_out, OP4);
  not not_132 (not_132_out, OP5);
  not not_133 (not_133_out, OP1);
  not not_134 (not_134_out, OP3);
  not not_135 (not_135_out, OP4);
  not not_136 (not_136_out, OP5);
  not not_137 (not_137_out, OP0);
  not not_138 (not_138_out, OP1);
  not not_139 (not_139_out, OP2);
  not not_140 (not_140_out, OP3);
  not not_141 (not_141_out, OP4);
  not not_142 (not_142_out, OP5);
  not not_143 (not_143_out, F0);
  not not_144 (not_144_out, F1);
  not not_145 (not_145_out, F2);
  not not_146 (not_146_out, F4);
  not not_147 (not_147_out, F5);
  not not_148 (not_148_out, OP0);
  not not_149 (not_149_out, OP2);
  not not_150 (not_150_out, OP3);
  not not_151 (not_151_out, OP4);
  not not_152 (not_152_out, OP5);
  not not_153 (not_153_out, F0);
  not not_154 (not_154_out, F1);
  not not_155 (not_155_out, F2);
  not not_156 (not_156_out, F4);
  not not_157 (not_157_out, F5);
  not not_158 (not_158_out, OP2);
  not not_159 (not_159_out, OP3);
  not not_160 (not_160_out, OP4);
  not not_161 (not_161_out, OP5);
  not not_162 (not_162_out, OP2);
  not not_163 (not_163_out, OP3);
  not not_164 (not_164_out, OP4);
  not not_165 (not_165_out, OP5);
  not not_166 (not_166_out, OP5);
  not not_167 (not_167_out, OP3);
  not not_168 (not_168_out, OP2);
  not not_169 (not_169_out, OP1);
  not not_170 (not_170_out, OP0);
  not not_171 (not_171_out, F5);
  not not_172 (not_172_out, F2);
  not not_173 (not_173_out, F1);
  not not_174 (not_174_out, F0);
  and and_1 (MemToReg, OP0, OP1, not_1_out, not_2_out, not_3_out, OP5);
  and and_2 (MemWrite, OP0, OP1, not_4_out, OP3, not_5_out, OP5);
  and and_3 (and_3_out, not_6_out, not_7_out, OP3, not_8_out, not_9_out);
  and and_4 (and_4_out, not_10_out, OP3, not_11_out, not_12_out);
  or or_1 (ALU_SRC, and_3_out, and_4_out, and_5_out);
  and and_5 (and_5_out, OP0, OP1, not_13_out, not_14_out, OP5);
  and and_6 (and_6_out, not_15_out, not_16_out, not_17_out, not_18_out, not_19_out, not_20_out, not_21_out, not_22_out, not_23_out);
  and and_7 (and_7_out, not_24_out, not_25_out, not_26_out, not_27_out, not_28_out, not_29_out, not_30_out, not_31_out, F5);
  and and_8 (and_8_out, not_32_out, not_33_out, not_34_out, not_35_out, not_36_out, F1, not_37_out, not_38_out, not_39_out, not_40_out);
  and and_9 (and_9_out, not_41_out, not_42_out, not_43_out, not_44_out, not_45_out, F1, not_46_out, F3, not_47_out, F5);
  and and_10 (and_10_out, not_48_out, not_49_out, not_50_out, not_51_out, not_52_out, F0, F2, not_53_out, not_54_out, F5);
  and and_11 (and_11_out, not_55_out, not_56_out, OP3, not_57_out, not_58_out);
  and and_12 (and_12_out, not_59_out, OP3, not_60_out, not_61_out);
  and and_13 (and_13_out, OP0, OP1, not_62_out, not_63_out, not_64_out);
  and and_14 (SysCALL, not_65_out, not_66_out, not_67_out, not_68_out, not_69_out, not_70_out, not_71_out, not_72_out, F2, F3, not_73_out, not_74_out);
  and and_15 (and_15_out, not_75_out, not_76_out, OP3, not_77_out, not_78_out);
  or or_2 (SignedExt, and_15_out, and_16_out);
  and and_16 (and_16_out, not_79_out, OP2, not_80_out, not_81_out, not_82_out);
  and and_17 (and_17_out, not_83_out, not_84_out, not_85_out, not_86_out, not_87_out, not_88_out, not_89_out, not_90_out, not_91_out, not_92_out);
  and and_18 (and_18_out, not_93_out, not_94_out, not_95_out, not_96_out, not_97_out, not_98_out, not_99_out, not_100_out, not_101_out, F5);
  and and_19 (and_19_out, not_102_out, not_103_out, not_104_out, not_105_out, not_106_out, not_107_out, F1, not_108_out, not_109_out, not_110_out, not_111_out);
  and and_20 (and_20_out, not_112_out, not_113_out, not_114_out, not_115_out, not_116_out, not_117_out, F1, not_118_out, F3, not_119_out, F5);
  and and_21 (and_21_out, not_120_out, not_121_out, not_122_out, not_123_out, not_124_out, not_125_out, F0, F2, not_126_out, not_127_out, F5);
  and and_22 (BEQ, not_128_out, not_129_out, OP2, not_130_out, not_131_out, not_132_out);
  and and_23 (BNE, OP0, not_133_out, OP2, not_134_out, not_135_out, not_136_out);
  and and_24 (JR, not_137_out, not_138_out, not_139_out, not_140_out, not_141_out, not_142_out, not_143_out, not_144_out, not_145_out, F3, not_146_out, not_147_out);
  and and_25 (and_25_out, not_148_out, not_149_out, not_150_out, not_151_out, not_152_out, not_153_out, not_154_out, not_155_out, F3, not_156_out, not_157_out);
  and and_26 (and_26_out, OP1, not_158_out, not_159_out, not_160_out, not_161_out);
  and and_27 (JAL, OP0, OP1, not_162_out, not_163_out, not_164_out, not_165_out);
  and and_28 (ERET, not_166_out, OP4, not_167_out, not_168_out, not_169_out, not_170_out, not_171_out, F4, F3, not_172_out, not_173_out, not_174_out);
  or or_3 (RegWrite, and_6_out, and_7_out, and_8_out, and_9_out, and_10_out, and_11_out, and_12_out, and_13_out);
  or or_4 (RegDst, and_17_out, and_18_out, and_19_out, and_20_out, and_21_out);
  or or_5 (JMP, and_25_out, and_26_out);
endmodule

module \中断按键参考电路  (
  input  clk,
  input  IR,
  input  Clr,
  output IR_2,
  output W
);

  wire and_1_out, d_ff_1_q, or_2_out;

  or or_1 (W, IR_2, d_ff_1_q);
  D_Flip_Flop #(.trigger("rising"), .Pre_Clr_Positions("LEGACY"), .NegatePresetClear("false"), .enable("true"), .NewFFLayout("false")) d_ff_1 (
    .clk(IR), .D(1'b1), .Q(d_ff_1_q), .reset(IR_2));  // open: Qn, preset, en
  or or_2 (or_2_out, d_ff_1_q, IR_2);
  and and_1 (and_1_out, or_2_out, ~Clr);  // AND_Gate
  D_Flip_Flop #(.trigger("rising"), .Pre_Clr_Positions("LEGACY"), .NegatePresetClear("false"), .enable("true"), .NewFFLayout("false")) u_IR (
    .clk(clk), .D(and_1_out), .Q(IR_2));  // open: Qn, preset, en, reset

  // Notes on the sheet:
  //   中断信号采样参考电路
  //   Reset 
endmodule

module MFC_MTC (
  input  [10:0] in_1,
  output MFC,
  output MTC
);

  Comparator #(.width(11), .mode("twosComplement")) comparator_1 (.a(in_1), .b(11'h200), .eq(MFC));  // open: gt, lt
  Comparator #(.width(11), .mode("twosComplement")) comparator_2 (.a(in_1), .b(11'h204), .eq(MTC));  // open: gt, lt
endmodule

module teamwork (
  input  in_1,
  input  \中断源 ,
  input  RST,
  output out_4,
  output out_5,
  output out_6,
  output enable,
  output [6:0] X,
  output CLK,
  output [6:0] Y,
  output RST_2,
  output [15:0] clolor
);

  wire ALU_SRC, and_1_out, and_2_out, and_3_out, and_4_out, and_5_out, and_6_out, and_7_out, and_9_out,
       and_10_out, and_12_out, and_14_out, Beq, Bne, comparator_3_gt, comparator_4_eq, comparator_5_eq,
       comparator_6_eq, d_ff_1_q, decoder_1_out1, decoder_1_out2, decoder_1_out3, down, Equal, ERET,
       Exception, Go, Halt, JAL, JMP, JR, left, MemToReg, MemWrite, MFC, MTC, multiplexer_13_out, nIE_q,
       not_1_out, or_1_out, or_2_out, or_3_out, or_4_out, or_5_out, or_7_out, RegDst, RegWrite, right,
       SignedExt, SysCALL, up, \中断按键参考电路_1_ir_2 , \中断按键参考电路_2_ir_2 , \中断按键参考电路_3_ir_2 , \中断按键参考电路_4_ir_2 ,
       \中断按键参考电路_5_ir_2 , \中断按键参考电路_6_ir_2 , \中断按键参考电路_7_ir_2 ;
  wire [0:0] comparator_7_lt, comparator_8_lt, or_6_out;
  wire [1:0] ExcepType, Execp2_q, Execp3_q, MDin, multiplexer_1_out, multiplexer_4_out, multiplexer_5_out,
       Pri, priority_encoder_1_out;
  wire [3:0] ALU_OP;
  wire [4:0] multiplexer_6_out, R1_num, R2_num, w_num;
  wire [5:0] FUNC;
  wire [15:0] \总周期数 , \无条件分支数 , \条件分支成功数 ;
  wire [27:0] adder_1_out;
  wire [31:0] adder_2_out, adder_3_out, AND_15_out, bit_extender_1_out, bit_extender_2_out, Din,
       divider_1_out, divider_1_rem, EPC1_q, EPC2_q, EPC3_q, in_PC, LedData, multiplexer_3_out,
       multiplexer_10_out, multiplexer_12_out, multiplexer_14_out, multiplexer_16_out, multiplexer_17_out,
       multiplexer_19_out, multiplier_1_cout, multiplier_1_out, next_PC, NOR_out, OR_9_out, PC, R1,
       ram_1_data, Result, Result2, shifter_1_out, shifter_2_out, shifter_3_out, shifter_4_out,
       subtractor_1_out, XOR_out, Y_t;
  wire [31:6] IR;
  wire [31:28] adder_1_out_2;

  Clock #(.highDuration(1), .lowDuration(1)) clock_1 (.out(CLK));
  Button \u_继续运行  (.out(Go));
  LED #(.active("true")) led_1 (.in(out_4));
  LED #(.active("true")) led_2 (.in(out_5));
  LED #(.active("true")) led_3 (.in(out_6));
  Hex_Digit_Display hex_digit_display_1 (.value(LedData[31:28]));  // open: dp
  Multiplexer #(.select(1), .width(2), .disabled("Z"), .enable("false")) multiplexer_1 (
    .in0(Pri), .in1(Execp2_q), .out(multiplexer_1_out), .sel(ERET));
  or or_1 (or_1_out, ERET, Exception);
  Hex_Digit_Display hex_digit_display_2 (.value(LedData[23:20]));  // open: dp
  Hex_Digit_Display hex_digit_display_3 (.value(LedData[27:24]));  // open: dp
  or or_2 (or_2_out, ~Halt, d_ff_1_q);  // OR_Gate
  Multiplexer #(.select(2), .width(32), .disabled("Z"), .enable("false")) multiplexer_2 (
    .in0({adder_1_out_2, adder_1_out}), .in1(adder_2_out), .in2(multiplexer_3_out), .out(next_PC),
    .sel({JMP, or_6_out[0]}));  // open: in3
  Multiplexer #(.select(1), .width(32), .disabled("Z"), .enable("false")) multiplexer_3 (
    .in0({adder_1_out_2, IR[25:6], FUNC, 2'b00}), .in1(R1), .out(multiplexer_3_out), .sel(JR));
  Register #(.width(2), .trigger("rising"), .Select("low")) Excep1 (
    .D(multiplexer_1_out), .en(or_1_out), .Q(ExcepType), .clk(CLK));  // open: clr
  Hex_Digit_Display hex_digit_display_4 (.value(LedData[15:12]));  // open: dp
  Hex_Digit_Display hex_digit_display_5 (.value(LedData[19:16]));  // open: dp
  Counter #(.width(16), .max('hffff), .ongoal("wrap"), .trigger("rising"), .behavior("old")) counter_1 (
    .count(or_6_out[0]), .Q(\条件分支成功数 ), .clk(CLK), .clr(RST));  // open: load, D, carry, preset
  Counter #(.width(16), .max('hffff), .ongoal("wrap"), .trigger("rising"), .behavior("old")) counter_2 (
    .count(JMP), .Q(\无条件分支数 ), .clk(CLK), .clr(RST));  // open: load, D, carry, preset
  Register #(.width(32), .trigger("rising"), .Select("low")) u_PC (
    .D(in_PC), .en(or_2_out), .Q(PC), .clk(CLK), .clr(RST));
  Multiplexer #(.select(1), .width(2), .disabled("Z"), .enable("false")) multiplexer_4 (
    .in0(ExcepType), .in1(Execp3_q), .out(multiplexer_4_out), .sel(ERET));
  Register #(.width(2), .trigger("rising"), .Select("low")) Execp2 (
    .D(multiplexer_4_out), .en(or_1_out), .Q(Execp2_q), .clk(CLK));  // open: clr
  Hex_Digit_Display hex_digit_display_6 (.value(LedData[7:4]));  // open: dp
  Hex_Digit_Display hex_digit_display_7 (.value(LedData[11:8]));  // open: dp
  D_Flip_Flop #(.trigger("rising"), .Pre_Clr_Positions("LEGACY"), .NegatePresetClear("false"), .enable("true"), .NewFFLayout("false")) d_ff_1 (
    .clk(CLK), .D(1'b0), .Q(d_ff_1_q), .preset(Go), .reset(RST));  // open: Qn, en
  Adder #(.width(32)) adder_1 (.a(PC), .b(32'h4), .out({adder_1_out_2, adder_1_out}));  // open: cin, cout
  \运算控制器自动生成  \u_运算控制器自动生成_1  (
    .OP0(IR[26]), .OP1(IR[27]), .OP2(IR[28]), .OP3(IR[29]), .OP4(IR[30]), .OP5(IR[31]), .F0(FUNC[0]),
    .F1(FUNC[1]), .F2(FUNC[2]), .F3(FUNC[3]), .F4(FUNC[4]), .F5(FUNC[5]), .S0(ALU_OP[0]), .S1(ALU_OP[1]),
    .S2(ALU_OP[2]), .S3(ALU_OP[3]));
  \控制信号自动生成  \u_控制信号自动生成_1  (
    .OP0(IR[26]), .OP1(IR[27]), .OP2(IR[28]), .OP3(IR[29]), .OP4(IR[30]), .OP5(IR[31]), .F0(FUNC[0]),
    .F1(FUNC[1]), .F2(FUNC[2]), .F3(FUNC[3]), .F4(FUNC[4]), .F5(FUNC[5]), .MemToReg(MemToReg),
    .MemWrite(MemWrite), .ALU_SRC(ALU_SRC), .RegWrite(RegWrite), .SysCALL(SysCALL), .SignedExt(SignedExt),
    .RegDst(RegDst), .BEQ(Beq), .BNE(Bne), .JR(JR), .JMP(JMP), .JAL(JAL), .ERET(ERET));
  Multiplexer #(.select(1), .width(2), .disabled("Z"), .enable("false")) multiplexer_5 (
    .in0(Execp2_q), .in1(2'b00), .out(multiplexer_5_out), .sel(ERET));
  Decoder #(.select(2), .tristate("false"), .disabled("Z"), .enable("false")) decoder_1 (
    .out1(decoder_1_out1), .out2(decoder_1_out2), .out3(decoder_1_out3), .sel(ExcepType));  // open: out0
  Hex_Digit_Display hex_digit_display_8 (.value(LedData[3:0]));  // open: dp
  // Probe on \总周期数 
  Adder #(.width(32)) adder_2 (
    .a({adder_1_out_2, adder_1_out}), .b(shifter_1_out), .out(adder_2_out));  // open: cin, cout
  Register #(.width(2), .trigger("rising"), .Select("low")) Execp3 (
    .D(multiplexer_5_out), .en(or_1_out), .Q(Execp3_q), .clk(CLK));  // open: clr
  and and_1 (and_1_out, ERET, decoder_1_out1);
  and and_2 (and_2_out, ERET, decoder_1_out2);
  and and_3 (and_3_out, ERET, decoder_1_out3);
  ROM #(.addrWidth(11), .dataWidth(32), .Select("high")) rom_1 (.addr(PC[12:2]), .data({IR, FUNC}));
  or or_3 (or_3_out, left, right, up, down);
  and and_4 (and_4_out, left, ~out_4);  // AND_Gate
  and and_5 (and_5_out, right, ~out_4);  // AND_Gate
  and and_6 (and_6_out, up, ~out_4);  // AND_Gate
  and and_7 (and_7_out, down, ~out_4);  // AND_Gate
  \中断按键参考电路  \u_中断按键参考电路_1  (.IR_2(\中断按键参考电路_1_ir_2 ), .Clr(and_1_out), .clk(CLK), .W(out_4), .IR(or_3_out));
  \中断按键参考电路  \u_中断按键参考电路_2  (.IR_2(\中断按键参考电路_2_ir_2 ), .Clr(and_2_out), .clk(CLK), .W(out_5), .IR(in_1));
  \中断按键参考电路  \u_中断按键参考电路_3  (.IR_2(\中断按键参考电路_3_ir_2 ), .Clr(and_3_out), .clk(CLK), .W(out_6), .IR(\中断源 ));
  \中断按键参考电路  \u_中断按键参考电路_4  (.IR_2(\中断按键参考电路_4_ir_2 ), .Clr(and_1_out), .clk(CLK), .IR(and_4_out));  // open: W
  \中断按键参考电路  \u_中断按键参考电路_5  (.IR_2(\中断按键参考电路_5_ir_2 ), .Clr(and_1_out), .clk(CLK), .IR(and_5_out));  // open: W
  \中断按键参考电路  \u_中断按键参考电路_6  (.IR_2(\中断按键参考电路_6_ir_2 ), .Clr(and_1_out), .clk(CLK), .IR(and_6_out));  // open: W
  \中断按键参考电路  \u_中断按键参考电路_7  (.IR_2(\中断按键参考电路_7_ir_2 ), .Clr(and_1_out), .clk(CLK), .IR(and_7_out));  // open: W
  Multiplexer #(.select(1), .width(5), .disabled("Z"), .enable("false")) multiplexer_6 (
    .in0(IR[20:16]), .in1(IR[15:11]), .out(multiplexer_6_out), .sel(RegDst));
  assign bit_extender_1_out = {{16{1'b0}}, {IR[15:6], FUNC}};  // Bit_Extender bit_extender_1
  assign bit_extender_2_out = {{16{IR[15]}}, {IR[15:6], FUNC}};  // Bit_Extender bit_extender_2
  Priority_Encoder #(.select(2), .disabled("Z")) priority_encoder_1 (
    .in0(\中断按键参考电路_4_ir_2 ), .in1(\中断按键参考电路_5_ir_2 ), .in2(\中断按键参考电路_6_ir_2 ), .in3(\中断按键参考电路_7_ir_2 ),
    .out(priority_encoder_1_out));  // open: gs, en_out, en_in
  Multiplexer #(.select(1), .width(5), .disabled("Z"), .enable("false")) multiplexer_7 (
    .in0(IR[25:21]), .in1(5'b00010), .out(R1_num), .sel(SysCALL));
  Multiplexer #(.select(1), .width(5), .disabled("Z"), .enable("false")) multiplexer_8 (
    .in0(IR[20:16]), .in1(5'b00100), .out(R2_num), .sel(SysCALL));
  Multiplexer #(.select(1), .width(5), .disabled("Z"), .enable("false")) multiplexer_9 (
    .in0(multiplexer_6_out), .in1({5{1'b1}}), .out(w_num), .sel(JAL));
  Shifter #(.width(32), .shift("ll")) shifter_1 (.in(bit_extender_2_out), .\dist (5'b00010), .out(shifter_1_out));
  Comparator #(.width(11), .mode("twosComplement")) comparator_1 (
    .a(IR[31:21]), .b(11'h200), .eq(MFC));  // open: gt, lt
  Comparator #(.width(11), .mode("twosComplement")) comparator_2 (
    .a(IR[31:21]), .b(11'h204), .eq(MTC));  // open: gt, lt
  or or_4 (or_4_out, Exception, ERET, MFC, MTC);
  Pull_Resistor #(.pull(0)) pull_resistor_1 (.node(Pri));
  Priority_Encoder #(.select(2), .disabled("Z")) priority_encoder_2 (
    .in1(\中断按键参考电路_1_ir_2 ), .in2(\中断按键参考电路_2_ir_2 ), .in3(\中断按键参考电路_3_ir_2 ), .out(Pri), .en_in(1'b1));  // open: in0, gs, en_out
  Multiplexer #(.select(2), .width(32), .disabled("Z"), .enable("false")) multiplexer_10 (
    .in0(32'h17c), .in1(32'h404), .in2(32'h68c), .in3(32'h914), .out(multiplexer_10_out),
    .sel(priority_encoder_1_out));
  Multiplexer #(.select(1), .width(32), .disabled("Z"), .enable("false")) multiplexer_11 (
    .in0(multiplexer_16_out), .in1({adder_1_out_2, adder_1_out}), .out(Din), .sel(JAL));
  Multiplexer #(.select(1), .width(32), .disabled("Z"), .enable("false")) multiplexer_12 (
    .in0(bit_extender_1_out), .in1(bit_extender_2_out), .out(multiplexer_12_out), .sel(SignedExt));
  or or_5 (or_5_out, MTC, Exception);
  Multiplexer #(.select(1), .width(1), .disabled("Z"), .enable("false")) multiplexer_13 (
    .in0(1'b0), .in1(1'b1), .out(multiplexer_13_out), .sel(or_5_out));
  Register #(.width(1), .trigger("rising"), .Select("low")) nIE (
    .D(multiplexer_13_out), .en(or_4_out), .Q(nIE_q), .clk(CLK));  // open: clr
  Multiplexer #(.select(2), .width(32), .disabled("Z"), .enable("false")) multiplexer_14 (
    .in0({32{1'b0}}), .in1(multiplexer_10_out), .in2({32{1'b0}}), .in3({32{1'b0}}), .out(multiplexer_14_out),
    .sel(Pri));
  Counter #(.width(16), .max('hffff), .ongoal("wrap"), .trigger("rising"), .behavior("old")) counter_3 (
    .count(not_1_out), .Q(\总周期数 ), .clk(CLK), .clr(RST));  // open: load, D, carry, preset
  not not_1 (not_1_out, Halt);
  Comparator #(.width(2), .mode("unsigned")) comparator_3 (
    .a(Pri), .b(ExcepType), .gt(comparator_3_gt));  // open: eq, lt
  Multiplexer #(.select(1), .width(32), .disabled("Z"), .enable("false")) multiplexer_15 (
    .in0({X, Y, clolor, MDin}), .in1(multiplexer_12_out), .out(Y_t), .sel(ALU_SRC));
  and and_8 (Exception, ~nIE_q, comparator_3_gt);  // AND_Gate
  Multiplexer #(.select(1), .width(32), .disabled("Z"), .enable("false")) multiplexer_16 (
    .in0(Result), .in1(ram_1_data), .out(multiplexer_16_out), .sel(MemToReg));
  Multiplexer #(.select(1), .width(32), .disabled("Z"), .enable("false")) multiplexer_17 (
    .in0(next_PC), .in1(EPC2_q), .out(multiplexer_17_out), .sel(ERET));
  Multiplexer #(.select(2), .width(32), .disabled("Z"), .enable("false")) multiplexer_18 (
    .in0(next_PC), .in1(multiplexer_14_out), .in2(EPC1_q), .out(in_PC), .sel({ERET, Exception}));  // open: in3
  and and_9 (and_9_out, Equal, Beq);
  or or_6 (or_6_out[0], and_9_out, and_10_out);
  and and_10 (and_10_out, ~Equal, Bne);  // AND_Gate
  Register #(.width(32), .trigger("rising"), .Select("low")) EPC1 (
    .D(multiplexer_17_out), .en(or_7_out), .Q(EPC1_q), .clk(CLK));  // open: clr
  or or_7 (or_7_out, ERET, Exception);
  Multiplexer #(.select(1), .width(32), .disabled("Z"), .enable("false")) multiplexer_19 (
    .in0(EPC1_q), .in1(EPC3_q), .out(multiplexer_19_out), .sel(ERET));
  RAM #(.addrWidth(24), .dataWidth(32), .bus("separate"), .Select("high")) ram_1 (
    .addr(Result[25:2]), .din({X, Y, clolor, MDin}), .data(ram_1_data), .str(MemWrite), .clk(CLK));  // open: sel, ld, clr
  Register #(.width(32), .trigger("rising"), .Select("low")) EPC2 (
    .D(multiplexer_19_out), .en(or_7_out), .Q(EPC2_q), .clk(CLK));  // open: clr
  Register #(.width(32), .trigger("rising"), .Select("low")) EPC3 (
    .D(EPC2_q), .en(Exception), .Q(EPC3_q), .clk(CLK));  // open: clr
  Comparator #(.width(32), .mode("twosComplement")) comparator_4 (
    .a(R1), .b(32'h32), .eq(comparator_4_eq));  // open: gt, lt
  Comparator #(.width(32), .mode("twosComplement")) comparator_5 (
    .a(R1), .b(32'h22), .eq(comparator_5_eq));  // open: gt, lt
  Comparator #(.width(32), .mode("twosComplement")) comparator_6 (
    .a(R1), .b(32'h147), .eq(comparator_6_eq));  // open: gt, lt
  Button button_1 (.out(up));
  Button button_2 (.out(left));
  Button button_3 (.out(down));
  and and_11 (Halt, comparator_4_eq, SysCALL);
  and and_12 (and_12_out, comparator_5_eq, SysCALL);
  and and_13 (enable, comparator_6_eq, SysCALL);
  Button button_4 (.out(right));
  Register #(.width(32), .trigger("rising"), .Select("low")) register_1 (
    .D({X, Y, clolor, MDin}), .en(and_12_out), .Q(LedData), .clk(CLK), .clr(RST));
  // RegisterFile registerfile_1: pin names not known; wires that end beside it: Din, CLK, RegWrite, w_num, R1_num, R2_num, R1, {X, Y, clolor, MDin}
  or or_8 (RST_2, RST, and_14_out);
  and and_14 (and_14_out, enable, MDin[1]);
  // LCD_Video lcd_video_1: pin names not known; wires that end beside it: RST_2, CLK, enable, X, Y, clolor
  Shifter #(.width(32), .shift("ll")) shifter_2 (.in(Y_t), .\dist (IR[10:6]), .out(shifter_2_out));
  Shifter #(.width(32), .shift("ar")) shifter_3 (.in(Y_t), .\dist (IR[10:6]), .out(shifter_3_out));
  Shifter #(.width(32), .shift("lr")) shifter_4 (.in(Y_t), .\dist (IR[10:6]), .out(shifter_4_out));
  Multiplier #(.width(32)) multiplier_1 (
    .a(R1), .b(Y_t), .out(multiplier_1_out), .cout(multiplier_1_cout));  // open: cin
  Divider #(.width(32)) divider_1 (.a(R1), .b(Y_t), .out(divider_1_out), .rem(divider_1_rem));  // open: upper
  Adder #(.width(32)) adder_3 (.a(R1), .b(Y_t), .out(adder_3_out));  // open: cin, cout
  Subtractor #(.width(32)) subtractor_1 (.a(R1), .b(Y_t), .out(subtractor_1_out));  // open: bin, bout
  assign AND_15_out = R1 & Y_t;  // AND_Gate AND_15, 32 bits wide
  assign OR_9_out = R1 | Y_t;  // OR_Gate OR_9, 32 bits wide
  assign XOR_out = R1 ^ Y_t;  // XOR_Gate XOR, 32 bits wide
  assign NOR_out = ~(R1 | Y_t);  // NOR_Gate NOR, 32 bits wide
  Comparator #(.width(32), .mode("twosComplement")) comparator_7 (
    .a(R1), .b(Y_t), .eq(Equal), .lt(comparator_7_lt[0]));  // open: gt
  Comparator #(.width(32), .mode("unsigned")) comparator_8 (.a(R1), .b(Y_t), .lt(comparator_8_lt[0]));  // open: gt, eq
  Multiplexer #(.select(4), .width(32), .disabled("Z"), .enable("false")) multiplexer_20 (
    .in0(shifter_2_out), .in1(shifter_3_out), .in2(shifter_4_out), .in3(multiplier_1_out),
    .in4(divider_1_out), .in5(adder_3_out), .in6(subtractor_1_out), .in7(AND_15_out), .in8(OR_9_out),
    .in9(XOR_out), .in10(NOR_out), .in11({{31{1'b0}}, comparator_7_lt[0]}),
    .in12({{31{1'b0}}, comparator_8_lt[0]}), .in13({32{1'b0}}), .in14({32{1'b0}}), .in15({32{1'b0}}),
    .out(Result), .sel(ALU_OP));
  Multiplexer #(.select(4), .width(32), .disabled("Z"), .enable("false")) multiplexer_21 (
    .in0({32{1'b0}}), .in1({32{1'b0}}), .in2({32{1'b0}}), .in3(multiplier_1_cout), .in4(divider_1_rem),
    .in5({32{1'b0}}), .in6({32{1'b0}}), .in7({32{1'b0}}), .in8({32{1'b0}}), .in9({32{1'b0}}),
    .in10({32{1'b0}}), .in11({32{1'b0}}), .in12({32{1'b0}}), .in13({32{1'b0}}), .in14({32{1'b0}}),
    .in15({32{1'b0}}), .out(Result2), .sel(ALU_OP));

  // Other names for the same wires on the sheet: IR[5:0] = FUNC; shamt[4:0] = IR[10:6]; OP_CODE[5:0] = IR[31:26];
  //   IR2 = in_1; IR3 = \中断源 ; R2[31:0] = {X, Y, clolor, MDin}; MDin[31:2] = {X, Y, clolor}; RDin[31:0] = Din;
  //   S[3:0] = ALU_OP; W1 = out_4; W2 = out_5; W3 = out_6; WE = RegWrite; X_t[31:0] = R1

  // Notes on the sheet:
  //   中断等待指示
  //   总复位信号应将除ROM以外所有存储组件全部清零
  //   单周期硬布线控制器
  //   中断相应逻辑
  //   数码管输出
  //   数码管输出应该用寄存器锁存，否则显示数据只能一闪而过
  //   instr_index
  //   contents of rom_1 (hex, n*v repeats v):
  //   201c1800 201d3ffc af800008 201a0000 201b0000 1a4100 11b4020 84080 8d060800 10c00008 20080003
  //   14c80003 8f880008 20080001 af880008 1a2020 1b2820 c00001b 237b0001 20080010 1768fff0 235a0001
  //   20080010 1748ffec 8000018 20020032 c 23bd0018 afa80000 afb0fffc afb1fff8 afb2fff4 afb3fff0 afb4ffec
  //   10c0000f 20080001 10c8000f 20080002 10c8000f 20080003 10c80011 20080004 10c80011 20080005 10c80011
  //   20080006 10c80007 8fa80000 23bdffe8 3e00008 20100000 800003f 20100100 800003f af840000 af850004
  //   20100200 800003f 20100300 800003f 20100400 800003f 20100500 488c0 20120000 598c0 20140000 124020
  //   840c0 1144020 84080 1104020 8d040000 2744020 84480 882020 2324020 84640 882020 20020147 c 22940001
  //   20080008 1688ffef 22520001 20080008 1648ffea 8fa80000 8fb0fffc 8fb1fff8 8fb2fff4 8fb3fff0 8fb4ffec
  //   23bdffe8 3e00008 23bd002c afa80000 afa9fffc afaafff8 afb0fff4 afb1fff0 afb2ffec afb3ffe8 afb4ffe4
  //   afa4ffe0 afa5ffdc afa6ffd8 8f900000 8f910004 104100 1114020 84080 8d120800 2209ffff 94100 1114020
  //   84080 8d130800 12600008 20080001 1268007b 20080003 12680006 20080004 12680028 20080005 12680028
  //   200a0002 80000ca 2209fffe 94100 1114020 84080 8d140800 12800003 20080004 1288000d 80000f4 200a0003
  //   2209fffe 94100 1114020 84080 ad0a0800 92020 112820 a3020 c00001b 200a0002 80000ca 8f880008 2008ffff
  //   af880008 200a0005 2209fffe 94100 1114020 84080 ad0a0800 92020 112820 a3020 c00001b 200a0002 80000ca
  //   200a0006 80000ca 2209fffe 94100 1114020 84080 8d140800 12800003 20080004 12880010 80000f4 8f880008
  //   20080001 af880008 200a0003 2209fffe 94100 1114020 84080 ad0a0800 92020 112820 a3020 c00001b 200a0006
  //   80000ca 200a0005 2209fffe 94100 1114020 84080 ad0a0800 92020 112820 a3020 c00001b 200a0006 2209ffff
  //   94100 1114020 84080 ad0a0800 92020 112820 a3020 c00001b 20080006 12480016 200a0000 104100 1114020
  //   84080 ad0a0800 102020 112820 a3020 c00001b 8fa80000 8fa9fffc 8faafff8 8fb0fff4 8fb1fff0 8fb2ffec
  //   8fb3ffe8 8fb4ffe4 8fa4ffe0 8fa5ffdc 8fa6ffd8 23bdffd4 42000018 200a0004 104100 1114020 84080
  //   ad0a0800 102020 112820 a3020 c00001b 8fa80000 8fa9fffc 8faafff8 8fb0fff4 8fb1fff0 8fb2ffec 8fb3ffe8
  //   8fb4ffe4 8fa4ffe0 8fa5ffdc 8fa6ffd8 23bdffd4 42000018 23bd002c afa80000 afa9fffc afaafff8 afb0fff4
  //   afb1fff0 afb2ffec afb3ffe8 afb4ffe4 afa4ffe0 afa5ffdc afa6ffd8 8f900000 8f910004 104100 1114020
  //   84080 8d120800 22090001 94100 1114020 84080 8d130800 12600008 20080001 1268007b 20080003 12680006
  //   20080004 12680028 20080005 12680028 200a0002 800016c 22090002 94100 1114020 84080 8d140800 12800003
  //   20080004 1288000d 8000196 200a0003 22090002 94100 1114020 84080 ad0a0800 92020 112820 a3020 c00001b
  //   200a0002 800016c 8f880008 2008ffff af880008 200a0005 22090002 94100 1114020 84080 ad0a0800 92020
  //   112820 a3020 c00001b 200a0002 800016c 200a0006 800016c 22090002 94100 1114020 84080 8d140800
  //   12800003 20080004 12880010 8000196 8f880008 20080001 af880008 200a0003 22090002 94100 1114020 84080
  //   ad0a0800 92020 112820 a3020 c00001b 200a0006 800016c 200a0005 22090002 94100 1114020 84080 ad0a0800
  //   92020 112820 a3020 c00001b 200a0006 22090001 94100 1114020 84080 ad0a0800 92020 112820 a3020 c00001b
  //   20080006 12480016 200a0000 104100 1114020 84080 ad0a0800 102020 112820 a3020 c00001b 8fa80000
  //   8fa9fffc 8faafff8 8fb0fff4 8fb1fff0 8fb2ffec 8fb3ffe8 8fb4ffe4 8fa4ffe0 8fa5ffdc 8fa6ffd8 23bdffd4
  //   42000018 200a0004 104100 1114020 84080 ad0a0800 102020 112820 a3020 c00001b 8fa80000 8fa9fffc
  //   8faafff8 8fb0fff4 8fb1fff0 8fb2ffec 8fb3ffe8 8fb4ffe4 8fa4ffe0 8fa5ffdc 8fa6ffd8 23bdffd4 42000018
  //   23bd002c afa80000 afa9fffc afaafff8 afb0fff4 afb1fff0 afb2ffec afb3ffe8 afb4ffe4 afa4ffe0 afa5ffdc
  //   afa6ffd8 8f900000 8f910004 104100 1114020 84080 8d120800 104100 2229ffff 1094020 84080 8d130800
  //   12600008 20080001 1268007b 20080003 12680006 20080004 12680028 20080005 12680028 200a0002 800020e
  //   104100 2229fffe 1094020 84080 8d140800 12800003 20080004 1288000d 8000238 200a0003 104100 2229fffe
  //   1094020 84080 ad0a0800 102020 92820 a3020 c00001b 200a0002 800020e 8f880008 2008ffff af880008
  //   200a0005 104100 2229fffe 1094020 84080 ad0a0800 102020 92820 a3020 c00001b 200a0002 8000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
  //   运算器控制器，根据指令生成运算器功能选择信号
  //   rs
  //   rt
  //   rd
  //   imm
  //   sa
  //   Syscall
  //   v0
  //   a0
  //   Beq
  //   Bne
  //   MemToReg
  //   MemWrite
  //   AluOP
  //   AluSrcB
  //   显像逻辑
  //   Regfile
  //   ALU
endmodule
